// Logisim project Mouse Prototype(evol).circ as structural Verilog: 1 circuit, main circuit main
module main (
);

  wire adder_1_cout, adder_2_cout, and_1_out, and_2_out, and_3_out, and_4_out, and_5_out, and_6_out,
       clock_1_out, comparator_1_eq, comparator_2_eq, comparator_3_eq, comparator_4_eq,
       controlled_buffer_1_out, controlled_buffer_3_out, or_1_out, or_2_out, or_3_out, subtractor_1_bout,
       subtractor_2_bout;
  wire [1:0] joystick_1_x, joystick_1_y;
  wire [4:0] adder_1_out, adder_2_out, multiplexer_1_out, multiplexer_2_out, register_1_q, register_2_q,
       subtractor_1_out, subtractor_2_out;
  wire [31:0] decoder_1_out0, demultiplexer_1_out0, demultiplexer_1_out1, demultiplexer_1_out2,
       demultiplexer_1_out3, demultiplexer_1_out4, demultiplexer_1_out5, demultiplexer_1_out6,
       demultiplexer_1_out7, demultiplexer_1_out8, demultiplexer_1_out9, demultiplexer_1_out10,
       demultiplexer_1_out11, demultiplexer_1_out12, demultiplexer_1_out13, demultiplexer_1_out14,
       demultiplexer_1_out15, demultiplexer_1_out16, demultiplexer_1_out17, demultiplexer_1_out18,
       demultiplexer_1_out19, demultiplexer_1_out20, demultiplexer_1_out21, demultiplexer_1_out22,
       demultiplexer_1_out23, demultiplexer_1_out24, demultiplexer_1_out25, demultiplexer_1_out26,
       demultiplexer_1_out27, demultiplexer_1_out28, demultiplexer_1_out29, demultiplexer_1_out30,
       demultiplexer_1_out31;

  // Probe on joystick_1_x
  Joystick #(.bits(2)) joystick_1 (.x(joystick_1_x), .y(joystick_1_y));
  // Probe on joystick_1_y
  Clock clock_1 (.out(clock_1_out));
  Demultiplexer #(.enable("false"), .select(5), .width(32)) demultiplexer_1 (
    .out0(demultiplexer_1_out0), .out1(demultiplexer_1_out1), .out2(demultiplexer_1_out2),
    .out3(demultiplexer_1_out3), .out4(demultiplexer_1_out4), .out5(demultiplexer_1_out5),
    .out6(demultiplexer_1_out6), .out7(demultiplexer_1_out7), .out8(demultiplexer_1_out8),
    .out9(demultiplexer_1_out9), .out10(demultiplexer_1_out10), .out11(demultiplexer_1_out11),
    .out12(demultiplexer_1_out12), .out13(demultiplexer_1_out13), .out14(demultiplexer_1_out14),
    .out15(demultiplexer_1_out15), .out16(demultiplexer_1_out16), .out17(demultiplexer_1_out17),
    .out18(demultiplexer_1_out18), .out19(demultiplexer_1_out19), .out20(demultiplexer_1_out20),
    .out21(demultiplexer_1_out21), .out22(demultiplexer_1_out22), .out23(demultiplexer_1_out23),
    .out24(demultiplexer_1_out24), .out25(demultiplexer_1_out25), .out26(demultiplexer_1_out26),
    .out27(demultiplexer_1_out27), .out28(demultiplexer_1_out28), .out29(demultiplexer_1_out29),
    .out30(demultiplexer_1_out30), .out31(demultiplexer_1_out31), .in(decoder_1_out0), .sel(register_1_q));
  Decoder #(.enable("false"), .select(5)) decoder_1 (
    .out0(decoder_1_out0[0]), .out1(decoder_1_out0[1]), .out2(decoder_1_out0[2]), .out3(decoder_1_out0[3]),
    .out4(decoder_1_out0[4]), .out5(decoder_1_out0[5]), .out6(decoder_1_out0[6]), .out7(decoder_1_out0[7]),
    .out8(decoder_1_out0[8]), .out9(decoder_1_out0[9]), .out10(decoder_1_out0[10]),
    .out11(decoder_1_out0[11]), .out12(decoder_1_out0[12]), .out13(decoder_1_out0[13]),
    .out14(decoder_1_out0[14]), .out15(decoder_1_out0[15]), .out16(decoder_1_out0[16]),
    .out17(decoder_1_out0[17]), .out18(decoder_1_out0[18]), .out19(decoder_1_out0[19]),
    .out20(decoder_1_out0[20]), .out21(decoder_1_out0[21]), .out22(decoder_1_out0[22]),
    .out23(decoder_1_out0[23]), .out24(decoder_1_out0[24]), .out25(decoder_1_out0[25]),
    .out26(decoder_1_out0[26]), .out27(decoder_1_out0[27]), .out28(decoder_1_out0[28]),
    .out29(decoder_1_out0[29]), .out30(decoder_1_out0[30]), .out31(decoder_1_out0[31]), .sel(register_2_q));
  or or_1 (or_1_out, comparator_1_eq, comparator_2_eq, comparator_4_eq, comparator_3_eq);
  Comparator #(.width(2)) comparator_1 (.a(2'b01), .b(joystick_1_x), .eq(comparator_1_eq));  // open: gt, lt
  Comparator #(.width(2)) comparator_2 (.a(2'b11), .b(joystick_1_x), .eq(comparator_2_eq));  // open: gt, lt
  Comparator #(.width(2)) comparator_3 (.a(2'b01), .b(joystick_1_y), .eq(comparator_3_eq));  // open: gt, lt
  Comparator #(.width(2)) comparator_4 (.a(2'b11), .b(joystick_1_y), .eq(comparator_4_eq));  // open: gt, lt
  DotMatrix #(.inputtype("row"), .matrixcols(32), .matrixrows(32)) dotmatrix_1 (
    .row0(demultiplexer_1_out0), .row1(demultiplexer_1_out1), .row2(demultiplexer_1_out2),
    .row3(demultiplexer_1_out3), .row4(demultiplexer_1_out4), .row5(demultiplexer_1_out5),
    .row6(demultiplexer_1_out6), .row7(demultiplexer_1_out7), .row8(demultiplexer_1_out8),
    .row9(demultiplexer_1_out9), .row10(demultiplexer_1_out10), .row11(demultiplexer_1_out11),
    .row12(demultiplexer_1_out12), .row13(demultiplexer_1_out13), .row14(demultiplexer_1_out14),
    .row15(demultiplexer_1_out15), .row16(demultiplexer_1_out16), .row17(demultiplexer_1_out17),
    .row18(demultiplexer_1_out18), .row19(demultiplexer_1_out19), .row20(demultiplexer_1_out20),
    .row21(demultiplexer_1_out21), .row22(demultiplexer_1_out22), .row23(demultiplexer_1_out23),
    .row24(demultiplexer_1_out24), .row25(demultiplexer_1_out25), .row26(demultiplexer_1_out26),
    .row27(demultiplexer_1_out27), .row28(demultiplexer_1_out28), .row29(demultiplexer_1_out29),
    .row30(demultiplexer_1_out30), .row31(demultiplexer_1_out31));
  Multiplexer #(.enable("false"), .width(5)) multiplexer_1 (
    .in0(adder_1_out), .in1(subtractor_1_out), .out(multiplexer_1_out), .sel(controlled_buffer_1_out));
  Multiplexer #(.enable("false"), .width(5)) multiplexer_2 (
    .in0(adder_2_out), .in1(subtractor_2_out), .out(multiplexer_2_out), .sel(controlled_buffer_3_out));
  Register #(.width(5)) register_1 (
    .D(multiplexer_1_out), .en(and_1_out), .Q(register_1_q), .clk(clock_1_out));  // open: clr
  and and_1 (and_1_out, or_1_out, or_2_out);
  or or_2 (or_2_out, comparator_4_eq, comparator_3_eq);
  Register #(.width(5)) register_2 (
    .D(multiplexer_2_out), .en(and_2_out), .Q(register_2_q), .clk(clock_1_out));  // open: clr
  and and_2 (and_2_out, or_1_out, or_3_out);
  or or_3 (or_3_out, comparator_1_eq, comparator_2_eq);
  Adder #(.width(5)) adder_1 (.a(5'b00001), .b(register_1_q), .out(adder_1_out), .cout(adder_1_cout));  // open: cin
  Subtractor #(.width(5)) subtractor_1 (
    .a(register_1_q), .b(5'b00001), .out(subtractor_1_out), .bout(subtractor_1_bout));  // open: bin
  Adder #(.width(5)) adder_2 (.a(5'b00001), .b(register_2_q), .out(adder_2_out), .cout(adder_2_cout));  // open: cin
  Subtractor #(.width(5)) subtractor_2 (
    .a(register_2_q), .b(5'b00001), .out(subtractor_2_out), .bout(subtractor_2_bout));  // open: bin
  and and_3 (and_3_out, ~adder_1_cout, ~comparator_3_eq);  // AND_Gate
  and and_4 (and_4_out, ~subtractor_1_bout, ~comparator_4_eq);  // AND_Gate
  and and_5 (and_5_out, ~adder_2_cout, ~comparator_2_eq);  // AND_Gate
  and and_6 (and_6_out, ~subtractor_2_bout, ~comparator_1_eq);  // AND_Gate
  assign controlled_buffer_1_out = and_3_out ? 1'b0 : 1'bz;  // Controlled_Buffer controlled_buffer_1
  assign controlled_buffer_1_out = and_4_out ? 1'b1 : 1'bz;  // Controlled_Buffer controlled_buffer_2
  assign controlled_buffer_3_out = and_5_out ? 1'b0 : 1'bz;  // Controlled_Buffer controlled_buffer_3
  assign controlled_buffer_3_out = and_6_out ? 1'b1 : 1'bz;  // Controlled_Buffer controlled_buffer_4
endmodule
