// Logisim project modified_projet_kraken.circ as structural Verilog: 28 circuits, main circuit decoderv2
module main (
);

  wire and_1_out, and_2_out, and_3_out, and_4_out, button_4_out, clock_1_out, did_eat_shroom_1_out_3,
       display_2_1_out_13, memories_1_out_4, memories_2_out_4, movement_1_d0, movement_1_d1, movement_1_d2,
       movement_1_out, movement_2_d0, movement_2_d1, movement_2_d2, movement_2_out, or_1_out, or_2_out,
       score_1_out_5, score_1_out_6, score_1_out_7, score_1_out_8, score_1_out_9, score_1_out_10,
       score_1_out_11;
  wire [1:0] direction_1_gauche_2, direction_1_haut_2, joystick_1_x, joystick_1_y;
  wire [2:0] score_1_out_4;
  wire [5:0] shroom_generator_1_out_2, statememory_1_out_8;
  wire [7:0] display_2_1_out_8, display_2_1_out_9, display_2_1_out_10, display_2_1_out_11,
       display_2_1_out_12, display_2_1_out_14, display_2_1_out_15, display_2_1_out_16;

  Clock #(.highDuration(3), .lowDuration(3)) clock_1 (.out(clock_1_out));
  StateMemory statememory_1 (
    .out_6(statememory_1_out_8[2]), .out_7(statememory_1_out_8[1]), .out_8(statememory_1_out_8[0]),
    .Reset(button_4_out), .in_2(movement_1_d0), .in_3(movement_1_d1), .in_4(movement_1_d2), .in_5(clock_1_out));
  StateMemory statememory_2 (
    .out_6(statememory_1_out_8[5]), .out_7(statememory_1_out_8[4]), .out_8(statememory_1_out_8[3]),
    .Reset(button_4_out), .in_2(movement_2_d0), .in_3(movement_2_d1), .in_4(movement_2_d2), .in_5(clock_1_out));
  shroom_generator shroom_generator_1 (.out_2(shroom_generator_1_out_2), .in_1(score_1_out_4));
  Movement movement_1 (
    .D0(movement_1_d0), .D1(movement_1_d1), .D2(movement_1_d2), .Out(movement_1_out),
    .Q0(statememory_1_out_8[2]), .Q1(statememory_1_out_8[1]), .Q2(statememory_1_out_8[0]),
    .SensMoins(direction_1_haut_2[1]), .SensPlus(direction_1_haut_2[0]));
  or or_1 (or_1_out, movement_1_out, movement_2_out);
  Movement movement_2 (
    .D0(movement_2_d0), .D1(movement_2_d1), .D2(movement_2_d2), .Out(movement_2_out),
    .Q0(statememory_1_out_8[5]), .Q1(statememory_1_out_8[4]), .Q2(statememory_1_out_8[3]),
    .SensMoins(direction_1_gauche_2[0]), .SensPlus(direction_1_gauche_2[1]));
  did_eat_shroom did_eat_shroom_1 (
    .out_3(did_eat_shroom_1_out_3), .in_1(shroom_generator_1_out_2), .in_2(statememory_1_out_8));
  Pull_Resistor pull_resistor_1 (.node(statememory_1_out_8));
  _7_Segment_Display u_7_segment_display_1 (
    .g(score_1_out_11), .f(score_1_out_10), .a(score_1_out_5), .b(score_1_out_6), .e(score_1_out_9),
    .d(score_1_out_8), .c(score_1_out_7));  // open: dp
  or or_2 (or_2_out, memories_1_out_4, memories_2_out_4);
  memories memories_1 (.in_1(clock_1_out), .in_2(display_2_1_out_13), .in_3(button_4_out), .out_4(memories_1_out_4));
  score score_1 (
    .out_4(score_1_out_4), .out_5(score_1_out_5), .out_6(score_1_out_6), .out_8(score_1_out_8),
    .out_9(score_1_out_9), .out_10(score_1_out_10), .out_11(score_1_out_11), .out_7(score_1_out_7),
    .in_1(did_eat_shroom_1_out_3), .in_2(button_4_out), .clock(clock_1_out));
  LED led_1 (.in(or_2_out));
  memories memories_2 (.in_1(or_1_out), .in_2(clock_1_out), .in_3(button_4_out), .out_4(memories_2_out_4));
  DotMatrix #(.matrixcols(8), .matrixrows(8)) dotmatrix_1 (
    .col0(display_2_1_out_8), .col1(display_2_1_out_9), .col2(display_2_1_out_10), .col3(display_2_1_out_11),
    .col4(display_2_1_out_12), .col5(display_2_1_out_14), .col6(display_2_1_out_15), .col7(display_2_1_out_16));
  Button button_1 ();  // open: out
  Button button_2 ();  // open: out
  Button button_3 ();  // open: out
  display_2 display_2_1 (
    .out_16(display_2_1_out_16), .out_14(display_2_1_out_14), .out_15(display_2_1_out_15),
    .out_12(display_2_1_out_12), .out_9(display_2_1_out_9), .out_10(display_2_1_out_10),
    .out_11(display_2_1_out_11), .out_13(display_2_1_out_13), .out_8(display_2_1_out_8), .clokc(clock_1_out),
    .in_3(score_1_out_4[2]), .in_4(score_1_out_4[1]), .in_5(score_1_out_4[0]), .in_6(button_4_out),
    .in_1(shroom_generator_1_out_2), .in_2(statememory_1_out_8));
  Button button_4 (.out(button_4_out));
  Direction direction_1 (
    .Bas_2(direction_1_haut_2[1]), .Droite_2(direction_1_gauche_2[1]), .Haut_2(direction_1_haut_2[0]),
    .Gauche_2(direction_1_gauche_2[0]), .Haut(and_4_out), .Reset(button_4_out), .Bas(and_3_out),
    .Gauche(and_1_out), .Droite(and_2_out), .clock(clock_1_out));
  Button button_5 ();  // open: out
  Joystick #(.bits(2)) joystick_1 (.x(joystick_1_x), .y(joystick_1_y));
  and and_1 (and_1_out, joystick_1_x[0], ~joystick_1_x[1]);  // AND_Gate
  and and_2 (and_2_out, joystick_1_x[0], joystick_1_x[1]);
  and and_3 (and_3_out, joystick_1_y[0], joystick_1_y[1]);
  and and_4 (and_4_out, joystick_1_y[0], ~joystick_1_y[1]);  // AND_Gate
endmodule

module add_right (
  input  q5,
  input  q4,
  input  q3,
  output d5,
  output d4,
  output d3
);

  wire and_1_out, and_2_out, and_3_out, and_4_out, and_5_out, not_1_out, not_2_out, not_3_out, not_4_out,
       not_5_out;

  not not_1 (not_1_out, q5);
  not not_2 (not_2_out, q4);
  not not_3 (not_3_out, q3);
  not not_4 (not_4_out, q4);
  not not_5 (not_5_out, q3);
  not not_6 (d3, q3);
  and and_1 (and_1_out, not_1_out, q4, q3);
  and and_2 (and_2_out, q5, not_2_out);
  and and_3 (and_3_out, q5, not_3_out);
  and and_4 (and_4_out, not_4_out, q3);
  and and_5 (and_5_out, q4, not_5_out);
  or or_1 (d5, and_1_out, and_2_out, and_3_out);
  or or_2 (d4, and_4_out, and_5_out);
endmodule

module decoderv2 (
  input  Q0,
  input  Q1,
  input  Q2,
  input  activate,
  output a,
  output b,
  output c,
  output d,
  output e,
  output f,
  output g,
  output h
);

  wire not_1_out, not_2_out, not_3_out, not_4_out, not_5_out, not_6_out, not_7_out, not_8_out, not_9_out,
       not_10_out, not_11_out, not_12_out;

  not not_1 (not_1_out, Q0);
  not not_2 (not_2_out, Q1);
  not not_3 (not_3_out, Q2);
  not not_4 (not_4_out, Q1);
  not not_5 (not_5_out, Q2);
  not not_6 (not_6_out, Q0);
  not not_7 (not_7_out, Q2);
  not not_8 (not_8_out, Q2);
  not not_9 (not_9_out, Q0);
  not not_10 (not_10_out, Q1);
  not not_11 (not_11_out, Q1);
  not not_12 (not_12_out, Q0);
  and and_1 (h, Q0, Q1, Q2, activate);
  and and_2 (a, not_1_out, not_2_out, not_3_out, activate);
  and and_3 (b, Q0, not_4_out, not_5_out, activate);
  and and_4 (c, not_6_out, Q1, not_7_out, activate);
  and and_5 (d, Q0, Q1, not_8_out, activate);
  and and_6 (e, not_9_out, not_10_out, Q2, activate);
  and and_7 (f, Q0, not_11_out, Q2, activate);
  and and_8 (g, not_12_out, Q1, Q2, activate);
endmodule

module row_select0 (
  input  [2:0] row,
  input  [2:0] column,
  output [7:0] out_3
);

  wire and_1_out, not_1_out, not_2_out, not_3_out;

  not not_1 (not_1_out, column[0]);
  not not_2 (not_2_out, column[1]);
  not not_3 (not_3_out, column[2]);
  and and_1 (and_1_out, not_1_out, not_2_out, not_3_out);
  decoderv2 decoderv2_1 (
    .Q0(row[0]), .Q1(row[1]), .Q2(row[2]), .activate(and_1_out), .a(out_3[0]), .b(out_3[1]), .c(out_3[2]),
    .d(out_3[3]), .e(out_3[4]), .f(out_3[5]), .g(out_3[6]), .h(out_3[7]));
endmodule

module row_select1 (
  input  [2:0] row,
  input  [2:0] column,
  output [7:0] out_3
);

  wire and_1_out, not_1_out, not_2_out;

  not not_1 (not_1_out, column[1]);
  not not_2 (not_2_out, column[2]);
  and and_1 (and_1_out, column[0], not_1_out, not_2_out);
  decoderv2 decoderv2_1 (
    .Q0(row[0]), .Q1(row[1]), .Q2(row[2]), .activate(and_1_out), .a(out_3[0]), .b(out_3[1]), .c(out_3[2]),
    .d(out_3[3]), .e(out_3[4]), .f(out_3[5]), .g(out_3[6]), .h(out_3[7]));
endmodule

module row_select2 (
  input  [2:0] row,
  input  [2:0] column,
  output [7:0] out_3
);

  wire and_1_out, not_1_out, not_2_out;

  not not_1 (not_1_out, column[0]);
  not not_2 (not_2_out, column[2]);
  and and_1 (and_1_out, not_1_out, column[1], not_2_out);
  decoderv2 decoderv2_1 (
    .Q0(row[0]), .Q1(row[1]), .Q2(row[2]), .activate(and_1_out), .a(out_3[0]), .b(out_3[1]), .c(out_3[2]),
    .d(out_3[3]), .e(out_3[4]), .f(out_3[5]), .g(out_3[6]), .h(out_3[7]));
endmodule

module row_select3 (
  input  [2:0] row,
  input  [2:0] column,
  output [7:0] out_3
);

  wire and_1_out, not_1_out;

  not not_1 (not_1_out, column[2]);
  and and_1 (and_1_out, column[0], column[1], not_1_out);
  decoderv2 decoderv2_1 (
    .Q0(row[0]), .Q1(row[1]), .Q2(row[2]), .activate(and_1_out), .a(out_3[0]), .b(out_3[1]), .c(out_3[2]),
    .d(out_3[3]), .e(out_3[4]), .f(out_3[5]), .g(out_3[6]), .h(out_3[7]));
endmodule

module row_select4 (
  input  [2:0] row,
  input  [2:0] column,
  output [7:0] out_3
);

  wire and_1_out, not_1_out, not_2_out;

  not not_1 (not_1_out, column[0]);
  not not_2 (not_2_out, column[1]);
  and and_1 (and_1_out, not_1_out, not_2_out, column[2]);
  decoderv2 decoderv2_1 (
    .Q0(row[0]), .Q1(row[1]), .Q2(row[2]), .activate(and_1_out), .a(out_3[0]), .b(out_3[1]), .c(out_3[2]),
    .d(out_3[3]), .e(out_3[4]), .f(out_3[5]), .g(out_3[6]), .h(out_3[7]));
endmodule

module row_select5 (
  input  [2:0] row,
  input  [2:0] column,
  output [7:0] out_3
);

  wire and_1_out, not_1_out;

  not not_1 (not_1_out, column[1]);
  and and_1 (and_1_out, column[0], not_1_out, column[2]);
  decoderv2 decoderv2_1 (
    .Q0(row[0]), .Q1(row[1]), .Q2(row[2]), .activate(and_1_out), .a(out_3[0]), .b(out_3[1]), .c(out_3[2]),
    .d(out_3[3]), .e(out_3[4]), .f(out_3[5]), .g(out_3[6]), .h(out_3[7]));
endmodule

module row_select6 (
  input  [2:0] row,
  input  [2:0] column,
  output [7:0] out_3
);

  wire and_1_out, not_1_out;

  not not_1 (not_1_out, column[0]);
  and and_1 (and_1_out, not_1_out, column[1], column[2]);
  decoderv2 decoderv2_1 (
    .Q0(row[0]), .Q1(row[1]), .Q2(row[2]), .activate(and_1_out), .a(out_3[0]), .b(out_3[1]), .c(out_3[2]),
    .d(out_3[3]), .e(out_3[4]), .f(out_3[5]), .g(out_3[6]), .h(out_3[7]));
endmodule

module row_select7 (
  input  [2:0] row,
  input  [2:0] column,
  output [7:0] out_3
);

  wire and_1_out;

  and and_1 (and_1_out, column[0], column[1], column[2]);
  decoderv2 decoderv2_1 (
    .Q0(row[0]), .Q1(row[1]), .Q2(row[2]), .activate(and_1_out), .a(out_3[0]), .b(out_3[1]), .c(out_3[2]),
    .d(out_3[3]), .e(out_3[4]), .f(out_3[5]), .g(out_3[6]), .h(out_3[7]));
endmodule

module Direction (
  input  Reset,
  input  Haut,
  input  Bas,
  input  Gauche,
  input  Droite,
  input  clock,
  output Haut_2,
  output Bas_2,
  output Gauche_2,
  output Droite_2
);

  wire and_1_out, and_2_out, and_3_out, and_4_out, not_1_out, not_2_out, not_3_out, not_4_out, or_1_out,
       or_2_out, or_3_out, or_4_out, or_5_out, or_6_out;

  not not_1 (not_1_out, Bas_2);
  and and_1 (and_1_out, not_1_out, Haut);
  not not_2 (not_2_out, Haut_2);
  and and_2 (and_2_out, not_2_out, Bas);
  not not_3 (not_3_out, Droite_2);
  and and_3 (and_3_out, not_3_out, Gauche);
  not not_4 (not_4_out, Gauche_2);
  and and_4 (and_4_out, not_4_out, Droite);
  or or_1 (or_1_out, Haut_2, and_1_out);
  or or_2 (or_2_out, Bas_2, and_2_out);
  or or_3 (or_3_out, Gauche_2, and_3_out);
  or or_4 (or_4_out, Droite_2, and_4_out);
  D_Flip_Flop d_ff_1 (.clk(clock), .D(or_1_out), .Q(Haut_2), .reset(or_5_out));  // open: Qn, preset
  D_Flip_Flop d_ff_2 (.clk(clock), .D(or_2_out), .Q(Bas_2), .reset(or_5_out));  // open: Qn, preset
  D_Flip_Flop d_ff_3 (.clk(clock), .D(or_3_out), .Q(Gauche_2), .reset(or_6_out));  // open: Qn, preset
  D_Flip_Flop d_ff_4 (.clk(clock), .D(or_4_out), .Q(Droite_2), .reset(or_6_out));  // open: Qn, preset
  or or_5 (or_5_out, and_4_out, Reset, and_3_out);
  or or_6 (or_6_out, and_2_out, Reset, and_1_out);
endmodule

module Movement (
  input  SensMoins,
  input  SensPlus,
  input  Q0,
  input  Q1,
  input  Q2,
  output D0,
  output D1,
  output D2,
  output Out
);

  wire and_1_out, and_2_out, and_3_out, and_4_out, and_5_out, and_6_out, and_7_out, and_8_out, and_9_out,
       and_10_out, and_11_out, and_12_out, and_13_out, and_14_out, and_15_out, and_16_out, not_1_out,
       not_2_out, not_3_out, not_4_out, not_5_out, not_6_out, not_7_out, not_8_out, not_9_out, not_10_out,
       not_11_out, not_12_out, not_13_out, not_14_out, not_15_out, not_16_out, not_17_out, not_18_out;

  not not_1 (not_1_out, SensMoins);
  not not_2 (not_2_out, SensMoins);
  not not_3 (not_3_out, Q2);
  not not_4 (not_4_out, SensPlus);
  not not_5 (not_5_out, SensMoins);
  not not_6 (not_6_out, Q1);
  not not_7 (not_7_out, Q2);
  not not_8 (not_8_out, Q1);
  not not_9 (not_9_out, SensPlus);
  not not_10 (not_10_out, SensMoins);
  not not_11 (not_11_out, Q2);
  not not_12 (not_12_out, Q2);
  not not_13 (not_13_out, Q2);
  not not_14 (not_14_out, SensPlus);
  not not_15 (not_15_out, Q0);
  not not_16 (not_16_out, Q1);
  not not_17 (not_17_out, Q2);
  not not_18 (not_18_out, SensMoins);
  and and_1 (and_1_out, not_1_out, Q0);
  and and_2 (and_2_out, Q0, Q2);
  and and_3 (and_3_out, Q0, Q1);
  and and_4 (and_4_out, SensPlus, Q1, Q2);
  and and_5 (and_5_out, not_2_out, Q1, not_3_out);
  and and_6 (and_6_out, not_4_out, Q1, Q2);
  and and_7 (and_7_out, not_5_out, Q0, Q1);
  and and_8 (and_8_out, SensMoins, Q0, not_6_out, not_7_out);
  and and_9 (and_9_out, SensPlus, not_8_out, Q2);
  and and_10 (and_10_out, not_9_out, not_10_out, Q2);
  and and_11 (and_11_out, SensMoins, Q1, not_11_out);
  and and_12 (and_12_out, SensMoins, Q0, not_12_out);
  and and_13 (and_13_out, SensPlus, not_13_out);
  and and_14 (and_14_out, SensPlus, Q0, Q1);
  and and_15 (and_15_out, not_14_out, SensMoins, not_15_out, not_16_out, not_17_out);
  and and_16 (and_16_out, SensPlus, not_18_out, Q0, Q1, Q2);
  or or_1 (D0, and_1_out, and_2_out, and_3_out, and_4_out);
  or or_2 (D1, and_5_out, and_6_out, and_7_out, and_8_out, and_9_out);
  or or_3 (D2, and_10_out, and_11_out, and_12_out, and_13_out, and_14_out);
  or or_4 (Out, and_15_out, and_16_out);
endmodule

module StateMemory (
  input  Reset,
  input  in_2,
  input  in_3,
  input  in_4,
  input  in_5,
  output out_6,
  output out_7,
  output out_8
);

  D_Flip_Flop d_ff_1 (.clk(in_5), .D(in_2), .Q(out_6), .reset(Reset));  // open: Qn, preset
  D_Flip_Flop d_ff_2 (.clk(in_5), .D(in_3), .Q(out_7), .reset(Reset));  // open: Qn, preset
  D_Flip_Flop d_ff_3 (.clk(in_5), .D(in_4), .Q(out_8), .reset(Reset));  // open: Qn, preset
endmodule

module display_2 (
  input  [5:0] in_1,
  input  [5:0] in_2,
  input  in_3,
  input  in_4,
  input  in_5,
  input  in_6,
  input  clokc,
  output [7:0] out_8,
  output [7:0] out_9,
  output [7:0] out_10,
  output [7:0] out_11,
  output [7:0] out_12,
  output out_13,
  output [7:0] out_14,
  output [7:0] out_15,
  output [7:0] out_16
);

  wire grow2_1_out_18, grow2_2_out_18, grow2_3_out_18, grow2_4_out_18, grow2_5_out_18, grow2_6_out_18,
       grow2_7_out_18, grow2_8_out_18;
  wire [7:0] or_1_out, or_8_bit_1_out_3, or_8_bit_2_out_3, or_8_bit_3_out_3, or_8_bit_4_out_3,
       or_8_bit_5_out_3, or_8_bit_6_out_3, or_8_bit_7_out_3, row_select0_1_out_3, row_select0_2_out_3,
       row_select1_1_out_3, row_select1_2_out_3, row_select2_1_out_3, row_select2_2_out_3,
       row_select3_1_out_3, row_select3_2_out_3, row_select4_1_out_3, row_select4_2_out_3,
       row_select5_1_out_3, row_select5_2_out_3, row_select6_1_out_3, row_select6_2_out_3,
       row_select7_1_out_3, row_select7_2_out_3;

  row_select0 row_select0_1 (.row(in_1[2:0]), .column(in_1[5:3]), .out_3(row_select0_1_out_3));
  row_select2 row_select2_1 (.row(in_1[2:0]), .column(in_1[5:3]), .out_3(row_select2_1_out_3));
  row_select6 row_select6_1 (.row(in_1[2:0]), .column(in_1[5:3]), .out_3(row_select6_1_out_3));
  row_select0 row_select0_2 (.row(in_2[2:0]), .column(in_2[5:3]), .out_3(row_select0_2_out_3));
  row_select2 row_select2_2 (.row(in_2[2:0]), .column(in_2[5:3]), .out_3(row_select2_2_out_3));
  row_select4 row_select4_1 (.row(in_2[2:0]), .column(in_2[5:3]), .out_3(row_select4_1_out_3));
  row_select7 row_select7_1 (.row(in_2[2:0]), .column(in_2[5:3]), .out_3(row_select7_1_out_3));
  row_select5 row_select5_1 (.row(in_2[2:0]), .column(in_2[5:3]), .out_3(row_select5_1_out_3));
  row_select6 row_select6_2 (.row(in_2[2:0]), .column(in_2[5:3]), .out_3(row_select6_2_out_3));
  row_select1 row_select1_1 (.row(in_1[2:0]), .column(in_1[5:3]), .out_3(row_select1_1_out_3));
  row_select3 row_select3_1 (.row(in_1[2:0]), .column(in_1[5:3]), .out_3(row_select3_1_out_3));
  row_select4 row_select4_2 (.row(in_1[2:0]), .column(in_1[5:3]), .out_3(row_select4_2_out_3));
  row_select5 row_select5_2 (.row(in_1[2:0]), .column(in_1[5:3]), .out_3(row_select5_2_out_3));
  row_select7 row_select7_2 (.row(in_1[2:0]), .column(in_1[5:3]), .out_3(row_select7_2_out_3));
  row_select1 row_select1_2 (.row(in_2[2:0]), .column(in_2[5:3]), .out_3(row_select1_2_out_3));
  OR_8_bit or_8_bit_1 (.in_1(row_select0_1_out_3), .in_2(row_select0_2_out_3), .out_3(or_8_bit_1_out_3));
  OR_8_bit or_8_bit_2 (.in_1(row_select1_1_out_3), .in_2(row_select1_2_out_3), .out_3(or_8_bit_2_out_3));
  row_select3 row_select3_2 (.row(in_2[2:0]), .column(in_2[5:3]), .out_3(row_select3_2_out_3));
  OR_8_bit or_8_bit_3 (.in_1(row_select2_1_out_3), .in_2(row_select2_2_out_3), .out_3(or_8_bit_3_out_3));
  OR_8_bit or_8_bit_4 (.in_1(row_select3_1_out_3), .in_2(row_select3_2_out_3), .out_3(or_8_bit_4_out_3));
  assign or_1_out = row_select5_2_out_3 | row_select5_1_out_3;  // OR_Gate or_1, 8 bits wide
  OR_8_bit or_8_bit_5 (.in_1(row_select6_1_out_3), .in_2(row_select6_2_out_3), .out_3(or_8_bit_5_out_3));
  OR_8_bit or_8_bit_6 (.in_1(row_select4_2_out_3), .in_2(row_select4_1_out_3), .out_3(or_8_bit_6_out_3));
  Grow2 grow2_1 (
    .out_15(out_8[6]), .out_16(out_8[5]), .out_17(out_8[4]), .out_19(out_8[3]), .out_20(out_8[2]),
    .out_21(out_8[1]), .out_22(out_8[0]), .out_14(out_8[7]), .out_18(grow2_1_out_18),
    .in_2(or_8_bit_1_out_3[6]), .in_3(or_8_bit_1_out_3[5]), .in_4(or_8_bit_1_out_3[4]),
    .in_5(or_8_bit_1_out_3[3]), .in_6(or_8_bit_1_out_3[2]), .in_7(or_8_bit_1_out_3[1]),
    .in_8(or_8_bit_1_out_3[0]), .in_9(in_3), .in_10(in_4), .in_1(or_8_bit_1_out_3[7]), .in_11(in_5),
    .in_12(in_6), .clock(clokc));
  OR_8_bit or_8_bit_7 (.in_1(row_select7_2_out_3), .in_2(row_select7_1_out_3), .out_3(or_8_bit_7_out_3));
  Grow2 grow2_2 (
    .out_15(out_14[6]), .out_16(out_14[5]), .out_17(out_14[4]), .out_19(out_14[3]), .out_20(out_14[2]),
    .out_21(out_14[1]), .out_22(out_14[0]), .out_14(out_14[7]), .out_18(grow2_2_out_18), .in_2(or_1_out[6]),
    .in_3(or_1_out[5]), .in_4(or_1_out[4]), .in_5(or_1_out[3]), .in_6(or_1_out[2]), .in_7(or_1_out[1]),
    .in_8(or_1_out[0]), .in_9(in_3), .in_10(in_4), .in_1(or_1_out[7]), .in_11(in_5), .in_12(in_6),
    .clock(clokc));
  Grow2 grow2_3 (
    .out_15(out_15[6]), .out_16(out_15[5]), .out_17(out_15[4]), .out_19(out_15[3]), .out_20(out_15[2]),
    .out_21(out_15[1]), .out_22(out_15[0]), .out_14(out_15[7]), .out_18(grow2_3_out_18),
    .in_2(or_8_bit_5_out_3[6]), .in_3(or_8_bit_5_out_3[5]), .in_4(or_8_bit_5_out_3[4]),
    .in_5(or_8_bit_5_out_3[3]), .in_6(or_8_bit_5_out_3[2]), .in_7(or_8_bit_5_out_3[1]),
    .in_8(or_8_bit_5_out_3[0]), .in_9(in_3), .in_10(in_4), .in_1(or_8_bit_5_out_3[7]), .in_11(in_5),
    .in_12(in_6), .clock(clokc));
  Grow2 grow2_4 (
    .out_15(out_16[6]), .out_16(out_16[5]), .out_17(out_16[4]), .out_19(out_16[3]), .out_20(out_16[2]),
    .out_21(out_16[1]), .out_22(out_16[0]), .out_14(out_16[7]), .out_18(grow2_4_out_18),
    .in_2(or_8_bit_7_out_3[6]), .in_3(or_8_bit_7_out_3[5]), .in_4(or_8_bit_7_out_3[4]),
    .in_5(or_8_bit_7_out_3[3]), .in_6(or_8_bit_7_out_3[2]), .in_7(or_8_bit_7_out_3[1]),
    .in_8(or_8_bit_7_out_3[0]), .in_9(in_3), .in_10(in_4), .in_1(or_8_bit_7_out_3[7]), .in_11(in_5),
    .in_12(in_6), .clock(clokc));
  Grow2 grow2_5 (
    .out_15(out_9[6]), .out_16(out_9[5]), .out_17(out_9[4]), .out_19(out_9[3]), .out_20(out_9[2]),
    .out_21(out_9[1]), .out_22(out_9[0]), .out_14(out_9[7]), .out_18(grow2_5_out_18),
    .in_2(or_8_bit_2_out_3[6]), .in_3(or_8_bit_2_out_3[5]), .in_4(or_8_bit_2_out_3[4]),
    .in_5(or_8_bit_2_out_3[3]), .in_6(or_8_bit_2_out_3[2]), .in_7(or_8_bit_2_out_3[1]),
    .in_8(or_8_bit_2_out_3[0]), .in_9(in_3), .in_10(in_4), .in_1(or_8_bit_2_out_3[7]), .in_11(in_5),
    .in_12(in_6), .clock(clokc));
  Grow2 grow2_6 (
    .out_15(out_10[6]), .out_16(out_10[5]), .out_17(out_10[4]), .out_19(out_10[3]), .out_20(out_10[2]),
    .out_21(out_10[1]), .out_22(out_10[0]), .out_14(out_10[7]), .out_18(grow2_6_out_18),
    .in_2(or_8_bit_3_out_3[6]), .in_3(or_8_bit_3_out_3[5]), .in_4(or_8_bit_3_out_3[4]),
    .in_5(or_8_bit_3_out_3[3]), .in_6(or_8_bit_3_out_3[2]), .in_7(or_8_bit_3_out_3[1]),
    .in_8(or_8_bit_3_out_3[0]), .in_9(in_3), .in_10(in_4), .in_1(or_8_bit_3_out_3[7]), .in_11(in_5),
    .in_12(in_6), .clock(clokc));
  Grow2 grow2_7 (
    .out_15(out_11[6]), .out_16(out_11[5]), .out_17(out_11[4]), .out_19(out_11[3]), .out_20(out_11[2]),
    .out_21(out_11[1]), .out_22(out_11[0]), .out_14(out_11[7]), .out_18(grow2_7_out_18),
    .in_2(or_8_bit_4_out_3[6]), .in_3(or_8_bit_4_out_3[5]), .in_4(or_8_bit_4_out_3[4]),
    .in_5(or_8_bit_4_out_3[3]), .in_6(or_8_bit_4_out_3[2]), .in_7(or_8_bit_4_out_3[1]),
    .in_8(or_8_bit_4_out_3[0]), .in_9(in_3), .in_10(in_4), .in_1(or_8_bit_4_out_3[7]), .in_11(in_5),
    .in_12(in_6), .clock(clokc));
  Grow2 grow2_8 (
    .out_15(out_12[6]), .out_16(out_12[5]), .out_17(out_12[4]), .out_19(out_12[3]), .out_20(out_12[2]),
    .out_21(out_12[1]), .out_22(out_12[0]), .out_14(out_12[7]), .out_18(grow2_8_out_18),
    .in_2(or_8_bit_6_out_3[6]), .in_3(or_8_bit_6_out_3[5]), .in_4(or_8_bit_6_out_3[4]),
    .in_5(or_8_bit_6_out_3[3]), .in_6(or_8_bit_6_out_3[2]), .in_7(or_8_bit_6_out_3[1]),
    .in_8(or_8_bit_6_out_3[0]), .in_9(in_3), .in_10(in_4), .in_1(or_8_bit_6_out_3[7]), .in_11(in_5),
    .in_12(in_6), .clock(clokc));
  or or_2 (out_13, grow2_1_out_18, grow2_5_out_18, grow2_6_out_18, grow2_7_out_18, grow2_8_out_18, grow2_2_out_18, grow2_3_out_18, grow2_4_out_18);
endmodule

module did_eat_shroom (
  input  [5:0] in_1,
  input  [5:0] in_2,
  output out_3
);

  wire [5:0] xnor_1_out;

  assign xnor_1_out = ~(in_1 ^ in_2);  // XNOR_Gate xnor_1, 6 bits wide
  and and_1 (out_3, xnor_1_out[0], xnor_1_out[1], xnor_1_out[2], xnor_1_out[3], xnor_1_out[4], xnor_1_out[5]);
endmodule

module OR_8_bit (
  input  [7:0] in_1,
  input  [7:0] in_2,
  output [7:0] out_3
);

  or or_1 (out_3[0], in_1[0], in_2[0]);
  or or_2 (out_3[1], in_1[1], in_2[1]);
  or or_3 (out_3[2], in_1[2], in_2[2]);
  or or_4 (out_3[3], in_1[3], in_2[3]);
  or or_5 (out_3[4], in_1[4], in_2[4]);
  or or_6 (out_3[5], in_1[5], in_2[5]);
  or or_7 (out_3[6], in_1[6], in_2[6]);
  or or_8 (out_3[7], in_1[7], in_2[7]);
endmodule

module Score (
  input  ScoreIncrement,
  input  Reset,
  input  in_3,
  output out_4,
  output out_5,
  output out_6
);

  wire scoreplus_1_q0, scoreplus_1_q1, scoreplus_1_q2;

  ScorePlus scoreplus_1 (
    .Inc(ScoreIncrement), .I0(out_4), .I1(out_5), .I2(out_6), .Q0(scoreplus_1_q0), .Q1(scoreplus_1_q1),
    .Q2(scoreplus_1_q2));
  D_Flip_Flop d_ff_1 (.clk(in_3), .D(scoreplus_1_q0), .Q(out_4), .reset(Reset));  // open: Qn, preset
  D_Flip_Flop d_ff_2 (.clk(in_3), .D(scoreplus_1_q1), .Q(out_5), .reset(Reset));  // open: Qn, preset
  D_Flip_Flop d_ff_3 (.clk(in_3), .D(scoreplus_1_q2), .Q(out_6), .reset(Reset));  // open: Qn, preset
endmodule

module ScorePlus (
  input  Inc,
  input  I0,
  input  I1,
  input  I2,
  output Q0,
  output Q1,
  output Q2
);

  wire and_1_out, and_2_out, and_3_out, and_4_out, and_5_out, and_6_out, and_7_out, and_8_out, not_1_out,
       not_2_out, not_3_out, not_4_out, not_5_out;

  and and_1 (and_1_out, Inc, I1, I2);
  not not_1 (not_1_out, Inc);
  and and_2 (and_2_out, not_1_out, I1);
  and and_3 (and_3_out, I1, not_2_out);
  not not_2 (not_2_out, I2);
  and and_4 (and_4_out, I0, I1);
  not not_3 (not_3_out, I1);
  and and_5 (and_5_out, Inc, not_3_out, I2);
  not not_4 (not_4_out, Inc);
  and and_6 (and_6_out, not_4_out, I2);
  and and_7 (and_7_out, I0, I1, I2);
  and and_8 (and_8_out, Inc, not_5_out);
  not not_5 (not_5_out, I2);
  or or_1 (Q0, I0, and_1_out);
  or or_2 (Q1, and_2_out, and_3_out, and_4_out, and_5_out);
  or or_3 (Q2, and_6_out, and_7_out, and_8_out);
endmodule

module ScoreAff (
  input  Q0,
  input  Q1,
  input  Q2,
  output a,
  output b,
  output c,
  output d,
  output e,
  output f,
  output g
);

  wire and_1_out, and_2_out, and_3_out, and_4_out, and_5_out, and_6_out, and_7_out, and_8_out, and_9_out,
       and_10_out, and_11_out, and_12_out, and_13_out, and_14_out, and_15_out, and_16_out, not_1_out,
       not_2_out, not_3_out, not_4_out, not_5_out, not_6_out, not_7_out, not_8_out, not_9_out, not_10_out,
       not_11_out, not_12_out, not_13_out, not_14_out, not_15_out, not_16_out, not_17_out, not_18_out,
       not_19_out, not_20_out, not_21_out;

  not not_1 (not_1_out, Q0);
  not not_2 (not_2_out, Q2);
  not not_3 (not_3_out, Q1);
  not not_4 (not_4_out, Q2);
  not not_5 (not_5_out, Q1);
  not not_6 (not_6_out, Q0);
  not not_7 (not_7_out, Q2);
  not not_8 (not_8_out, Q0);
  not not_9 (not_9_out, Q2);
  not not_10 (not_10_out, Q1);
  not not_11 (not_11_out, Q0);
  not not_12 (not_12_out, Q2);
  not not_13 (not_13_out, Q2);
  not not_14 (not_14_out, Q1);
  not not_15 (not_15_out, Q2);
  not not_16 (not_16_out, Q1);
  not not_17 (not_17_out, Q2);
  not not_18 (not_18_out, Q0);
  not not_19 (not_19_out, Q1);
  not not_20 (not_20_out, Q2);
  and and_1 (and_1_out, not_1_out, not_2_out);
  and and_2 (and_2_out, Q0, Q2);
  not not_21 (not_21_out, Q0);
  and and_3 (and_3_out, not_3_out, not_4_out);
  and and_4 (and_4_out, Q1, Q2);
  or or_1 (c, not_5_out, Q2, Q0);
  and and_5 (and_5_out, not_6_out, not_7_out);
  and and_6 (and_6_out, not_8_out, Q1);
  and and_7 (and_7_out, Q1, not_9_out);
  and and_8 (and_8_out, Q0, not_10_out, Q2);
  and and_9 (and_9_out, not_11_out, not_12_out);
  and and_10 (and_10_out, Q1, not_13_out);
  and and_11 (and_11_out, not_14_out, not_15_out);
  and and_12 (and_12_out, Q0, not_16_out);
  and and_13 (and_13_out, Q0, not_17_out);
  and and_14 (and_14_out, not_18_out, Q1);
  and and_15 (and_15_out, Q0, not_19_out);
  and and_16 (and_16_out, Q0, not_20_out);
  or or_2 (a, and_1_out, Q1, and_2_out);
  or or_3 (b, not_21_out, and_3_out, and_4_out);
  or or_4 (d, and_5_out, and_6_out, and_7_out, and_8_out);
  or or_5 (e, and_9_out, and_10_out);
  or or_6 (f, and_11_out, and_12_out, and_13_out);
  or or_7 (g, and_14_out, and_15_out, and_16_out);
endmodule

module score (
  input  in_1,
  input  in_2,
  input  clock,
  output [2:0] out_4,
  output out_5,
  output out_6,
  output out_7,
  output out_8,
  output out_9,
  output out_10,
  output out_11
);

  Score score_1 (
    .ScoreIncrement(in_1), .Reset(in_2), .in_3(clock), .out_4(out_4[0]), .out_5(out_4[1]), .out_6(out_4[2]));
  ScoreAff scoreaff_1 (
    .Q0(out_4[0]), .Q1(out_4[1]), .Q2(out_4[2]), .a(out_5), .b(out_6), .c(out_7), .d(out_8), .e(out_9),
    .f(out_10), .g(out_11));
endmodule

module shroom_generator (
  input  [2:0] in_1,
  output [5:0] out_2
);

  wire and_1_out, and_2_out, and_3_out, and_5_out, and_6_out, and_7_out, and_8_out, not_1_out, not_2_out,
       not_3_out, not_4_out, not_5_out, not_6_out, not_7_out, not_8_out, not_9_out, not_10_out;

  not not_1 (not_1_out, in_1[1]);
  not not_2 (not_2_out, in_1[0]);
  and and_1 (and_1_out, in_1[2], in_1[1]);
  not not_3 (not_3_out, in_1[2]);
  not not_4 (not_4_out, in_1[1]);
  and and_2 (and_2_out, in_1[1], in_1[0]);
  and and_3 (and_3_out, in_1[2], in_1[1]);
  not not_5 (not_5_out, in_1[1]);
  not not_6 (not_6_out, in_1[2]);
  not not_7 (not_7_out, in_1[1]);
  not not_8 (not_8_out, in_1[2]);
  not not_9 (not_9_out, in_1[0]);
  and and_4 (out_2[5], in_1[2], not_1_out);
  or or_1 (out_2[4], not_2_out, and_1_out);
  and and_5 (and_5_out, not_3_out, not_4_out);
  or or_2 (out_2[2], and_2_out, and_3_out);
  not not_10 (not_10_out, in_1[0]);
  and and_6 (and_6_out, in_1[2], not_5_out);
  and and_7 (and_7_out, not_6_out, not_7_out, in_1[0]);
  and and_8 (and_8_out, not_8_out, in_1[1], not_9_out);
  or or_3 (out_2[3], and_5_out, in_1[0]);
  or or_4 (out_2[1], not_10_out, and_6_out);
  or or_5 (out_2[0], and_7_out, and_8_out);
endmodule

module ReintiScore (
  input  in_1,
  input  in_2,
  input  in_3,
  output out_4
);

  wire d_ff_1_q;

  D_Flip_Flop d_ff_1 (.clk(in_1), .D(in_2), .Q(d_ff_1_q));  // open: Qn, preset, reset
  and and_1 (out_4, d_ff_1_q, in_3);
endmodule

module Traducteur (
  input  Q0,
  input  Q1,
  input  Q2,
  output b,
  output c,
  output d,
  output e,
  output f,
  output g,
  output h
);

  wire and_1_out, and_2_out, and_3_out;

  or or_1 (b, Q2, Q1, Q0);
  or or_2 (c, Q1, Q0);
  and and_1 (and_1_out, Q1, Q2);
  and and_2 (and_2_out, Q0, Q2);
  and and_3 (and_3_out, Q0, Q1);
  and and_4 (g, Q0, Q1);
  and and_5 (h, Q0, Q1, Q2);
  or or_3 (d, and_1_out, Q0);
  or or_4 (f, and_2_out, and_3_out);

  assign e = Q0;
endmodule

module Grow (
  input  in_1,
  input  in_2,
  input  in_3,
  input  in_4,
  input  in_5,
  input  clock,
  output out_7,
  output GameOver
);

  wire controlled_buffer_1_out, controlled_buffer_2_out, controlled_buffer_3_out, controlled_buffer_4_out,
       controlled_buffer_5_out, controlled_buffer_6_out, controlled_buffer_7_out, d_ff_1_q, d_ff_2_q,
       d_ff_3_q, d_ff_4_q, d_ff_5_q, d_ff_6_q, d_ff_7_q, d_ff_8_q, gover_1_gameover, gover_2_gameover,
       gover_3_gameover, gover_4_gameover, traducteur_1_b, traducteur_1_c, traducteur_1_d, traducteur_1_e,
       traducteur_1_f, traducteur_1_g, traducteur_1_h;

  Traducteur traducteur_1 (
    .Q0(in_2), .Q1(in_3), .Q2(in_4), .b(traducteur_1_b), .c(traducteur_1_c), .d(traducteur_1_d),
    .e(traducteur_1_e), .f(traducteur_1_f), .g(traducteur_1_g), .h(traducteur_1_h));
  assign controlled_buffer_1_out = traducteur_1_b ? d_ff_1_q : 1'bz;  // Controlled_Buffer controlled_buffer_1
  assign controlled_buffer_2_out = traducteur_1_c ? d_ff_2_q : 1'bz;  // Controlled_Buffer controlled_buffer_2
  assign controlled_buffer_3_out = traducteur_1_d ? d_ff_3_q : 1'bz;  // Controlled_Buffer controlled_buffer_3
  assign controlled_buffer_4_out = traducteur_1_e ? d_ff_4_q : 1'bz;  // Controlled_Buffer controlled_buffer_4
  assign controlled_buffer_5_out = traducteur_1_f ? d_ff_5_q : 1'bz;  // Controlled_Buffer controlled_buffer_5
  assign controlled_buffer_6_out = traducteur_1_g ? d_ff_6_q : 1'bz;  // Controlled_Buffer controlled_buffer_6
  assign controlled_buffer_7_out = traducteur_1_h ? d_ff_7_q : 1'bz;  // Controlled_Buffer controlled_buffer_7
  D_Flip_Flop d_ff_1 (.clk(clock), .D(in_1), .Q(d_ff_1_q), .reset(in_5));  // open: Qn, preset
  D_Flip_Flop d_ff_2 (.clk(clock), .D(controlled_buffer_1_out), .Q(d_ff_2_q), .reset(in_5));  // open: Qn, preset
  D_Flip_Flop d_ff_3 (.clk(clock), .D(controlled_buffer_2_out), .Q(d_ff_3_q), .reset(in_5));  // open: Qn, preset
  D_Flip_Flop d_ff_4 (.clk(clock), .D(controlled_buffer_3_out), .Q(d_ff_4_q), .reset(in_5));  // open: Qn, preset
  D_Flip_Flop d_ff_5 (.clk(clock), .D(controlled_buffer_4_out), .Q(d_ff_5_q), .reset(in_5));  // open: Qn, preset
  D_Flip_Flop d_ff_6 (.clk(clock), .D(controlled_buffer_5_out), .Q(d_ff_6_q), .reset(in_5));  // open: Qn, preset
  D_Flip_Flop d_ff_7 (.clk(clock), .D(controlled_buffer_6_out), .Q(d_ff_7_q), .reset(in_5));  // open: Qn, preset
  D_Flip_Flop d_ff_8 (.clk(clock), .D(controlled_buffer_7_out), .Q(d_ff_8_q), .reset(in_5));  // open: Qn, preset
  GOver gover_1 (.S2(in_2), .Tete(d_ff_1_q), .Corps(d_ff_5_q), .GameOver(gover_1_gameover));
  GOver gover_2 (.S2(in_2), .Tete(d_ff_1_q), .Corps(d_ff_6_q), .GameOver(gover_2_gameover));
  GOver gover_3 (.S2(in_2), .Tete(d_ff_1_q), .Corps(d_ff_7_q), .GameOver(gover_3_gameover));
  GOver gover_4 (.S2(in_2), .Tete(d_ff_1_q), .Corps(d_ff_8_q), .GameOver(gover_4_gameover));
  or or_1 (out_7, d_ff_1_q, d_ff_2_q, d_ff_3_q, d_ff_4_q, d_ff_5_q, d_ff_6_q, d_ff_7_q, d_ff_8_q);
  or or_2 (GameOver, gover_1_gameover, gover_2_gameover, gover_3_gameover, gover_4_gameover);
endmodule

module Grow2 (
  input  in_1,
  input  in_2,
  input  in_3,
  input  in_4,
  input  in_5,
  input  in_6,
  input  in_7,
  input  in_8,
  input  in_9,
  input  in_10,
  input  in_11,
  input  in_12,
  input  clock,
  output out_14,
  output out_15,
  output out_16,
  output out_17,
  output out_18,
  output out_19,
  output out_20,
  output out_21,
  output out_22
);

  wire grow_1_gameover, grow_2_gameover, grow_3_gameover, grow_4_gameover, grow_5_gameover, grow_6_gameover,
       grow_7_gameover, grow_8_gameover;

  Grow grow_1 (
    .out_7(out_14), .GameOver(grow_1_gameover), .in_1(in_1), .clock(clock), .in_2(in_11), .in_3(in_10),
    .in_4(in_9), .in_5(in_12));
  Grow grow_2 (
    .out_7(out_15), .GameOver(grow_2_gameover), .in_1(in_2), .clock(clock), .in_2(in_11), .in_3(in_10),
    .in_4(in_9), .in_5(in_12));
  Grow grow_3 (
    .out_7(out_16), .GameOver(grow_3_gameover), .in_1(in_3), .clock(clock), .in_2(in_11), .in_3(in_10),
    .in_4(in_9), .in_5(in_12));
  Grow grow_4 (
    .out_7(out_17), .GameOver(grow_4_gameover), .in_1(in_4), .clock(clock), .in_2(in_11), .in_3(in_10),
    .in_4(in_9), .in_5(in_12));
  Grow grow_5 (
    .out_7(out_19), .GameOver(grow_5_gameover), .in_1(in_5), .clock(clock), .in_2(in_11), .in_3(in_10),
    .in_4(in_9), .in_5(in_12));
  Grow grow_6 (
    .out_7(out_20), .GameOver(grow_6_gameover), .in_1(in_6), .clock(clock), .in_2(in_11), .in_3(in_10),
    .in_4(in_9), .in_5(in_12));
  Grow grow_7 (
    .out_7(out_21), .GameOver(grow_7_gameover), .in_1(in_7), .clock(clock), .in_2(in_11), .in_3(in_10),
    .in_4(in_9), .in_5(in_12));
  Grow grow_8 (
    .out_7(out_22), .GameOver(grow_8_gameover), .in_1(in_8), .clock(clock), .in_2(in_11), .in_3(in_10),
    .in_4(in_9), .in_5(in_12));
  or or_1 (out_18, grow_1_gameover, grow_2_gameover, grow_3_gameover, grow_4_gameover, grow_5_gameover, grow_6_gameover, grow_7_gameover, grow_8_gameover);
endmodule

module GOver (
  input  S2,
  input  Tete,
  input  Corps,
  output GameOver
);

  and and_1 (GameOver, S2, Tete, Corps);
endmodule

module memories (
  input  in_1,
  input  in_2,
  input  in_3,
  output out_4
);

  D_Flip_Flop d_ff_1 (.clk(in_1), .D(in_2), .Q(out_4), .reset(in_3));  // open: Qn, preset
endmodule
