// Logisim project комп_v5.circ as structural Verilog
module CPU (
  input  [31:0] Disk_in,
  input  Power,
  input  Clk,
  input  Reset,
  input  Start_CPU,
  input  [31:0] Execute_Device,
  input  [31:0] Data_in__U,
  input  [31:0] Data_in,
  output [23:0] Disk_Adress,
  output [31:0] Disk_out,
  output [2:0] CPU_condition
);

  wire A_to_Z, Access_to_RAM__US, ALU_ERROR, and_2_out, and_6_out, and_7_out, Clk_t, Comparation,
       initiate_load_device, \initiate_load_device_сomand , j_k_ff_1_q, j_k_ff_1_qn, L1, L2, L_complete,
       Load__loading_device, Load_A, Load_C, Load_PCP, Load_PCSP, Load_Program_select, Load_select__PC,
       Load_USP, Load_Y, loading_proqrams_device_1_load_ram, loading_proqrams_device_1_ram_type_loading,
       not_1_out, or_1_out, or_3_out, Pop, Push, register_1_q, Reset_RAM__CP, Reset_t, Stop_load_device,
       UP_DOWN__PC, UP_DOWN__US, UPop, UPush, Z_to_UCom_or_PCom, \пользовательская_остановка ,
       \программная_остановка ;
  wire [2:0] ALU_select_B, C_select, Comand_Place, RAM_number_CPP__for_oper;
  wire [22:0] ALU_operation;
  wire [23:0] C1, comand_protocol_programs_cpp_1_p12, L,
       loading_proqrams_device_1_adress_for_loading_to_comand_protocol, undriven_8;
  wire [31:0] A, ALU_result, bit_extender_2_out, C2, comand_protocol_programs_cpp_1_p9,
       comand_protocol_programs_cpp_1_p10, comand_protocol_programs_cpp_1_p11,
       comand_protocol_programs_cpp_1_p19, comand_protocol_programs_cpp_1_p20, D, Data_in_Program_Comand,
       loading_proqrams_device_1__1, loading_proqrams_device_1__2, loading_proqrams_device_1__3,
       loading_proqrams_device_1__4, multiplexer_2_out, multiplexer_3_out, multiplexer_6_out,
       multiplexer_9_out, multiplexer_10_out, multiplexer_11_out, PC_out, undriven, undriven_2, undriven_3,
       undriven_4, undriven_5, undriven_6, undriven_7, undriven_9, undriven_10, undriven_11, undriven_12,
       undriven_13, UStack_out, Y, Z;
  wire [31:14] comand_protocol_programs_cpp_1_p18;

  or or_1 (or_1_out, 1'b0, Load__loading_device);
  Multiplexer #(.width(24), .disabled(0)) multiplexer_1 (
    .in0(L), .out(Disk_Adress), .sel(1'b0), .en(or_1_out));  // open: in1
  and and_1 (Clk_t, Power, Clk);
  D_Flip_Flop d_ff_1 (
    .clk(Start_CPU), .D(Power), .Q(CPU_condition[0]), .preset(1'b0), .en(Power), .reset(Reset_t));  // open: Qn
  or or_2 (Reset_t, ~Power, Reset);  // OR_Gate
  and and_2 (and_2_out, CPU_condition[0], Clk_t);
  J_K_Flip_Flop j_k_ff_1 (
    .J(Power), .clk(and_2_out), .K(Power), .Q(j_k_ff_1_q), .Qn(j_k_ff_1_qn), .preset(1'b0), .en(Power),
    .reset(Reset_t));
  and and_3 (CPU_condition[1], and_2_out, j_k_ff_1_q);
  and and_4 (CPU_condition[2], j_k_ff_1_qn, and_2_out);
  or or_3 (or_3_out, L2, loading_proqrams_device_1_load_ram);
  Multiplexer #(.width(32), .disabled(0), .enable("false")) multiplexer_2 (
    .in0(loading_proqrams_device_1__1), .in1(undriven), .out(multiplexer_2_out), .sel(L2));
  Loading_proqrams_device loading_proqrams_device_1 (
    .Data_in(Disk_in), .Clk(Clk_t), .Reset_Stop_loading(Stop_load_device), .Power(Power),
    .Load__Access_to_Load(initiate_load_device), ._1(loading_proqrams_device_1__1),
    ._2(loading_proqrams_device_1__2), ._3(loading_proqrams_device_1__3), ._4(loading_proqrams_device_1__4),
    .Loading_Complete(L_complete), .Load_RAM(loading_proqrams_device_1_load_ram),
    .Adress_for_loading_to_Comand_Protocol(loading_proqrams_device_1_adress_for_loading_to_comand_protocol),
    .Loading(Load__loading_device), .\Сдвиг_Адреса_загрузки__Диск (C1), .Adress_for_loading__for_Disk(L),
    .RAM_TYPE_LOADING(loading_proqrams_device_1_ram_type_loading));
  Register #(.width(32)) u_A (.D(multiplexer_3_out), .en(Load_A), .Q(A), .clk(not_1_out), .clr(Reset_t));
  not not_1 (not_1_out, Clk_t);
  Multiplexer #(.width(32), .disabled(0)) multiplexer_3 (
    .in0(Data_in), .in1(Z), .out(multiplexer_3_out), .sel(A_to_Z), .en(Power));
  // Comand_Protocol_Programs__CPP comand_protocol_programs_cpp_1: pin names not known; wires that end beside it: Reset_t, Power, Z[23:0], Clk_t, Comand_Place, or_3_out, Reset_RAM__CP, multiplexer_2_out, comand_protocol_programs_cpp_1_p9, comand_protocol_programs_cpp_1_p10, comand_protocol_programs_cpp_1_p11, comand_protocol_programs_cpp_1_p12, comand_protocol_programs_cpp_1_p12, RAM_number_CPP__for_oper, loading_proqrams_device_1_ram_type_loading, loading_proqrams_device_1_ram_type_loading, {\программная_остановка , Load_C, \initiate_load_device_сomand , Z_to_UCom_or_PCom, Load_Y, Load_A, ALU_select_B, ALU_operation}, {comand_protocol_programs_cpp_1_p18[31:16], Load_Program_select, comand_protocol_programs_cpp_1_p18[14], \программная_остановка , Load_USP, UP_DOWN__US, UPop, Access_to_RAM__US, UPush, Reset_RAM__CP, Load_select__PC, UP_DOWN__PC, Load_PCSP, A_to_Z, Load_PCP, Pop, Push}, comand_protocol_programs_cpp_1_p19, comand_protocol_programs_cpp_1_p20
  Multiplexer #(.width(32), .disabled(0), .enable("false")) multiplexer_4 (
    .in0(loading_proqrams_device_1__2), .in1(undriven_2), .out(comand_protocol_programs_cpp_1_p9), .sel(L2));
  Multiplexer #(.width(32), .disabled(0), .enable("false")) multiplexer_5 (
    .in0(loading_proqrams_device_1__3), .in1(undriven_3), .out(comand_protocol_programs_cpp_1_p10), .sel(L2));
  Multiplexer #(.select(3), .width(32), .disabled(0)) multiplexer_6 (
    .in0(Execute_Device), .in1(Z), .in2(ALU_result), .in3(A), .in4(D), .in5(C2), .in6(undriven_6),
    .in7(undriven_7), .out(multiplexer_6_out), .en(Power));  // open: sel
  User_Stack user_stack_1 (
    .Z_Access_to_memory(Z), .Load_US_Pointer(undriven_5), .Data_in(Data_in), .Power(Power), .Clk(Clk_t),
    .Reset(Reset_t), .Load_US(Load_USP), .UP_0__DOWN_1(UP_DOWN__US), .Access(Access_to_RAM__US),
    .UPush(UPush), .UPop(UPop), .Data_out(UStack_out));
  Multiplexer #(.width(24), .disabled(0), .enable("false")) multiplexer_7 (
    .in0(loading_proqrams_device_1_adress_for_loading_to_comand_protocol), .in1(undriven_8),
    .out(comand_protocol_programs_cpp_1_p12), .sel(L2));
  Multiplexer #(.width(32), .disabled(0), .enable("false")) multiplexer_8 (
    .in0(loading_proqrams_device_1__4), .in1(undriven_4), .out(comand_protocol_programs_cpp_1_p11), .sel(L2));
  Register #(.width(32)) u_Y (.D(multiplexer_6_out), .en(Load_Y), .Q(Y), .clk(not_1_out), .clr(Reset_t));
  Multiplexer #(.width(32), .disabled(0)) multiplexer_9 (
    .in0(Data_in_Program_Comand), .in1(Data_in__U), .out(multiplexer_9_out), .sel(Z_to_UCom_or_PCom),
    .en(Power));
  Register #(.width(32)) IR_Z (.D(multiplexer_9_out), .en(CPU_condition[2]), .Q(Z), .clk(not_1_out), .clr(Reset_t));
  Register #(.width(32)) u_D (.D(Data_in), .en(CPU_condition[2]), .Q(D), .clk(not_1_out), .clr(Reset_t));
  Bit_Extender #(.in_width(32), .out_width(24)) bit_extender_1 (.in(C2), .out(C1));
  Register #(.width(32)) C (.D(multiplexer_10_out), .en(Load_C), .Q(C2), .clk(not_1_out), .clr(Reset_t));
  Multiplexer #(.select(3), .width(32), .disabled(0)) multiplexer_10 (
    .in0(A), .in1(Y), .in2(Z), .in3(D), .in4(ALU_result), .in5(undriven_9), .in6(undriven_10),
    .in7(undriven_11), .out(multiplexer_10_out), .sel(C_select), .en(Load_C));
  PC pc_1 (
    .sRam(Data_in), .Stack_Pointer__in(C2), .Z(Z), .Power(Power), .Reset(Reset_t), .Clk(Clk_t),
    .Load_PC_Pointer(Load_PCP), .Load_Stack_Pointer(Load_PCSP), .Push(Push), .Pop(Pop),
    .UP_0__DOWN_1(UP_DOWN__PC), .Load_Select(Load_select__PC), .Data_out(PC_out));
  assign bit_extender_2_out = {{24{1'b0}}, Z[31:24]};  // Bit_Extender bit_extender_2
  \ALU__СPU_GPU  \alu_сpu_gpu_1  (
    .Power(Power), .Operation(ALU_operation), .A(Y), .B(multiplexer_11_out), .C(ALU_result),
    .compare(Comparation), .Error(ALU_ERROR));
  Multiplexer #(.select(3), .width(32), .disabled(0)) multiplexer_11 (
    .in0(bit_extender_2_out), .in1(D), .in2(A), .in3(Y), .in4(Data_in), .in5(C2), .in6(undriven_12),
    .in7(undriven_13), .out(multiplexer_11_out), .sel(ALU_select_B), .en(Power));
  and and_5 (initiate_load_device, L1, \initiate_load_device_сomand );
  Pull_Resistor pull_resistor_1 (.node(\пользовательская_остановка ));
  Register #(.width(1)) register_1 (
    .D(initiate_load_device), .en(initiate_load_device), .Q(register_1_q), .clk(initiate_load_device),
    .clr(Stop_load_device));
  or or_4 (Stop_load_device, and_6_out, ~Power, L2, and_7_out, L_complete);  // OR_Gate
  Decoder #(.disabled(0)) decoder_1 (.out0(L1), .out1(L2), .sel(Load_Program_select), .en(Power));
  and and_6 (and_6_out, \пользовательская_остановка , register_1_q);
  buf and_7 (and_7_out, \программная_остановка );  // AND_Gate

  // Other names for the same wires on the sheet: Execute = CPU_condition[1]; Fetch = CPU_condition[2];
  //   Data_in__Users_Comand[31:0] = Data_in__U; ED[31:0] = Execute_Device

  // Notes on the sheet:
  //   условие выполнения
  //   условие выполнения
endmodule

module \ALU__СPU_GPU  (
  input  Power,
  input  [22:0] Operation,
  input  [31:0] A,
  input  [31:0] B,
  output [31:0] C,
  output Error,
  output compare
);

  wire and_2_out, and_3_out, and_4_out, bitselector_1_out, bitselector_2_out, bitselector_3_out,
       comparator_1_eq, comparator_1_gt, comparator_1_lt, comparator_2_p3, comparator_2_p4, comparator_2_p5,
       comparator_3_eq, comparator_4_eq, comparator_5_eq, comparator_6_eq, comparator_7_eq, comparator_8_eq,
       comparator_9_eq, comparator_10_eq, comparator_10_gt, comparator_10_lt, or_2_out, pull_resistor_11_node;
  wire [0:0] pull_resistor_7_node;
  wire [4:0] bit_extender_7_out, multiplexer_3_out, priority_encoder_1_out, priority_encoder_2_out,
       priority_encoder_3_out, priority_encoder_4_out;
  wire [5:0] bitadder_1_out, bitadder_2_out, bitadder_4_out, bitadder_5_out;
  wire [6:0] bitadder_3_out, bitadder_6_out;
  wire [11:0] pull_resistor_10_node;
  wire [31:0] adder_1_p3, adder_2_out, adder_3_out, and_1_out, and_5_out, bit_extender_1_out,
       bit_extender_2_out, bit_extender_3_out, bit_extender_4_out, bit_extender_5_out, bit_extender_6_out,
       bit_extender_8_out, bit_extender_9_out, bit_extender_10_out, bit_extender_11_out, bit_extender_12_out,
       bit_extender_13_out, bit_extender_14_out, cos_1_p2, divider_1_p3, divider_2_out, divider_2_rem,
       divider_3_out, divider_3_rem, even_parity_1_out, even_parity_2_out, exponentiate_1_p3, fp_to_int_1_p2,
       fp_to_int_2_p4, fp_to_int_3_p2, increesor_1_out_2, increesor_2_out_2, increesor_3_out_2,
       increesor_4_out_2, int_to_fp_1_p2, ln_1_p2, log_1_p3, mod_1_p3, multiplexer_2_out, multiplier_1_p3,
       multiplier_2_cout, multiplier_2_out, multiplier_3_cout, multiplier_3_out, negator_1_out,
       negator_2_out, negator_3_out, odd_parity_1_out, odd_parity_2_out, or_1_out, or_4_out, pow_1_p2,
       pull_resistor_8_node, pull_resistor_9_node, pull_resistor_12_node, root_1_p3, shifter_1_out,
       shifter_2_out, shifter_3_out, shifter_4_out, shifter_5_out, shifter_6_out, shifter_7_out,
       shifter_8_out, shifter_9_out, shifter_10_out, shifter_11_out, shifter_12_out, shifter_13_out,
       shifter_14_out, shifter_15_out, sin_1_p2, sqrt_1_p2, subtractor_1_p3, subtractor_2_out,
       subtractor_3_out, tan_1_p2, xor_1_out, xor_2_out;

  Pull_Resistor pull_resistor_1 (.node(B));
  Pull_Resistor pull_resistor_2 (.node(Operation));
  Pull_Resistor pull_resistor_3 (.node(A));
  Pull_Resistor pull_resistor_4 (.node(Power));
  // Adder adder_1: pin names not known; wires that end beside it: A, B, adder_1_p3
  // Subtractor subtractor_1: pin names not known; wires that end beside it: A, B, subtractor_1_p3
  // Multiplier multiplier_1: pin names not known; wires that end beside it: A, B, multiplier_1_p3
  // Divider divider_1: pin names not known; wires that end beside it: A, B, divider_1_p3
  // Sin sin_1: pin names not known; wires that end beside it: A, sin_1_p2
  // Cos cos_1: pin names not known; wires that end beside it: A, cos_1_p2
  // Tan tan_1: pin names not known; wires that end beside it: A, tan_1_p2
  // Sqrt sqrt_1: pin names not known; wires that end beside it: A, sqrt_1_p2
  // Mod mod_1: pin names not known; wires that end beside it: A, B, mod_1_p3
  // Root root_1: pin names not known; wires that end beside it: A, B, root_1_p3
  // Log log_1: pin names not known; wires that end beside it: A, B, log_1_p3
  // Exponentiate exponentiate_1: pin names not known; wires that end beside it: A, B, exponentiate_1_p3
  // Pow pow_1: pin names not known; wires that end beside it: A, pow_1_p2
  // LN ln_1: pin names not known; wires that end beside it: A, ln_1_p2
  // Int_To_FP int_to_fp_1: pin names not known; wires that end beside it: A, int_to_fp_1_p2
  // FP_to_Int fp_to_int_1: pin names not known; wires that end beside it: A, fp_to_int_1_p2
  increesor increesor_1 (.in(A), .out_2(increesor_1_out_2));
  increesor increesor_2 (.in(B), .out_2(increesor_2_out_2));
  assign bit_extender_1_out = {{26{1'b0}}, bitadder_1_out};  // Bit_Extender bit_extender_1
  BitAdder #(.width(32)) bitadder_1 (.in0(A), .out(bitadder_1_out));
  BitAdder #(.width(32)) bitadder_2 (.in0(B), .out(bitadder_2_out));
  assign bit_extender_2_out = {{26{1'b0}}, bitadder_2_out};  // Bit_Extender bit_extender_2
  BitAdder #(.width(32)) bitadder_3 (.in0(A), .in1(B), .out(bitadder_3_out));
  assign bit_extender_3_out = {{25{1'b0}}, bitadder_3_out};  // Bit_Extender bit_extender_3
  assign or_1_out = A | B;  // OR_Gate or_1, 32 bits wide
  assign and_1_out = A & B;  // AND_Gate and_1, 32 bits wide
  assign xor_1_out = A ^ B;  // XOR_Gate xor_1, 32 bits wide
  assign odd_parity_1_out = A ^ B;  // Odd_Parity odd_parity_1, 32 bits wide
  assign even_parity_1_out = ~(A ^ B);  // Even_Parity even_parity_1, 32 bits wide
  assign bit_extender_4_out = {{31{1'b0}}, bitselector_1_out};  // Bit_Extender bit_extender_4
  BitSelector #(.width(32)) bitselector_1 (.in(A), .out(bitselector_1_out), .sel(Operation[22:18]));
  Comparator #(.width(32), .mode("unsigned")) comparator_1 (
    .a(A), .b(B), .gt(comparator_1_gt), .eq(comparator_1_eq), .lt(comparator_1_lt));
  // Comparator comparator_2: pin names not known; wires that end beside it: A, B, comparator_2_p3, comparator_2_p4, comparator_2_p5
  Priority_Encoder #(.select(5), .disabled(0)) priority_encoder_1 (
    .in0(A[31]), .in1(A[30]), .in2(A[29]), .in3(A[28]), .in4(A[27]), .in5(A[26]), .in6(A[25]), .in7(A[24]),
    .in8(A[23]), .in9(A[22]), .in10(A[21]), .in11(A[20]), .in12(A[19]), .in13(A[18]), .in14(A[17]),
    .in15(A[16]), .in16(A[15]), .in17(A[14]), .in18(A[13]), .in19(A[12]), .in20(A[11]), .in21(A[10]),
    .in22(A[9]), .in23(A[8]), .in24(A[7]), .in25(A[6]), .in26(A[5]), .in27(A[4]), .in28(A[3]), .in29(A[2]),
    .in30(A[1]), .in31(A[0]), .out(priority_encoder_1_out));
  Priority_Encoder #(.select(5), .disabled(0)) priority_encoder_2 (
    .in0(B[31]), .in1(B[30]), .in2(B[29]), .in3(B[28]), .in4(B[27]), .in5(B[26]), .in6(B[25]), .in7(B[24]),
    .in8(B[23]), .in9(B[22]), .in10(B[21]), .in11(B[20]), .in12(B[19]), .in13(B[18]), .in14(B[17]),
    .in15(B[16]), .in16(B[15]), .in17(B[14]), .in18(B[13]), .in19(B[12]), .in20(B[11]), .in21(B[10]),
    .in22(B[9]), .in23(B[8]), .in24(B[7]), .in25(B[6]), .in26(B[5]), .in27(B[4]), .in28(B[3]), .in29(B[2]),
    .in30(B[1]), .in31(B[0]), .out(priority_encoder_2_out));
  assign bit_extender_5_out = {{27{1'b0}}, priority_encoder_1_out};  // Bit_Extender bit_extender_5
  assign bit_extender_6_out = {{27{1'b0}}, priority_encoder_2_out};  // Bit_Extender bit_extender_6
  Pull_Resistor pull_resistor_5 (.node(compare));
  Multiplexer #(.select(3), .disabled(0)) multiplexer_1 (
    .in0(1'b0), .in1(comparator_1_gt), .in2(comparator_1_eq), .in3(comparator_1_lt), .in4(1'b1),
    .in5(comparator_2_p3), .in6(comparator_2_p4), .in7(comparator_2_p5), .out(compare),
    .sel(Operation[13:11]), .en(Power));
  Bit_Extender #(.in_width(32), .out_width(5)) bit_extender_7 (.in(B), .out(bit_extender_7_out));
  Multiplexer #(.select(5), .width(32)) multiplexer_2 (
    .in0(A), .in1(B), .in2(adder_1_p3), .in3(subtractor_1_p3), .in4(multiplier_1_p3), .in5(divider_1_p3),
    .in6(sin_1_p2), .in7(cos_1_p2), .in8(tan_1_p2), .in9(sqrt_1_p2), .in10(mod_1_p3), .in11(root_1_p3),
    .in12(log_1_p3), .in13(exponentiate_1_p3), .in14(pow_1_p2), .in15(ln_1_p2), .in16(int_to_fp_1_p2),
    .in17(fp_to_int_1_p2), .in18(bit_extender_1_out), .in19(bit_extender_2_out), .in20(bit_extender_3_out),
    .in21(or_1_out), .in22(and_1_out), .in23(xor_1_out), .in24(odd_parity_1_out), .in25(even_parity_1_out),
    .in26(increesor_1_out_2), .in27(increesor_2_out_2), .in28(bit_extender_5_out), .in29(bit_extender_6_out),
    .in30(bit_extender_4_out), .in31({32{1'b1}}), .out(multiplexer_2_out), .sel(Operation[4:0]), .en(Power));
  Multiplexer #(.width(5)) multiplexer_3 (
    .in0(bit_extender_7_out), .in1(Operation[10:6]), .out(multiplexer_3_out), .sel(Operation[5]), .en(Power));
  Negator #(.width(32)) negator_1 (.in(multiplexer_2_out), .out(negator_1_out));
  Shifter #(.width(32)) shifter_1 (.in(multiplexer_2_out), .\dist (multiplexer_3_out), .out(shifter_1_out));
  Shifter #(.width(32), .shift("lr")) shifter_2 (
    .in(multiplexer_2_out), .\dist (multiplexer_3_out), .out(shifter_2_out));
  Shifter #(.width(32), .shift("ar")) shifter_3 (
    .in(multiplexer_2_out), .\dist (multiplexer_3_out), .out(shifter_3_out));
  Shifter #(.width(32), .shift("rl")) shifter_4 (
    .in(multiplexer_2_out), .\dist (multiplexer_3_out), .out(shifter_4_out));
  Shifter #(.width(32), .shift("rr")) shifter_5 (
    .in(multiplexer_2_out), .\dist (multiplexer_3_out), .out(shifter_5_out));
  Adder #(.width(32)) adder_2 (.a(A), .b(B), .out(adder_2_out));  // open: cin, cout
  Subtractor #(.width(32)) subtractor_2 (.a(A), .b(B), .out(subtractor_2_out));  // open: bin, bout
  Multiplier #(.width(32)) multiplier_2 (.a(A), .b(B), .out(multiplier_2_out), .cout(multiplier_2_cout));  // open: cin
  Divider #(.width(32)) divider_2 (.a(A), .b(B), .out(divider_2_out), .rem(divider_2_rem));  // open: upper
  Comparator #(.width(4)) comparator_3 (.a(Operation[17:14]), .b(4'b1011), .eq(comparator_3_eq));  // open: gt, lt
  Comparator #(.width(4)) comparator_4 (.a(Operation[17:14]), .b(4'b1100), .eq(comparator_4_eq));  // open: gt, lt
  Comparator #(.width(32)) comparator_5 (.a(B), .b({32{1'b0}}), .eq(comparator_5_eq));  // open: gt, lt
  // FP_to_Int fp_to_int_2: pin names not known; wires that end beside it: 4'b1011, 4'b1100, sin_1_p2, fp_to_int_2_p4
  // FP_to_Int fp_to_int_3: pin names not known; wires that end beside it: B, fp_to_int_3_p2
  or or_2 (or_2_out, comparator_3_eq, comparator_4_eq);
  Comparator #(.width(32)) comparator_6 (.a({32{1'b0}}), .b(fp_to_int_2_p4), .eq(comparator_6_eq));  // open: gt, lt
  Comparator #(.width(32)) comparator_7 (.a({32{1'b0}}), .b(fp_to_int_3_p2), .eq(comparator_7_eq));  // open: gt, lt
  Comparator #(.width(5)) comparator_8 (.a(Operation[4:0]), .b(5'b00101), .eq(comparator_8_eq));  // open: gt, lt
  Comparator #(.width(5)) comparator_9 (.a(Operation[4:0]), .b(5'b01000), .eq(comparator_9_eq));  // open: gt, lt
  and and_2 (and_2_out, or_2_out, comparator_5_eq);
  or or_3 (Error, and_2_out, and_3_out, and_4_out);
  and and_3 (and_3_out, comparator_7_eq, comparator_8_eq);
  and and_4 (and_4_out, comparator_6_eq, comparator_9_eq);
  Pull_Resistor pull_resistor_6 (.node(C));
  Multiplexer #(.select(4), .width(32), .disabled(0)) multiplexer_4 (
    .in0(multiplexer_2_out), .in1(negator_1_out), .in2(shifter_1_out), .in3(shifter_2_out),
    .in4(shifter_3_out), .in5(shifter_4_out), .in6(shifter_5_out), .in7(adder_2_out), .in8(subtractor_2_out),
    .in9(multiplier_2_out), .in10(multiplier_2_cout), .in11(divider_2_out), .in12(divider_2_rem),
    .in13({32{1'b0}}), .in14({32{1'b0}}), .in15({32{1'b0}}), .out(C), .sel(Operation[17:14]), .en(Power));
  Pull_Resistor pull_resistor_7 (.node(pull_resistor_7_node[0]));
  Pull_Resistor pull_resistor_8 (.node(pull_resistor_8_node));
  Pull_Resistor pull_resistor_9 (.node(pull_resistor_9_node));
  Pull_Resistor pull_resistor_10 (.node(pull_resistor_10_node));
  assign or_4_out = pull_resistor_8_node | pull_resistor_9_node;  // OR_Gate or_4, 32 bits wide
  assign and_5_out = pull_resistor_8_node & pull_resistor_9_node;  // AND_Gate and_5, 32 bits wide
  assign odd_parity_2_out = pull_resistor_8_node ^ pull_resistor_9_node;  // Odd_Parity odd_parity_2, 32 bits wide
  assign even_parity_2_out = ~(pull_resistor_8_node ^ pull_resistor_9_node);  // Even_Parity even_parity_2, 32 bits wide
  increesor increesor_3 (.in(pull_resistor_8_node), .out_2(increesor_3_out_2));
  increesor increesor_4 (.in(pull_resistor_9_node), .out_2(increesor_4_out_2));
  BitSelector #(.width(32)) bitselector_2 (
    .in(pull_resistor_8_node), .out(bitselector_2_out), .sel(pull_resistor_10_node[9:5]));
  BitSelector #(.width(32)) bitselector_3 (
    .in(pull_resistor_9_node), .out(bitselector_3_out), .sel(pull_resistor_10_node[9:5]));
  Adder #(.width(32)) adder_3 (
    .a(pull_resistor_8_node), .b(pull_resistor_9_node), .out(adder_3_out));  // open: cin, cout
  Subtractor #(.width(32)) subtractor_3 (
    .a(pull_resistor_8_node), .b(pull_resistor_9_node), .out(subtractor_3_out));  // open: bin, bout
  Multiplier #(.width(32)) multiplier_3 (
    .a(pull_resistor_8_node), .b(pull_resistor_9_node), .out(multiplier_3_out), .cout(multiplier_3_cout));  // open: cin
  Divider #(.width(32)) divider_3 (
    .a(pull_resistor_8_node), .b(pull_resistor_9_node), .out(divider_3_out), .rem(divider_3_rem));  // open: upper
  Negator #(.width(32)) negator_2 (.in(pull_resistor_8_node), .out(negator_2_out));
  Negator #(.width(32)) negator_3 (.in(pull_resistor_9_node), .out(negator_3_out));
  Shifter #(.width(32)) shifter_6 (.in(pull_resistor_8_node), .\dist (pull_resistor_10_node[9:5]), .out(shifter_6_out));
  Shifter #(.width(32), .shift("lr")) shifter_7 (
    .in(pull_resistor_8_node), .\dist (pull_resistor_10_node[9:5]), .out(shifter_7_out));
  Shifter #(.width(32), .shift("ar")) shifter_8 (
    .in(pull_resistor_8_node), .\dist (pull_resistor_10_node[9:5]), .out(shifter_8_out));
  Shifter #(.width(32), .shift("rl")) shifter_9 (
    .in(pull_resistor_8_node), .\dist (pull_resistor_10_node[9:5]), .out(shifter_9_out));
  Shifter #(.width(32), .shift("rr")) shifter_10 (
    .in(pull_resistor_8_node), .\dist (pull_resistor_10_node[9:5]), .out(shifter_10_out));
  Shifter #(.width(32)) shifter_11 (
    .in(pull_resistor_9_node), .\dist (pull_resistor_10_node[9:5]), .out(shifter_11_out));
  Shifter #(.width(32), .shift("lr")) shifter_12 (
    .in(pull_resistor_9_node), .\dist (pull_resistor_10_node[9:5]), .out(shifter_12_out));
  Shifter #(.width(32), .shift("ar")) shifter_13 (
    .in(pull_resistor_9_node), .\dist (pull_resistor_10_node[9:5]), .out(shifter_13_out));
  Shifter #(.width(32), .shift("rl")) shifter_14 (
    .in(pull_resistor_9_node), .\dist (pull_resistor_10_node[9:5]), .out(shifter_14_out));
  Shifter #(.width(32), .shift("rr")) shifter_15 (
    .in(pull_resistor_9_node), .\dist (pull_resistor_10_node[9:5]), .out(shifter_15_out));
  BitAdder #(.width(32)) bitadder_4 (.in0(pull_resistor_8_node), .out(bitadder_4_out));
  assign bit_extender_8_out = {{26{1'b0}}, bitadder_4_out};  // Bit_Extender bit_extender_8
  assign bit_extender_9_out = {{26{1'b0}}, bitadder_5_out};  // Bit_Extender bit_extender_9
  BitAdder #(.width(32)) bitadder_5 (.in0(pull_resistor_9_node), .out(bitadder_5_out));
  BitAdder #(.width(32)) bitadder_6 (.in0(pull_resistor_8_node), .in1(pull_resistor_9_node), .out(bitadder_6_out));
  assign bit_extender_10_out = {{25{1'b0}}, bitadder_6_out};  // Bit_Extender bit_extender_10
  assign xor_2_out = pull_resistor_8_node ^ pull_resistor_9_node;  // XOR_Gate xor_2, 32 bits wide
  assign bit_extender_11_out = {{31{1'b0}}, bitselector_2_out};  // Bit_Extender bit_extender_11
  assign bit_extender_12_out = {{31{1'b0}}, bitselector_3_out};  // Bit_Extender bit_extender_12
  Comparator #(.width(32)) comparator_10 (
    .a(pull_resistor_8_node), .b(pull_resistor_9_node), .gt(comparator_10_gt), .eq(comparator_10_eq),
    .lt(comparator_10_lt));
  Priority_Encoder #(.select(5), .disabled(0)) priority_encoder_3 (
    .in0(pull_resistor_8_node[31]), .in1(pull_resistor_8_node[30]), .in2(pull_resistor_8_node[29]),
    .in3(pull_resistor_8_node[28]), .in4(pull_resistor_8_node[27]), .in5(pull_resistor_8_node[26]),
    .in6(pull_resistor_8_node[25]), .in7(pull_resistor_8_node[24]), .in8(pull_resistor_8_node[23]),
    .in9(pull_resistor_8_node[22]), .in10(pull_resistor_8_node[21]), .in11(pull_resistor_8_node[20]),
    .in12(pull_resistor_8_node[19]), .in13(pull_resistor_8_node[18]), .in14(pull_resistor_8_node[17]),
    .in15(pull_resistor_8_node[16]), .in16(pull_resistor_8_node[15]), .in17(pull_resistor_8_node[14]),
    .in18(pull_resistor_8_node[13]), .in19(pull_resistor_8_node[12]), .in20(pull_resistor_8_node[11]),
    .in21(pull_resistor_8_node[10]), .in22(pull_resistor_8_node[9]), .in23(pull_resistor_8_node[8]),
    .in24(pull_resistor_8_node[7]), .in25(pull_resistor_8_node[6]), .in26(pull_resistor_8_node[5]),
    .in27(pull_resistor_8_node[4]), .in28(pull_resistor_8_node[3]), .in29(pull_resistor_8_node[2]),
    .in30(pull_resistor_8_node[1]), .in31(pull_resistor_8_node[0]), .out(priority_encoder_3_out));
  Priority_Encoder #(.select(5), .disabled(0)) priority_encoder_4 (
    .in0(pull_resistor_9_node[31]), .in1(pull_resistor_9_node[30]), .in2(pull_resistor_9_node[29]),
    .in3(pull_resistor_9_node[28]), .in4(pull_resistor_9_node[27]), .in5(pull_resistor_9_node[26]),
    .in6(pull_resistor_9_node[25]), .in7(pull_resistor_9_node[24]), .in8(pull_resistor_9_node[23]),
    .in9(pull_resistor_9_node[22]), .in10(pull_resistor_9_node[21]), .in11(pull_resistor_9_node[20]),
    .in12(pull_resistor_9_node[19]), .in13(pull_resistor_9_node[18]), .in14(pull_resistor_9_node[17]),
    .in15(pull_resistor_9_node[16]), .in16(pull_resistor_9_node[15]), .in17(pull_resistor_9_node[14]),
    .in18(pull_resistor_9_node[13]), .in19(pull_resistor_9_node[12]), .in20(pull_resistor_9_node[11]),
    .in21(pull_resistor_9_node[10]), .in22(pull_resistor_9_node[9]), .in23(pull_resistor_9_node[8]),
    .in24(pull_resistor_9_node[7]), .in25(pull_resistor_9_node[6]), .in26(pull_resistor_9_node[5]),
    .in27(pull_resistor_9_node[4]), .in28(pull_resistor_9_node[3]), .in29(pull_resistor_9_node[2]),
    .in30(pull_resistor_9_node[1]), .in31(pull_resistor_9_node[0]), .out(priority_encoder_4_out));
  Pull_Resistor pull_resistor_11 (.node(pull_resistor_11_node));
  Multiplexer #(.select(2), .disabled(0)) multiplexer_5 (
    .in0(1'b0), .in1(comparator_10_gt), .in2(comparator_10_eq), .in3(comparator_10_lt),
    .out(pull_resistor_11_node), .sel(pull_resistor_10_node[11:10]), .en(pull_resistor_7_node[0]));
  assign bit_extender_13_out = {{27{1'b0}}, priority_encoder_3_out};  // Bit_Extender bit_extender_13
  assign bit_extender_14_out = {{27{1'b0}}, priority_encoder_4_out};  // Bit_Extender bit_extender_14
  Pull_Resistor pull_resistor_12 (.node(pull_resistor_12_node));
  Multiplexer #(.select(5), .width(32)) multiplexer_6 (
    .in0(adder_3_out), .in1(subtractor_3_out), .in2(multiplier_3_out), .in3(divider_3_out),
    .in4(negator_2_out), .in5(negator_3_out), .in6(shifter_6_out), .in7(shifter_7_out), .in8(shifter_8_out),
    .in9(shifter_9_out), .in10(shifter_10_out), .in11(shifter_11_out), .in12(shifter_12_out),
    .in13(shifter_13_out), .in14(shifter_14_out), .in15(shifter_15_out), .in16(bit_extender_8_out),
    .in17(bit_extender_9_out), .in18(bit_extender_10_out), .in19(or_4_out), .in20(and_5_out),
    .in21(xor_2_out), .in22(odd_parity_2_out), .in23(even_parity_2_out), .in24(increesor_3_out_2),
    .in25(increesor_4_out_2), .in26(bit_extender_13_out), .in27(bit_extender_14_out),
    .in28(bit_extender_11_out), .in29(bit_extender_12_out), .in30(multiplier_3_cout), .in31(divider_3_rem),
    .out(pull_resistor_12_node), .sel(pull_resistor_10_node[4:0]), .en(pull_resistor_7_node[0]));

  // Notes on the sheet:
  //   +
  //   _
  //   *
  //   /
  //   sin
  //   cos
  //   tg
  //   ln
  //   sqrt
  //   mod
  //   root
  //   log
  //   exponent
  //   pow
  //   int()->float()
  //   float()->int()
endmodule

module User_Stack (
  input  [31:0] Z_Access_to_memory,
  input  [31:0] Load_US_Pointer,
  input  [31:0] Data_in,
  input  Power,
  input  Clk,
  input  Reset,
  input  Load_US,
  input  UP_0__DOWN_1,
  input  Access,
  input  UPush,
  input  UPop,
  output [31:0] Data_out
);

  wire and_1_out, controlled_buffer_1_out, controlled_buffer_2_out, not_1_out, not_2_out, not_3_out,
       or_1_out, or_2_out, or_3_out;
  wire [23:0] adder_1_out, bit_extender_1_out, bit_extender_2_out, controlled_buffer_3_out, US_Pointer_q;

  Pull_Resistor pull_resistor_1 (.node(Power));
  Pull_Resistor pull_resistor_2 (.node(Data_in));
  Pull_Resistor pull_resistor_3 (.node(Z_Access_to_memory));
  Pull_Resistor pull_resistor_4 (.node(Load_US_Pointer));
  Pull_Resistor pull_resistor_5 (.node(Access));
  Pull_Resistor pull_resistor_6 (.node(Load_US));
  Pull_Resistor pull_resistor_7 (.node(UPop));
  Pull_Resistor pull_resistor_8 (.node(UP_0__DOWN_1));
  Pull_Resistor pull_resistor_9 (.node(Reset));
  Pull_Resistor pull_resistor_10 (.node(UPush));
  Pull_Resistor pull_resistor_11 (.node(Clk));
  Bit_Extender #(.in_width(32), .out_width(24)) bit_extender_1 (.in(Z_Access_to_memory), .out(bit_extender_1_out));
  Bit_Extender #(.in_width(32), .out_width(24)) bit_extender_2 (.in(Load_US_Pointer), .out(bit_extender_2_out));
  not not_1 (not_1_out, Access);
  or or_1 (or_1_out, Load_US, UP_0__DOWN_1);
  and and_1 (and_1_out, ~Load_US, ~UP_0__DOWN_1);  // AND_Gate
  or or_2 (or_2_out, UPush, UPop);
  assign controlled_buffer_1_out = not_1_out ? or_1_out : 1'bz;  // Controlled_Buffer controlled_buffer_1
  assign controlled_buffer_2_out = not_1_out ? or_3_out : 1'bz;  // Controlled_Buffer controlled_buffer_2
  or or_3 (or_3_out, and_1_out, UP_0__DOWN_1);
  assign controlled_buffer_3_out = not_1_out ? US_Pointer_q : 24'bz;  // Controlled_Buffer controlled_buffer_3
  Counter #(.width(24), .max('hffffff)) US_Pointer (
    .load(controlled_buffer_1_out), .D(bit_extender_2_out), .count(controlled_buffer_2_out),
    .Q(US_Pointer_q), .clk(or_2_out), .clr(Reset));  // open: carry
  Adder #(.width(24)) adder_1 (.a(bit_extender_1_out), .b(US_Pointer_q), .out(adder_1_out));  // open: cin, cout
  not not_2 (not_2_out, not_1_out);
  assign controlled_buffer_3_out = not_2_out ? adder_1_out : 24'bz;  // Controlled_Buffer controlled_buffer_4
  not not_3 (not_3_out, UPush);
  Pull_Resistor pull_resistor_12 (.node(Data_out));
  RAM #(.addrWidth(24), .dataWidth(32), .bus("separate")) ram_1 (
    .addr(controlled_buffer_3_out), .din(Data_in), .data(Data_out), .str(UPush), .sel(Power), .clk(Clk),
    .ld(not_3_out), .clr(Reset));
endmodule
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module Shader_Program_Cashe (
  input  [31:0] Data_in,
  input  [31:0] Operation_in,
  input  [15:0] PA,
  input  [15:0] Adress,
  input  Clk,
  input  Reading,
  input  WR,
  input  Reset,
  input  Power,
  output [31:0] Data_out,
  output [31:0] Operation_out
);

  wire and_1_out, and_2_out, and_3_out, and_4_out, and_5_out, and_6_out, and_7_out, and_8_out, and_9_out,
       and_10_out, and_11_out, and_12_out, and_13_out, and_14_out, and_15_out, and_16_out, and_17_out,
       and_18_out, and_19_out, and_20_out, and_21_out, and_22_out, and_23_out, and_24_out, and_25_out,
       and_26_out, and_27_out, and_28_out, and_29_out, and_30_out, and_31_out, and_32_out, and_33_out,
       and_34_out, comparator_1_eq, comparator_2_eq, comparator_3_eq, comparator_4_eq, comparator_5_eq,
       comparator_6_eq, comparator_7_eq, comparator_8_eq, comparator_9_eq, comparator_10_eq,
       comparator_11_eq, comparator_12_eq, comparator_13_eq, comparator_14_eq, comparator_15_eq,
       comparator_16_eq, comparator_17_eq, comparator_18_eq, comparator_19_eq, comparator_20_eq,
       comparator_21_eq, comparator_22_eq, comparator_23_eq, comparator_24_eq, comparator_25_eq,
       comparator_26_eq, comparator_27_eq, comparator_28_eq, comparator_29_eq, comparator_30_eq,
       comparator_31_eq, comparator_32_eq, comparator_33_eq, comparator_34_eq, not_1_out, not_2_out,
       not_3_out, not_4_out, not_5_out, not_6_out, not_7_out, not_8_out, not_9_out, not_10_out, not_11_out,
       not_12_out, not_13_out, not_14_out, not_15_out, not_16_out, not_17_out, not_18_out, not_19_out,
       not_20_out, not_21_out, not_22_out, not_23_out, not_24_out, not_25_out, not_26_out, not_27_out,
       not_28_out, not_29_out, not_30_out, not_31_out, not_32_out, not_33_out, not_34_out, undriven_2,
       undriven_3, undriven_10, undriven_11, undriven_12;
  wire [3:0] undriven, undriven_4, undriven_6;
  wire [11:0] multiplexer_1_out, multiplexer_2_out, multiplexer_3_out, multiplexer_4_out, multiplexer_5_out,
       multiplexer_6_out, multiplexer_7_out, multiplexer_8_out, multiplexer_9_out, multiplexer_10_out,
       multiplexer_11_out, multiplexer_12_out, multiplexer_13_out, multiplexer_14_out, multiplexer_15_out,
       multiplexer_16_out, multiplexer_17_out, undriven_5, undriven_7;
  wire [31:0] controlled_buffer_33_out, controlled_buffer_34_out, ram_1_data, ram_2_data, ram_3_data,
       ram_4_data, ram_5_data, ram_6_data, ram_7_data, ram_8_data, ram_9_data, ram_10_data, ram_11_data,
       ram_12_data, ram_13_data, ram_14_data, ram_15_data, ram_16_data, ram_17_data, ram_18_data,
       ram_19_data, ram_20_data, ram_21_data, ram_22_data, ram_23_data, ram_24_data, ram_25_data,
       ram_26_data, ram_27_data, ram_28_data, ram_29_data, ram_30_data, ram_31_data, ram_32_data,
       ram_33_data, ram_34_data, undriven_8, undriven_9;

  Pull_Resistor pull_resistor_1 (.node(Power));
  Pull_Resistor pull_resistor_2 (.node(Reading));
  Pull_Resistor pull_resistor_3 (.node(PA));
  Pull_Resistor pull_resistor_4 (.node(Adress));
  Pull_Resistor pull_resistor_5 (.node(Reset));
  Pull_Resistor pull_resistor_6 (.node(Clk));
  Pull_Resistor pull_resistor_7 (.node(WR));
  Pull_Resistor pull_resistor_8 (.node(Operation_in));
  Pull_Resistor pull_resistor_9 (.node(Data_in));
  Comparator #(.width(4)) comparator_1 (.a(4'b0000), .b(PA[15:12]), .eq(comparator_1_eq));  // open: gt, lt
  Comparator #(.width(4)) comparator_2 (.a(4'b0000), .b(Adress[15:12]), .eq(comparator_2_eq));  // open: gt, lt
  Comparator #(.width(4)) comparator_3 (.a(4'b0001), .b(PA[15:12]), .eq(comparator_3_eq));  // open: gt, lt
  Comparator #(.width(4)) comparator_4 (.a(4'b0001), .b(Adress[15:12]), .eq(comparator_4_eq));  // open: gt, lt
  Comparator #(.width(4)) comparator_5 (.a(4'b0010), .b(PA[15:12]), .eq(comparator_5_eq));  // open: gt, lt
  Comparator #(.width(4)) comparator_6 (.a(4'b0010), .b(Adress[15:12]), .eq(comparator_6_eq));  // open: gt, lt
  Comparator #(.width(4)) comparator_7 (.a(4'b0011), .b(PA[15:12]), .eq(comparator_7_eq));  // open: gt, lt
  Comparator #(.width(4)) comparator_8 (.a(4'b0011), .b(Adress[15:12]), .eq(comparator_8_eq));  // open: gt, lt
  Comparator #(.width(4)) comparator_9 (.a(4'b0100), .b(PA[15:12]), .eq(comparator_9_eq));  // open: gt, lt
  Comparator #(.width(4)) comparator_10 (.a(4'b0100), .b(Adress[15:12]), .eq(comparator_10_eq));  // open: gt, lt
  Comparator #(.width(4)) comparator_11 (.a(4'b0101), .b(PA[15:12]), .eq(comparator_11_eq));  // open: gt, lt
  Comparator #(.width(4)) comparator_12 (.a(4'b0101), .b(Adress[15:12]), .eq(comparator_12_eq));  // open: gt, lt
  Comparator #(.width(4)) comparator_13 (.a(4'b0110), .b(PA[15:12]), .eq(comparator_13_eq));  // open: gt, lt
  Comparator #(.width(4)) comparator_14 (.a(4'b0110), .b(Adress[15:12]), .eq(comparator_14_eq));  // open: gt, lt
  Comparator #(.width(4)) comparator_15 (.a(4'b0111), .b(PA[15:12]), .eq(comparator_15_eq));  // open: gt, lt
  Comparator #(.width(4)) comparator_16 (.a(4'b0111), .b(Adress[15:12]), .eq(comparator_16_eq));  // open: gt, lt
  Comparator #(.width(4)) comparator_17 (.a(4'b1000), .b(PA[15:12]), .eq(comparator_17_eq));  // open: gt, lt
  Comparator #(.width(4)) comparator_18 (.a(4'b1000), .b(Adress[15:12]), .eq(comparator_18_eq));  // open: gt, lt
  Comparator #(.width(4)) comparator_19 (.a(4'b1001), .b(PA[15:12]), .eq(comparator_19_eq));  // open: gt, lt
  Comparator #(.width(4)) comparator_20 (.a(4'b1001), .b(Adress[15:12]), .eq(comparator_20_eq));  // open: gt, lt
  Comparator #(.width(4)) comparator_21 (.a(4'b1010), .b(PA[15:12]), .eq(comparator_21_eq));  // open: gt, lt
  Comparator #(.width(4)) comparator_22 (.a(4'b1010), .b(Adress[15:12]), .eq(comparator_22_eq));  // open: gt, lt
  Comparator #(.width(4)) comparator_23 (.a(4'b1011), .b(PA[15:12]), .eq(comparator_23_eq));  // open: gt, lt
  Comparator #(.width(4)) comparator_24 (.a(4'b1011), .b(Adress[15:12]), .eq(comparator_24_eq));  // open: gt, lt
  Comparator #(.width(4)) comparator_25 (.a(4'b1100), .b(PA[15:12]), .eq(comparator_25_eq));  // open: gt, lt
  Comparator #(.width(4)) comparator_26 (.a(4'b1100), .b(Adress[15:12]), .eq(comparator_26_eq));  // open: gt, lt
  Comparator #(.width(4)) comparator_27 (.a(4'b1101), .b(PA[15:12]), .eq(comparator_27_eq));  // open: gt, lt
  Comparator #(.width(4)) comparator_28 (.a(4'b1101), .b(Adress[15:12]), .eq(comparator_28_eq));  // open: gt, lt
  Comparator #(.width(4)) comparator_29 (.a(4'b1110), .b(PA[15:12]), .eq(comparator_29_eq));  // open: gt, lt
  Comparator #(.width(4)) comparator_30 (.a(4'b1110), .b(Adress[15:12]), .eq(comparator_30_eq));  // open: gt, lt
  Comparator #(.width(4)) comparator_31 (.a(4'b1111), .b(PA[15:12]), .eq(comparator_31_eq));  // open: gt, lt
  Comparator #(.width(4)) comparator_32 (.a(4'b1111), .b(Adress[15:12]), .eq(comparator_32_eq));  // open: gt, lt
  and and_1 (and_1_out, comparator_1_eq, Reading);
  and and_2 (and_2_out, WR, comparator_2_eq);
  and and_3 (and_3_out, comparator_3_eq, Reading);
  and and_4 (and_4_out, WR, comparator_4_eq);
  and and_5 (and_5_out, comparator_5_eq, Reading);
  and and_6 (and_6_out, WR, comparator_6_eq);
  and and_7 (and_7_out, comparator_7_eq, Reading);
  and and_8 (and_8_out, WR, comparator_8_eq);
  and and_9 (and_9_out, comparator_9_eq, Reading);
  and and_10 (and_10_out, WR, comparator_10_eq);
  and and_11 (and_11_out, comparator_11_eq, Reading);
  and and_12 (and_12_out, WR, comparator_12_eq);
  and and_13 (and_13_out, comparator_13_eq, Reading);
  and and_14 (and_14_out, WR, comparator_14_eq);
  and and_15 (and_15_out, comparator_15_eq, Reading);
  and and_16 (and_16_out, WR, comparator_16_eq);
  and and_17 (and_17_out, comparator_17_eq, Reading);
  and and_18 (and_18_out, WR, comparator_18_eq);
  and and_19 (and_19_out, comparator_19_eq, Reading);
  and and_20 (and_20_out, WR, comparator_20_eq);
  and and_21 (and_21_out, comparator_21_eq, Reading);
  and and_22 (and_22_out, WR, comparator_22_eq);
  and and_23 (and_23_out, comparator_23_eq, Reading);
  and and_24 (and_24_out, WR, comparator_24_eq);
  and and_25 (and_25_out, comparator_25_eq, Reading);
  and and_26 (and_26_out, WR, comparator_26_eq);
  and and_27 (and_27_out, comparator_27_eq, Reading);
  and and_28 (and_28_out, WR, comparator_28_eq);
  and and_29 (and_29_out, comparator_29_eq, Reading);
  and and_30 (and_30_out, WR, comparator_30_eq);
  and and_31 (and_31_out, comparator_31_eq, Reading);
  and and_32 (and_32_out, WR, comparator_32_eq);
  Multiplexer #(.width(12), .disabled(0), .enable("false")) multiplexer_1 (
    .in0(Adress[11:0]), .in1(PA[11:0]), .out(multiplexer_1_out), .sel(and_1_out));
  Multiplexer #(.width(12), .disabled(0), .enable("false")) multiplexer_2 (
    .in0(Adress[11:0]), .in1(PA[11:0]), .out(multiplexer_2_out), .sel(and_3_out));
  Multiplexer #(.width(12), .disabled(0), .enable("false")) multiplexer_3 (
    .in0(Adress[11:0]), .in1(PA[11:0]), .out(multiplexer_3_out), .sel(and_5_out));
  Multiplexer #(.width(12), .disabled(0), .enable("false")) multiplexer_4 (
    .in0(Adress[11:0]), .in1(PA[11:0]), .out(multiplexer_4_out), .sel(and_7_out));
  Multiplexer #(.width(12), .disabled(0), .enable("false")) multiplexer_5 (
    .in0(Adress[11:0]), .in1(PA[11:0]), .out(multiplexer_5_out), .sel(and_9_out));
  Multiplexer #(.width(12), .disabled(0), .enable("false")) multiplexer_6 (
    .in0(Adress[11:0]), .in1(PA[11:0]), .out(multiplexer_6_out), .sel(and_11_out));
  Multiplexer #(.width(12), .disabled(0), .enable("false")) multiplexer_7 (
    .in0(Adress[11:0]), .in1(PA[11:0]), .out(multiplexer_7_out), .sel(and_13_out));
  Multiplexer #(.width(12), .disabled(0), .enable("false")) multiplexer_8 (
    .in0(Adress[11:0]), .in1(PA[11:0]), .out(multiplexer_8_out), .sel(and_15_out));
  Multiplexer #(.width(12), .disabled(0), .enable("false")) multiplexer_9 (
    .in0(Adress[11:0]), .in1(PA[11:0]), .out(multiplexer_9_out), .sel(and_17_out));
  Multiplexer #(.width(12), .disabled(0), .enable("false")) multiplexer_10 (
    .in0(Adress[11:0]), .in1(PA[11:0]), .out(multiplexer_10_out), .sel(and_19_out));
  Multiplexer #(.width(12), .disabled(0), .enable("false")) multiplexer_11 (
    .in0(Adress[11:0]), .in1(PA[11:0]), .out(multiplexer_11_out), .sel(and_21_out));
  Multiplexer #(.width(12), .disabled(0), .enable("false")) multiplexer_12 (
    .in0(Adress[11:0]), .in1(PA[11:0]), .out(multiplexer_12_out), .sel(and_23_out));
  Multiplexer #(.width(12), .disabled(0), .enable("false")) multiplexer_13 (
    .in0(Adress[11:0]), .in1(PA[11:0]), .out(multiplexer_13_out), .sel(and_25_out));
  Multiplexer #(.width(12), .disabled(0), .enable("false")) multiplexer_14 (
    .in0(Adress[11:0]), .in1(PA[11:0]), .out(multiplexer_14_out), .sel(and_27_out));
  Multiplexer #(.width(12), .disabled(0), .enable("false")) multiplexer_15 (
    .in0(Adress[11:0]), .in1(PA[11:0]), .out(multiplexer_15_out), .sel(and_29_out));
  Multiplexer #(.width(12), .disabled(0), .enable("false")) multiplexer_16 (
    .in0(Adress[11:0]), .in1(PA[11:0]), .out(multiplexer_16_out), .sel(and_31_out));
  not not_1 (not_1_out, and_2_out);
  not not_2 (not_2_out, and_4_out);
  not not_3 (not_3_out, and_6_out);
  not not_4 (not_4_out, and_8_out);
  not not_5 (not_5_out, and_10_out);
  not not_6 (not_6_out, and_12_out);
  not not_7 (not_7_out, and_14_out);
  not not_8 (not_8_out, and_16_out);
  not not_9 (not_9_out, and_18_out);
  not not_10 (not_10_out, and_20_out);
  not not_11 (not_11_out, and_22_out);
  not not_12 (not_12_out, and_24_out);
  not not_13 (not_13_out, and_26_out);
  not not_14 (not_14_out, and_28_out);
  not not_15 (not_15_out, and_30_out);
  not not_16 (not_16_out, and_32_out);
  RAM #(.addrWidth(12), .dataWidth(32), .bus("separate")) ram_1 (
    .addr(multiplexer_1_out), .din(Data_in), .data(ram_1_data), .str(and_2_out), .sel(Power), .clk(Clk),
    .ld(not_1_out), .clr(Reset));
  RAM #(.addrWidth(12), .dataWidth(32), .bus("separate")) ram_2 (
    .addr(multiplexer_2_out), .din(Data_in), .data(ram_2_data), .str(and_4_out), .sel(Power), .clk(Clk),
    .ld(not_2_out), .clr(Reset));
  RAM #(.addrWidth(12), .dataWidth(32), .bus("separate")) ram_3 (
    .addr(multiplexer_3_out), .din(Data_in), .data(ram_3_data), .str(and_6_out), .sel(Power), .clk(Clk),
    .ld(not_3_out), .clr(Reset));
  RAM #(.addrWidth(12), .dataWidth(32), .bus("separate")) ram_4 (
    .addr(multiplexer_4_out), .din(Data_in), .data(ram_4_data), .str(and_8_out), .sel(Power), .clk(Clk),
    .ld(not_4_out), .clr(Reset));
  RAM #(.addrWidth(12), .dataWidth(32), .bus("separate")) ram_5 (
    .addr(multiplexer_5_out), .din(Data_in), .data(ram_5_data), .str(and_10_out), .sel(Power), .clk(Clk),
    .ld(not_5_out), .clr(Reset));
  RAM #(.addrWidth(12), .dataWidth(32), .bus("separate")) ram_6 (
    .addr(multiplexer_6_out), .din(Data_in), .data(ram_6_data), .str(and_12_out), .sel(Power), .clk(Clk),
    .ld(not_6_out), .clr(Reset));
  RAM #(.addrWidth(12), .dataWidth(32), .bus("separate")) ram_7 (
    .addr(multiplexer_7_out), .din(Data_in), .data(ram_7_data), .str(and_14_out), .sel(Power), .clk(Clk),
    .ld(not_7_out), .clr(Reset));
  RAM #(.addrWidth(12), .dataWidth(32), .bus("separate")) ram_8 (
    .addr(multiplexer_8_out), .din(Data_in), .data(ram_8_data), .str(and_16_out), .sel(Power), .clk(Clk),
    .ld(not_8_out), .clr(Reset));
  RAM #(.addrWidth(12), .dataWidth(32), .bus("separate")) ram_9 (
    .addr(multiplexer_9_out), .din(Data_in), .data(ram_9_data), .str(and_18_out), .sel(Power), .clk(Clk),
    .ld(not_9_out), .clr(Reset));
  RAM #(.addrWidth(12), .dataWidth(32), .bus("separate")) ram_10 (
    .addr(multiplexer_10_out), .din(Data_in), .data(ram_10_data), .str(and_20_out), .sel(Power), .clk(Clk),
    .ld(not_10_out), .clr(Reset));
  RAM #(.addrWidth(12), .dataWidth(32), .bus("separate")) ram_11 (
    .addr(multiplexer_11_out), .din(Data_in), .data(ram_11_data), .str(and_22_out), .sel(Power), .clk(Clk),
    .ld(not_11_out), .clr(Reset));
  RAM #(.addrWidth(12), .dataWidth(32), .bus("separate")) ram_12 (
    .addr(multiplexer_12_out), .din(Data_in), .data(ram_12_data), .str(and_24_out), .sel(Power), .clk(Clk),
    .ld(not_12_out), .clr(Reset));
  RAM #(.addrWidth(12), .dataWidth(32), .bus("separate")) ram_13 (
    .addr(multiplexer_13_out), .din(Data_in), .data(ram_13_data), .str(and_26_out), .sel(Power), .clk(Clk),
    .ld(not_13_out), .clr(Reset));
  RAM #(.addrWidth(12), .dataWidth(32), .bus("separate")) ram_14 (
    .addr(multiplexer_14_out), .din(Data_in), .data(ram_14_data), .str(and_28_out), .sel(Power), .clk(Clk),
    .ld(not_14_out), .clr(Reset));
  RAM #(.addrWidth(12), .dataWidth(32), .bus("separate")) ram_15 (
    .addr(multiplexer_15_out), .din(Data_in), .data(ram_15_data), .str(and_30_out), .sel(Power), .clk(Clk),
    .ld(not_15_out), .clr(Reset));
  RAM #(.addrWidth(12), .dataWidth(32), .bus("separate")) ram_16 (
    .addr(multiplexer_16_out), .din(Data_in), .data(ram_16_data), .str(and_32_out), .sel(Power), .clk(Clk),
    .ld(not_16_out), .clr(Reset));
  not not_17 (not_17_out, and_2_out);
  not not_18 (not_18_out, and_4_out);
  not not_19 (not_19_out, and_6_out);
  not not_20 (not_20_out, and_8_out);
  not not_21 (not_21_out, and_10_out);
  not not_22 (not_22_out, and_12_out);
  not not_23 (not_23_out, and_14_out);
  not not_24 (not_24_out, and_16_out);
  not not_25 (not_25_out, and_18_out);
  not not_26 (not_26_out, and_20_out);
  not not_27 (not_27_out, and_22_out);
  not not_28 (not_28_out, and_24_out);
  not not_29 (not_29_out, and_26_out);
  not not_30 (not_30_out, and_28_out);
  not not_31 (not_31_out, and_30_out);
  not not_32 (not_32_out, and_32_out);
  assign Data_out = and_1_out ? ram_1_data : 32'bz;  // Controlled_Buffer controlled_buffer_1
  assign Operation_out = and_1_out ? ram_17_data : 32'bz;  // Controlled_Buffer controlled_buffer_2
  RAM #(.addrWidth(12), .dataWidth(32), .bus("separate")) ram_17 (
    .din(Operation_in), .data(ram_17_data), .str(and_2_out), .sel(Power), .clk(Clk), .ld(not_17_out),
    .clr(Reset));  // open: addr
  assign Data_out = and_3_out ? ram_2_data : 32'bz;  // Controlled_Buffer controlled_buffer_3
  assign Operation_out = and_3_out ? ram_18_data : 32'bz;  // Controlled_Buffer controlled_buffer_4
  RAM #(.addrWidth(12), .dataWidth(32), .bus("separate")) ram_18 (
    .din(Operation_in), .data(ram_18_data), .str(and_4_out), .sel(Power), .clk(Clk), .ld(not_18_out),
    .clr(Reset));  // open: addr
  assign Data_out = and_5_out ? ram_3_data : 32'bz;  // Controlled_Buffer controlled_buffer_5
  RAM #(.addrWidth(12), .dataWidth(32), .bus("separate")) ram_19 (
    .din(Operation_in), .data(ram_19_data), .str(and_6_out), .sel(Power), .clk(Clk), .ld(not_19_out),
    .clr(Reset));  // open: addr
  assign Operation_out = and_5_out ? ram_19_data : 32'bz;  // Controlled_Buffer controlled_buffer_6
  assign Data_out = and_7_out ? ram_4_data : 32'bz;  // Controlled_Buffer controlled_buffer_7
  RAM #(.addrWidth(12), .dataWidth(32), .bus("separate")) ram_20 (
    .din(Operation_in), .data(ram_20_data), .str(and_8_out), .sel(Power), .clk(Clk), .ld(not_20_out),
    .clr(Reset));  // open: addr
  assign Operation_out = and_7_out ? ram_20_data : 32'bz;  // Controlled_Buffer controlled_buffer_8
  assign Data_out = and_9_out ? ram_5_data : 32'bz;  // Controlled_Buffer controlled_buffer_9
  assign Operation_out = and_9_out ? ram_21_data : 32'bz;  // Controlled_Buffer controlled_buffer_10
  RAM #(.addrWidth(12), .dataWidth(32), .bus("separate")) ram_21 (
    .din(Operation_in), .data(ram_21_data), .str(and_10_out), .sel(Power), .clk(Clk), .ld(not_21_out),
    .clr(Reset));  // open: addr
  assign Data_out = and_11_out ? ram_6_data : 32'bz;  // Controlled_Buffer controlled_buffer_11
  assign Operation_out = and_11_out ? ram_22_data : 32'bz;  // Controlled_Buffer controlled_buffer_12
  RAM #(.addrWidth(12), .dataWidth(32), .bus("separate")) ram_22 (
    .din(Operation_in), .data(ram_22_data), .str(and_12_out), .sel(Power), .clk(Clk), .ld(not_22_out),
    .clr(Reset));  // open: addr
  assign Data_out = and_13_out ? ram_7_data : 32'bz;  // Controlled_Buffer controlled_buffer_13
  RAM #(.addrWidth(12), .dataWidth(32), .bus("separate")) ram_23 (
    .din(Operation_in), .data(ram_23_data), .str(and_14_out), .sel(Power), .clk(Clk), .ld(not_23_out),
    .clr(Reset));  // open: addr
  assign Operation_out = and_13_out ? ram_23_data : 32'bz;  // Controlled_Buffer controlled_buffer_14
  assign Data_out = and_15_out ? ram_8_data : 32'bz;  // Controlled_Buffer controlled_buffer_15
  assign Operation_out = and_15_out ? ram_24_data : 32'bz;  // Controlled_Buffer controlled_buffer_16
  RAM #(.addrWidth(12), .dataWidth(32), .bus("separate")) ram_24 (
    .din(Operation_in), .data(ram_24_data), .str(and_16_out), .sel(Power), .clk(Clk), .ld(not_24_out),
    .clr(Reset));  // open: addr
  assign Data_out = and_17_out ? ram_9_data : 32'bz;  // Controlled_Buffer controlled_buffer_17
  assign Operation_out = and_17_out ? ram_25_data : 32'bz;  // Controlled_Buffer controlled_buffer_18
  RAM #(.addrWidth(12), .dataWidth(32), .bus("separate")) ram_25 (
    .din(Operation_in), .data(ram_25_data), .str(and_18_out), .sel(Power), .clk(Clk), .ld(not_25_out),
    .clr(Reset));  // open: addr
  assign Data_out = and_19_out ? ram_10_data : 32'bz;  // Controlled_Buffer controlled_buffer_19
  RAM #(.addrWidth(12), .dataWidth(32), .bus("separate")) ram_26 (
    .din(Operation_in), .data(ram_26_data), .str(and_20_out), .sel(Power), .clk(Clk), .ld(not_26_out),
    .clr(Reset));  // open: addr
  assign Operation_out = and_19_out ? ram_26_data : 32'bz;  // Controlled_Buffer controlled_buffer_20
  assign Data_out = and_21_out ? ram_11_data : 32'bz;  // Controlled_Buffer controlled_buffer_21
  RAM #(.addrWidth(12), .dataWidth(32), .bus("separate")) ram_27 (
    .din(Operation_in), .data(ram_27_data), .str(and_22_out), .sel(Power), .clk(Clk), .ld(not_27_out),
    .clr(Reset));  // open: addr
  assign Operation_out = and_21_out ? ram_27_data : 32'bz;  // Controlled_Buffer controlled_buffer_22
  assign Data_out = and_23_out ? ram_12_data : 32'bz;  // Controlled_Buffer controlled_buffer_23
  assign Operation_out = and_23_out ? ram_28_data : 32'bz;  // Controlled_Buffer controlled_buffer_24
  RAM #(.addrWidth(12), .dataWidth(32), .bus("separate")) ram_28 (
    .din(Operation_in), .data(ram_28_data), .str(and_24_out), .sel(Power), .clk(Clk), .ld(not_28_out),
    .clr(Reset));  // open: addr
  assign Data_out = and_25_out ? ram_13_data : 32'bz;  // Controlled_Buffer controlled_buffer_25
  RAM #(.addrWidth(12), .dataWidth(32), .bus("separate")) ram_29 (
    .din(Operation_in), .data(ram_29_data), .str(and_26_out), .sel(Power), .clk(Clk), .ld(not_29_out),
    .clr(Reset));  // open: addr
  assign Operation_out = and_25_out ? ram_29_data : 32'bz;  // Controlled_Buffer controlled_buffer_26
  assign Data_out = and_27_out ? ram_14_data : 32'bz;  // Controlled_Buffer controlled_buffer_27
  assign Operation_out = and_27_out ? ram_30_data : 32'bz;  // Controlled_Buffer controlled_buffer_28
  RAM #(.addrWidth(12), .dataWidth(32), .bus("separate")) ram_30 (
    .din(Operation_in), .data(ram_30_data), .str(and_28_out), .sel(Power), .clk(Clk), .ld(not_30_out),
    .clr(Reset));  // open: addr
  assign Data_out = and_29_out ? ram_15_data : 32'bz;  // Controlled_Buffer controlled_buffer_29
  assign Operation_out = and_29_out ? ram_31_data : 32'bz;  // Controlled_Buffer controlled_buffer_30
  RAM #(.addrWidth(12), .dataWidth(32), .bus("separate")) ram_31 (
    .din(Operation_in), .data(ram_31_data), .str(and_30_out), .sel(Power), .clk(Clk), .ld(not_31_out),
    .clr(Reset));  // open: addr
  assign Data_out = and_31_out ? ram_16_data : 32'bz;  // Controlled_Buffer controlled_buffer_31
  RAM #(.addrWidth(12), .dataWidth(32), .bus("separate")) ram_32 (
    .din(Operation_in), .data(ram_32_data), .str(and_32_out), .sel(Power), .clk(Clk), .ld(not_32_out),
    .clr(Reset));  // open: addr
  assign Operation_out = and_31_out ? ram_32_data : 32'bz;  // Controlled_Buffer controlled_buffer_32
  Pull_Resistor pull_resistor_10 (.node(Data_out));
  Pull_Resistor pull_resistor_11 (.node(Operation_out));
  Comparator #(.width(4)) comparator_33 (.a(undriven), .b(undriven_6), .eq(comparator_33_eq));  // open: gt, lt
  Comparator #(.width(4)) comparator_34 (.a(undriven), .b(undriven_4), .eq(comparator_34_eq));  // open: gt, lt
  Multiplexer #(.width(12), .disabled(0), .enable("false")) multiplexer_17 (
    .in0(undriven_5), .in1(undriven_7), .out(multiplexer_17_out), .sel(and_33_out));
  and and_33 (and_33_out, comparator_33_eq, undriven_3);
  and and_34 (and_34_out, undriven_2, comparator_34_eq);
  RAM #(.addrWidth(12), .dataWidth(32), .bus("separate")) ram_33 (
    .addr(multiplexer_17_out), .din(undriven_9), .data(ram_33_data), .str(and_34_out), .sel(undriven_10),
    .clk(undriven_11), .ld(not_33_out), .clr(undriven_12));
  not not_33 (not_33_out, and_34_out);
  not not_34 (not_34_out, and_34_out);
  assign controlled_buffer_33_out = and_33_out ? ram_33_data : 32'bz;  // Controlled_Buffer controlled_buffer_33
  RAM #(.addrWidth(12), .dataWidth(32), .bus("separate")) ram_34 (
    .din(undriven_8), .data(ram_34_data), .str(and_34_out), .sel(undriven_10), .clk(undriven_11),
    .ld(not_34_out), .clr(undriven_12));  // open: addr
  assign controlled_buffer_34_out = and_33_out ? ram_34_data : 32'bz;  // Controlled_Buffer controlled_buffer_34

  // Notes on the sheet:
  //   Data
  //   Operation
endmodule

module DDR_Shader_Register (
  input  [4:0] Adress_1,
  input  [4:0] Adress_2,
  input  Power,
  input  Reset,
  input  Clk,
  input  WE_1,
  input  WE_2,
  input  [31:0] Data_in_1,
  input  [31:0] Data_in_2,
  output [31:0] Data_out
);

  wire and_1_out, and_2_out, not_1_out, or_1_out;
  wire [4:0] multiplexer_1_out;
  wire [31:0] controlled_buffer_1_out, ram_1_data;

  and and_1 (and_1_out, Clk, WE_1);
  and and_2 (and_2_out, ~Clk, WE_2);  // AND_Gate
  assign controlled_buffer_1_out = and_1_out ? Data_in_1 : 32'bz;  // Controlled_Buffer controlled_buffer_1
  assign controlled_buffer_1_out = and_2_out ? Data_in_2 : 32'bz;  // Controlled_Buffer controlled_buffer_2
  Multiplexer #(.width(5)) multiplexer_1 (
    .in0(Adress_1), .in1(Adress_2), .out(multiplexer_1_out), .sel(Clk), .en(Power));
  or or_1 (or_1_out, and_1_out, and_2_out);
  not not_1 (not_1_out, and_2_out);
  RAM #(.addrWidth(5), .dataWidth(32), .bus("separate")) ram_1 (
    .addr(multiplexer_1_out), .din(controlled_buffer_1_out), .data(ram_1_data), .str(or_1_out), .sel(Power),
    .clk(or_1_out), .ld(not_1_out), .clr(Reset));
  Register #(.width(32)) register_1 (.D(ram_1_data), .en(Power), .Q(Data_out), .clk(Clk), .clr(Reset));
  Pull_Resistor pull_resistor_1 (.node(Data_out));
endmodule

module File_Register (
  input  [31:0] ALU_result,
  input  [31:0] Data_in__A,
  input  [31:0] Data_in__ALU,
  input  Enable_REG,
  input  Clk,
  input  Reset,
  input  Power,
  input  [31:0] Data_in__B,
  output [31:0] ALU_result_1,
  output [31:0] ALU_result_2,
  output [22:0] ALU_comand_1,
  output [22:0] ALU_comand_2,
  output [31:0] Data_out__A__1,
  output [31:0] Data_out__A__2,
  output [31:0] Data_out__B__1,
  output [31:0] Data_out__B__2
);

  wire not_1_out, not_2_out, not_3_out, not_4_out, or_1_out;
  wire [22:0] bit_extender_1_out;

  Pull_Resistor pull_resistor_1 (.node(Data_in__ALU));
  Pull_Resistor pull_resistor_2 (.node(ALU_result));
  Pull_Resistor pull_resistor_3 (.node(Power));
  Pull_Resistor pull_resistor_4 (.node(Clk));
  Pull_Resistor pull_resistor_5 (.node(Enable_REG));
  Pull_Resistor pull_resistor_6 (.node(Reset));
  Pull_Resistor pull_resistor_7 (.node(Data_in__B));
  Pull_Resistor pull_resistor_8 (.node(Data_in__A));
  Bit_Extender #(.in_width(32), .out_width(23)) bit_extender_1 (.in(Data_in__ALU), .out(bit_extender_1_out));
  or or_1 (or_1_out, Reset, ~Power);  // OR_Gate
  not not_1 (not_1_out, Clk);
  not not_2 (not_2_out, Clk);
  not not_3 (not_3_out, Clk);
  not not_4 (not_4_out, Clk);
  Pull_Resistor pull_resistor_9 (.node(ALU_comand_2));
  Pull_Resistor pull_resistor_10 (.node(Data_out__A__1));
  Pull_Resistor pull_resistor_11 (.node(ALU_comand_1));
  Pull_Resistor pull_resistor_12 (.node(ALU_result_2));
  Pull_Resistor pull_resistor_13 (.node(ALU_result_1));
  Pull_Resistor pull_resistor_14 (.node(Data_out__A__2));
  Register #(.width(32)) register_1 (
    .D(ALU_result), .en(Enable_REG), .Q(ALU_result_1), .clk(not_1_out), .clr(or_1_out));
  Register #(.width(32)) register_2 (.D(ALU_result), .en(Enable_REG), .Q(ALU_result_2), .clk(Clk), .clr(or_1_out));
  Register #(.width(23)) register_3 (
    .D(bit_extender_1_out), .en(Enable_REG), .Q(ALU_comand_1), .clk(not_2_out), .clr(or_1_out));
  Register #(.width(23)) register_4 (
    .D(bit_extender_1_out), .en(Enable_REG), .Q(ALU_comand_2), .clk(Clk), .clr(or_1_out));
  Register #(.width(32)) register_5 (
    .D(Data_in__A), .en(Enable_REG), .Q(Data_out__A__1), .clk(not_3_out), .clr(or_1_out));
  Register #(.width(32)) register_6 (.D(Data_in__A), .en(Enable_REG), .Q(Data_out__A__2), .clk(Clk), .clr(or_1_out));
  Register #(.width(32)) register_7 (
    .D(Data_in__B), .en(Enable_REG), .Q(Data_out__B__1), .clk(not_4_out), .clr(or_1_out));
  Register #(.width(32)) register_8 (.D(Data_in__B), .en(Enable_REG), .Q(Data_out__B__2), .clk(Clk), .clr(or_1_out));
endmodule

module empty_spaces_counter__ESC (
  input  [31:0] in_1,
  input  [4:0] Counter_in,
  output [4:0] Counter_out,
  output Count,
  output Load
);

  wire and_1_out, and_2_out, and_3_out, and_4_out, and_5_out, and_6_out, and_7_out, and_8_out, and_9_out,
       and_10_out, and_11_out, and_12_out, and_13_out, and_14_out, and_15_out, and_16_out, and_17_out,
       and_18_out, and_19_out, and_20_out, and_21_out, and_22_out, and_23_out, and_24_out, and_25_out,
       and_26_out, and_27_out, and_28_out, and_29_out, and_30_out, and_31_out, and_32_out, and_33_out,
       and_34_out, and_35_out, and_36_out, and_37_out, and_38_out, and_39_out, and_40_out, and_41_out,
       and_42_out, and_43_out, and_44_out, and_45_out, and_46_out, and_47_out, and_48_out, and_49_out,
       and_50_out, and_51_out, and_52_out, and_53_out, and_54_out, and_55_out, and_56_out, and_57_out,
       and_58_out, and_59_out, and_60_out, bitselector_2_out, bitselector_3_out, bitselector_4_out,
       bitselector_5_out, bitselector_6_out, bitselector_7_out, bitselector_8_out, bitselector_9_out,
       bitselector_10_out, bitselector_11_out, bitselector_12_out, bitselector_13_out, bitselector_14_out,
       bitselector_15_out, bitselector_16_out, bitselector_17_out, bitselector_18_out, bitselector_19_out,
       bitselector_20_out, bitselector_21_out, bitselector_22_out, bitselector_23_out, bitselector_24_out,
       bitselector_25_out, bitselector_26_out, bitselector_27_out, bitselector_28_out, bitselector_29_out,
       bitselector_30_out, bitselector_31_out, bitselector_32_out, comparator_1_lt, comparator_2_lt,
       comparator_3_lt, comparator_4_lt, comparator_5_lt, comparator_6_lt, comparator_7_lt, comparator_8_lt,
       comparator_9_lt, comparator_10_lt, comparator_11_lt, comparator_12_lt, comparator_13_lt,
       comparator_14_lt, comparator_15_lt, comparator_16_lt, comparator_17_lt, comparator_18_lt,
       comparator_19_lt, comparator_20_lt, comparator_21_lt, comparator_22_lt, comparator_23_lt,
       comparator_24_lt, comparator_25_lt, comparator_26_lt, comparator_27_lt, comparator_28_lt,
       comparator_29_lt, comparator_30_lt, comparator_31_lt;
  wire [4:0] adder_1_out, adder_2_out, adder_3_out, adder_4_out, adder_5_out, adder_6_out, adder_7_out,
       adder_8_out, adder_9_out, adder_10_out, adder_11_out, adder_12_out, adder_13_out, adder_14_out,
       adder_15_out, adder_16_out, adder_17_out, adder_18_out, adder_19_out, adder_20_out, adder_21_out,
       adder_22_out, adder_23_out, adder_24_out, adder_25_out, adder_26_out, adder_27_out, adder_28_out,
       adder_29_out, adder_30_out, adder_31_out, adder_32_out, adder_33_out, bitadder_1_out;
  wire [31:0] multiplexer_1_out, multiplexer_2_out, multiplexer_3_out, multiplexer_4_out, multiplexer_5_out,
       multiplexer_6_out, multiplexer_7_out, multiplexer_8_out, multiplexer_9_out, multiplexer_10_out,
       multiplexer_11_out, multiplexer_12_out, multiplexer_13_out, multiplexer_14_out, multiplexer_15_out,
       multiplexer_16_out, multiplexer_17_out, multiplexer_18_out, multiplexer_19_out, multiplexer_20_out,
       multiplexer_21_out, multiplexer_22_out, multiplexer_23_out, multiplexer_24_out, multiplexer_25_out,
       multiplexer_26_out, multiplexer_27_out, multiplexer_28_out, multiplexer_29_out, multiplexer_30_out;

  Pull_Resistor pull_resistor_1 (.node(Counter_in));
  Pull_Resistor pull_resistor_2 (.node(in_1));
  BitSelector #(.width(32)) bitselector_1 (.in(in_1), .out(Count), .sel(adder_1_out));
  Adder #(.width(5)) adder_1 (.a(Counter_in), .b(5'b00001), .out(adder_1_out));  // open: cin, cout
  Comparator #(.width(5), .mode("unsigned")) comparator_1 (
    .a(Counter_in), .b({5{1'b1}}), .lt(comparator_1_lt));  // open: gt, eq
  Adder #(.width(5)) adder_2 (.a(Counter_in), .b(5'b00001), .out(adder_2_out));  // open: cin, cout
  Comparator #(.width(5), .mode("unsigned")) comparator_2 (
    .a(Counter_in), .b(5'b11110), .lt(comparator_2_lt));  // open: gt, eq
  Multiplexer #(.width(32), .disabled(0), .enable("false")) multiplexer_1 (
    .in0({32{1'b1}}), .in1(in_1), .out(multiplexer_1_out), .sel(and_1_out));
  Adder #(.width(5)) adder_3 (.a(Counter_in), .b(5'b00010), .out(adder_3_out));  // open: cin, cout
  Comparator #(.width(5), .mode("unsigned")) comparator_3 (
    .a(Counter_in), .b(5'b11101), .lt(comparator_3_lt));  // open: gt, eq
  Multiplexer #(.width(32), .disabled(0), .enable("false")) multiplexer_2 (
    .in0({32{1'b1}}), .in1(in_1), .out(multiplexer_2_out), .sel(and_4_out));
  Adder #(.width(5)) adder_4 (.a(Counter_in), .b(5'b00011), .out(adder_4_out));  // open: cin, cout
  Comparator #(.width(5), .mode("unsigned")) comparator_4 (
    .a(Counter_in), .b(5'b11100), .lt(comparator_4_lt));  // open: gt, eq
  Multiplexer #(.width(32), .disabled(0), .enable("false")) multiplexer_3 (
    .in0({32{1'b1}}), .in1(in_1), .out(multiplexer_3_out), .sel(and_6_out));
  Adder #(.width(5)) adder_5 (.a(Counter_in), .b(5'b00100), .out(adder_5_out));  // open: cin, cout
  Comparator #(.width(5), .mode("unsigned")) comparator_5 (
    .a(Counter_in), .b(5'b11011), .lt(comparator_5_lt));  // open: gt, eq
  Multiplexer #(.width(32), .disabled(0), .enable("false")) multiplexer_4 (
    .in0({32{1'b1}}), .in1(in_1), .out(multiplexer_4_out), .sel(and_8_out));
  Adder #(.width(5)) adder_6 (.a(Counter_in), .b(5'b00101), .out(adder_6_out));  // open: cin, cout
  Comparator #(.width(5), .mode("unsigned")) comparator_6 (
    .a(Counter_in), .b(5'b11010), .lt(comparator_6_lt));  // open: gt, eq
  Multiplexer #(.width(32), .disabled(0), .enable("false")) multiplexer_5 (
    .in0({32{1'b1}}), .in1(in_1), .out(multiplexer_5_out), .sel(and_10_out));
  Adder #(.width(5)) adder_7 (.a(Counter_in), .b(5'b00110), .out(adder_7_out));  // open: cin, cout
  Comparator #(.width(5), .mode("unsigned")) comparator_7 (
    .a(Counter_in), .b(5'b11001), .lt(comparator_7_lt));  // open: gt, eq
  Multiplexer #(.width(32), .disabled(0), .enable("false")) multiplexer_6 (
    .in0({32{1'b1}}), .in1(in_1), .out(multiplexer_6_out), .sel(and_12_out));
  Adder #(.width(5)) adder_8 (.a(Counter_in), .b(5'b00111), .out(adder_8_out));  // open: cin, cout
  Comparator #(.width(5), .mode("unsigned")) comparator_8 (
    .a(Counter_in), .b(5'b11000), .lt(comparator_8_lt));  // open: gt, eq
  Multiplexer #(.width(32), .disabled(0), .enable("false")) multiplexer_7 (
    .in0({32{1'b1}}), .in1(in_1), .out(multiplexer_7_out), .sel(and_14_out));
  Adder #(.width(5)) adder_9 (.a(Counter_in), .b(5'b01000), .out(adder_9_out));  // open: cin, cout
  Comparator #(.width(5), .mode("unsigned")) comparator_9 (
    .a(Counter_in), .b(5'b10111), .lt(comparator_9_lt));  // open: gt, eq
  Multiplexer #(.width(32), .disabled(0), .enable("false")) multiplexer_8 (
    .in0({32{1'b1}}), .in1(in_1), .out(multiplexer_8_out), .sel(and_16_out));
  Adder #(.width(5)) adder_10 (.a(Counter_in), .b(5'b01001), .out(adder_10_out));  // open: cin, cout
  Comparator #(.width(5), .mode("unsigned")) comparator_10 (
    .a(Counter_in), .b(5'b10110), .lt(comparator_10_lt));  // open: gt, eq
  Multiplexer #(.width(32), .disabled(0), .enable("false")) multiplexer_9 (
    .in0({32{1'b1}}), .in1(in_1), .out(multiplexer_9_out), .sel(and_18_out));
  Adder #(.width(5)) adder_11 (.a(Counter_in), .b(5'b01010), .out(adder_11_out));  // open: cin, cout
  Comparator #(.width(5), .mode("unsigned")) comparator_11 (
    .a(Counter_in), .b(5'b10101), .lt(comparator_11_lt));  // open: gt, eq
  Multiplexer #(.width(32), .disabled(0), .enable("false")) multiplexer_10 (
    .in0({32{1'b1}}), .in1(in_1), .out(multiplexer_10_out), .sel(and_20_out));
  Adder #(.width(5)) adder_12 (.a(Counter_in), .b(5'b01011), .out(adder_12_out));  // open: cin, cout
  Comparator #(.width(5), .mode("unsigned")) comparator_12 (
    .a(Counter_in), .b(5'b10100), .lt(comparator_12_lt));  // open: gt, eq
  Multiplexer #(.width(32), .disabled(0), .enable("false")) multiplexer_11 (
    .in0({32{1'b1}}), .in1(in_1), .out(multiplexer_11_out), .sel(and_22_out));
  Adder #(.width(5)) adder_13 (.a(Counter_in), .b(5'b01100), .out(adder_13_out));  // open: cin, cout
  Comparator #(.width(5), .mode("unsigned")) comparator_13 (
    .a(Counter_in), .b(5'b10011), .lt(comparator_13_lt));  // open: gt, eq
  Multiplexer #(.width(32), .disabled(0), .enable("false")) multiplexer_12 (
    .in0({32{1'b1}}), .in1(in_1), .out(multiplexer_12_out), .sel(and_24_out));
  Adder #(.width(5)) adder_14 (.a(Counter_in), .b(5'b01101), .out(adder_14_out));  // open: cin, cout
  Comparator #(.width(5), .mode("unsigned")) comparator_14 (
    .a(Counter_in), .b(5'b10010), .lt(comparator_14_lt));  // open: gt, eq
  Multiplexer #(.width(32), .disabled(0), .enable("false")) multiplexer_13 (
    .in0({32{1'b1}}), .in1(in_1), .out(multiplexer_13_out), .sel(and_26_out));
  Adder #(.width(5)) adder_15 (.a(Counter_in), .b(5'b01110), .out(adder_15_out));  // open: cin, cout
  Comparator #(.width(5), .mode("unsigned")) comparator_15 (
    .a(Counter_in), .b(5'b10001), .lt(comparator_15_lt));  // open: gt, eq
  Multiplexer #(.width(32), .disabled(0), .enable("false")) multiplexer_14 (
    .in0({32{1'b1}}), .in1(in_1), .out(multiplexer_14_out), .sel(and_28_out));
  Adder #(.width(5)) adder_16 (.a(Counter_in), .b(5'b01111), .out(adder_16_out));  // open: cin, cout
  Comparator #(.width(5), .mode("unsigned")) comparator_16 (
    .a(Counter_in), .b(5'b10000), .lt(comparator_16_lt));  // open: gt, eq
  Multiplexer #(.width(32), .disabled(0), .enable("false")) multiplexer_15 (
    .in0({32{1'b1}}), .in1(in_1), .out(multiplexer_15_out), .sel(and_30_out));
  Adder #(.width(5)) adder_17 (.a(Counter_in), .b(5'b10000), .out(adder_17_out));  // open: cin, cout
  Comparator #(.width(5), .mode("unsigned")) comparator_17 (
    .a(Counter_in), .b(5'b01111), .lt(comparator_17_lt));  // open: gt, eq
  Multiplexer #(.width(32), .disabled(0), .enable("false")) multiplexer_16 (
    .in0({32{1'b1}}), .in1(in_1), .out(multiplexer_16_out), .sel(and_32_out));
  Adder #(.width(5)) adder_18 (.a(Counter_in), .b(5'b10001), .out(adder_18_out));  // open: cin, cout
  Comparator #(.width(5), .mode("unsigned")) comparator_18 (
    .a(Counter_in), .b(5'b01110), .lt(comparator_18_lt));  // open: gt, eq
  Multiplexer #(.width(32), .disabled(0), .enable("false")) multiplexer_17 (
    .in0({32{1'b1}}), .in1(in_1), .out(multiplexer_17_out), .sel(and_34_out));
  Adder #(.width(5)) adder_19 (.a(Counter_in), .b(5'b10010), .out(adder_19_out));  // open: cin, cout
  Comparator #(.width(5), .mode("unsigned")) comparator_19 (
    .a(Counter_in), .b(5'b01101), .lt(comparator_19_lt));  // open: gt, eq
  Multiplexer #(.width(32), .disabled(0), .enable("false")) multiplexer_18 (
    .in0({32{1'b1}}), .in1(in_1), .out(multiplexer_18_out), .sel(and_36_out));
  Adder #(.width(5)) adder_20 (.a(Counter_in), .b(5'b10011), .out(adder_20_out));  // open: cin, cout
  Comparator #(.width(5), .mode("unsigned")) comparator_20 (
    .a(Counter_in), .b(5'b01100), .lt(comparator_20_lt));  // open: gt, eq
  Multiplexer #(.width(32), .disabled(0), .enable("false")) multiplexer_19 (
    .in0({32{1'b1}}), .in1(in_1), .out(multiplexer_19_out), .sel(and_38_out));
  Adder #(.width(5)) adder_21 (.a(Counter_in), .b(5'b10100), .out(adder_21_out));  // open: cin, cout
  Comparator #(.width(5), .mode("unsigned")) comparator_21 (
    .a(Counter_in), .b(5'b01011), .lt(comparator_21_lt));  // open: gt, eq
  Multiplexer #(.width(32), .disabled(0), .enable("false")) multiplexer_20 (
    .in0({32{1'b1}}), .in1(in_1), .out(multiplexer_20_out), .sel(and_40_out));
  Adder #(.width(5)) adder_22 (.a(Counter_in), .b(5'b10101), .out(adder_22_out));  // open: cin, cout
  Comparator #(.width(5), .mode("unsigned")) comparator_22 (
    .a(Counter_in), .b(5'b01010), .lt(comparator_22_lt));  // open: gt, eq
  Multiplexer #(.width(32), .disabled(0), .enable("false")) multiplexer_21 (
    .in0({32{1'b1}}), .in1(in_1), .out(multiplexer_21_out), .sel(and_42_out));
  Adder #(.width(5)) adder_23 (.a(Counter_in), .b(5'b10110), .out(adder_23_out));  // open: cin, cout
  Comparator #(.width(5), .mode("unsigned")) comparator_23 (
    .a(Counter_in), .b(5'b01001), .lt(comparator_23_lt));  // open: gt, eq
  Multiplexer #(.width(32), .disabled(0), .enable("false")) multiplexer_22 (
    .in0({32{1'b1}}), .in1(in_1), .out(multiplexer_22_out), .sel(and_44_out));
  Adder #(.width(5)) adder_24 (.a(Counter_in), .b(5'b10111), .out(adder_24_out));  // open: cin, cout
  Comparator #(.width(5), .mode("unsigned")) comparator_24 (
    .a(Counter_in), .b(5'b01000), .lt(comparator_24_lt));  // open: gt, eq
  Multiplexer #(.width(32), .disabled(0), .enable("false")) multiplexer_23 (
    .in0({32{1'b1}}), .in1(in_1), .out(multiplexer_23_out), .sel(and_46_out));
  Adder #(.width(5)) adder_25 (.a(Counter_in), .b(5'b11000), .out(adder_25_out));  // open: cin, cout
  Comparator #(.width(5), .mode("unsigned")) comparator_25 (
    .a(Counter_in), .b(5'b00111), .lt(comparator_25_lt));  // open: gt, eq
  Multiplexer #(.width(32), .disabled(0), .enable("false")) multiplexer_24 (
    .in0({32{1'b1}}), .in1(in_1), .out(multiplexer_24_out), .sel(and_48_out));
  Adder #(.width(5)) adder_26 (.a(Counter_in), .b(5'b11001), .out(adder_26_out));  // open: cin, cout
  Comparator #(.width(5), .mode("unsigned")) comparator_26 (
    .a(Counter_in), .b(5'b00110), .lt(comparator_26_lt));  // open: gt, eq
  Multiplexer #(.width(32), .disabled(0), .enable("false")) multiplexer_25 (
    .in0({32{1'b1}}), .in1(in_1), .out(multiplexer_25_out), .sel(and_50_out));
  Adder #(.width(5)) adder_27 (.a(Counter_in), .b(5'b11010), .out(adder_27_out));  // open: cin, cout
  Comparator #(.width(5), .mode("unsigned")) comparator_27 (
    .a(Counter_in), .b(5'b00101), .lt(comparator_27_lt));  // open: gt, eq
  Multiplexer #(.width(32), .disabled(0), .enable("false")) multiplexer_26 (
    .in0({32{1'b1}}), .in1(in_1), .out(multiplexer_26_out), .sel(and_52_out));
  Adder #(.width(5)) adder_28 (.a(Counter_in), .b(5'b11011), .out(adder_28_out));  // open: cin, cout
  Comparator #(.width(5), .mode("unsigned")) comparator_28 (
    .a(Counter_in), .b(5'b00100), .lt(comparator_28_lt));  // open: gt, eq
  Multiplexer #(.width(32), .disabled(0), .enable("false")) multiplexer_27 (
    .in0({32{1'b1}}), .in1(in_1), .out(multiplexer_27_out), .sel(and_54_out));
  Adder #(.width(5)) adder_29 (.a(Counter_in), .b(5'b11100), .out(adder_29_out));  // open: cin, cout
  Comparator #(.width(5), .mode("unsigned")) comparator_29 (
    .a(Counter_in), .b(5'b00011), .lt(comparator_29_lt));  // open: gt, eq
  Multiplexer #(.width(32), .disabled(0), .enable("false")) multiplexer_28 (
    .in0({32{1'b1}}), .in1(in_1), .out(multiplexer_28_out), .sel(and_56_out));
  Adder #(.width(5)) adder_30 (.a(Counter_in), .b(5'b11101), .out(adder_30_out));  // open: cin, cout
  Comparator #(.width(5), .mode("unsigned")) comparator_30 (
    .a(Counter_in), .b(5'b00010), .lt(comparator_30_lt));  // open: gt, eq
  Multiplexer #(.width(32), .disabled(0), .enable("false")) multiplexer_29 (
    .in0({32{1'b1}}), .in1(in_1), .out(multiplexer_29_out), .sel(and_58_out));
  Adder #(.width(5)) adder_31 (.a(Counter_in), .b(5'b11110), .out(adder_31_out));  // open: cin, cout
  Comparator #(.width(5), .mode("unsigned")) comparator_31 (
    .a(Counter_in), .b(5'b00001), .lt(comparator_31_lt));  // open: gt, eq
  Multiplexer #(.width(32), .disabled(0), .enable("false")) multiplexer_30 (
    .in0({32{1'b1}}), .in1(in_1), .out(multiplexer_30_out), .sel(and_60_out));
  Adder #(.width(5)) adder_32 (.a(Counter_in), .b({5{1'b1}}), .out(adder_32_out));  // open: cin, cout
  and and_1 (and_1_out, comparator_1_lt, ~bitselector_2_out);  // AND_Gate
  BitSelector #(.width(32)) bitselector_2 (.in(in_1), .out(bitselector_2_out), .sel(adder_2_out));
  and and_2 (and_2_out, comparator_2_lt, ~bitselector_3_out);  // AND_Gate
  BitSelector #(.width(32)) bitselector_3 (.in(multiplexer_1_out), .out(bitselector_3_out), .sel(adder_3_out));
  and and_3 (and_3_out, comparator_3_lt, ~bitselector_4_out);  // AND_Gate
  BitSelector #(.width(32)) bitselector_4 (.in(multiplexer_2_out), .out(bitselector_4_out), .sel(adder_4_out));
  and and_4 (and_4_out, and_1_out, and_2_out);
  and and_5 (and_5_out, comparator_4_lt, ~bitselector_5_out);  // AND_Gate
  BitSelector #(.width(32)) bitselector_5 (.in(multiplexer_3_out), .out(bitselector_5_out), .sel(adder_5_out));
  and and_6 (and_6_out, and_4_out, and_3_out);
  and and_7 (and_7_out, comparator_5_lt, ~bitselector_6_out);  // AND_Gate
  BitSelector #(.width(32)) bitselector_6 (.in(multiplexer_4_out), .out(bitselector_6_out), .sel(adder_6_out));
  and and_8 (and_8_out, and_6_out, and_5_out);
  and and_9 (and_9_out, comparator_6_lt, ~bitselector_7_out);  // AND_Gate
  BitSelector #(.width(32)) bitselector_7 (.in(multiplexer_5_out), .out(bitselector_7_out), .sel(adder_7_out));
  and and_10 (and_10_out, and_8_out, and_7_out);
  and and_11 (and_11_out, comparator_7_lt, ~bitselector_8_out);  // AND_Gate
  BitSelector #(.width(32)) bitselector_8 (.in(multiplexer_6_out), .out(bitselector_8_out), .sel(adder_8_out));
  and and_12 (and_12_out, and_10_out, and_9_out);
  and and_13 (and_13_out, comparator_8_lt, ~bitselector_9_out);  // AND_Gate
  BitSelector #(.width(32)) bitselector_9 (.in(multiplexer_7_out), .out(bitselector_9_out), .sel(adder_9_out));
  and and_14 (and_14_out, and_12_out, and_11_out);
  and and_15 (and_15_out, comparator_9_lt, ~bitselector_10_out);  // AND_Gate
  BitSelector #(.width(32)) bitselector_10 (.in(multiplexer_8_out), .out(bitselector_10_out), .sel(adder_10_out));
  and and_16 (and_16_out, and_14_out, and_13_out);
  and and_17 (and_17_out, comparator_10_lt, ~bitselector_11_out);  // AND_Gate
  BitSelector #(.width(32)) bitselector_11 (.in(multiplexer_9_out), .out(bitselector_11_out), .sel(adder_11_out));
  and and_18 (and_18_out, and_16_out, and_15_out);
  and and_19 (and_19_out, comparator_11_lt, ~bitselector_12_out);  // AND_Gate
  BitSelector #(.width(32)) bitselector_12 (.in(multiplexer_10_out), .out(bitselector_12_out), .sel(adder_12_out));
  and and_20 (and_20_out, and_18_out, and_17_out);
  and and_21 (and_21_out, comparator_12_lt, ~bitselector_13_out);  // AND_Gate
  BitSelector #(.width(32)) bitselector_13 (.in(multiplexer_11_out), .out(bitselector_13_out), .sel(adder_13_out));
  and and_22 (and_22_out, and_20_out, and_19_out);
  and and_23 (and_23_out, comparator_13_lt, ~bitselector_14_out);  // AND_Gate
  BitSelector #(.width(32)) bitselector_14 (.in(multiplexer_12_out), .out(bitselector_14_out), .sel(adder_14_out));
  and and_24 (and_24_out, and_22_out, and_21_out);
  and and_25 (and_25_out, comparator_14_lt, ~bitselector_15_out);  // AND_Gate
  BitSelector #(.width(32)) bitselector_15 (.in(multiplexer_13_out), .out(bitselector_15_out), .sel(adder_15_out));
  and and_26 (and_26_out, and_24_out, and_23_out);
  and and_27 (and_27_out, comparator_15_lt, ~bitselector_16_out);  // AND_Gate
  BitSelector #(.width(32)) bitselector_16 (.in(multiplexer_14_out), .out(bitselector_16_out), .sel(adder_16_out));
  and and_28 (and_28_out, and_26_out, and_25_out);
  and and_29 (and_29_out, comparator_16_lt, ~bitselector_17_out);  // AND_Gate
  BitSelector #(.width(32)) bitselector_17 (.in(multiplexer_15_out), .out(bitselector_17_out), .sel(adder_17_out));
  and and_30 (and_30_out, and_28_out, and_27_out);
  and and_31 (and_31_out, comparator_17_lt, ~bitselector_18_out);  // AND_Gate
  BitSelector #(.width(32)) bitselector_18 (.in(multiplexer_16_out), .out(bitselector_18_out), .sel(adder_18_out));
  and and_32 (and_32_out, and_30_out, and_29_out);
  and and_33 (and_33_out, comparator_18_lt, ~bitselector_19_out);  // AND_Gate
  BitSelector #(.width(32)) bitselector_19 (.in(multiplexer_17_out), .out(bitselector_19_out), .sel(adder_19_out));
  and and_34 (and_34_out, and_32_out, and_31_out);
  and and_35 (and_35_out, comparator_19_lt, ~bitselector_20_out);  // AND_Gate
  BitSelector #(.width(32)) bitselector_20 (.in(multiplexer_18_out), .out(bitselector_20_out), .sel(adder_20_out));
  and and_36 (and_36_out, and_34_out, and_33_out);
  and and_37 (and_37_out, comparator_20_lt, ~bitselector_21_out);  // AND_Gate
  BitSelector #(.width(32)) bitselector_21 (.in(multiplexer_19_out), .out(bitselector_21_out), .sel(adder_21_out));
  and and_38 (and_38_out, and_36_out, and_35_out);
  and and_39 (and_39_out, comparator_21_lt, ~bitselector_22_out);  // AND_Gate
  BitSelector #(.width(32)) bitselector_22 (.in(multiplexer_20_out), .out(bitselector_22_out), .sel(adder_22_out));
  and and_40 (and_40_out, and_38_out, and_37_out);
  and and_41 (and_41_out, comparator_22_lt, ~bitselector_23_out);  // AND_Gate
  BitSelector #(.width(32)) bitselector_23 (.in(multiplexer_21_out), .out(bitselector_23_out), .sel(adder_23_out));
  and and_42 (and_42_out, and_40_out, and_39_out);
  and and_43 (and_43_out, comparator_23_lt, ~bitselector_24_out);  // AND_Gate
  BitSelector #(.width(32)) bitselector_24 (.in(multiplexer_22_out), .out(bitselector_24_out), .sel(adder_24_out));
  and and_44 (and_44_out, and_42_out, and_41_out);
  and and_45 (and_45_out, comparator_24_lt, ~bitselector_25_out);  // AND_Gate
  BitSelector #(.width(32)) bitselector_25 (.in(multiplexer_23_out), .out(bitselector_25_out), .sel(adder_25_out));
  and and_46 (and_46_out, and_44_out, and_43_out);
  and and_47 (and_47_out, comparator_25_lt, ~bitselector_26_out);  // AND_Gate
  BitSelector #(.width(32)) bitselector_26 (.in(multiplexer_24_out), .out(bitselector_26_out), .sel(adder_26_out));
  and and_48 (and_48_out, and_46_out, and_45_out);
  and and_49 (and_49_out, comparator_26_lt, ~bitselector_27_out);  // AND_Gate
  BitSelector #(.width(32)) bitselector_27 (.in(multiplexer_25_out), .out(bitselector_27_out), .sel(adder_27_out));
  and and_50 (and_50_out, and_48_out, and_47_out);
  and and_51 (and_51_out, comparator_27_lt, ~bitselector_28_out);  // AND_Gate
  BitSelector #(.width(32)) bitselector_28 (.in(multiplexer_26_out), .out(bitselector_28_out), .sel(adder_28_out));
  and and_52 (and_52_out, and_50_out, and_49_out);
  and and_53 (and_53_out, comparator_28_lt, ~bitselector_29_out);  // AND_Gate
  BitSelector #(.width(32)) bitselector_29 (.in(multiplexer_27_out), .out(bitselector_29_out), .sel(adder_29_out));
  and and_54 (and_54_out, and_52_out, and_51_out);
  and and_55 (and_55_out, comparator_29_lt, ~bitselector_30_out);  // AND_Gate
  BitSelector #(.width(32)) bitselector_30 (.in(multiplexer_28_out), .out(bitselector_30_out), .sel(adder_30_out));
  and and_56 (and_56_out, and_54_out, and_53_out);
  and and_57 (and_57_out, comparator_30_lt, ~bitselector_31_out);  // AND_Gate
  BitSelector #(.width(32)) bitselector_31 (.in(multiplexer_29_out), .out(bitselector_31_out), .sel(adder_31_out));
  and and_58 (and_58_out, and_56_out, and_55_out);
  and and_59 (and_59_out, comparator_31_lt, ~bitselector_32_out);  // AND_Gate
  BitSelector #(.width(32)) bitselector_32 (.in(multiplexer_30_out), .out(bitselector_32_out), .sel(adder_32_out));
  and and_60 (and_60_out, and_58_out, and_57_out);
  Adder #(.width(5)) adder_33 (.a(bitadder_1_out), .b(5'b00001), .out(adder_33_out));  // open: cin, cout
  Adder #(.width(5)) adder_34 (.a(Counter_in), .b(adder_33_out), .out(Counter_out));  // open: cin, cout
  not not_1 (Load, Count);
  BitAdder #(.width(1)) bitadder_1 (
    .in0(and_1_out), .in1(and_2_out), .in2(and_3_out), .in3(and_5_out), .in4(and_7_out), .in5(and_9_out),
    .in6(and_11_out), .in7(and_13_out), .in8(and_15_out), .in9(and_17_out), .in10(and_19_out),
    .in11(and_21_out), .in12(and_23_out), .in13(and_25_out), .in14(and_27_out), .in15(and_29_out),
    .in16(and_31_out), .in17(and_33_out), .in18(and_35_out), .in19(and_37_out), .in20(and_39_out),
    .in21(and_41_out), .in22(and_43_out), .in23(and_45_out), .in24(and_47_out), .in25(and_49_out),
    .in26(and_51_out), .in27(and_53_out), .in28(and_55_out), .in29(and_57_out), .in30(and_59_out),
    .out(bitadder_1_out));
endmodule
