// Logisim project комп_v6.circ as structural Verilog
module \CPU_Сore__CPUC  (
  input  Overtimed,
  input  Data_in,
  input  [31:0] Data_in_2,
  input  [31:0] Main_core_comand,
  input  Power,
  input  Clk,
  input  Start_CPU_Core,
  input  [31:0] Execute_Device,
  input  [31:0] Data_in__U,
  output [31:0] Data_in_3,
  output Occured,
  output [31:0] Data_adress_out,
  output [31:0] Data_out,
  output compare,
  output Error,
  output [31:0] ETYPE,
  output [2:0] CPU_Core_condition
);

  wire _1, _2, _3, _4, _5, _6, _7, Access_to_RAM__US, and_2_out, and_3_out, and_4_out, and_7_out, and_8_out,
       and_11_out, Clk_t, comparator_1_eq, Enable_Date_reg, Enable_operation_with_TM, j_k_ff_1_q,
       j_k_ff_1_qn, Load_A, Load_C, Load_D, Load_PCP, Load_PCSP, Load_select__PC, Load_timer, Load_USP,
       Load_Y, not_1_out, not_2_out, or_1_out, or_4_out, or_6_out, or_7_out, Pop, priority_encoder_2_gs,
       Program_reset, Push, Reset, Reset_clk_reg, Reset_RAM__CP, Reset_speed_clk, Reset_timer, Reset_TM,
       UP_DOWN__PC, UP_DOWN__US, UPop, UPush, Z_control, \программная_остановка ;
  wire [0:0] simplified_cpp_scpp_1__0_31;
  wire [1:0] counter_1_q, DA_in, DA_out, priority_encoder_1_out, \Сlock_load_control ;
  wire [2:0] A_load_control_bits, ALU_select_B, \alu_сpu_gpu_1_error_type , C_load_control_bits,
       multiplexer_6_out, priority_encoder_2_out, Y_load_control_bits, Z_Load_control_bits;
  wire [3:0] TM_adress;
  wire [4:0] TM_COMAND;
  wire [22:0] ALU_operation;
  wire [23:0] multiplexer_3_out;
  wire [31:0] A, ALU_result, \alu_сpu_gpu_1_c , C, \const , D, multiplexer_4_out, multiplexer_5_out,
       multiplexer_7_out, multiplexer_8_out, multiplexer_10_out, or_5_out, PC_out, random_1_out,
       random_2_out, Timer_time, UStack_out, Y, Z;
  wire [31:17] simplified_cpp_scpp_1__64_95;

  Multiplexer #(.select(2), .width(32), .disabled(0)) multiplexer_1 (
    .in0(PC_out), .in1(\const ), .in2(C), .in3(Z), .out(Data_in_3), .sel(DA_in), .en(Power));
  Multiplexer #(.select(2), .width(32), .disabled(0)) multiplexer_2 (
    .in0(PC_out), .in1(ALU_result), .in2(\const ), .in3(C), .out(Data_adress_out), .sel(DA_out), .en(Power));
  Pull_Resistor pull_resistor_1 (.node(Data_in));
  Pull_Resistor pull_resistor_2 (.node(Data_in_2));
  Pull_Resistor pull_resistor_3 (.node(Main_core_comand));
  Pull_Resistor pull_resistor_4 (.node(Start_CPU_Core));
  Pull_Resistor pull_resistor_5 (.node(Clk));
  Pull_Resistor pull_resistor_6 (.node(Execute_Device));
  Pull_Resistor pull_resistor_7 (.node(Data_in__U));
  and and_1 (Clk_t, Power, ~or_1_out, Clk);  // AND_Gate
  Pull_Resistor pull_resistor_8 (.node(Power));
  or or_1 (or_1_out, and_4_out, and_3_out);
  D_Flip_Flop d_ff_1 (
    .clk(Start_CPU_Core), .D(Power), .Q(CPU_Core_condition[0]), .preset(1'b0), .en(Power), .reset(Reset));  // open: Qn
  and and_2 (and_2_out, CPU_Core_condition[0], Clk_t);
  and and_3 (and_3_out, ~Overtimed, _7);  // AND_Gate
  and and_4 (and_4_out, ~Data_in, _1);  // AND_Gate
  or or_2 (Reset, ~Power, Program_reset, Main_core_comand[5]);  // OR_Gate
  J_K_Flip_Flop j_k_ff_1 (
    .J(Power), .clk(and_2_out), .K(Power), .Q(j_k_ff_1_q), .Qn(j_k_ff_1_qn), .preset(1'b0), .en(Power),
    .reset(Reset));
  or or_3 (Z_control, Data_in__U[0], Data_in__U[1], Data_in__U[2], Data_in__U[3], Data_in__U[4], Data_in__U[5], Data_in__U[6], Data_in__U[7], Data_in__U[8], Data_in__U[9], Data_in__U[10], Data_in__U[11], Data_in__U[12], Data_in__U[13], Data_in__U[14], Data_in__U[15], Data_in__U[17], Data_in__U[18], Data_in__U[19], Data_in__U[20], Data_in__U[21], Data_in__U[22], Data_in__U[23], Data_in__U[24], Data_in__U[25], Data_in__U[26], Data_in__U[27], Data_in__U[28], Data_in__U[29], Data_in__U[30], Data_in__U[31], Data_in__U[16]);
  and and_5 (CPU_Core_condition[1], and_2_out, j_k_ff_1_q);
  and and_6 (CPU_Core_condition[2], j_k_ff_1_qn, and_2_out);
  Counter #(.width(2), .max('h3)) counter_1 (
    .load(1'b0), .D(2'b00), .count(Main_core_comand[0]), .Q(counter_1_q), .clk(Clk_t), .clr(not_1_out));  // open: carry
  not not_1 (not_1_out, Main_core_comand[0]);
  Priority_Encoder #(.select(2), .disabled(0)) priority_encoder_1 (
    .in0(1'b1), .in1(_4), .in2(_3), .in3(Main_core_comand[0]), .out(priority_encoder_1_out), .en_in(Power));  // open: gs, en_out
  and and_7 (and_7_out, compare, _5);
  or or_4 (or_4_out, _2, and_7_out, Reset);
  Multiplexer #(.select(2), .width(24), .disabled(0)) multiplexer_3 (
    .in0(PC_out[23:0]), .in1(C[23:0]), .in2(\const [23:0]), .in3(Main_core_comand[31:8]),
    .out(multiplexer_3_out), .sel(priority_encoder_1_out), .en(Power));
  File_Register__Cash file_register_cash_1 (
    .Data_in(multiplexer_4_out), .Clk(Clk_t), .Reset(Reset), .Load_Reg(Load_A), .Power(Power), .Data_out(A));
  Multiplexer #(.select(3), .width(32), .disabled(0)) multiplexer_4 (
    .in0(Data_in_2), .in1(random_1_out), .in2(D), .in3(UStack_out), .in4(Z), .in5(\const ), .in6(PC_out),
    .in7(Timer_time), .out(multiplexer_4_out), .sel(A_load_control_bits), .en(Power));
  Simplified_CPP__SCPP simplified_cpp_scpp_1 (
    .Power(Power), .\Сlk (Clk_t), .Load(Main_core_comand[0]), .Load_completed(Main_core_comand[2]),
    .Reset(or_4_out), .adress(multiplexer_3_out), .Data_in(Data_in_2), .Occured(Occured),
    ._0_31({Load_PCP, Load_C, Push, Pop, Load_Y, simplified_cpp_scpp_1__0_31[0], ALU_select_B, ALU_operation}),
    ._32_63({Load_timer, Enable_operation_with_TM, Reset_clk_reg, TM_adress, Enable_Date_reg, \Сlock_load_control , Y_load_control_bits, C_load_control_bits, A_load_control_bits, Z_Load_control_bits, \программная_остановка , Load_USP, UP_DOWN__US, UPop, Access_to_RAM__US, UPush, Reset_RAM__CP, Load_select__PC, UP_DOWN__PC, Load_PCSP}),
    ._64_95({simplified_cpp_scpp_1__64_95[31:24], DA_in, simplified_cpp_scpp_1__64_95[21:17], _7, Load_D, _1, _2, _5, _4, _3, DA_out, TM_COMAND, Reset_speed_clk, Reset_timer, Reset_TM}),
    ._96_127(\const ), .RAM_number(counter_1_q));
  Multiplexer #(.select(3), .width(32), .disabled(0)) multiplexer_5 (
    .in0(Execute_Device), .in1(Z), .in2(ALU_result), .in3(A), .in4(UStack_out), .in5(C), .in6(random_1_out),
    .in7(\const ), .out(multiplexer_5_out), .sel(Y_load_control_bits), .en(Power));
  Random #(.width(32)) random_1 (.clk(Clk_t), .next(Clk_t), .out(random_1_out));  // open: clr
  File_Register__Cash file_register_cash_2 (
    .Data_in(multiplexer_5_out), .Clk(Clk_t), .Reset(Reset), .Load_Reg(Load_Y), .Power(Power), .Data_out(Y));
  and and_8 (and_8_out, _6, CPU_Core_condition[2]);
  Multiplexer #(.width(3)) multiplexer_6 (
    .in0(Z_Load_control_bits), .in1(3'b111), .out(multiplexer_6_out), .sel(Z_control), .en(Power));
  assign or_5_out = \const  | {simplified_cpp_scpp_1__64_95[31:24], DA_in, simplified_cpp_scpp_1__64_95[21:17], _7, Load_D, _1, _2, _5, _4, _3, DA_out, TM_COMAND, Reset_speed_clk, Reset_timer, Reset_TM} | {Load_timer, Enable_operation_with_TM, Reset_clk_reg, TM_adress, Enable_Date_reg, \Сlock_load_control , Y_load_control_bits, C_load_control_bits, A_load_control_bits, Z_Load_control_bits, \программная_остановка , Load_USP, UP_DOWN__US, UPop, Access_to_RAM__US, UPush, Reset_RAM__CP, Load_select__PC, UP_DOWN__PC, Load_PCSP} | {Load_PCP, Load_C, Push, Pop, Load_Y, simplified_cpp_scpp_1__0_31[0], ALU_select_B, ALU_operation};  // OR_Gate or_5, 32 bits wide
  File_Register__Cash file_register_cash_3 (
    .Data_in(multiplexer_7_out), .Clk(Clk_t), .Reset(Reset), .Load_Reg(and_8_out), .Power(Power), .Data_out(Z));
  Multiplexer #(.select(3), .width(32), .disabled(0)) multiplexer_7 (
    .in0(Data_in_2), .in1(C), .in2(PC_out), .in3(Execute_Device), .in4(ALU_result), .in5(UStack_out),
    .in6(\const ), .in7(Data_in__U), .out(multiplexer_7_out), .sel(multiplexer_6_out), .en(Power));
  or or_6 (or_6_out, or_5_out[31], or_5_out[30], or_5_out[29], or_5_out[28], or_5_out[27], or_5_out[26], or_5_out[25], or_5_out[24], or_5_out[23], or_5_out[22], or_5_out[21], or_5_out[20], or_5_out[19], or_5_out[18], or_5_out[17], or_5_out[16], or_5_out[14], or_5_out[13], or_5_out[12], or_5_out[11], or_5_out[10], or_5_out[9], or_5_out[8], or_5_out[7], or_5_out[6], or_5_out[5], or_5_out[4], or_5_out[3], or_5_out[2], or_5_out[1], or_5_out[0], or_5_out[15]);
  not not_2 (not_2_out, or_6_out);
  and and_9 (Program_reset, not_2_out, Occured);
  File_Register__Cash file_register_cash_4 (
    .Data_in(Data_in_2), .Clk(Clk_t), .Reset(Reset), .Load_Reg(Load_D), .Power(Power), .Data_out(D));
  File_Register__Cash file_register_cash_5 (
    .Data_in(multiplexer_8_out), .Clk(Clk_t), .Reset(Reset), .Load_Reg(Load_C), .Power(Power), .Data_out(C));
  Random #(.width(32)) random_2 (.clk(Clk_t), .next(Clk_t), .out(random_2_out));  // open: clr
  Multiplexer #(.select(3), .width(32), .disabled(0)) multiplexer_8 (
    .in0(Y), .in1(A), .in2(Z), .in3(D), .in4(UStack_out), .in5(random_2_out), .in6(\const ),
    .in7(Timer_time), .out(multiplexer_8_out), .sel(C_load_control_bits), .en(Power));
  Priority_Encoder priority_encoder_2 (
    .in0(simplified_cpp_scpp_1__64_95[24]), .in1(simplified_cpp_scpp_1__64_95[25]),
    .in2(simplified_cpp_scpp_1__64_95[26]), .in3(simplified_cpp_scpp_1__64_95[27]),
    .in4(simplified_cpp_scpp_1__64_95[28]), .in5(simplified_cpp_scpp_1__64_95[29]),
    .in6(simplified_cpp_scpp_1__64_95[30]), .in7(simplified_cpp_scpp_1__64_95[31]),
    .out(priority_encoder_2_out), .en_in(Power), .gs(priority_encoder_2_gs));  // open: en_out
  Multiplexer #(.select(3), .width(32), .disabled(0)) multiplexer_9 (
    .in0(A), .in1(Y), .in2(Z), .in3(D), .in4(C), .in5(ALU_result), .in6(PC_out), .out(Data_out),
    .sel(priority_encoder_2_out), .en(priority_encoder_2_gs));  // open: in7
  or or_7 (or_7_out, Z_control, Load_PCP);
  and and_10 (Load_A, 1'b1, and_11_out);
  PC pc_1 (
    .sRam(Data_in_2), .Stack_Pointer__in(C), .Z(Z), .Power(Power), .Reset(Reset), .Clk(Clk_t),
    .Load_PC_Pointer(or_7_out), .Load_Stack_Pointer(Load_PCSP), .Push(Push), .Pop(Pop),
    .UP_0__DOWN_1(UP_DOWN__PC), .Load_Select(Load_select__PC), .Data_out(PC_out));
  \ALU__СPU_GPU  \alu_сpu_gpu_1  (
    .Power(Power), .Operation(ALU_operation), .A(Y), .B(multiplexer_10_out), .C(\alu_сpu_gpu_1_c ),
    .compare(compare), .Error(Error), .Error_type(\alu_сpu_gpu_1_error_type ));
  Multiplexer #(.select(3), .width(32), .disabled(0)) multiplexer_10 (
    .in0(Z), .in1(D), .in2(A), .in3(Y), .in4(Data_in_2), .in5(C), .in6(\const ), .out(multiplexer_10_out),
    .sel(ALU_select_B), .en(Power));  // open: in7
  and and_11 (and_11_out, Data_in, comparator_1_eq);
  Comparator #(.width(3), .mode("unsigned")) comparator_1 (
    .a(3'b000), .b(A_load_control_bits), .eq(comparator_1_eq));  // open: gt, lt
  assign ETYPE = {{29{1'b0}}, \alu_сpu_gpu_1_error_type };  // Bit_Extender bit_extender_1
  Comparator #(.width(3), .mode("unsigned")) comparator_2 (
    .a(3'b000), .b(Z_Load_control_bits), .eq(_6));  // open: gt, lt
  Multiplexer #(.width(32), .disabled(0)) multiplexer_11 (
    .in0(\alu_сpu_gpu_1_c ), .in1({32{1'b0}}), .out(ALU_result), .sel(Error), .en(Power));

  // Other names for the same wires on the sheet: ALU_ERROR = Error; Comparation = compare;
  //   Execute = CPU_Core_condition[1]; Fetch = CPU_Core_condition[2]; Data_in__Users_Comand[31:0] = Data_in__U;
  //   Data_in_t[31:0] = Data_in_2; E_TYPE[31:0] = ETYPE; ED[31:0] = Execute_Device; Load = Main_core_comand[0];
  //   LC = Main_core_comand[2]; RAM_Adress[23:0] = Main_core_comand[31:8]
endmodule

module \ALU__СPU_GPU  (
  input  Power,
  input  [22:0] Operation,
  input  [31:0] A,
  input  [31:0] B,
  output [31:0] C,
  output Error,
  output [2:0] Error_type,
  output compare
);

  wire bitselector_1_out, bitselector_2_out, bitselector_3_out, comparator_1_eq, comparator_1_gt,
       comparator_1_lt, comparator_2_p3, comparator_2_p4, comparator_2_p5, comparator_3_eq, comparator_4_eq,
       comparator_5_eq, comparator_6_eq, comparator_7_eq, comparator_8_eq, comparator_9_eq, comparator_10_eq,
       comparator_10_gt, comparator_10_lt, multiplexer_5_out, or_2_out;
  wire [0:0] pull_resistor_9_node;
  wire [2:0] and_2_out;
  wire [4:0] bit_extender_7_out, multiplexer_3_out, priority_encoder_1_out, priority_encoder_2_out,
       priority_encoder_3_out, priority_encoder_4_out;
  wire [5:0] bitadder_1_out, bitadder_2_out, bitadder_4_out, bitadder_5_out;
  wire [6:0] bitadder_3_out, bitadder_6_out;
  wire [11:0] pull_resistor_8_node;
  wire [31:0] adder_1_p3, adder_2_out, adder_3_out, and_1_out, and_5_out, bit_extender_1_out,
       bit_extender_2_out, bit_extender_3_out, bit_extender_4_out, bit_extender_5_out, bit_extender_6_out,
       bit_extender_8_out, bit_extender_9_out, bit_extender_10_out, bit_extender_11_out, bit_extender_12_out,
       bit_extender_13_out, bit_extender_14_out, cos_1_p2, divider_1_p3, divider_2_out, divider_2_rem,
       divider_3_out, divider_3_rem, even_parity_1_out, even_parity_2_out, exponentiate_1_p3, fp_to_int_1_p2,
       fp_to_int_2_p4, fp_to_int_3_p2, increesor_1_out_2, increesor_2_out_2, increesor_3_out_2,
       increesor_4_out_2, int_to_fp_1_p2, ln_1_p2, log_1_p3, mod_1_p3, multiplexer_2_out, multiplexer_6_out,
       multiplier_1_p3, multiplier_2_cout, multiplier_2_out, multiplier_3_cout, multiplier_3_out,
       negator_1_out, negator_2_out, negator_3_out, odd_parity_1_out, odd_parity_2_out, or_1_out, or_4_out,
       pow_1_p2, pull_resistor_7_node, pull_resistor_10_node, root_1_p3, shifter_1_out, shifter_2_out,
       shifter_3_out, shifter_4_out, shifter_5_out, shifter_6_out, shifter_7_out, shifter_8_out,
       shifter_9_out, shifter_10_out, shifter_11_out, shifter_12_out, shifter_13_out, shifter_14_out,
       shifter_15_out, sin_1_p2, sqrt_1_p2, subtractor_1_p3, subtractor_2_out, subtractor_3_out, tan_1_p2,
       xor_1_out, xor_2_out;

  Pull_Resistor pull_resistor_1 (.node(B));
  Pull_Resistor pull_resistor_2 (.node(A));
  Pull_Resistor pull_resistor_3 (.node(Operation));
  Pull_Resistor pull_resistor_4 (.node(Power));
  // Adder adder_1: pin names not known; wires that end beside it: A, B, adder_1_p3
  // Subtractor subtractor_1: pin names not known; wires that end beside it: A, B, subtractor_1_p3
  // Multiplier multiplier_1: pin names not known; wires that end beside it: A, B, multiplier_1_p3
  // Divider divider_1: pin names not known; wires that end beside it: A, B, divider_1_p3
  // Sin sin_1: pin names not known; wires that end beside it: A, sin_1_p2
  // Cos cos_1: pin names not known; wires that end beside it: A, cos_1_p2
  // Tan tan_1: pin names not known; wires that end beside it: A, tan_1_p2
  // Sqrt sqrt_1: pin names not known; wires that end beside it: A, sqrt_1_p2
  // Mod mod_1: pin names not known; wires that end beside it: A, B, mod_1_p3
  // Root root_1: pin names not known; wires that end beside it: A, B, root_1_p3
  // Log log_1: pin names not known; wires that end beside it: A, B, log_1_p3
  // Exponentiate exponentiate_1: pin names not known; wires that end beside it: A, B, exponentiate_1_p3
  // Pow pow_1: pin names not known; wires that end beside it: A, pow_1_p2
  // LN ln_1: pin names not known; wires that end beside it: A, ln_1_p2
  // Int_To_FP int_to_fp_1: pin names not known; wires that end beside it: A, int_to_fp_1_p2
  // FP_to_Int fp_to_int_1: pin names not known; wires that end beside it: A, fp_to_int_1_p2
  increesor increesor_1 (.in(A), .out_2(increesor_1_out_2));
  increesor increesor_2 (.in(B), .out_2(increesor_2_out_2));
  BitAdder #(.width(32)) bitadder_1 (.in0(A), .out(bitadder_1_out));
  assign bit_extender_1_out = {{26{1'b0}}, bitadder_1_out};  // Bit_Extender bit_extender_1
  assign bit_extender_2_out = {{26{1'b0}}, bitadder_2_out};  // Bit_Extender bit_extender_2
  BitAdder #(.width(32)) bitadder_2 (.in0(B), .out(bitadder_2_out));
  assign bit_extender_3_out = {{25{1'b0}}, bitadder_3_out};  // Bit_Extender bit_extender_3
  BitAdder #(.width(32)) bitadder_3 (.in0(A), .in1(B), .out(bitadder_3_out));
  assign or_1_out = A | B;  // OR_Gate or_1, 32 bits wide
  assign and_1_out = A & B;  // AND_Gate and_1, 32 bits wide
  assign xor_1_out = A ^ B;  // XOR_Gate xor_1, 32 bits wide
  assign odd_parity_1_out = A ^ B;  // Odd_Parity odd_parity_1, 32 bits wide
  assign even_parity_1_out = ~(A ^ B);  // Even_Parity even_parity_1, 32 bits wide
  assign bit_extender_4_out = {{31{1'b0}}, bitselector_1_out};  // Bit_Extender bit_extender_4
  BitSelector #(.width(32)) bitselector_1 (.in(A), .out(bitselector_1_out), .sel(Operation[22:18]));
  Comparator #(.width(32), .mode("unsigned")) comparator_1 (
    .a(A), .b(B), .gt(comparator_1_gt), .eq(comparator_1_eq), .lt(comparator_1_lt));
  // Comparator comparator_2: pin names not known; wires that end beside it: A, B, comparator_2_p3, comparator_2_p4, comparator_2_p5
  Priority_Encoder #(.select(5), .disabled(0)) priority_encoder_1 (
    .in0(A[31]), .in1(A[30]), .in2(A[29]), .in3(A[28]), .in4(A[27]), .in5(A[26]), .in6(A[25]), .in7(A[24]),
    .in8(A[23]), .in9(A[22]), .in10(A[21]), .in11(A[20]), .in12(A[19]), .in13(A[18]), .in14(A[17]),
    .in15(A[16]), .in16(A[15]), .in17(A[14]), .in18(A[13]), .in19(A[12]), .in20(A[11]), .in21(A[10]),
    .in22(A[9]), .in23(A[8]), .in24(A[7]), .in25(A[6]), .in26(A[5]), .in27(A[4]), .in28(A[3]), .in29(A[2]),
    .in30(A[1]), .in31(A[0]), .out(priority_encoder_1_out));
  Priority_Encoder #(.select(5), .disabled(0)) priority_encoder_2 (
    .in0(B[31]), .in1(B[30]), .in2(B[29]), .in3(B[28]), .in4(B[27]), .in5(B[26]), .in6(B[25]), .in7(B[24]),
    .in8(B[23]), .in9(B[22]), .in10(B[21]), .in11(B[20]), .in12(B[19]), .in13(B[18]), .in14(B[17]),
    .in15(B[16]), .in16(B[15]), .in17(B[14]), .in18(B[13]), .in19(B[12]), .in20(B[11]), .in21(B[10]),
    .in22(B[9]), .in23(B[8]), .in24(B[7]), .in25(B[6]), .in26(B[5]), .in27(B[4]), .in28(B[3]), .in29(B[2]),
    .in30(B[1]), .in31(B[0]), .out(priority_encoder_2_out));
  assign bit_extender_5_out = {{27{1'b0}}, priority_encoder_1_out};  // Bit_Extender bit_extender_5
  assign bit_extender_6_out = {{27{1'b0}}, priority_encoder_2_out};  // Bit_Extender bit_extender_6
  Pull_Resistor pull_resistor_5 (.node(compare));
  Multiplexer #(.select(3), .disabled(0)) multiplexer_1 (
    .in0(1'b0), .in1(comparator_1_gt), .in2(comparator_1_eq), .in3(comparator_1_lt), .in4(1'b1),
    .in5(comparator_2_p3), .in6(comparator_2_p4), .in7(comparator_2_p5), .out(compare),
    .sel(Operation[13:11]), .en(Power));
  Bit_Extender #(.in_width(32), .out_width(5)) bit_extender_7 (.in(B), .out(bit_extender_7_out));
  Multiplexer #(.select(5), .width(32)) multiplexer_2 (
    .in0(A), .in1(B), .in2(adder_1_p3), .in3(subtractor_1_p3), .in4(multiplier_1_p3), .in5(divider_1_p3),
    .in6(sin_1_p2), .in7(cos_1_p2), .in8(tan_1_p2), .in9(sqrt_1_p2), .in10(mod_1_p3), .in11(root_1_p3),
    .in12(log_1_p3), .in13(exponentiate_1_p3), .in14(pow_1_p2), .in15(ln_1_p2), .in16(int_to_fp_1_p2),
    .in17(fp_to_int_1_p2), .in18(bit_extender_1_out), .in19(bit_extender_2_out), .in20(bit_extender_3_out),
    .in21(or_1_out), .in22(and_1_out), .in23(xor_1_out), .in24(odd_parity_1_out), .in25(even_parity_1_out),
    .in26(increesor_1_out_2), .in27(increesor_2_out_2), .in28(bit_extender_5_out), .in29(bit_extender_6_out),
    .in30(bit_extender_4_out), .in31({32{1'b1}}), .out(multiplexer_2_out), .sel(Operation[4:0]), .en(Power));
  Multiplexer #(.width(5), .disabled(0)) multiplexer_3 (
    .in0(bit_extender_7_out), .in1(Operation[10:6]), .out(multiplexer_3_out), .sel(Operation[5]), .en(Power));
  Negator #(.width(32)) negator_1 (.in(multiplexer_2_out), .out(negator_1_out));
  Shifter #(.width(32)) shifter_1 (.in(multiplexer_2_out), .\dist (multiplexer_3_out), .out(shifter_1_out));
  Shifter #(.width(32), .shift("lr")) shifter_2 (
    .in(multiplexer_2_out), .\dist (multiplexer_3_out), .out(shifter_2_out));
  Shifter #(.width(32), .shift("ar")) shifter_3 (
    .in(multiplexer_2_out), .\dist (multiplexer_3_out), .out(shifter_3_out));
  Shifter #(.width(32), .shift("rl")) shifter_4 (
    .in(multiplexer_2_out), .\dist (multiplexer_3_out), .out(shifter_4_out));
  Shifter #(.width(32), .shift("rr")) shifter_5 (
    .in(multiplexer_2_out), .\dist (multiplexer_3_out), .out(shifter_5_out));
  Adder #(.width(32)) adder_2 (.a(A), .b(B), .out(adder_2_out));  // open: cin, cout
  Subtractor #(.width(32)) subtractor_2 (.a(A), .b(B), .out(subtractor_2_out));  // open: bin, bout
  Multiplier #(.width(32)) multiplier_2 (.a(A), .b(B), .out(multiplier_2_out), .cout(multiplier_2_cout));  // open: cin
  Divider #(.width(32)) divider_2 (.a(A), .b(B), .out(divider_2_out), .rem(divider_2_rem));  // open: upper
  Comparator #(.width(4)) comparator_3 (.a(Operation[17:14]), .b(4'b1011), .eq(comparator_3_eq));  // open: gt, lt
  Comparator #(.width(4)) comparator_4 (.a(Operation[17:14]), .b(4'b1100), .eq(comparator_4_eq));  // open: gt, lt
  Comparator #(.width(32)) comparator_5 (.a(B), .b({32{1'b0}}), .eq(comparator_5_eq));  // open: gt, lt
  // FP_to_Int fp_to_int_2: pin names not known; wires that end beside it: 4'b1011, 4'b1100, sin_1_p2, fp_to_int_2_p4
  // FP_to_Int fp_to_int_3: pin names not known; wires that end beside it: B, fp_to_int_3_p2
  or or_2 (or_2_out, comparator_3_eq, comparator_4_eq);
  Comparator #(.width(32)) comparator_6 (.a({32{1'b0}}), .b(fp_to_int_2_p4), .eq(comparator_6_eq));  // open: gt, lt
  Comparator #(.width(32)) comparator_7 (.a({32{1'b0}}), .b(fp_to_int_3_p2), .eq(comparator_7_eq));  // open: gt, lt
  Comparator #(.width(5)) comparator_8 (.a(Operation[4:0]), .b(5'b00101), .eq(comparator_8_eq));  // open: gt, lt
  Comparator #(.width(5)) comparator_9 (.a(Operation[4:0]), .b(5'b01000), .eq(comparator_9_eq));  // open: gt, lt
  and and_2 (and_2_out[0], or_2_out, comparator_5_eq);
  and and_3 (and_2_out[1], comparator_7_eq, comparator_8_eq);
  and and_4 (and_2_out[2], comparator_6_eq, comparator_9_eq);
  Pull_Resistor pull_resistor_6 (.node(C));
  Multiplexer #(.select(4), .width(32), .disabled(0)) multiplexer_4 (
    .in0(multiplexer_2_out), .in1(negator_1_out), .in2(shifter_1_out), .in3(shifter_2_out),
    .in4(shifter_3_out), .in5(shifter_4_out), .in6(shifter_5_out), .in7(adder_2_out), .in8(subtractor_2_out),
    .in9(multiplier_2_out), .in10(multiplier_2_cout), .in11(divider_2_out), .in12(divider_2_rem),
    .in13({32{1'b0}}), .in14({32{1'b0}}), .in15({32{1'b0}}), .out(C), .sel(Operation[17:14]), .en(Power));
  or or_3 (Error, and_2_out[0], and_2_out[1], and_2_out[2]);
  Register #(.width(3)) register_1 (.D(and_2_out), .en(Error), .Q(Error_type), .clk(Error), .clr(1'b0));
  Pull_Resistor pull_resistor_7 (.node(pull_resistor_7_node));
  Pull_Resistor pull_resistor_8 (.node(pull_resistor_8_node));
  Pull_Resistor pull_resistor_9 (.node(pull_resistor_9_node[0]));
  Pull_Resistor pull_resistor_10 (.node(pull_resistor_10_node));
  assign or_4_out = pull_resistor_7_node | pull_resistor_10_node;  // OR_Gate or_4, 32 bits wide
  assign and_5_out = pull_resistor_7_node & pull_resistor_10_node;  // AND_Gate and_5, 32 bits wide
  assign odd_parity_2_out = pull_resistor_7_node ^ pull_resistor_10_node;  // Odd_Parity odd_parity_2, 32 bits wide
  assign even_parity_2_out = ~(pull_resistor_7_node ^ pull_resistor_10_node);  // Even_Parity even_parity_2, 32 bits wide
  increesor increesor_3 (.in(pull_resistor_7_node), .out_2(increesor_3_out_2));
  increesor increesor_4 (.in(pull_resistor_10_node), .out_2(increesor_4_out_2));
  BitSelector #(.width(32)) bitselector_2 (
    .in(pull_resistor_7_node), .out(bitselector_2_out), .sel(pull_resistor_8_node[9:5]));
  BitSelector #(.width(32)) bitselector_3 (
    .in(pull_resistor_10_node), .out(bitselector_3_out), .sel(pull_resistor_8_node[9:5]));
  Adder #(.width(32)) adder_3 (
    .a(pull_resistor_7_node), .b(pull_resistor_10_node), .out(adder_3_out));  // open: cin, cout
  Subtractor #(.width(32)) subtractor_3 (
    .a(pull_resistor_7_node), .b(pull_resistor_10_node), .out(subtractor_3_out));  // open: bin, bout
  Multiplier #(.width(32)) multiplier_3 (
    .a(pull_resistor_7_node), .b(pull_resistor_10_node), .out(multiplier_3_out), .cout(multiplier_3_cout));  // open: cin
  Divider #(.width(32)) divider_3 (
    .a(pull_resistor_7_node), .b(pull_resistor_10_node), .out(divider_3_out), .rem(divider_3_rem));  // open: upper
  Negator #(.width(32)) negator_2 (.in(pull_resistor_7_node), .out(negator_2_out));
  Negator #(.width(32)) negator_3 (.in(pull_resistor_10_node), .out(negator_3_out));
  Shifter #(.width(32)) shifter_6 (.in(pull_resistor_7_node), .\dist (pull_resistor_8_node[9:5]), .out(shifter_6_out));
  Shifter #(.width(32), .shift("lr")) shifter_7 (
    .in(pull_resistor_7_node), .\dist (pull_resistor_8_node[9:5]), .out(shifter_7_out));
  Shifter #(.width(32), .shift("ar")) shifter_8 (
    .in(pull_resistor_7_node), .\dist (pull_resistor_8_node[9:5]), .out(shifter_8_out));
  Shifter #(.width(32), .shift("rl")) shifter_9 (
    .in(pull_resistor_7_node), .\dist (pull_resistor_8_node[9:5]), .out(shifter_9_out));
  Shifter #(.width(32), .shift("rr")) shifter_10 (
    .in(pull_resistor_7_node), .\dist (pull_resistor_8_node[9:5]), .out(shifter_10_out));
  Shifter #(.width(32)) shifter_11 (
    .in(pull_resistor_10_node), .\dist (pull_resistor_8_node[9:5]), .out(shifter_11_out));
  Shifter #(.width(32), .shift("lr")) shifter_12 (
    .in(pull_resistor_10_node), .\dist (pull_resistor_8_node[9:5]), .out(shifter_12_out));
  Shifter #(.width(32), .shift("ar")) shifter_13 (
    .in(pull_resistor_10_node), .\dist (pull_resistor_8_node[9:5]), .out(shifter_13_out));
  Shifter #(.width(32), .shift("rl")) shifter_14 (
    .in(pull_resistor_10_node), .\dist (pull_resistor_8_node[9:5]), .out(shifter_14_out));
  Shifter #(.width(32), .shift("rr")) shifter_15 (
    .in(pull_resistor_10_node), .\dist (pull_resistor_8_node[9:5]), .out(shifter_15_out));
  BitAdder #(.width(32)) bitadder_4 (.in0(pull_resistor_7_node), .out(bitadder_4_out));
  assign bit_extender_8_out = {{26{1'b0}}, bitadder_4_out};  // Bit_Extender bit_extender_8
  BitAdder #(.width(32)) bitadder_5 (.in0(pull_resistor_10_node), .out(bitadder_5_out));
  assign bit_extender_9_out = {{26{1'b0}}, bitadder_5_out};  // Bit_Extender bit_extender_9
  assign bit_extender_10_out = {{25{1'b0}}, bitadder_6_out};  // Bit_Extender bit_extender_10
  BitAdder #(.width(32)) bitadder_6 (.in0(pull_resistor_7_node), .in1(pull_resistor_10_node), .out(bitadder_6_out));
  assign xor_2_out = pull_resistor_7_node ^ pull_resistor_10_node;  // XOR_Gate xor_2, 32 bits wide
  assign bit_extender_11_out = {{31{1'b0}}, bitselector_2_out};  // Bit_Extender bit_extender_11
  assign bit_extender_12_out = {{31{1'b0}}, bitselector_3_out};  // Bit_Extender bit_extender_12
  Comparator #(.width(32)) comparator_10 (
    .a(pull_resistor_7_node), .b(pull_resistor_10_node), .gt(comparator_10_gt), .eq(comparator_10_eq),
    .lt(comparator_10_lt));
  Priority_Encoder #(.select(5), .disabled(0)) priority_encoder_3 (
    .in0(pull_resistor_7_node[31]), .in1(pull_resistor_7_node[30]), .in2(pull_resistor_7_node[29]),
    .in3(pull_resistor_7_node[28]), .in4(pull_resistor_7_node[27]), .in5(pull_resistor_7_node[26]),
    .in6(pull_resistor_7_node[25]), .in7(pull_resistor_7_node[24]), .in8(pull_resistor_7_node[23]),
    .in9(pull_resistor_7_node[22]), .in10(pull_resistor_7_node[21]), .in11(pull_resistor_7_node[20]),
    .in12(pull_resistor_7_node[19]), .in13(pull_resistor_7_node[18]), .in14(pull_resistor_7_node[17]),
    .in15(pull_resistor_7_node[16]), .in16(pull_resistor_7_node[15]), .in17(pull_resistor_7_node[14]),
    .in18(pull_resistor_7_node[13]), .in19(pull_resistor_7_node[12]), .in20(pull_resistor_7_node[11]),
    .in21(pull_resistor_7_node[10]), .in22(pull_resistor_7_node[9]), .in23(pull_resistor_7_node[8]),
    .in24(pull_resistor_7_node[7]), .in25(pull_resistor_7_node[6]), .in26(pull_resistor_7_node[5]),
    .in27(pull_resistor_7_node[4]), .in28(pull_resistor_7_node[3]), .in29(pull_resistor_7_node[2]),
    .in30(pull_resistor_7_node[1]), .in31(pull_resistor_7_node[0]), .out(priority_encoder_3_out));
  Priority_Encoder #(.select(5), .disabled(0)) priority_encoder_4 (
    .in0(pull_resistor_10_node[31]), .in1(pull_resistor_10_node[30]), .in2(pull_resistor_10_node[29]),
    .in3(pull_resistor_10_node[28]), .in4(pull_resistor_10_node[27]), .in5(pull_resistor_10_node[26]),
    .in6(pull_resistor_10_node[25]), .in7(pull_resistor_10_node[24]), .in8(pull_resistor_10_node[23]),
    .in9(pull_resistor_10_node[22]), .in10(pull_resistor_10_node[21]), .in11(pull_resistor_10_node[20]),
    .in12(pull_resistor_10_node[19]), .in13(pull_resistor_10_node[18]), .in14(pull_resistor_10_node[17]),
    .in15(pull_resistor_10_node[16]), .in16(pull_resistor_10_node[15]), .in17(pull_resistor_10_node[14]),
    .in18(pull_resistor_10_node[13]), .in19(pull_resistor_10_node[12]), .in20(pull_resistor_10_node[11]),
    .in21(pull_resistor_10_node[10]), .in22(pull_resistor_10_node[9]), .in23(pull_resistor_10_node[8]),
    .in24(pull_resistor_10_node[7]), .in25(pull_resistor_10_node[6]), .in26(pull_resistor_10_node[5]),
    .in27(pull_resistor_10_node[4]), .in28(pull_resistor_10_node[3]), .in29(pull_resistor_10_node[2]),
    .in30(pull_resistor_10_node[1]), .in31(pull_resistor_10_node[0]), .out(priority_encoder_4_out));
  Multiplexer #(.select(2), .disabled(0)) multiplexer_5 (
    .in0(1'b0), .in1(comparator_10_gt), .in2(comparator_10_eq), .in3(comparator_10_lt),
    .out(multiplexer_5_out), .sel(pull_resistor_8_node[11:10]), .en(pull_resistor_9_node[0]));
  Pull_Resistor pull_resistor_11 (.node(multiplexer_5_out));
  assign bit_extender_13_out = {{27{1'b0}}, priority_encoder_3_out};  // Bit_Extender bit_extender_13
  assign bit_extender_14_out = {{27{1'b0}}, priority_encoder_4_out};  // Bit_Extender bit_extender_14
  Multiplexer #(.select(5), .width(32)) multiplexer_6 (
    .in0(adder_3_out), .in1(subtractor_3_out), .in2(multiplier_3_out), .in3(divider_3_out),
    .in4(negator_2_out), .in5(negator_3_out), .in6(shifter_6_out), .in7(shifter_7_out), .in8(shifter_8_out),
    .in9(shifter_9_out), .in10(shifter_10_out), .in11(shifter_11_out), .in12(shifter_12_out),
    .in13(shifter_13_out), .in14(shifter_14_out), .in15(shifter_15_out), .in16(bit_extender_8_out),
    .in17(bit_extender_9_out), .in18(bit_extender_10_out), .in19(or_4_out), .in20(and_5_out),
    .in21(xor_2_out), .in22(odd_parity_2_out), .in23(even_parity_2_out), .in24(increesor_3_out_2),
    .in25(increesor_4_out_2), .in26(bit_extender_13_out), .in27(bit_extender_14_out),
    .in28(bit_extender_11_out), .in29(bit_extender_12_out), .in30(multiplier_3_cout), .in31(divider_3_rem),
    .out(multiplexer_6_out), .sel(pull_resistor_8_node[4:0]), .en(pull_resistor_9_node[0]));
  Pull_Resistor pull_resistor_12 (.node(multiplexer_6_out));

  // Notes on the sheet:
  //   +
  //   _
  //   *
  //   /
  //   sin
  //   cos
  //   tg
  //   ln
  //   sqrt
  //   mod
  //   root
  //   log
  //   exponent
  //   pow
  //   int()->float()
  //   float()->int()
endmodule

module User_Stack__US (
  input  [31:0] Z_Access_to_memory,
  input  [31:0] Load_US_Pointer,
  input  [31:0] Data_in,
  input  Power,
  input  Clk,
  input  Reset,
  input  Load_US,
  input  UP_0__DOWN_1,
  input  Access,
  input  UPush,
  input  UPop,
  output [31:0] Data_out
);

  wire and_1_out, controlled_buffer_1_out, controlled_buffer_2_out, not_1_out, not_2_out, not_3_out,
       or_1_out, or_2_out, or_3_out;
  wire [23:0] adder_1_out, bit_extender_1_out, bit_extender_2_out, controlled_buffer_3_out, US_Pointer_q;

  Pull_Resistor pull_resistor_1 (.node(Power));
  Pull_Resistor pull_resistor_2 (.node(Data_in));
  Pull_Resistor pull_resistor_3 (.node(Load_US_Pointer));
  Pull_Resistor pull_resistor_4 (.node(Z_Access_to_memory));
  Pull_Resistor pull_resistor_5 (.node(Reset));
  Pull_Resistor pull_resistor_6 (.node(UPop));
  Pull_Resistor pull_resistor_7 (.node(Load_US));
  Pull_Resistor pull_resistor_8 (.node(UP_0__DOWN_1));
  Pull_Resistor pull_resistor_9 (.node(Access));
  Pull_Resistor pull_resistor_10 (.node(Clk));
  Pull_Resistor pull_resistor_11 (.node(UPush));
  Bit_Extender #(.in_width(32), .out_width(24)) bit_extender_1 (.in(Z_Access_to_memory), .out(bit_extender_1_out));
  Bit_Extender #(.in_width(32), .out_width(24)) bit_extender_2 (.in(Load_US_Pointer), .out(bit_extender_2_out));
  not not_1 (not_1_out, Access);
  or or_1 (or_1_out, Load_US, UP_0__DOWN_1);
  and and_1 (and_1_out, ~Load_US, ~UP_0__DOWN_1);  // AND_Gate
  or or_2 (or_2_out, UPush, UPop);
  assign controlled_buffer_1_out = not_1_out ? or_1_out : 1'bz;  // Controlled_Buffer controlled_buffer_1
  assign controlled_buffer_2_out = not_1_out ? or_3_out : 1'bz;  // Controlled_Buffer controlled_buffer_2
  or or_3 (or_3_out, and_1_out, UP_0__DOWN_1);
  Counter #(.width(24), .max('hffffff)) US_Pointer (
    .load(controlled_buffer_1_out), .D(bit_extender_2_out), .count(controlled_buffer_2_out),
    .Q(US_Pointer_q), .clk(or_2_out), .clr(Reset));  // open: carry
  assign controlled_buffer_3_out = not_1_out ? US_Pointer_q : 24'bz;  // Controlled_Buffer controlled_buffer_3
  Adder #(.width(24)) adder_1 (.a(bit_extender_1_out), .b(US_Pointer_q), .out(adder_1_out));  // open: cin, cout
  not not_2 (not_2_out, not_1_out);
  assign controlled_buffer_3_out = not_2_out ? adder_1_out : 24'bz;  // Controlled_Buffer controlled_buffer_4
  not not_3 (not_3_out, UPush);
  Pull_Resistor pull_resistor_12 (.node(Data_out));
  RAM #(.addrWidth(24), .dataWidth(32), .bus("separate")) ram_1 (
    .addr(controlled_buffer_3_out), .din(Data_in), .data(Data_out), .str(UPush), .sel(Power), .clk(Clk),
    .ld(not_3_out), .clr(Reset));
endmodule
module Comand_Protocol_Programs__CPP (
  input  [31:0] Data_in_to_Ram_0_31,
  input  [31:0] Data_in_to_Ram_32_63,
  input  [31:0] Data_in_to_Ram_64_95,
  input  [31:0] Data_in_to_Ram_96_127,
  input  [23:0] \Сomand_Number ,
  input  [23:0] \Сomand_Number_When_Loading_RAM ,
  input  [4:0] Program_number,
  input  Load_program_number,
  input  Load_Comand_Numder,
  input  Reset_RAM,
  input  Reset_all_RAM,
  input  [4:0] RAM_Number__When_have_operation_with_RAM,
  input  Load_RAM,
  input  RAM_indicator,
  input  load_completed,
  input  Clk,
  input  Power,
  output [4:0] Comand_place_condition,
  output [31:0] comand_0_31bit,
  output [31:0] comand_32_63bit,
  output [31:0] comand_64_95bit,
  output [31:0] comand_96_127bit
);

  wire and_1_out, and_2_out, and_3_out, and_4_out, and_5_out, and_6_out, comparator_1_eq, comparator_2_eq,
       comparator_3_eq, comparator_4_eq, comparator_5_eq, comparator_5_gt, counter_1_carry, decoder_1_out0,
       decoder_1_out1, decoder_1_out2, decoder_1_out3, decoder_1_out4, decoder_1_out5, decoder_1_out6,
       decoder_1_out7, decoder_1_out8, decoder_1_out9, decoder_1_out10, decoder_1_out11, decoder_1_out12,
       decoder_1_out13, decoder_1_out14, decoder_1_out15, decoder_1_out16, decoder_1_out17, decoder_1_out18,
       decoder_1_out19, decoder_1_out20, decoder_1_out21, decoder_1_out22, decoder_1_out23, decoder_1_out24,
       decoder_1_out25, decoder_1_out26, decoder_1_out27, decoder_1_out28, decoder_1_out29, decoder_1_out30,
       decoder_1_out31, empty_spaces_counter_esc_1_count, empty_spaces_counter_esc_1_load_2, not_1_out,
       not_2_out, not_3_out, not_4_out, not_5_out, not_6_out, not_7_out, not_8_out, not_9_out, not_10_out,
       not_11_out, not_12_out, not_13_out, not_14_out, not_15_out, not_16_out, not_17_out, not_18_out,
       not_19_out, not_20_out, not_21_out, not_22_out, not_23_out, not_24_out, not_25_out, not_26_out,
       not_27_out, not_28_out, not_29_out, not_30_out, not_31_out, not_32_out, not_33_out, not_34_out,
       not_35_out, not_36_out, not_37_out, not_38_out, not_39_out, not_40_out, not_41_out, not_42_out,
       not_43_out, not_44_out, not_45_out, not_46_out, not_47_out, not_48_out, not_49_out, not_50_out,
       not_51_out, not_52_out, not_53_out, not_54_out, not_55_out, not_56_out, not_57_out, not_58_out,
       not_59_out, not_60_out, not_61_out, not_62_out, not_63_out, not_64_out, not_65_out, not_66_out,
       not_67_out, not_68_out, not_69_out, not_70_out, not_71_out, not_72_out, not_73_out, not_74_out,
       not_75_out, not_76_out, not_77_out, not_78_out, not_79_out, not_80_out, not_81_out, not_82_out,
       not_83_out, not_84_out, not_85_out, not_86_out, not_87_out, not_88_out, not_89_out, not_90_out,
       not_91_out, not_92_out, not_93_out, not_94_out, not_95_out, not_96_out, not_97_out, not_98_out,
       not_99_out, not_100_out, not_101_out, not_102_out, not_103_out, not_104_out, not_105_out, not_106_out,
       not_107_out, not_108_out, not_109_out, not_110_out, not_111_out, not_112_out, not_113_out,
       not_114_out, not_115_out, not_116_out, not_117_out, not_118_out, not_119_out, not_120_out,
       not_121_out, not_122_out, not_123_out, not_124_out, not_125_out, not_126_out, not_127_out,
       not_128_out, not_129_out, not_130_out, not_131_out, not_132_out, not_133_out, not_134_out,
       not_135_out, not_136_out, not_137_out, not_138_out, not_139_out, not_140_out, not_141_out,
       not_142_out, not_143_out, not_144_out, not_145_out, not_146_out, not_147_out, not_148_out,
       not_149_out, not_150_out, not_151_out, not_152_out, not_153_out, not_154_out, not_155_out,
       not_156_out, not_157_out, not_158_out, not_159_out, not_160_out, not_161_out, not_162_out,
       not_163_out, not_164_out, not_165_out, not_166_out, not_167_out, not_168_out, not_169_out,
       not_170_out, not_171_out, not_172_out, not_173_out, not_174_out, not_175_out, not_176_out,
       not_177_out, not_178_out, not_179_out, not_180_out, not_181_out, not_182_out, not_183_out,
       not_184_out, not_185_out, not_186_out, not_187_out, not_188_out, not_189_out, not_190_out,
       not_191_out, not_192_out, not_193_out, not_194_out, not_195_out, not_196_out, not_197_out,
       not_198_out, not_199_out, not_200_out, not_201_out, not_202_out, not_203_out, not_204_out,
       not_205_out, not_206_out, not_207_out, not_208_out, not_209_out, not_210_out, not_211_out,
       not_212_out, not_213_out, not_214_out, not_215_out, not_216_out, not_217_out, not_218_out,
       not_219_out, not_220_out, not_221_out, not_222_out, not_223_out, not_224_out, not_225_out,
       not_226_out, not_227_out, not_228_out, not_229_out, not_230_out, not_231_out, not_232_out,
       not_233_out, not_234_out, not_235_out, not_236_out, not_237_out, not_238_out, not_239_out,
       not_240_out, not_241_out, not_242_out, not_243_out, not_244_out, or_25_out, or_26_out, or_33_out,
       or_34_out, or_35_out, or_36_out, register_1_q;
  wire [1:0] or_5_out, or_27_out;
  wire [3:0] or_1_out, or_9_out, or_17_out;
  wire [4:0] empty_spaces_counter_esc_1_counter_out, multiplexer_14_out;
  wire [12:0] decoder_3_out19;
  wire [13:0] decoder_2_out18, decoder_4_out18, or_7_out, register_34_q, register_35_q;
  wire [15:0] decoder_2_out2, decoder_4_out2, register_2_q, register_3_q;
  wire [16:0] decoder_3_out2;
  wire [23:0] counter_1_q, multiplexer_15_out, multiplexer_16_out, multiplexer_17_out, multiplexer_18_out,
       multiplexer_19_out, multiplexer_20_out, multiplexer_21_out, multiplexer_22_out, multiplexer_23_out,
       multiplexer_24_out, multiplexer_25_out, multiplexer_26_out, multiplexer_27_out, multiplexer_28_out,
       multiplexer_29_out, multiplexer_30_out, multiplexer_31_out, multiplexer_32_out, multiplexer_33_out,
       multiplexer_34_out, multiplexer_35_out, multiplexer_36_out, multiplexer_37_out, multiplexer_38_out,
       multiplexer_39_out, multiplexer_40_out, multiplexer_41_out, multiplexer_42_out, multiplexer_43_out,
       multiplexer_44_out, multiplexer_45_out, multiplexer_46_out, multiplexer_47_out, multiplexer_48_out,
       multiplexer_49_out, multiplexer_50_out, multiplexer_51_out, multiplexer_52_out, multiplexer_53_out,
       multiplexer_54_out, multiplexer_55_out, multiplexer_56_out, multiplexer_57_out, multiplexer_58_out,
       multiplexer_59_out, multiplexer_60_out, multiplexer_61_out, multiplexer_62_out, multiplexer_63_out,
       multiplexer_64_out, multiplexer_65_out, multiplexer_66_out, multiplexer_67_out, multiplexer_68_out,
       multiplexer_69_out, multiplexer_70_out, multiplexer_71_out, multiplexer_72_out, multiplexer_73_out,
       multiplexer_74_out, multiplexer_75_out, multiplexer_76_out, multiplexer_77_out, multiplexer_78_out,
       multiplexer_79_out, multiplexer_80_out, multiplexer_81_out, multiplexer_82_out, multiplexer_83_out,
       multiplexer_84_out, multiplexer_85_out, multiplexer_86_out, multiplexer_87_out, multiplexer_88_out,
       multiplexer_89_out, multiplexer_90_out, multiplexer_91_out, multiplexer_92_out, multiplexer_93_out,
       multiplexer_94_out, multiplexer_95_out, multiplexer_96_out, multiplexer_97_out, multiplexer_98_out,
       multiplexer_99_out, multiplexer_100_out, multiplexer_101_out, multiplexer_102_out,
       multiplexer_103_out, multiplexer_104_out, multiplexer_105_out, multiplexer_106_out,
       multiplexer_107_out, multiplexer_108_out, multiplexer_109_out, multiplexer_110_out,
       multiplexer_111_out, multiplexer_112_out, multiplexer_113_out, multiplexer_114_out,
       multiplexer_115_out, multiplexer_116_out, multiplexer_117_out, multiplexer_118_out,
       multiplexer_119_out, multiplexer_120_out, multiplexer_121_out, multiplexer_122_out,
       multiplexer_123_out, multiplexer_124_out, multiplexer_125_out, multiplexer_126_out,
       multiplexer_127_out, multiplexer_128_out, multiplexer_129_out, multiplexer_130_out,
       multiplexer_131_out, multiplexer_132_out, multiplexer_133_out, multiplexer_134_out,
       multiplexer_135_out, multiplexer_136_out, multiplexer_137_out, multiplexer_138_out,
       multiplexer_139_out, multiplexer_140_out, multiplexer_141_out, multiplexer_142_out,
       multiplexer_143_out, multiplexer_144_out, multiplexer_145_out, multiplexer_146_out,
       multiplexer_147_out, multiplexer_148_out, multiplexer_149_out, multiplexer_150_out,
       multiplexer_151_out, multiplexer_152_out, multiplexer_153_out, multiplexer_154_out,
       multiplexer_155_out, multiplexer_156_out, multiplexer_157_out, multiplexer_158_out,
       multiplexer_159_out, multiplexer_160_out, multiplexer_161_out, multiplexer_162_out,
       multiplexer_163_out, multiplexer_164_out, multiplexer_165_out, multiplexer_166_out,
       multiplexer_167_out, multiplexer_168_out, multiplexer_169_out, multiplexer_170_out,
       multiplexer_171_out, multiplexer_172_out, multiplexer_173_out, multiplexer_174_out,
       multiplexer_175_out, multiplexer_176_out, multiplexer_177_out, multiplexer_178_out,
       multiplexer_179_out, multiplexer_180_out, multiplexer_181_out, multiplexer_182_out,
       multiplexer_183_out, multiplexer_184_out, multiplexer_185_out, multiplexer_186_out,
       multiplexer_187_out, multiplexer_188_out, multiplexer_189_out, multiplexer_190_out,
       multiplexer_191_out, multiplexer_192_out, multiplexer_193_out, multiplexer_194_out,
       multiplexer_195_out, multiplexer_196_out, multiplexer_197_out, multiplexer_198_out,
       multiplexer_199_out, multiplexer_200_out, multiplexer_201_out, multiplexer_202_out,
       multiplexer_203_out, multiplexer_204_out, multiplexer_205_out, multiplexer_206_out,
       multiplexer_207_out, multiplexer_208_out, multiplexer_209_out, multiplexer_210_out,
       multiplexer_211_out, multiplexer_212_out, multiplexer_213_out, multiplexer_214_out,
       multiplexer_215_out, multiplexer_216_out, multiplexer_217_out, multiplexer_218_out,
       multiplexer_219_out, multiplexer_220_out, multiplexer_221_out, multiplexer_222_out,
       multiplexer_223_out, multiplexer_224_out, multiplexer_225_out, multiplexer_226_out,
       multiplexer_227_out, multiplexer_228_out, multiplexer_229_out, multiplexer_230_out,
       multiplexer_231_out, multiplexer_232_out, multiplexer_233_out, multiplexer_234_out,
       multiplexer_235_out, multiplexer_236_out, multiplexer_237_out, multiplexer_238_out,
       multiplexer_239_out, multiplexer_240_out, multiplexer_241_out, multiplexer_242_out,
       multiplexer_243_out, multiplexer_244_out, multiplexer_245_out, multiplexer_246_out,
       multiplexer_247_out, multiplexer_248_out, multiplexer_249_out, multiplexer_250_out,
       multiplexer_251_out, multiplexer_252_out, multiplexer_253_out, multiplexer_254_out;
  wire [29:0] multiplexer_5_out;
  wire [31:0] multiplexer_6_out, multiplexer_7_out, multiplexer_8_out, multiplexer_9_out, multiplexer_10_out,
       multiplexer_11_out, multiplexer_12_out, multiplexer_13_out, ram_1_data, ram_2_data, ram_3_data,
       ram_4_data, ram_5_data, ram_6_data, ram_7_data, ram_8_data, ram_9_data, ram_10_data, ram_11_data,
       ram_12_data, ram_13_data, ram_14_data, ram_15_data, ram_16_data, ram_17_data, ram_18_data,
       ram_19_data, ram_20_data, ram_21_data, ram_22_data, ram_23_data, ram_24_data, ram_25_data,
       ram_26_data, ram_27_data, ram_28_data, ram_29_data, ram_30_data, ram_31_data, ram_32_data,
       ram_33_data, ram_34_data, ram_35_data, ram_36_data, ram_37_data, ram_38_data, ram_39_data,
       ram_40_data, ram_41_data, ram_42_data, ram_43_data, ram_44_data, ram_45_data, ram_46_data,
       ram_47_data, ram_48_data, ram_49_data, ram_50_data, ram_51_data, ram_52_data, ram_53_data,
       ram_54_data, ram_55_data, ram_56_data, ram_57_data, ram_58_data, ram_59_data, ram_60_data,
       ram_61_data, ram_62_data, ram_63_data, ram_64_data, ram_65_data, ram_66_data, ram_67_data,
       ram_68_data, ram_69_data, ram_70_data, ram_71_data, ram_72_data, ram_73_data, ram_74_data,
       ram_75_data, ram_76_data, ram_77_data, ram_78_data, ram_79_data, ram_80_data, ram_81_data,
       ram_82_data, ram_83_data, ram_84_data, ram_85_data, ram_86_data, ram_87_data, ram_88_data,
       ram_89_data, ram_90_data, ram_91_data, ram_92_data, ram_93_data, ram_94_data, ram_95_data,
       ram_96_data, ram_97_data, ram_98_data, ram_99_data, ram_100_data, ram_101_data, ram_102_data,
       ram_103_data, ram_104_data, ram_105_data, ram_106_data, ram_107_data, ram_108_data, ram_109_data,
       ram_110_data, ram_111_data, ram_112_data, ram_113_data, ram_114_data, ram_115_data, ram_116_data,
       ram_117_data, ram_118_data, ram_119_data, ram_120_data, ram_121_data, ram_122_data, ram_123_data,
       ram_124_data, ram_125_data, ram_126_data, ram_127_data, ram_128_data, ram_129_data, ram_130_data,
       ram_131_data, ram_132_data, ram_133_data, ram_134_data, ram_135_data, ram_136_data, ram_137_data,
       ram_138_data, ram_139_data, ram_140_data, ram_141_data, ram_142_data, ram_143_data, ram_144_data,
       ram_145_data, ram_146_data, ram_147_data, ram_148_data, ram_149_data, ram_150_data, ram_151_data,
       ram_152_data, ram_153_data, ram_154_data, ram_155_data, ram_156_data, ram_157_data, ram_158_data,
       ram_159_data, ram_160_data, ram_161_data, ram_162_data, ram_163_data, ram_164_data, ram_165_data,
       ram_166_data, ram_167_data, ram_168_data, ram_169_data, ram_170_data, ram_171_data, ram_172_data,
       ram_173_data, ram_174_data, ram_175_data, ram_176_data, ram_177_data, ram_178_data, ram_179_data,
       ram_180_data, ram_181_data, ram_182_data, ram_183_data, ram_184_data, ram_185_data, ram_186_data,
       ram_187_data, ram_188_data, ram_189_data, ram_190_data, ram_191_data, ram_192_data, ram_193_data,
       ram_194_data, ram_195_data, ram_196_data, ram_197_data, ram_198_data, ram_199_data, ram_200_data,
       ram_201_data, ram_202_data, ram_203_data, ram_204_data, ram_205_data, ram_206_data, ram_207_data,
       ram_208_data, ram_209_data, ram_210_data, ram_211_data, ram_212_data, ram_213_data, ram_214_data,
       ram_215_data, ram_216_data, ram_217_data, ram_218_data, ram_219_data, ram_220_data, ram_221_data,
       ram_222_data, ram_223_data, ram_224_data, ram_225_data, ram_226_data, ram_227_data, ram_228_data,
       ram_229_data, ram_230_data, ram_231_data, ram_232_data, ram_233_data, ram_234_data, ram_235_data,
       ram_236_data, ram_237_data, ram_238_data, ram_239_data, ram_240_data, rom_1_data, rom_2_data,
       rom_3_data, rom_4_data, rom_5_data, rom_6_data, rom_7_data, rom_8_data, rom_9_data, rom_10_data,
       rom_11_data, rom_12_data, rom_13_data, rom_14_data, rom_15_data, rom_16_data;

  and and_1 (and_1_out, Load_RAM, RAM_indicator);
  and and_2 (and_2_out, Load_RAM, ~RAM_indicator);  // AND_Gate
  Decoder #(.select(5), .disabled(0)) decoder_1 (
    .out0(decoder_1_out0), .out1(decoder_1_out1), .out2(decoder_1_out2), .out3(decoder_1_out3),
    .out4(decoder_1_out4), .out5(decoder_1_out5), .out6(decoder_1_out6), .out7(decoder_1_out7),
    .out8(decoder_1_out8), .out9(decoder_1_out9), .out10(decoder_1_out10), .out11(decoder_1_out11),
    .out12(decoder_1_out12), .out13(decoder_1_out13), .out14(decoder_1_out14), .out15(decoder_1_out15),
    .out16(decoder_1_out16), .out17(decoder_1_out17), .out18(decoder_1_out18), .out19(decoder_1_out19),
    .out20(decoder_1_out20), .out21(decoder_1_out21), .out22(decoder_1_out22), .out23(decoder_1_out23),
    .out24(decoder_1_out24), .out25(decoder_1_out25), .out26(decoder_1_out26), .out27(decoder_1_out27),
    .out28(decoder_1_out28), .out29(decoder_1_out29), .out30(decoder_1_out30), .out31(decoder_1_out31),
    .sel(RAM_Number__When_have_operation_with_RAM), .en(Reset_RAM));
  Decoder #(.select(5), .disabled(0)) decoder_2 (
    .out2(decoder_2_out2[0]), .out3(decoder_2_out2[1]), .out4(decoder_2_out2[2]), .out5(decoder_2_out2[3]),
    .out6(decoder_2_out2[4]), .out7(decoder_2_out2[5]), .out8(decoder_2_out2[6]), .out9(decoder_2_out2[7]),
    .out10(decoder_2_out2[8]), .out11(decoder_2_out2[9]), .out12(decoder_2_out2[10]),
    .out13(decoder_2_out2[11]), .out14(decoder_2_out2[12]), .out15(decoder_2_out2[13]),
    .out16(decoder_2_out2[14]), .out17(decoder_2_out2[15]), .out18(decoder_2_out18[0]),
    .out19(decoder_2_out18[1]), .out20(decoder_2_out18[2]), .out21(decoder_2_out18[3]),
    .out22(decoder_2_out18[4]), .out23(decoder_2_out18[5]), .out24(decoder_2_out18[6]),
    .out25(decoder_2_out18[7]), .out26(decoder_2_out18[8]), .out27(decoder_2_out18[9]),
    .out28(decoder_2_out18[10]), .out29(decoder_2_out18[11]), .out30(decoder_2_out18[12]),
    .out31(decoder_2_out18[13]), .sel(RAM_Number__When_have_operation_with_RAM), .en(and_1_out));  // open: out0, out1
  Decoder #(.select(5), .disabled(0)) decoder_3 (
    .out2(decoder_3_out2[0]), .out3(decoder_3_out2[1]), .out4(decoder_3_out2[2]), .out5(decoder_3_out2[3]),
    .out6(decoder_3_out2[4]), .out7(decoder_3_out2[5]), .out8(decoder_3_out2[6]), .out9(decoder_3_out2[7]),
    .out10(decoder_3_out2[8]), .out11(decoder_3_out2[9]), .out12(decoder_3_out2[10]),
    .out13(decoder_3_out2[11]), .out14(decoder_3_out2[12]), .out15(decoder_3_out2[13]),
    .out16(decoder_3_out2[14]), .out17(decoder_3_out2[15]), .out18(decoder_3_out2[16]),
    .out19(decoder_3_out19[0]), .out20(decoder_3_out19[1]), .out21(decoder_3_out19[2]),
    .out22(decoder_3_out19[3]), .out23(decoder_3_out19[4]), .out24(decoder_3_out19[5]),
    .out25(decoder_3_out19[6]), .out26(decoder_3_out19[7]), .out27(decoder_3_out19[8]),
    .out28(decoder_3_out19[9]), .out29(decoder_3_out19[10]), .out30(decoder_3_out19[11]),
    .out31(decoder_3_out19[12]), .sel(RAM_Number__When_have_operation_with_RAM), .en(load_completed));  // open: out0, out1
  Decoder #(.select(5), .disabled(0)) decoder_4 (
    .out2(decoder_4_out2[0]), .out3(decoder_4_out2[1]), .out4(decoder_4_out2[2]), .out5(decoder_4_out2[3]),
    .out6(decoder_4_out2[4]), .out7(decoder_4_out2[5]), .out8(decoder_4_out2[6]), .out9(decoder_4_out2[7]),
    .out10(decoder_4_out2[8]), .out11(decoder_4_out2[9]), .out12(decoder_4_out2[10]),
    .out13(decoder_4_out2[11]), .out14(decoder_4_out2[12]), .out15(decoder_4_out2[13]),
    .out16(decoder_4_out2[14]), .out17(decoder_4_out2[15]), .out18(decoder_4_out18[0]),
    .out19(decoder_4_out18[1]), .out20(decoder_4_out18[2]), .out21(decoder_4_out18[3]),
    .out22(decoder_4_out18[4]), .out23(decoder_4_out18[5]), .out24(decoder_4_out18[6]),
    .out25(decoder_4_out18[7]), .out26(decoder_4_out18[8]), .out27(decoder_4_out18[9]),
    .out28(decoder_4_out18[10]), .out29(decoder_4_out18[11]), .out30(decoder_4_out18[12]),
    .out31(decoder_4_out18[13]), .sel(RAM_Number__When_have_operation_with_RAM), .en(and_2_out));  // open: out0, out1
  or or_1 (or_1_out[0], Reset_all_RAM, decoder_1_out12);
  or or_2 (or_1_out[1], Reset_all_RAM, decoder_1_out13);
  or or_3 (or_1_out[2], Reset_all_RAM, decoder_1_out14);
  or or_4 (or_1_out[3], Reset_all_RAM, decoder_1_out15);
  or or_5 (or_5_out[0], decoder_1_out16, Reset_all_RAM);
  or or_6 (or_5_out[1], decoder_1_out17, Reset_all_RAM);
  or or_7 (or_7_out[0], decoder_1_out18, Reset_all_RAM);
  or or_8 (or_7_out[1], decoder_1_out19, Reset_all_RAM);
  or or_9 (or_9_out[0], Reset_all_RAM, decoder_1_out8);
  or or_10 (or_9_out[1], Reset_all_RAM, decoder_1_out9);
  or or_11 (or_9_out[2], Reset_all_RAM, decoder_1_out10);
  or or_12 (or_9_out[3], Reset_all_RAM, decoder_1_out11);
  or or_13 (or_7_out[2], decoder_1_out20, Reset_all_RAM);
  or or_14 (or_7_out[3], decoder_1_out21, Reset_all_RAM);
  or or_15 (or_7_out[4], decoder_1_out22, Reset_all_RAM);
  or or_16 (or_7_out[5], decoder_1_out23, Reset_all_RAM);
  or or_17 (or_17_out[0], Reset_all_RAM, decoder_1_out4);
  or or_18 (or_17_out[1], Reset_all_RAM, decoder_1_out5);
  or or_19 (or_17_out[2], Reset_all_RAM, decoder_1_out6);
  or or_20 (or_17_out[3], Reset_all_RAM, decoder_1_out7);
  or or_21 (or_7_out[6], decoder_1_out24, Reset_all_RAM);
  or or_22 (or_7_out[7], decoder_1_out25, Reset_all_RAM);
  or or_23 (or_7_out[8], decoder_1_out26, Reset_all_RAM);
  or or_24 (or_7_out[9], decoder_1_out27, Reset_all_RAM);
  or or_25 (or_25_out, Reset_all_RAM, decoder_1_out0);
  or or_26 (or_26_out, Reset_all_RAM, decoder_1_out1);
  or or_27 (or_27_out[0], Reset_all_RAM, decoder_1_out2);
  or or_28 (or_27_out[1], Reset_all_RAM, decoder_1_out3);
  or or_29 (or_7_out[10], decoder_1_out28, Reset_all_RAM);
  or or_30 (or_7_out[11], decoder_1_out29, Reset_all_RAM);
  or or_31 (or_7_out[12], decoder_1_out30, Reset_all_RAM);
  or or_32 (or_7_out[13], decoder_1_out31, Reset_all_RAM);
  Register #(.width(1)) register_1 (.D(and_4_out), .en(Power), .Q(register_1_q), .clk(not_1_out), .clr(or_33_out));
  not not_1 (not_1_out, Clk);
  or or_33 (or_33_out, comparator_5_eq, not_2_out);
  and and_3 (and_3_out, register_1_q, ~Clk);  // AND_Gate
  not not_2 (not_2_out, Power);
  Multiplexer #(.width(32), .disabled(0)) multiplexer_1 (
    .in0(multiplexer_10_out), .in1(multiplexer_6_out), .out(comand_0_31bit), .sel(Clk), .en(Power));
  Multiplexer #(.width(32), .disabled(0)) multiplexer_2 (
    .in0(multiplexer_11_out), .in1(multiplexer_7_out), .out(comand_32_63bit), .sel(Clk), .en(Power));
  Multiplexer #(.width(32), .disabled(0)) multiplexer_3 (
    .in0(multiplexer_12_out), .in1(multiplexer_8_out), .out(comand_64_95bit), .sel(Clk), .en(Power));
  Multiplexer #(.width(32), .disabled(0)) multiplexer_4 (
    .in0(multiplexer_13_out), .in1(multiplexer_9_out), .out(comand_96_127bit), .sel(Clk), .en(Power));
  Comparator #(.width(32), .mode("unsigned")) comparator_1 (
    .a({32{1'b0}}), .b(comand_96_127bit), .eq(comparator_1_eq));  // open: gt, lt
  Comparator #(.width(32), .mode("unsigned")) comparator_2 (
    .a({32{1'b0}}), .b(comand_64_95bit), .eq(comparator_2_eq));  // open: gt, lt
  and and_4 (and_4_out, comparator_2_eq, comparator_1_eq, comparator_5_gt, comparator_4_eq, comparator_3_eq);
  Comparator #(.width(32), .mode("unsigned")) comparator_3 (
    .a({32{1'b0}}), .b(comand_32_63bit), .eq(comparator_3_eq));  // open: gt, lt
  Comparator #(.width(32), .mode("unsigned")) comparator_4 (
    .a(comand_0_31bit), .b({32{1'b0}}), .eq(comparator_4_eq));  // open: gt, lt
  Comparator #(.width(24), .mode("unsigned")) comparator_5 (
    .a(counter_1_q), .b({24{1'b0}}), .gt(comparator_5_gt), .eq(comparator_5_eq));  // open: lt
  Counter #(.width(24), .max('hffffff)) counter_1 (
    .load(Load_Comand_Numder), .D(\Сomand_Number ), .count(and_5_out), .Q(counter_1_q),
    .carry(counter_1_carry), .clk(Clk), .clr(or_34_out));
  and and_5 (and_5_out, ~Load_Comand_Numder, Power);  // AND_Gate
  or or_34 (or_34_out, empty_spaces_counter_esc_1_load_2, or_35_out, counter_1_carry);
  or or_35 (or_35_out, and_3_out, ~Power);  // OR_Gate
  not not_3 (not_3_out, Clk);
  Multiplexer #(.width(30)) multiplexer_5 (
    .in0({register_35_q, register_3_q}), .in1({register_34_q, register_2_q}), .out(multiplexer_5_out),
    .sel(Clk), .en(Power));
  Multiplexer #(.select(5), .width(32), .disabled(0)) multiplexer_6 (
    .in0(rom_1_data), .in1(rom_9_data), .in2(ram_1_data), .in3(ram_9_data), .in4(ram_17_data),
    .in5(ram_25_data), .in6(ram_33_data), .in7(ram_41_data), .in8(ram_49_data), .in9(ram_57_data),
    .in10(ram_65_data), .in11(ram_73_data), .in12(ram_81_data), .in13(ram_89_data), .in14(ram_97_data),
    .in15(ram_105_data), .in16(ram_113_data), .in17(ram_121_data), .in18(ram_129_data), .in19(ram_137_data),
    .in20(ram_145_data), .in21(ram_153_data), .in22(ram_161_data), .in23(ram_169_data), .in24(ram_177_data),
    .in25(ram_185_data), .in26(ram_193_data), .in27(ram_201_data), .in28(ram_209_data), .in29(ram_217_data),
    .in30(ram_225_data), .in31(ram_233_data), .out(multiplexer_6_out), .sel(Comand_place_condition),
    .en(Power));
  Multiplexer #(.select(5), .width(32), .disabled(0)) multiplexer_7 (
    .in0(rom_2_data), .in1(rom_10_data), .in2(ram_2_data), .in3(ram_10_data), .in4(ram_18_data),
    .in5(ram_26_data), .in6(ram_34_data), .in7(ram_42_data), .in8(ram_50_data), .in9(ram_58_data),
    .in10(ram_66_data), .in11(ram_74_data), .in12(ram_82_data), .in13(ram_90_data), .in14(ram_98_data),
    .in15(ram_106_data), .in16(ram_114_data), .in17(ram_122_data), .in18(ram_130_data), .in19(ram_138_data),
    .in20(ram_146_data), .in21(ram_154_data), .in22(ram_162_data), .in23(ram_170_data), .in24(ram_178_data),
    .in25(ram_186_data), .in26(ram_194_data), .in27(ram_202_data), .in28(ram_210_data), .in29(ram_218_data),
    .in30(ram_226_data), .in31(ram_234_data), .out(multiplexer_7_out), .sel(Comand_place_condition),
    .en(Power));
  Multiplexer #(.select(5), .width(32), .disabled(0)) multiplexer_8 (
    .in0(rom_3_data), .in1(rom_11_data), .in2(ram_3_data), .in3(ram_11_data), .in4(ram_19_data),
    .in5(ram_27_data), .in6(ram_35_data), .in7(ram_43_data), .in8(ram_51_data), .in9(ram_59_data),
    .in10(ram_67_data), .in11(ram_75_data), .in12(ram_83_data), .in13(ram_91_data), .in14(ram_99_data),
    .in15(ram_107_data), .in16(ram_115_data), .in17(ram_123_data), .in18(ram_131_data), .in19(ram_139_data),
    .in20(ram_147_data), .in21(ram_155_data), .in22(ram_163_data), .in23(ram_171_data), .in24(ram_179_data),
    .in25(ram_187_data), .in26(ram_195_data), .in27(ram_203_data), .in28(ram_211_data), .in29(ram_219_data),
    .in30(ram_227_data), .in31(ram_235_data), .out(multiplexer_8_out), .sel(Comand_place_condition),
    .en(Power));
  Multiplexer #(.select(5), .width(32), .disabled(0)) multiplexer_9 (
    .in0(rom_4_data), .in1(rom_12_data), .in2(ram_4_data), .in3(ram_12_data), .in4(ram_20_data),
    .in5(ram_28_data), .in6(ram_36_data), .in7(ram_44_data), .in8(ram_52_data), .in9(ram_60_data),
    .in10(ram_68_data), .in11(ram_76_data), .in12(ram_84_data), .in13(ram_92_data), .in14(ram_100_data),
    .in15(ram_108_data), .in16(ram_116_data), .in17(ram_124_data), .in18(ram_132_data), .in19(ram_140_data),
    .in20(ram_148_data), .in21(ram_156_data), .in22(ram_164_data), .in23(ram_172_data), .in24(ram_180_data),
    .in25(ram_188_data), .in26(ram_196_data), .in27(ram_204_data), .in28(ram_212_data), .in29(ram_220_data),
    .in30(ram_228_data), .in31(ram_236_data), .out(multiplexer_9_out), .sel(Comand_place_condition),
    .en(Power));
  Multiplexer #(.select(5), .width(32), .disabled(0)) multiplexer_10 (
    .in0(rom_5_data), .in1(rom_13_data), .in2(ram_5_data), .in3(ram_13_data), .in4(ram_21_data),
    .in5(ram_29_data), .in6(ram_37_data), .in7(ram_45_data), .in8(ram_53_data), .in9(ram_61_data),
    .in10(ram_69_data), .in11(ram_77_data), .in12(ram_85_data), .in13(ram_93_data), .in14(ram_101_data),
    .in15(ram_109_data), .in16(ram_117_data), .in17(ram_125_data), .in18(ram_133_data), .in19(ram_141_data),
    .in20(ram_149_data), .in21(ram_157_data), .in22(ram_165_data), .in23(ram_173_data), .in24(ram_181_data),
    .in25(ram_189_data), .in26(ram_197_data), .in27(ram_205_data), .in28(ram_213_data), .in29(ram_221_data),
    .in30(ram_229_data), .in31(ram_237_data), .out(multiplexer_10_out), .sel(Comand_place_condition),
    .en(Power));
  Multiplexer #(.select(5), .width(32), .disabled(0)) multiplexer_11 (
    .in0(rom_6_data), .in1(rom_14_data), .in2(ram_6_data), .in3(ram_14_data), .in4(ram_22_data),
    .in5(ram_30_data), .in6(ram_38_data), .in7(ram_46_data), .in8(ram_54_data), .in9(ram_62_data),
    .in10(ram_70_data), .in11(ram_78_data), .in12(ram_86_data), .in13(ram_94_data), .in14(ram_102_data),
    .in15(ram_110_data), .in16(ram_118_data), .in17(ram_126_data), .in18(ram_134_data), .in19(ram_142_data),
    .in20(ram_150_data), .in21(ram_158_data), .in22(ram_166_data), .in23(ram_174_data), .in24(ram_182_data),
    .in25(ram_190_data), .in26(ram_198_data), .in27(ram_206_data), .in28(ram_214_data), .in29(ram_222_data),
    .in30(ram_230_data), .in31(ram_238_data), .out(multiplexer_11_out), .sel(Comand_place_condition),
    .en(Power));
  Multiplexer #(.select(5), .width(32), .disabled(0)) multiplexer_12 (
    .in0(rom_7_data), .in1(rom_15_data), .in2(ram_7_data), .in3(ram_15_data), .in4(ram_23_data),
    .in5(ram_31_data), .in6(ram_39_data), .in7(ram_47_data), .in8(ram_55_data), .in9(ram_63_data),
    .in10(ram_71_data), .in11(ram_79_data), .in12(ram_87_data), .in13(ram_95_data), .in14(ram_103_data),
    .in15(ram_111_data), .in16(ram_119_data), .in17(ram_127_data), .in18(ram_135_data), .in19(ram_143_data),
    .in20(ram_151_data), .in21(ram_159_data), .in22(ram_167_data), .in23(ram_175_data), .in24(ram_183_data),
    .in25(ram_191_data), .in26(ram_199_data), .in27(ram_207_data), .in28(ram_215_data), .in29(ram_223_data),
    .in30(ram_231_data), .in31(ram_239_data), .out(multiplexer_12_out), .sel(Comand_place_condition),
    .en(Power));
  Multiplexer #(.select(5), .width(32), .disabled(0)) multiplexer_13 (
    .in0(rom_8_data), .in1(rom_16_data), .in2(ram_8_data), .in3(ram_16_data), .in4(ram_24_data),
    .in5(ram_32_data), .in6(ram_40_data), .in7(ram_48_data), .in8(ram_56_data), .in9(ram_64_data),
    .in10(ram_72_data), .in11(ram_80_data), .in12(ram_88_data), .in13(ram_96_data), .in14(ram_104_data),
    .in15(ram_112_data), .in16(ram_120_data), .in17(ram_128_data), .in18(ram_136_data), .in19(ram_144_data),
    .in20(ram_152_data), .in21(ram_160_data), .in22(ram_168_data), .in23(ram_176_data), .in24(ram_184_data),
    .in25(ram_192_data), .in26(ram_200_data), .in27(ram_208_data), .in28(ram_216_data), .in29(ram_224_data),
    .in30(ram_232_data), .in31(ram_240_data), .out(multiplexer_13_out), .sel(Comand_place_condition),
    .en(Power));
  empty_spaces_counter__ESC empty_spaces_counter_esc_1 (
    .in_1({multiplexer_5_out, 2'b11}), .Counter_in(Comand_place_condition),
    .Counter_out(empty_spaces_counter_esc_1_counter_out), .Count(empty_spaces_counter_esc_1_count),
    .Load_2(empty_spaces_counter_esc_1_load_2), .Load(Load_program_number));
  Counter #(.width(5), .max('h1f), .trigger("falling")) counter_2 (
    .load(empty_spaces_counter_esc_1_load_2), .D(multiplexer_14_out),
    .count(empty_spaces_counter_esc_1_count), .Q(Comand_place_condition), .clk(or_36_out), .clr(not_4_out));  // open: carry
  not not_4 (not_4_out, Power);
  or or_36 (or_36_out, and_6_out, and_3_out);
  ROM #(.addrWidth(24), .dataWidth(32)) rom_1 (.addr(counter_1_q), .data(rom_1_data), .sel(Power));
  ROM #(.addrWidth(24), .dataWidth(32)) rom_2 (.addr(counter_1_q), .data(rom_2_data), .sel(Power));
  ROM #(.addrWidth(24), .dataWidth(32)) rom_3 (.addr(counter_1_q), .data(rom_3_data), .sel(Power));
  ROM #(.addrWidth(24), .dataWidth(32)) rom_4 (.addr(counter_1_q), .data(rom_4_data), .sel(Power));
  ROM #(.addrWidth(24), .dataWidth(32)) rom_5 (.addr(counter_1_q), .data(rom_5_data), .sel(Power));
  ROM #(.addrWidth(24), .dataWidth(32)) rom_6 (.addr(counter_1_q), .data(rom_6_data), .sel(Power));
  ROM #(.addrWidth(24), .dataWidth(32)) rom_7 (.addr(counter_1_q), .data(rom_7_data), .sel(Power));
  ROM #(.addrWidth(24), .dataWidth(32)) rom_8 (.addr(counter_1_q), .data(rom_8_data), .sel(Power));
  and and_6 (and_6_out, ~Clk, empty_spaces_counter_esc_1_load_2);  // AND_Gate
  Multiplexer #(.width(5), .disabled(0)) multiplexer_14 (
    .in0(empty_spaces_counter_esc_1_counter_out), .in1(Program_number), .out(multiplexer_14_out),
    .sel(Load_program_number), .en(Power));
  ROM #(.addrWidth(24), .dataWidth(32)) rom_9 (.addr(counter_1_q), .data(rom_9_data), .sel(Power));
  ROM #(.addrWidth(24), .dataWidth(32)) rom_10 (.addr(counter_1_q), .data(rom_10_data), .sel(Power));
  ROM #(.addrWidth(24), .dataWidth(32)) rom_11 (.addr(counter_1_q), .data(rom_11_data), .sel(Power));
  ROM #(.addrWidth(24), .dataWidth(32)) rom_12 (.addr(counter_1_q), .data(rom_12_data), .sel(Power));
  ROM #(.addrWidth(24), .dataWidth(32)) rom_13 (.addr(counter_1_q), .data(rom_13_data), .sel(Power));
  ROM #(.addrWidth(24), .dataWidth(32)) rom_14 (.addr(counter_1_q), .data(rom_14_data), .sel(Power));
  ROM #(.addrWidth(24), .dataWidth(32)) rom_15 (.addr(counter_1_q), .data(rom_15_data), .sel(Power));
  ROM #(.addrWidth(24), .dataWidth(32)) rom_16 (.addr(counter_1_q), .data(rom_16_data), .sel(Power));
  Register #(.width(1)) register_2 (
    .D(Power), .en(Power), .Q(register_2_q[0]), .clk(decoder_3_out2[0]), .clr(or_27_out[0]));
  Register #(.width(1)) register_3 (
    .D(Power), .en(Power), .Q(register_3_q[0]), .clk(decoder_3_out2[0]), .clr(or_27_out[0]));
  Multiplexer #(.width(24)) multiplexer_15 (
    .in0(counter_1_q), .in1(\Сomand_Number_When_Loading_RAM ), .out(multiplexer_15_out),
    .sel(decoder_2_out2[0]), .en(Power));
  Multiplexer #(.width(24)) multiplexer_16 (
    .in0(counter_1_q), .in1(\Сomand_Number_When_Loading_RAM ), .out(multiplexer_16_out),
    .sel(decoder_2_out2[0]), .en(Power));
  Multiplexer #(.width(24)) multiplexer_17 (
    .in0(counter_1_q), .in1(\Сomand_Number_When_Loading_RAM ), .out(multiplexer_17_out),
    .sel(decoder_2_out2[0]), .en(Power));
  Multiplexer #(.width(24)) multiplexer_18 (
    .in0(counter_1_q), .in1(\Сomand_Number_When_Loading_RAM ), .out(multiplexer_18_out),
    .sel(decoder_2_out2[0]), .en(Power));
  Multiplexer #(.width(24)) multiplexer_19 (
    .in0(counter_1_q), .in1(\Сomand_Number_When_Loading_RAM ), .out(multiplexer_19_out),
    .sel(decoder_4_out2[0]), .en(Power));
  Multiplexer #(.width(24)) multiplexer_20 (
    .in0(counter_1_q), .in1(\Сomand_Number_When_Loading_RAM ), .out(multiplexer_20_out),
    .sel(decoder_4_out2[0]), .en(Power));
  Multiplexer #(.width(24)) multiplexer_21 (
    .in0(counter_1_q), .in1(\Сomand_Number_When_Loading_RAM ), .out(multiplexer_21_out),
    .sel(decoder_4_out2[0]), .en(Power));
  Multiplexer #(.width(24)) multiplexer_22 (
    .in0(counter_1_q), .in1(\Сomand_Number_When_Loading_RAM ), .out(multiplexer_22_out),
    .sel(decoder_4_out2[0]), .en(Power));
  not not_5 (not_5_out, decoder_2_out2[0]);
  not not_6 (not_6_out, decoder_2_out2[0]);
  not not_7 (not_7_out, decoder_2_out2[0]);
  not not_8 (not_8_out, decoder_2_out2[0]);
  not not_9 (not_9_out, decoder_4_out2[0]);
  not not_10 (not_10_out, decoder_4_out2[0]);
  not not_11 (not_11_out, decoder_4_out2[0]);
  not not_12 (not_12_out, decoder_4_out2[0]);
  RAM #(.addrWidth(24), .dataWidth(32), .bus("separate")) ram_1 (
    .addr(multiplexer_15_out), .din(Data_in_to_Ram_0_31), .data(ram_1_data), .str(decoder_2_out2[0]),
    .sel(Power), .clk(Clk), .ld(not_5_out), .clr(or_27_out[0]));
  RAM #(.addrWidth(24), .dataWidth(32), .bus("separate")) ram_2 (
    .addr(multiplexer_16_out), .din(Data_in_to_Ram_32_63), .data(ram_2_data), .str(decoder_2_out2[0]),
    .sel(Power), .clk(Clk), .ld(not_6_out), .clr(or_27_out[0]));
  RAM #(.addrWidth(24), .dataWidth(32), .bus("separate")) ram_3 (
    .addr(multiplexer_17_out), .din(Data_in_to_Ram_64_95), .data(ram_3_data), .str(decoder_2_out2[0]),
    .sel(Power), .clk(Clk), .ld(not_7_out), .clr(or_27_out[0]));
  RAM #(.addrWidth(24), .dataWidth(32), .bus("separate")) ram_4 (
    .addr(multiplexer_18_out), .din(Data_in_to_Ram_96_127), .data(ram_4_data), .str(decoder_2_out2[0]),
    .sel(Power), .clk(Clk), .ld(not_8_out), .clr(or_27_out[0]));
  RAM #(.addrWidth(24), .dataWidth(32), .bus("separate")) ram_5 (
    .addr(multiplexer_19_out), .din(Data_in_to_Ram_0_31), .data(ram_5_data), .str(decoder_4_out2[0]),
    .sel(Power), .clk(not_3_out), .ld(not_9_out), .clr(or_27_out[0]));
  RAM #(.addrWidth(24), .dataWidth(32), .bus("separate")) ram_6 (
    .addr(multiplexer_20_out), .din(Data_in_to_Ram_32_63), .data(ram_6_data), .str(decoder_4_out2[0]),
    .sel(Power), .clk(not_3_out), .ld(not_10_out), .clr(or_27_out[0]));
  RAM #(.addrWidth(24), .dataWidth(32), .bus("separate")) ram_7 (
    .addr(multiplexer_21_out), .din(Data_in_to_Ram_64_95), .data(ram_7_data), .str(decoder_4_out2[0]),
    .sel(Power), .clk(not_3_out), .ld(not_11_out), .clr(or_27_out[0]));
  RAM #(.addrWidth(24), .dataWidth(32), .bus("separate")) ram_8 (
    .addr(multiplexer_22_out), .din(Data_in_to_Ram_96_127), .data(ram_8_data), .str(decoder_4_out2[0]),
    .sel(Power), .clk(not_3_out), .ld(not_12_out), .clr(or_27_out[0]));
  Register #(.width(1)) register_4 (
    .D(Power), .en(Power), .Q(register_2_q[1]), .clk(decoder_3_out2[1]), .clr(or_27_out[1]));
  Register #(.width(1)) register_5 (
    .D(Power), .en(Power), .Q(register_3_q[1]), .clk(decoder_3_out2[1]), .clr(or_27_out[1]));
  Multiplexer #(.width(24)) multiplexer_23 (
    .in0(counter_1_q), .in1(\Сomand_Number_When_Loading_RAM ), .out(multiplexer_23_out),
    .sel(decoder_2_out2[1]), .en(Power));
  Multiplexer #(.width(24)) multiplexer_24 (
    .in0(counter_1_q), .in1(\Сomand_Number_When_Loading_RAM ), .out(multiplexer_24_out),
    .sel(decoder_2_out2[1]), .en(Power));
  Multiplexer #(.width(24)) multiplexer_25 (
    .in0(counter_1_q), .in1(\Сomand_Number_When_Loading_RAM ), .out(multiplexer_25_out),
    .sel(decoder_2_out2[1]), .en(Power));
  Multiplexer #(.width(24)) multiplexer_26 (
    .in0(counter_1_q), .in1(\Сomand_Number_When_Loading_RAM ), .out(multiplexer_26_out),
    .sel(decoder_2_out2[1]), .en(Power));
  Multiplexer #(.width(24)) multiplexer_27 (
    .in0(counter_1_q), .in1(\Сomand_Number_When_Loading_RAM ), .out(multiplexer_27_out),
    .sel(decoder_4_out2[1]), .en(Power));
  Multiplexer #(.width(24)) multiplexer_28 (
    .in0(counter_1_q), .in1(\Сomand_Number_When_Loading_RAM ), .out(multiplexer_28_out),
    .sel(decoder_4_out2[1]), .en(Power));
  Multiplexer #(.width(24)) multiplexer_29 (
    .in0(counter_1_q), .in1(\Сomand_Number_When_Loading_RAM ), .out(multiplexer_29_out),
    .sel(decoder_4_out2[1]), .en(Power));
  Multiplexer #(.width(24)) multiplexer_30 (
    .in0(counter_1_q), .in1(\Сomand_Number_When_Loading_RAM ), .out(multiplexer_30_out),
    .sel(decoder_4_out2[1]), .en(Power));
  not not_13 (not_13_out, decoder_2_out2[1]);
  not not_14 (not_14_out, decoder_2_out2[1]);
  not not_15 (not_15_out, decoder_2_out2[1]);
  not not_16 (not_16_out, decoder_2_out2[1]);
  not not_17 (not_17_out, decoder_4_out2[1]);
  not not_18 (not_18_out, decoder_4_out2[1]);
  not not_19 (not_19_out, decoder_4_out2[1]);
  not not_20 (not_20_out, decoder_4_out2[1]);
  RAM #(.addrWidth(24), .dataWidth(32), .bus("separate")) ram_9 (
    .addr(multiplexer_23_out), .din(Data_in_to_Ram_0_31), .data(ram_9_data), .str(decoder_2_out2[1]),
    .sel(Power), .clk(Clk), .ld(not_13_out), .clr(or_27_out[1]));
  RAM #(.addrWidth(24), .dataWidth(32), .bus("separate")) ram_10 (
    .addr(multiplexer_24_out), .din(Data_in_to_Ram_32_63), .data(ram_10_data), .str(decoder_2_out2[1]),
    .sel(Power), .clk(Clk), .ld(not_14_out), .clr(or_27_out[1]));
  RAM #(.addrWidth(24), .dataWidth(32), .bus("separate")) ram_11 (
    .addr(multiplexer_25_out), .din(Data_in_to_Ram_64_95), .data(ram_11_data), .str(decoder_2_out2[1]),
    .sel(Power), .clk(Clk), .ld(not_15_out), .clr(or_27_out[1]));
  RAM #(.addrWidth(24), .dataWidth(32), .bus("separate")) ram_12 (
    .addr(multiplexer_26_out), .din(Data_in_to_Ram_96_127), .data(ram_12_data), .str(decoder_2_out2[1]),
    .sel(Power), .clk(Clk), .ld(not_16_out), .clr(or_27_out[1]));
  RAM #(.addrWidth(24), .dataWidth(32), .bus("separate")) ram_13 (
    .addr(multiplexer_27_out), .din(Data_in_to_Ram_0_31), .data(ram_13_data), .str(decoder_4_out2[1]),
    .sel(Power), .clk(not_3_out), .ld(not_17_out), .clr(or_27_out[1]));
  RAM #(.addrWidth(24), .dataWidth(32), .bus("separate")) ram_14 (
    .addr(multiplexer_28_out), .din(Data_in_to_Ram_32_63), .data(ram_14_data), .str(decoder_4_out2[1]),
    .sel(Power), .clk(not_3_out), .ld(not_18_out), .clr(or_27_out[1]));
  RAM #(.addrWidth(24), .dataWidth(32), .bus("separate")) ram_15 (
    .addr(multiplexer_29_out), .din(Data_in_to_Ram_64_95), .data(ram_15_data), .str(decoder_4_out2[1]),
    .sel(Power), .clk(not_3_out), .ld(not_19_out), .clr(or_27_out[1]));
  RAM #(.addrWidth(24), .dataWidth(32), .bus("separate")) ram_16 (
    .addr(multiplexer_30_out), .din(Data_in_to_Ram_96_127), .data(ram_16_data), .str(decoder_4_out2[1]),
    .sel(Power), .clk(not_3_out), .ld(not_20_out), .clr(or_27_out[1]));
  Register #(.width(1)) register_6 (
    .D(Power), .en(Power), .Q(register_2_q[2]), .clk(decoder_3_out2[2]), .clr(or_17_out[0]));
  Register #(.width(1)) register_7 (
    .D(Power), .en(Power), .Q(register_3_q[2]), .clk(decoder_3_out2[2]), .clr(or_17_out[0]));
  Multiplexer #(.width(24)) multiplexer_31 (
    .in0(counter_1_q), .in1(\Сomand_Number_When_Loading_RAM ), .out(multiplexer_31_out),
    .sel(decoder_2_out2[2]), .en(Power));
  Multiplexer #(.width(24)) multiplexer_32 (
    .in0(counter_1_q), .in1(\Сomand_Number_When_Loading_RAM ), .out(multiplexer_32_out),
    .sel(decoder_2_out2[2]), .en(Power));
  Multiplexer #(.width(24)) multiplexer_33 (
    .in0(counter_1_q), .in1(\Сomand_Number_When_Loading_RAM ), .out(multiplexer_33_out),
    .sel(decoder_2_out2[2]), .en(Power));
  Multiplexer #(.width(24)) multiplexer_34 (
    .in0(counter_1_q), .in1(\Сomand_Number_When_Loading_RAM ), .out(multiplexer_34_out),
    .sel(decoder_2_out2[2]), .en(Power));
  Multiplexer #(.width(24)) multiplexer_35 (
    .in0(counter_1_q), .in1(\Сomand_Number_When_Loading_RAM ), .out(multiplexer_35_out),
    .sel(decoder_4_out2[2]), .en(Power));
  Multiplexer #(.width(24)) multiplexer_36 (
    .in0(counter_1_q), .in1(\Сomand_Number_When_Loading_RAM ), .out(multiplexer_36_out),
    .sel(decoder_4_out2[2]), .en(Power));
  Multiplexer #(.width(24)) multiplexer_37 (
    .in0(counter_1_q), .in1(\Сomand_Number_When_Loading_RAM ), .out(multiplexer_37_out),
    .sel(decoder_4_out2[2]), .en(Power));
  Multiplexer #(.width(24)) multiplexer_38 (
    .in0(counter_1_q), .in1(\Сomand_Number_When_Loading_RAM ), .out(multiplexer_38_out),
    .sel(decoder_4_out2[2]), .en(Power));
  RAM #(.addrWidth(24), .dataWidth(32), .bus("separate")) ram_17 (
    .addr(multiplexer_31_out), .din(Data_in_to_Ram_0_31), .data(ram_17_data), .str(decoder_2_out2[2]),
    .sel(Power), .clk(Clk), .ld(not_21_out), .clr(or_17_out[0]));
  not not_21 (not_21_out, decoder_2_out2[2]);
  RAM #(.addrWidth(24), .dataWidth(32), .bus("separate")) ram_18 (
    .addr(multiplexer_32_out), .din(Data_in_to_Ram_32_63), .data(ram_18_data), .str(decoder_2_out2[2]),
    .sel(Power), .clk(Clk), .ld(not_22_out), .clr(or_17_out[0]));
  not not_22 (not_22_out, decoder_2_out2[2]);
  RAM #(.addrWidth(24), .dataWidth(32), .bus("separate")) ram_19 (
    .addr(multiplexer_33_out), .din(Data_in_to_Ram_64_95), .data(ram_19_data), .str(decoder_2_out2[2]),
    .sel(Power), .clk(Clk), .ld(not_23_out), .clr(or_17_out[0]));
  not not_23 (not_23_out, decoder_2_out2[2]);
  RAM #(.addrWidth(24), .dataWidth(32), .bus("separate")) ram_20 (
    .addr(multiplexer_34_out), .din(Data_in_to_Ram_96_127), .data(ram_20_data), .str(decoder_2_out2[2]),
    .sel(Power), .clk(Clk), .ld(not_24_out), .clr(or_17_out[0]));
  not not_24 (not_24_out, decoder_2_out2[2]);
  RAM #(.addrWidth(24), .dataWidth(32), .bus("separate")) ram_21 (
    .addr(multiplexer_35_out), .din(Data_in_to_Ram_0_31), .data(ram_21_data), .str(decoder_4_out2[2]),
    .sel(Power), .clk(not_3_out), .ld(not_25_out), .clr(or_17_out[0]));
  not not_25 (not_25_out, decoder_4_out2[2]);
  RAM #(.addrWidth(24), .dataWidth(32), .bus("separate")) ram_22 (
    .addr(multiplexer_36_out), .din(Data_in_to_Ram_32_63), .data(ram_22_data), .str(decoder_4_out2[2]),
    .sel(Power), .clk(not_3_out), .ld(not_26_out), .clr(or_17_out[0]));
  not not_26 (not_26_out, decoder_4_out2[2]);
  RAM #(.addrWidth(24), .dataWidth(32), .bus("separate")) ram_23 (
    .addr(multiplexer_37_out), .din(Data_in_to_Ram_64_95), .data(ram_23_data), .str(decoder_4_out2[2]),
    .sel(Power), .clk(not_3_out), .ld(not_27_out), .clr(or_17_out[0]));
  not not_27 (not_27_out, decoder_4_out2[2]);
  RAM #(.addrWidth(24), .dataWidth(32), .bus("separate")) ram_24 (
    .addr(multiplexer_38_out), .din(Data_in_to_Ram_96_127), .data(ram_24_data), .str(decoder_4_out2[2]),
    .sel(Power), .clk(not_3_out), .ld(not_28_out), .clr(or_17_out[0]));
  not not_28 (not_28_out, decoder_4_out2[2]);
  Register #(.width(1)) register_8 (
    .D(Power), .en(Power), .Q(register_2_q[3]), .clk(decoder_3_out2[3]), .clr(or_17_out[1]));
  Register #(.width(1)) register_9 (
    .D(Power), .en(Power), .Q(register_3_q[3]), .clk(decoder_3_out2[3]), .clr(or_17_out[1]));
  Multiplexer #(.width(24)) multiplexer_39 (
    .in0(counter_1_q), .in1(\Сomand_Number_When_Loading_RAM ), .out(multiplexer_39_out),
    .sel(decoder_2_out2[3]), .en(Power));
  Multiplexer #(.width(24)) multiplexer_40 (
    .in0(counter_1_q), .in1(\Сomand_Number_When_Loading_RAM ), .out(multiplexer_40_out),
    .sel(decoder_2_out2[3]), .en(Power));
  Multiplexer #(.width(24)) multiplexer_41 (
    .in0(counter_1_q), .in1(\Сomand_Number_When_Loading_RAM ), .out(multiplexer_41_out),
    .sel(decoder_2_out2[3]), .en(Power));
  Multiplexer #(.width(24)) multiplexer_42 (
    .in0(counter_1_q), .in1(\Сomand_Number_When_Loading_RAM ), .out(multiplexer_42_out),
    .sel(decoder_2_out2[3]), .en(Power));
  Multiplexer #(.width(24)) multiplexer_43 (
    .in0(counter_1_q), .in1(\Сomand_Number_When_Loading_RAM ), .out(multiplexer_43_out),
    .sel(decoder_4_out2[3]), .en(Power));
  Multiplexer #(.width(24)) multiplexer_44 (
    .in0(counter_1_q), .in1(\Сomand_Number_When_Loading_RAM ), .out(multiplexer_44_out),
    .sel(decoder_4_out2[3]), .en(Power));
  Multiplexer #(.width(24)) multiplexer_45 (
    .in0(counter_1_q), .in1(\Сomand_Number_When_Loading_RAM ), .out(multiplexer_45_out),
    .sel(decoder_4_out2[3]), .en(Power));
  Multiplexer #(.width(24)) multiplexer_46 (
    .in0(counter_1_q), .in1(\Сomand_Number_When_Loading_RAM ), .out(multiplexer_46_out),
    .sel(decoder_4_out2[3]), .en(Power));
  RAM #(.addrWidth(24), .dataWidth(32), .bus("separate")) ram_25 (
    .addr(multiplexer_39_out), .din(Data_in_to_Ram_0_31), .data(ram_25_data), .str(decoder_2_out2[3]),
    .sel(Power), .clk(Clk), .ld(not_29_out), .clr(or_17_out[1]));
  not not_29 (not_29_out, decoder_2_out2[3]);
  RAM #(.addrWidth(24), .dataWidth(32), .bus("separate")) ram_26 (
    .addr(multiplexer_40_out), .din(Data_in_to_Ram_32_63), .data(ram_26_data), .str(decoder_2_out2[3]),
    .sel(Power), .clk(Clk), .ld(not_30_out), .clr(or_17_out[1]));
  not not_30 (not_30_out, decoder_2_out2[3]);
  RAM #(.addrWidth(24), .dataWidth(32), .bus("separate")) ram_27 (
    .addr(multiplexer_41_out), .din(Data_in_to_Ram_64_95), .data(ram_27_data), .str(decoder_2_out2[3]),
    .sel(Power), .clk(Clk), .ld(not_31_out), .clr(or_17_out[1]));
  not not_31 (not_31_out, decoder_2_out2[3]);
  RAM #(.addrWidth(24), .dataWidth(32), .bus("separate")) ram_28 (
    .addr(multiplexer_42_out), .din(Data_in_to_Ram_96_127), .data(ram_28_data), .str(decoder_2_out2[3]),
    .sel(Power), .clk(Clk), .ld(not_32_out), .clr(or_17_out[1]));
  not not_32 (not_32_out, decoder_2_out2[3]);
  RAM #(.addrWidth(24), .dataWidth(32), .bus("separate")) ram_29 (
    .addr(multiplexer_43_out), .din(Data_in_to_Ram_0_31), .data(ram_29_data), .str(decoder_4_out2[3]),
    .sel(Power), .clk(not_3_out), .ld(not_33_out), .clr(or_17_out[1]));
  not not_33 (not_33_out, decoder_4_out2[3]);
  RAM #(.addrWidth(24), .dataWidth(32), .bus("separate")) ram_30 (
    .addr(multiplexer_44_out), .din(Data_in_to_Ram_32_63), .data(ram_30_data), .str(decoder_4_out2[3]),
    .sel(Power), .clk(not_3_out), .ld(not_34_out), .clr(or_17_out[1]));
  not not_34 (not_34_out, decoder_4_out2[3]);
  RAM #(.addrWidth(24), .dataWidth(32), .bus("separate")) ram_31 (
    .addr(multiplexer_45_out), .din(Data_in_to_Ram_64_95), .data(ram_31_data), .str(decoder_4_out2[3]),
    .sel(Power), .clk(not_3_out), .ld(not_35_out), .clr(or_17_out[1]));
  not not_35 (not_35_out, decoder_4_out2[3]);
  RAM #(.addrWidth(24), .dataWidth(32), .bus("separate")) ram_32 (
    .addr(multiplexer_46_out), .din(Data_in_to_Ram_96_127), .data(ram_32_data), .str(decoder_4_out2[3]),
    .sel(Power), .clk(not_3_out), .ld(not_36_out), .clr(or_17_out[1]));
  not not_36 (not_36_out, decoder_4_out2[3]);
  Register #(.width(1)) register_10 (
    .D(Power), .en(Power), .Q(register_2_q[4]), .clk(decoder_3_out2[4]), .clr(or_17_out[2]));
  Register #(.width(1)) register_11 (
    .D(Power), .en(Power), .Q(register_3_q[4]), .clk(decoder_3_out2[4]), .clr(or_17_out[2]));
  Multiplexer #(.width(24)) multiplexer_47 (
    .in0(counter_1_q), .in1(\Сomand_Number_When_Loading_RAM ), .out(multiplexer_47_out),
    .sel(decoder_2_out2[4]), .en(Power));
  Multiplexer #(.width(24)) multiplexer_48 (
    .in0(counter_1_q), .in1(\Сomand_Number_When_Loading_RAM ), .out(multiplexer_48_out),
    .sel(decoder_2_out2[4]), .en(Power));
  Multiplexer #(.width(24)) multiplexer_49 (
    .in0(counter_1_q), .in1(\Сomand_Number_When_Loading_RAM ), .out(multiplexer_49_out),
    .sel(decoder_2_out2[4]), .en(Power));
  Multiplexer #(.width(24)) multiplexer_50 (
    .in0(counter_1_q), .in1(\Сomand_Number_When_Loading_RAM ), .out(multiplexer_50_out),
    .sel(decoder_2_out2[4]), .en(Power));
  Multiplexer #(.width(24)) multiplexer_51 (
    .in0(counter_1_q), .in1(\Сomand_Number_When_Loading_RAM ), .out(multiplexer_51_out),
    .sel(decoder_4_out2[4]), .en(Power));
  Multiplexer #(.width(24)) multiplexer_52 (
    .in0(counter_1_q), .in1(\Сomand_Number_When_Loading_RAM ), .out(multiplexer_52_out),
    .sel(decoder_4_out2[4]), .en(Power));
  Multiplexer #(.width(24)) multiplexer_53 (
    .in0(counter_1_q), .in1(\Сomand_Number_When_Loading_RAM ), .out(multiplexer_53_out),
    .sel(decoder_4_out2[4]), .en(Power));
  Multiplexer #(.width(24)) multiplexer_54 (
    .in0(counter_1_q), .in1(\Сomand_Number_When_Loading_RAM ), .out(multiplexer_54_out),
    .sel(decoder_4_out2[4]), .en(Power));
  not not_37 (not_37_out, decoder_2_out2[4]);
  not not_38 (not_38_out, decoder_2_out2[4]);
  not not_39 (not_39_out, decoder_2_out2[4]);
  not not_40 (not_40_out, decoder_2_out2[4]);
  not not_41 (not_41_out, decoder_4_out2[4]);
  not not_42 (not_42_out, decoder_4_out2[4]);
  not not_43 (not_43_out, decoder_4_out2[4]);
  not not_44 (not_44_out, decoder_4_out2[4]);
  RAM #(.addrWidth(24), .dataWidth(32), .bus("separate")) ram_33 (
    .addr(multiplexer_47_out), .din(Data_in_to_Ram_0_31), .data(ram_33_data), .str(decoder_2_out2[4]),
    .sel(Power), .clk(Clk), .ld(not_37_out), .clr(or_17_out[2]));
  RAM #(.addrWidth(24), .dataWidth(32), .bus("separate")) ram_34 (
    .addr(multiplexer_48_out), .din(Data_in_to_Ram_32_63), .data(ram_34_data), .str(decoder_2_out2[4]),
    .sel(Power), .clk(Clk), .ld(not_38_out), .clr(or_17_out[2]));
  RAM #(.addrWidth(24), .dataWidth(32), .bus("separate")) ram_35 (
    .addr(multiplexer_49_out), .din(Data_in_to_Ram_64_95), .data(ram_35_data), .str(decoder_2_out2[4]),
    .sel(Power), .clk(Clk), .ld(not_39_out), .clr(or_17_out[2]));
  RAM #(.addrWidth(24), .dataWidth(32), .bus("separate")) ram_36 (
    .addr(multiplexer_50_out), .din(Data_in_to_Ram_96_127), .data(ram_36_data), .str(decoder_2_out2[4]),
    .sel(Power), .clk(Clk), .ld(not_40_out), .clr(or_17_out[2]));
  RAM #(.addrWidth(24), .dataWidth(32), .bus("separate")) ram_37 (
    .addr(multiplexer_51_out), .din(Data_in_to_Ram_0_31), .data(ram_37_data), .str(decoder_4_out2[4]),
    .sel(Power), .clk(not_3_out), .ld(not_41_out), .clr(or_17_out[2]));
  RAM #(.addrWidth(24), .dataWidth(32), .bus("separate")) ram_38 (
    .addr(multiplexer_52_out), .din(Data_in_to_Ram_32_63), .data(ram_38_data), .str(decoder_4_out2[4]),
    .sel(Power), .clk(not_3_out), .ld(not_42_out), .clr(or_17_out[2]));
  RAM #(.addrWidth(24), .dataWidth(32), .bus("separate")) ram_39 (
    .addr(multiplexer_53_out), .din(Data_in_to_Ram_64_95), .data(ram_39_data), .str(decoder_4_out2[4]),
    .sel(Power), .clk(not_3_out), .ld(not_43_out), .clr(or_17_out[2]));
  RAM #(.addrWidth(24), .dataWidth(32), .bus("separate")) ram_40 (
    .addr(multiplexer_54_out), .din(Data_in_to_Ram_96_127), .data(ram_40_data), .str(decoder_4_out2[4]),
    .sel(Power), .clk(not_3_out), .ld(not_44_out), .clr(or_17_out[2]));
  Register #(.width(1)) register_12 (
    .D(Power), .en(Power), .Q(register_2_q[5]), .clk(decoder_3_out2[5]), .clr(or_17_out[3]));
  Register #(.width(1)) register_13 (
    .D(Power), .en(Power), .Q(register_3_q[5]), .clk(decoder_3_out2[5]), .clr(or_17_out[3]));
  Multiplexer #(.width(24)) multiplexer_55 (
    .in0(counter_1_q), .in1(\Сomand_Number_When_Loading_RAM ), .out(multiplexer_55_out),
    .sel(decoder_2_out2[5]), .en(Power));
  Multiplexer #(.width(24)) multiplexer_56 (
    .in0(counter_1_q), .in1(\Сomand_Number_When_Loading_RAM ), .out(multiplexer_56_out),
    .sel(decoder_2_out2[5]), .en(Power));
  Multiplexer #(.width(24)) multiplexer_57 (
    .in0(counter_1_q), .in1(\Сomand_Number_When_Loading_RAM ), .out(multiplexer_57_out),
    .sel(decoder_2_out2[5]), .en(Power));
  Multiplexer #(.width(24)) multiplexer_58 (
    .in0(counter_1_q), .in1(\Сomand_Number_When_Loading_RAM ), .out(multiplexer_58_out),
    .sel(decoder_2_out2[5]), .en(Power));
  Multiplexer #(.width(24)) multiplexer_59 (
    .in0(counter_1_q), .in1(\Сomand_Number_When_Loading_RAM ), .out(multiplexer_59_out),
    .sel(decoder_4_out2[5]), .en(Power));
  Multiplexer #(.width(24)) multiplexer_60 (
    .in0(counter_1_q), .in1(\Сomand_Number_When_Loading_RAM ), .out(multiplexer_60_out),
    .sel(decoder_4_out2[5]), .en(Power));
  Multiplexer #(.width(24)) multiplexer_61 (
    .in0(counter_1_q), .in1(\Сomand_Number_When_Loading_RAM ), .out(multiplexer_61_out),
    .sel(decoder_4_out2[5]), .en(Power));
  Multiplexer #(.width(24)) multiplexer_62 (
    .in0(counter_1_q), .in1(\Сomand_Number_When_Loading_RAM ), .out(multiplexer_62_out),
    .sel(decoder_4_out2[5]), .en(Power));
  not not_45 (not_45_out, decoder_2_out2[5]);
  not not_46 (not_46_out, decoder_2_out2[5]);
  not not_47 (not_47_out, decoder_2_out2[5]);
  not not_48 (not_48_out, decoder_2_out2[5]);
  not not_49 (not_49_out, decoder_4_out2[5]);
  not not_50 (not_50_out, decoder_4_out2[5]);
  not not_51 (not_51_out, decoder_4_out2[5]);
  not not_52 (not_52_out, decoder_4_out2[5]);
  RAM #(.addrWidth(24), .dataWidth(32), .bus("separate")) ram_41 (
    .addr(multiplexer_55_out), .din(Data_in_to_Ram_0_31), .data(ram_41_data), .str(decoder_2_out2[5]),
    .sel(Power), .clk(Clk), .ld(not_45_out), .clr(or_17_out[3]));
  RAM #(.addrWidth(24), .dataWidth(32), .bus("separate")) ram_42 (
    .addr(multiplexer_56_out), .din(Data_in_to_Ram_32_63), .data(ram_42_data), .str(decoder_2_out2[5]),
    .sel(Power), .clk(Clk), .ld(not_46_out), .clr(or_17_out[3]));
  RAM #(.addrWidth(24), .dataWidth(32), .bus("separate")) ram_43 (
    .addr(multiplexer_57_out), .din(Data_in_to_Ram_64_95), .data(ram_43_data), .str(decoder_2_out2[5]),
    .sel(Power), .clk(Clk), .ld(not_47_out), .clr(or_17_out[3]));
  RAM #(.addrWidth(24), .dataWidth(32), .bus("separate")) ram_44 (
    .addr(multiplexer_58_out), .din(Data_in_to_Ram_96_127), .data(ram_44_data), .str(decoder_2_out2[5]),
    .sel(Power), .clk(Clk), .ld(not_48_out), .clr(or_17_out[3]));
  RAM #(.addrWidth(24), .dataWidth(32), .bus("separate")) ram_45 (
    .addr(multiplexer_59_out), .din(Data_in_to_Ram_0_31), .data(ram_45_data), .str(decoder_4_out2[5]),
    .sel(Power), .clk(not_3_out), .ld(not_49_out), .clr(or_17_out[3]));
  RAM #(.addrWidth(24), .dataWidth(32), .bus("separate")) ram_46 (
    .addr(multiplexer_60_out), .din(Data_in_to_Ram_32_63), .data(ram_46_data), .str(decoder_4_out2[5]),
    .sel(Power), .clk(not_3_out), .ld(not_50_out), .clr(or_17_out[3]));
  RAM #(.addrWidth(24), .dataWidth(32), .bus("separate")) ram_47 (
    .addr(multiplexer_61_out), .din(Data_in_to_Ram_64_95), .data(ram_47_data), .str(decoder_4_out2[5]),
    .sel(Power), .clk(not_3_out), .ld(not_51_out), .clr(or_17_out[3]));
  RAM #(.addrWidth(24), .dataWidth(32), .bus("separate")) ram_48 (
    .addr(multiplexer_62_out), .din(Data_in_to_Ram_96_127), .data(ram_48_data), .str(decoder_4_out2[5]),
    .sel(Power), .clk(not_3_out), .ld(not_52_out), .clr(or_17_out[3]));
  Register #(.width(1)) register_14 (
    .D(Power), .en(Power), .Q(register_2_q[6]), .clk(decoder_3_out2[6]), .clr(or_9_out[0]));
  Register #(.width(1)) register_15 (
    .D(Power), .en(Power), .Q(register_3_q[6]), .clk(decoder_3_out2[6]), .clr(or_9_out[0]));
  Multiplexer #(.width(24)) multiplexer_63 (
    .in0(counter_1_q), .in1(\Сomand_Number_When_Loading_RAM ), .out(multiplexer_63_out),
    .sel(decoder_2_out2[6]), .en(Power));
  Multiplexer #(.width(24)) multiplexer_64 (
    .in0(counter_1_q), .in1(\Сomand_Number_When_Loading_RAM ), .out(multiplexer_64_out),
    .sel(decoder_2_out2[6]), .en(Power));
  Multiplexer #(.width(24)) multiplexer_65 (
    .in0(counter_1_q), .in1(\Сomand_Number_When_Loading_RAM ), .out(multiplexer_65_out),
    .sel(decoder_2_out2[6]), .en(Power));
  Multiplexer #(.width(24)) multiplexer_66 (
    .in0(counter_1_q), .in1(\Сomand_Number_When_Loading_RAM ), .out(multiplexer_66_out),
    .sel(decoder_2_out2[6]), .en(Power));
  Multiplexer #(.width(24)) multiplexer_67 (
    .in0(counter_1_q), .in1(\Сomand_Number_When_Loading_RAM ), .out(multiplexer_67_out),
    .sel(decoder_4_out2[6]), .en(Power));
  Multiplexer #(.width(24)) multiplexer_68 (
    .in0(counter_1_q), .in1(\Сomand_Number_When_Loading_RAM ), .out(multiplexer_68_out),
    .sel(decoder_4_out2[6]), .en(Power));
  Multiplexer #(.width(24)) multiplexer_69 (
    .in0(counter_1_q), .in1(\Сomand_Number_When_Loading_RAM ), .out(multiplexer_69_out),
    .sel(decoder_4_out2[6]), .en(Power));
  Multiplexer #(.width(24)) multiplexer_70 (
    .in0(counter_1_q), .in1(\Сomand_Number_When_Loading_RAM ), .out(multiplexer_70_out),
    .sel(decoder_4_out2[6]), .en(Power));
  RAM #(.addrWidth(24), .dataWidth(32), .bus("separate")) ram_49 (
    .addr(multiplexer_63_out), .din(Data_in_to_Ram_0_31), .data(ram_49_data), .str(decoder_2_out2[6]),
    .sel(Power), .clk(Clk), .ld(not_53_out), .clr(or_9_out[0]));
  not not_53 (not_53_out, decoder_2_out2[6]);
  RAM #(.addrWidth(24), .dataWidth(32), .bus("separate")) ram_50 (
    .addr(multiplexer_64_out), .din(Data_in_to_Ram_32_63), .data(ram_50_data), .str(decoder_2_out2[6]),
    .sel(Power), .clk(Clk), .ld(not_54_out), .clr(or_9_out[0]));
  not not_54 (not_54_out, decoder_2_out2[6]);
  RAM #(.addrWidth(24), .dataWidth(32), .bus("separate")) ram_51 (
    .addr(multiplexer_65_out), .din(Data_in_to_Ram_64_95), .data(ram_51_data), .str(decoder_2_out2[6]),
    .sel(Power), .clk(Clk), .ld(not_55_out), .clr(or_9_out[0]));
  not not_55 (not_55_out, decoder_2_out2[6]);
  RAM #(.addrWidth(24), .dataWidth(32), .bus("separate")) ram_52 (
    .addr(multiplexer_66_out), .din(Data_in_to_Ram_96_127), .data(ram_52_data), .str(decoder_2_out2[6]),
    .sel(Power), .clk(Clk), .ld(not_56_out), .clr(or_9_out[0]));
  not not_56 (not_56_out, decoder_2_out2[6]);
  RAM #(.addrWidth(24), .dataWidth(32), .bus("separate")) ram_53 (
    .addr(multiplexer_67_out), .din(Data_in_to_Ram_0_31), .data(ram_53_data), .str(decoder_4_out2[6]),
    .sel(Power), .clk(not_3_out), .ld(not_57_out), .clr(or_9_out[0]));
  not not_57 (not_57_out, decoder_4_out2[6]);
  RAM #(.addrWidth(24), .dataWidth(32), .bus("separate")) ram_54 (
    .addr(multiplexer_68_out), .din(Data_in_to_Ram_32_63), .data(ram_54_data), .str(decoder_4_out2[6]),
    .sel(Power), .clk(not_3_out), .ld(not_58_out), .clr(or_9_out[0]));
  not not_58 (not_58_out, decoder_4_out2[6]);
  RAM #(.addrWidth(24), .dataWidth(32), .bus("separate")) ram_55 (
    .addr(multiplexer_69_out), .din(Data_in_to_Ram_64_95), .data(ram_55_data), .str(decoder_4_out2[6]),
    .sel(Power), .clk(not_3_out), .ld(not_59_out), .clr(or_9_out[0]));
  not not_59 (not_59_out, decoder_4_out2[6]);
  RAM #(.addrWidth(24), .dataWidth(32), .bus("separate")) ram_56 (
    .addr(multiplexer_70_out), .din(Data_in_to_Ram_96_127), .data(ram_56_data), .str(decoder_4_out2[6]),
    .sel(Power), .clk(not_3_out), .ld(not_60_out), .clr(or_9_out[0]));
  not not_60 (not_60_out, decoder_4_out2[6]);
  Register #(.width(1)) register_16 (
    .D(Power), .en(Power), .Q(register_2_q[7]), .clk(decoder_3_out2[7]), .clr(or_9_out[1]));
  Register #(.width(1)) register_17 (
    .D(Power), .en(Power), .Q(register_3_q[7]), .clk(decoder_3_out2[7]), .clr(or_9_out[1]));
  Multiplexer #(.width(24)) multiplexer_71 (
    .in0(counter_1_q), .in1(\Сomand_Number_When_Loading_RAM ), .out(multiplexer_71_out),
    .sel(decoder_2_out2[7]), .en(Power));
  Multiplexer #(.width(24)) multiplexer_72 (
    .in0(counter_1_q), .in1(\Сomand_Number_When_Loading_RAM ), .out(multiplexer_72_out),
    .sel(decoder_2_out2[7]), .en(Power));
  Multiplexer #(.width(24)) multiplexer_73 (
    .in0(counter_1_q), .in1(\Сomand_Number_When_Loading_RAM ), .out(multiplexer_73_out),
    .sel(decoder_2_out2[7]), .en(Power));
  Multiplexer #(.width(24)) multiplexer_74 (
    .in0(counter_1_q), .in1(\Сomand_Number_When_Loading_RAM ), .out(multiplexer_74_out),
    .sel(decoder_2_out2[7]), .en(Power));
  Multiplexer #(.width(24)) multiplexer_75 (
    .in0(counter_1_q), .in1(\Сomand_Number_When_Loading_RAM ), .out(multiplexer_75_out),
    .sel(decoder_4_out2[7]), .en(Power));
  Multiplexer #(.width(24)) multiplexer_76 (
    .in0(counter_1_q), .in1(\Сomand_Number_When_Loading_RAM ), .out(multiplexer_76_out),
    .sel(decoder_4_out2[7]), .en(Power));
  Multiplexer #(.width(24)) multiplexer_77 (
    .in0(counter_1_q), .in1(\Сomand_Number_When_Loading_RAM ), .out(multiplexer_77_out),
    .sel(decoder_4_out2[7]), .en(Power));
  Multiplexer #(.width(24)) multiplexer_78 (
    .in0(counter_1_q), .in1(\Сomand_Number_When_Loading_RAM ), .out(multiplexer_78_out),
    .sel(decoder_4_out2[7]), .en(Power));
  RAM #(.addrWidth(24), .dataWidth(32), .bus("separate")) ram_57 (
    .addr(multiplexer_71_out), .din(Data_in_to_Ram_0_31), .data(ram_57_data), .str(decoder_2_out2[7]),
    .sel(Power), .clk(Clk), .ld(not_61_out), .clr(or_9_out[1]));
  not not_61 (not_61_out, decoder_2_out2[7]);
  RAM #(.addrWidth(24), .dataWidth(32), .bus("separate")) ram_58 (
    .addr(multiplexer_72_out), .din(Data_in_to_Ram_32_63), .data(ram_58_data), .str(decoder_2_out2[7]),
    .sel(Power), .clk(Clk), .ld(not_62_out), .clr(or_9_out[1]));
  not not_62 (not_62_out, decoder_2_out2[7]);
  RAM #(.addrWidth(24), .dataWidth(32), .bus("separate")) ram_59 (
    .addr(multiplexer_73_out), .din(Data_in_to_Ram_64_95), .data(ram_59_data), .str(decoder_2_out2[7]),
    .sel(Power), .clk(Clk), .ld(not_63_out), .clr(or_9_out[1]));
  not not_63 (not_63_out, decoder_2_out2[7]);
  RAM #(.addrWidth(24), .dataWidth(32), .bus("separate")) ram_60 (
    .addr(multiplexer_74_out), .din(Data_in_to_Ram_96_127), .data(ram_60_data), .str(decoder_2_out2[7]),
    .sel(Power), .clk(Clk), .ld(not_64_out), .clr(or_9_out[1]));
  not not_64 (not_64_out, decoder_2_out2[7]);
  RAM #(.addrWidth(24), .dataWidth(32), .bus("separate")) ram_61 (
    .addr(multiplexer_75_out), .din(Data_in_to_Ram_0_31), .data(ram_61_data), .str(decoder_4_out2[7]),
    .sel(Power), .clk(not_3_out), .ld(not_65_out), .clr(or_9_out[1]));
  not not_65 (not_65_out, decoder_4_out2[7]);
  RAM #(.addrWidth(24), .dataWidth(32), .bus("separate")) ram_62 (
    .addr(multiplexer_76_out), .din(Data_in_to_Ram_32_63), .data(ram_62_data), .str(decoder_4_out2[7]),
    .sel(Power), .clk(not_3_out), .ld(not_66_out), .clr(or_9_out[1]));
  not not_66 (not_66_out, decoder_4_out2[7]);
  RAM #(.addrWidth(24), .dataWidth(32), .bus("separate")) ram_63 (
    .addr(multiplexer_77_out), .din(Data_in_to_Ram_64_95), .data(ram_63_data), .str(decoder_4_out2[7]),
    .sel(Power), .clk(not_3_out), .ld(not_67_out), .clr(or_9_out[1]));
  not not_67 (not_67_out, decoder_4_out2[7]);
  RAM #(.addrWidth(24), .dataWidth(32), .bus("separate")) ram_64 (
    .addr(multiplexer_78_out), .din(Data_in_to_Ram_96_127), .data(ram_64_data), .str(decoder_4_out2[7]),
    .sel(Power), .clk(not_3_out), .ld(not_68_out), .clr(or_9_out[1]));
  not not_68 (not_68_out, decoder_4_out2[7]);
  Register #(.width(1)) register_18 (
    .D(Power), .en(Power), .Q(register_2_q[8]), .clk(decoder_3_out2[8]), .clr(or_9_out[2]));
  Register #(.width(1)) register_19 (
    .D(Power), .en(Power), .Q(register_3_q[8]), .clk(decoder_3_out2[8]), .clr(or_9_out[2]));
  Multiplexer #(.width(24)) multiplexer_79 (
    .in0(counter_1_q), .in1(\Сomand_Number_When_Loading_RAM ), .out(multiplexer_79_out),
    .sel(decoder_2_out2[8]), .en(Power));
  Multiplexer #(.width(24)) multiplexer_80 (
    .in0(counter_1_q), .in1(\Сomand_Number_When_Loading_RAM ), .out(multiplexer_80_out),
    .sel(decoder_2_out2[8]), .en(Power));
  Multiplexer #(.width(24)) multiplexer_81 (
    .in0(counter_1_q), .in1(\Сomand_Number_When_Loading_RAM ), .out(multiplexer_81_out),
    .sel(decoder_2_out2[8]), .en(Power));
  Multiplexer #(.width(24)) multiplexer_82 (
    .in0(counter_1_q), .in1(\Сomand_Number_When_Loading_RAM ), .out(multiplexer_82_out),
    .sel(decoder_2_out2[8]), .en(Power));
  Multiplexer #(.width(24)) multiplexer_83 (
    .in0(counter_1_q), .in1(\Сomand_Number_When_Loading_RAM ), .out(multiplexer_83_out),
    .sel(decoder_4_out2[8]), .en(Power));
  Multiplexer #(.width(24)) multiplexer_84 (
    .in0(counter_1_q), .in1(\Сomand_Number_When_Loading_RAM ), .out(multiplexer_84_out),
    .sel(decoder_4_out2[8]), .en(Power));
  Multiplexer #(.width(24)) multiplexer_85 (
    .in0(counter_1_q), .in1(\Сomand_Number_When_Loading_RAM ), .out(multiplexer_85_out),
    .sel(decoder_4_out2[8]), .en(Power));
  Multiplexer #(.width(24)) multiplexer_86 (
    .in0(counter_1_q), .in1(\Сomand_Number_When_Loading_RAM ), .out(multiplexer_86_out),
    .sel(decoder_4_out2[8]), .en(Power));
  not not_69 (not_69_out, decoder_2_out2[8]);
  not not_70 (not_70_out, decoder_2_out2[8]);
  not not_71 (not_71_out, decoder_2_out2[8]);
  not not_72 (not_72_out, decoder_2_out2[8]);
  not not_73 (not_73_out, decoder_4_out2[8]);
  not not_74 (not_74_out, decoder_4_out2[8]);
  not not_75 (not_75_out, decoder_4_out2[8]);
  not not_76 (not_76_out, decoder_4_out2[8]);
  RAM #(.addrWidth(24), .dataWidth(32), .bus("separate")) ram_65 (
    .addr(multiplexer_79_out), .din(Data_in_to_Ram_0_31), .data(ram_65_data), .str(decoder_2_out2[8]),
    .sel(Power), .clk(Clk), .ld(not_69_out), .clr(or_9_out[2]));
  RAM #(.addrWidth(24), .dataWidth(32), .bus("separate")) ram_66 (
    .addr(multiplexer_80_out), .din(Data_in_to_Ram_32_63), .data(ram_66_data), .str(decoder_2_out2[8]),
    .sel(Power), .clk(Clk), .ld(not_70_out), .clr(or_9_out[2]));
  RAM #(.addrWidth(24), .dataWidth(32), .bus("separate")) ram_67 (
    .addr(multiplexer_81_out), .din(Data_in_to_Ram_64_95), .data(ram_67_data), .str(decoder_2_out2[8]),
    .sel(Power), .clk(Clk), .ld(not_71_out), .clr(or_9_out[2]));
  RAM #(.addrWidth(24), .dataWidth(32), .bus("separate")) ram_68 (
    .addr(multiplexer_82_out), .din(Data_in_to_Ram_96_127), .data(ram_68_data), .str(decoder_2_out2[8]),
    .sel(Power), .clk(Clk), .ld(not_72_out), .clr(or_9_out[2]));
  RAM #(.addrWidth(24), .dataWidth(32), .bus("separate")) ram_69 (
    .addr(multiplexer_83_out), .din(Data_in_to_Ram_0_31), .data(ram_69_data), .str(decoder_4_out2[8]),
    .sel(Power), .clk(not_3_out), .ld(not_73_out), .clr(or_9_out[2]));
  RAM #(.addrWidth(24), .dataWidth(32), .bus("separate")) ram_70 (
    .addr(multiplexer_84_out), .din(Data_in_to_Ram_32_63), .data(ram_70_data), .str(decoder_4_out2[8]),
    .sel(Power), .clk(not_3_out), .ld(not_74_out), .clr(or_9_out[2]));
  RAM #(.addrWidth(24), .dataWidth(32), .bus("separate")) ram_71 (
    .addr(multiplexer_85_out), .din(Data_in_to_Ram_64_95), .data(ram_71_data), .str(decoder_4_out2[8]),
    .sel(Power), .clk(not_3_out), .ld(not_75_out), .clr(or_9_out[2]));
  RAM #(.addrWidth(24), .dataWidth(32), .bus("separate")) ram_72 (
    .addr(multiplexer_86_out), .din(Data_in_to_Ram_96_127), .data(ram_72_data), .str(decoder_4_out2[8]),
    .sel(Power), .clk(not_3_out), .ld(not_76_out), .clr(or_9_out[2]));
  Register #(.width(1)) register_20 (
    .D(Power), .en(Power), .Q(register_2_q[9]), .clk(decoder_3_out2[9]), .clr(or_9_out[3]));
  Register #(.width(1)) register_21 (
    .D(Power), .en(Power), .Q(register_3_q[9]), .clk(decoder_3_out2[9]), .clr(or_9_out[3]));
  Multiplexer #(.width(24)) multiplexer_87 (
    .in0(counter_1_q), .in1(\Сomand_Number_When_Loading_RAM ), .out(multiplexer_87_out),
    .sel(decoder_2_out2[9]), .en(Power));
  Multiplexer #(.width(24)) multiplexer_88 (
    .in0(counter_1_q), .in1(\Сomand_Number_When_Loading_RAM ), .out(multiplexer_88_out),
    .sel(decoder_2_out2[9]), .en(Power));
  Multiplexer #(.width(24)) multiplexer_89 (
    .in0(counter_1_q), .in1(\Сomand_Number_When_Loading_RAM ), .out(multiplexer_89_out),
    .sel(decoder_2_out2[9]), .en(Power));
  Multiplexer #(.width(24)) multiplexer_90 (
    .in0(counter_1_q), .in1(\Сomand_Number_When_Loading_RAM ), .out(multiplexer_90_out),
    .sel(decoder_2_out2[9]), .en(Power));
  Multiplexer #(.width(24)) multiplexer_91 (
    .in0(counter_1_q), .in1(\Сomand_Number_When_Loading_RAM ), .out(multiplexer_91_out),
    .sel(decoder_4_out2[9]), .en(Power));
  Multiplexer #(.width(24)) multiplexer_92 (
    .in0(counter_1_q), .in1(\Сomand_Number_When_Loading_RAM ), .out(multiplexer_92_out),
    .sel(decoder_4_out2[9]), .en(Power));
  Multiplexer #(.width(24)) multiplexer_93 (
    .in0(counter_1_q), .in1(\Сomand_Number_When_Loading_RAM ), .out(multiplexer_93_out),
    .sel(decoder_4_out2[9]), .en(Power));
  Multiplexer #(.width(24)) multiplexer_94 (
    .in0(counter_1_q), .in1(\Сomand_Number_When_Loading_RAM ), .out(multiplexer_94_out),
    .sel(decoder_4_out2[9]), .en(Power));
  not not_77 (not_77_out, decoder_2_out2[9]);
  not not_78 (not_78_out, decoder_2_out2[9]);
  not not_79 (not_79_out, decoder_2_out2[9]);
  not not_80 (not_80_out, decoder_2_out2[9]);
  not not_81 (not_81_out, decoder_4_out2[9]);
  not not_82 (not_82_out, decoder_4_out2[9]);
  not not_83 (not_83_out, decoder_4_out2[9]);
  not not_84 (not_84_out, decoder_4_out2[9]);
  RAM #(.addrWidth(24), .dataWidth(32), .bus("separate")) ram_73 (
    .addr(multiplexer_87_out), .din(Data_in_to_Ram_0_31), .data(ram_73_data), .str(decoder_2_out2[9]),
    .sel(Power), .clk(Clk), .ld(not_77_out), .clr(or_9_out[3]));
  RAM #(.addrWidth(24), .dataWidth(32), .bus("separate")) ram_74 (
    .addr(multiplexer_88_out), .din(Data_in_to_Ram_32_63), .data(ram_74_data), .str(decoder_2_out2[9]),
    .sel(Power), .clk(Clk), .ld(not_78_out), .clr(or_9_out[3]));
  RAM #(.addrWidth(24), .dataWidth(32), .bus("separate")) ram_75 (
    .addr(multiplexer_89_out), .din(Data_in_to_Ram_64_95), .data(ram_75_data), .str(decoder_2_out2[9]),
    .sel(Power), .clk(Clk), .ld(not_79_out), .clr(or_9_out[3]));
  RAM #(.addrWidth(24), .dataWidth(32), .bus("separate")) ram_76 (
    .addr(multiplexer_90_out), .din(Data_in_to_Ram_96_127), .data(ram_76_data), .str(decoder_2_out2[9]),
    .sel(Power), .clk(Clk), .ld(not_80_out), .clr(or_9_out[3]));
  RAM #(.addrWidth(24), .dataWidth(32), .bus("separate")) ram_77 (
    .addr(multiplexer_91_out), .din(Data_in_to_Ram_0_31), .data(ram_77_data), .str(decoder_4_out2[9]),
    .sel(Power), .clk(not_3_out), .ld(not_81_out), .clr(or_9_out[3]));
  RAM #(.addrWidth(24), .dataWidth(32), .bus("separate")) ram_78 (
    .addr(multiplexer_92_out), .din(Data_in_to_Ram_32_63), .data(ram_78_data), .str(decoder_4_out2[9]),
    .sel(Power), .clk(not_3_out), .ld(not_82_out), .clr(or_9_out[3]));
  RAM #(.addrWidth(24), .dataWidth(32), .bus("separate")) ram_79 (
    .addr(multiplexer_93_out), .din(Data_in_to_Ram_64_95), .data(ram_79_data), .str(decoder_4_out2[9]),
    .sel(Power), .clk(not_3_out), .ld(not_83_out), .clr(or_9_out[3]));
  RAM #(.addrWidth(24), .dataWidth(32), .bus("separate")) ram_80 (
    .addr(multiplexer_94_out), .din(Data_in_to_Ram_96_127), .data(ram_80_data), .str(decoder_4_out2[9]),
    .sel(Power), .clk(not_3_out), .ld(not_84_out), .clr(or_9_out[3]));
  Register #(.width(1)) register_22 (
    .D(Power), .en(Power), .Q(register_2_q[10]), .clk(decoder_3_out2[10]), .clr(or_1_out[0]));
  Register #(.width(1)) register_23 (
    .D(Power), .en(Power), .Q(register_3_q[10]), .clk(decoder_3_out2[10]), .clr(or_1_out[0]));
  Multiplexer #(.width(24)) multiplexer_95 (
    .in0(counter_1_q), .in1(\Сomand_Number_When_Loading_RAM ), .out(multiplexer_95_out),
    .sel(decoder_2_out2[10]), .en(Power));
  Multiplexer #(.width(24)) multiplexer_96 (
    .in0(counter_1_q), .in1(\Сomand_Number_When_Loading_RAM ), .out(multiplexer_96_out),
    .sel(decoder_2_out2[10]), .en(Power));
  Multiplexer #(.width(24)) multiplexer_97 (
    .in0(counter_1_q), .in1(\Сomand_Number_When_Loading_RAM ), .out(multiplexer_97_out),
    .sel(decoder_2_out2[10]), .en(Power));
  Multiplexer #(.width(24)) multiplexer_98 (
    .in0(counter_1_q), .in1(\Сomand_Number_When_Loading_RAM ), .out(multiplexer_98_out),
    .sel(decoder_2_out2[10]), .en(Power));
  Multiplexer #(.width(24)) multiplexer_99 (
    .in0(counter_1_q), .in1(\Сomand_Number_When_Loading_RAM ), .out(multiplexer_99_out),
    .sel(decoder_4_out2[10]), .en(Power));
  Multiplexer #(.width(24)) multiplexer_100 (
    .in0(counter_1_q), .in1(\Сomand_Number_When_Loading_RAM ), .out(multiplexer_100_out),
    .sel(decoder_4_out2[10]), .en(Power));
  Multiplexer #(.width(24)) multiplexer_101 (
    .in0(counter_1_q), .in1(\Сomand_Number_When_Loading_RAM ), .out(multiplexer_101_out),
    .sel(decoder_4_out2[10]), .en(Power));
  Multiplexer #(.width(24)) multiplexer_102 (
    .in0(counter_1_q), .in1(\Сomand_Number_When_Loading_RAM ), .out(multiplexer_102_out),
    .sel(decoder_4_out2[10]), .en(Power));
  RAM #(.addrWidth(24), .dataWidth(32), .bus("separate")) ram_81 (
    .addr(multiplexer_95_out), .din(Data_in_to_Ram_0_31), .data(ram_81_data), .str(decoder_2_out2[10]),
    .sel(Power), .clk(Clk), .ld(not_85_out), .clr(or_1_out[0]));
  not not_85 (not_85_out, decoder_2_out2[10]);
  RAM #(.addrWidth(24), .dataWidth(32), .bus("separate")) ram_82 (
    .addr(multiplexer_96_out), .din(Data_in_to_Ram_32_63), .data(ram_82_data), .str(decoder_2_out2[10]),
    .sel(Power), .clk(Clk), .ld(not_86_out), .clr(or_1_out[0]));
  not not_86 (not_86_out, decoder_2_out2[10]);
  RAM #(.addrWidth(24), .dataWidth(32), .bus("separate")) ram_83 (
    .addr(multiplexer_97_out), .din(Data_in_to_Ram_64_95), .data(ram_83_data), .str(decoder_2_out2[10]),
    .sel(Power), .clk(Clk), .ld(not_87_out), .clr(or_1_out[0]));
  not not_87 (not_87_out, decoder_2_out2[10]);
  RAM #(.addrWidth(24), .dataWidth(32), .bus("separate")) ram_84 (
    .addr(multiplexer_98_out), .din(Data_in_to_Ram_96_127), .data(ram_84_data), .str(decoder_2_out2[10]),
    .sel(Power), .clk(Clk), .ld(not_88_out), .clr(or_1_out[0]));
  not not_88 (not_88_out, decoder_2_out2[10]);
  RAM #(.addrWidth(24), .dataWidth(32), .bus("separate")) ram_85 (
    .addr(multiplexer_99_out), .din(Data_in_to_Ram_0_31), .data(ram_85_data), .str(decoder_4_out2[10]),
    .sel(Power), .clk(not_3_out), .ld(not_89_out), .clr(or_1_out[0]));
  not not_89 (not_89_out, decoder_4_out2[10]);
  RAM #(.addrWidth(24), .dataWidth(32), .bus("separate")) ram_86 (
    .addr(multiplexer_100_out), .din(Data_in_to_Ram_32_63), .data(ram_86_data), .str(decoder_4_out2[10]),
    .sel(Power), .clk(not_3_out), .ld(not_90_out), .clr(or_1_out[0]));
  not not_90 (not_90_out, decoder_4_out2[10]);
  RAM #(.addrWidth(24), .dataWidth(32), .bus("separate")) ram_87 (
    .addr(multiplexer_101_out), .din(Data_in_to_Ram_64_95), .data(ram_87_data), .str(decoder_4_out2[10]),
    .sel(Power), .clk(not_3_out), .ld(not_91_out), .clr(or_1_out[0]));
  not not_91 (not_91_out, decoder_4_out2[10]);
  RAM #(.addrWidth(24), .dataWidth(32), .bus("separate")) ram_88 (
    .addr(multiplexer_102_out), .din(Data_in_to_Ram_96_127), .data(ram_88_data), .str(decoder_4_out2[10]),
    .sel(Power), .clk(not_3_out), .ld(not_92_out), .clr(or_1_out[0]));
  not not_92 (not_92_out, decoder_4_out2[10]);
  Register #(.width(1)) register_24 (
    .D(Power), .en(Power), .Q(register_2_q[11]), .clk(decoder_3_out2[11]), .clr(or_1_out[1]));
  Register #(.width(1)) register_25 (
    .D(Power), .en(Power), .Q(register_3_q[11]), .clk(decoder_3_out2[11]), .clr(or_1_out[1]));
  Multiplexer #(.width(24)) multiplexer_103 (
    .in0(counter_1_q), .in1(\Сomand_Number_When_Loading_RAM ), .out(multiplexer_103_out),
    .sel(decoder_2_out2[11]), .en(Power));
  Multiplexer #(.width(24)) multiplexer_104 (
    .in0(counter_1_q), .in1(\Сomand_Number_When_Loading_RAM ), .out(multiplexer_104_out),
    .sel(decoder_2_out2[11]), .en(Power));
  Multiplexer #(.width(24)) multiplexer_105 (
    .in0(counter_1_q), .in1(\Сomand_Number_When_Loading_RAM ), .out(multiplexer_105_out),
    .sel(decoder_2_out2[11]), .en(Power));
  Multiplexer #(.width(24)) multiplexer_106 (
    .in0(counter_1_q), .in1(\Сomand_Number_When_Loading_RAM ), .out(multiplexer_106_out),
    .sel(decoder_2_out2[11]), .en(Power));
  Multiplexer #(.width(24)) multiplexer_107 (
    .in0(counter_1_q), .in1(\Сomand_Number_When_Loading_RAM ), .out(multiplexer_107_out),
    .sel(decoder_4_out2[11]), .en(Power));
  Multiplexer #(.width(24)) multiplexer_108 (
    .in0(counter_1_q), .in1(\Сomand_Number_When_Loading_RAM ), .out(multiplexer_108_out),
    .sel(decoder_4_out2[11]), .en(Power));
  Multiplexer #(.width(24)) multiplexer_109 (
    .in0(counter_1_q), .in1(\Сomand_Number_When_Loading_RAM ), .out(multiplexer_109_out),
    .sel(decoder_4_out2[11]), .en(Power));
  Multiplexer #(.width(24)) multiplexer_110 (
    .in0(counter_1_q), .in1(\Сomand_Number_When_Loading_RAM ), .out(multiplexer_110_out),
    .sel(decoder_4_out2[11]), .en(Power));
  RAM #(.addrWidth(24), .dataWidth(32), .bus("separate")) ram_89 (
    .addr(multiplexer_103_out), .din(Data_in_to_Ram_0_31), .data(ram_89_data), .str(decoder_2_out2[11]),
    .sel(Power), .clk(Clk), .ld(not_93_out), .clr(or_1_out[1]));
  not not_93 (not_93_out, decoder_2_out2[11]);
  RAM #(.addrWidth(24), .dataWidth(32), .bus("separate")) ram_90 (
    .addr(multiplexer_104_out), .din(Data_in_to_Ram_32_63), .data(ram_90_data), .str(decoder_2_out2[11]),
    .sel(Power), .clk(Clk), .ld(not_94_out), .clr(or_1_out[1]));
  not not_94 (not_94_out, decoder_2_out2[11]);
  RAM #(.addrWidth(24), .dataWidth(32), .bus("separate")) ram_91 (
    .addr(multiplexer_105_out), .din(Data_in_to_Ram_64_95), .data(ram_91_data), .str(decoder_2_out2[11]),
    .sel(Power), .clk(Clk), .ld(not_95_out), .clr(or_1_out[1]));
  not not_95 (not_95_out, decoder_2_out2[11]);
  RAM #(.addrWidth(24), .dataWidth(32), .bus("separate")) ram_92 (
    .addr(multiplexer_106_out), .din(Data_in_to_Ram_96_127), .data(ram_92_data), .str(decoder_2_out2[11]),
    .sel(Power), .clk(Clk), .ld(not_96_out), .clr(or_1_out[1]));
  not not_96 (not_96_out, decoder_2_out2[11]);
  RAM #(.addrWidth(24), .dataWidth(32), .bus("separate")) ram_93 (
    .addr(multiplexer_107_out), .din(Data_in_to_Ram_0_31), .data(ram_93_data), .str(decoder_4_out2[11]),
    .sel(Power), .clk(not_3_out), .ld(not_97_out), .clr(or_1_out[1]));
  not not_97 (not_97_out, decoder_4_out2[11]);
  RAM #(.addrWidth(24), .dataWidth(32), .bus("separate")) ram_94 (
    .addr(multiplexer_108_out), .din(Data_in_to_Ram_32_63), .data(ram_94_data), .str(decoder_4_out2[11]),
    .sel(Power), .clk(not_3_out), .ld(not_98_out), .clr(or_1_out[1]));
  not not_98 (not_98_out, decoder_4_out2[11]);
  RAM #(.addrWidth(24), .dataWidth(32), .bus("separate")) ram_95 (
    .addr(multiplexer_109_out), .din(Data_in_to_Ram_64_95), .data(ram_95_data), .str(decoder_4_out2[11]),
    .sel(Power), .clk(not_3_out), .ld(not_99_out), .clr(or_1_out[1]));
  not not_99 (not_99_out, decoder_4_out2[11]);
  RAM #(.addrWidth(24), .dataWidth(32), .bus("separate")) ram_96 (
    .addr(multiplexer_110_out), .din(Data_in_to_Ram_96_127), .data(ram_96_data), .str(decoder_4_out2[11]),
    .sel(Power), .clk(not_3_out), .ld(not_100_out), .clr(or_1_out[1]));
  not not_100 (not_100_out, decoder_4_out2[11]);
  Register #(.width(1)) register_26 (
    .D(Power), .en(Power), .Q(register_2_q[12]), .clk(decoder_3_out2[12]), .clr(or_1_out[2]));
  Register #(.width(1)) register_27 (
    .D(Power), .en(Power), .Q(register_3_q[12]), .clk(decoder_3_out2[12]), .clr(or_1_out[2]));
  Multiplexer #(.width(24)) multiplexer_111 (
    .in0(counter_1_q), .in1(\Сomand_Number_When_Loading_RAM ), .out(multiplexer_111_out),
    .sel(decoder_2_out2[12]), .en(Power));
  Multiplexer #(.width(24)) multiplexer_112 (
    .in0(counter_1_q), .in1(\Сomand_Number_When_Loading_RAM ), .out(multiplexer_112_out),
    .sel(decoder_2_out2[12]), .en(Power));
  Multiplexer #(.width(24)) multiplexer_113 (
    .in0(counter_1_q), .in1(\Сomand_Number_When_Loading_RAM ), .out(multiplexer_113_out),
    .sel(decoder_2_out2[12]), .en(Power));
  Multiplexer #(.width(24)) multiplexer_114 (
    .in0(counter_1_q), .in1(\Сomand_Number_When_Loading_RAM ), .out(multiplexer_114_out),
    .sel(decoder_2_out2[12]), .en(Power));
  Multiplexer #(.width(24)) multiplexer_115 (
    .in0(counter_1_q), .in1(\Сomand_Number_When_Loading_RAM ), .out(multiplexer_115_out),
    .sel(decoder_4_out2[12]), .en(Power));
  Multiplexer #(.width(24)) multiplexer_116 (
    .in0(counter_1_q), .in1(\Сomand_Number_When_Loading_RAM ), .out(multiplexer_116_out),
    .sel(decoder_4_out2[12]), .en(Power));
  Multiplexer #(.width(24)) multiplexer_117 (
    .in0(counter_1_q), .in1(\Сomand_Number_When_Loading_RAM ), .out(multiplexer_117_out),
    .sel(decoder_4_out2[12]), .en(Power));
  Multiplexer #(.width(24)) multiplexer_118 (
    .in0(counter_1_q), .in1(\Сomand_Number_When_Loading_RAM ), .out(multiplexer_118_out),
    .sel(decoder_4_out2[12]), .en(Power));
  not not_101 (not_101_out, decoder_2_out2[12]);
  not not_102 (not_102_out, decoder_2_out2[12]);
  not not_103 (not_103_out, decoder_2_out2[12]);
  not not_104 (not_104_out, decoder_2_out2[12]);
  not not_105 (not_105_out, decoder_4_out2[12]);
  not not_106 (not_106_out, decoder_4_out2[12]);
  not not_107 (not_107_out, decoder_4_out2[12]);
  not not_108 (not_108_out, decoder_4_out2[12]);
  RAM #(.addrWidth(24), .dataWidth(32), .bus("separate")) ram_97 (
    .addr(multiplexer_111_out), .din(Data_in_to_Ram_0_31), .data(ram_97_data), .str(decoder_2_out2[12]),
    .sel(Power), .clk(Clk), .ld(not_101_out), .clr(or_1_out[2]));
  RAM #(.addrWidth(24), .dataWidth(32), .bus("separate")) ram_98 (
    .addr(multiplexer_112_out), .din(Data_in_to_Ram_32_63), .data(ram_98_data), .str(decoder_2_out2[12]),
    .sel(Power), .clk(Clk), .ld(not_102_out), .clr(or_1_out[2]));
  RAM #(.addrWidth(24), .dataWidth(32), .bus("separate")) ram_99 (
    .addr(multiplexer_113_out), .din(Data_in_to_Ram_64_95), .data(ram_99_data), .str(decoder_2_out2[12]),
    .sel(Power), .clk(Clk), .ld(not_103_out), .clr(or_1_out[2]));
  RAM #(.addrWidth(24), .dataWidth(32), .bus("separate")) ram_100 (
    .addr(multiplexer_114_out), .din(Data_in_to_Ram_96_127), .data(ram_100_data), .str(decoder_2_out2[12]),
    .sel(Power), .clk(Clk), .ld(not_104_out), .clr(or_1_out[2]));
  RAM #(.addrWidth(24), .dataWidth(32), .bus("separate")) ram_101 (
    .addr(multiplexer_115_out), .din(Data_in_to_Ram_0_31), .data(ram_101_data), .str(decoder_4_out2[12]),
    .sel(Power), .clk(not_3_out), .ld(not_105_out), .clr(or_1_out[2]));
  RAM #(.addrWidth(24), .dataWidth(32), .bus("separate")) ram_102 (
    .addr(multiplexer_116_out), .din(Data_in_to_Ram_32_63), .data(ram_102_data), .str(decoder_4_out2[12]),
    .sel(Power), .clk(not_3_out), .ld(not_106_out), .clr(or_1_out[2]));
  RAM #(.addrWidth(24), .dataWidth(32), .bus("separate")) ram_103 (
    .addr(multiplexer_117_out), .din(Data_in_to_Ram_64_95), .data(ram_103_data), .str(decoder_4_out2[12]),
    .sel(Power), .clk(not_3_out), .ld(not_107_out), .clr(or_1_out[2]));
  RAM #(.addrWidth(24), .dataWidth(32), .bus("separate")) ram_104 (
    .addr(multiplexer_118_out), .din(Data_in_to_Ram_96_127), .data(ram_104_data), .str(decoder_4_out2[12]),
    .sel(Power), .clk(not_3_out), .ld(not_108_out), .clr(or_1_out[2]));
  Register #(.width(1)) register_28 (
    .D(Power), .en(Power), .Q(register_2_q[13]), .clk(decoder_3_out2[13]), .clr(or_1_out[3]));
  Register #(.width(1)) register_29 (
    .D(Power), .en(Power), .Q(register_3_q[13]), .clk(decoder_3_out2[13]), .clr(or_1_out[3]));
  Multiplexer #(.width(24)) multiplexer_119 (
    .in0(counter_1_q), .in1(\Сomand_Number_When_Loading_RAM ), .out(multiplexer_119_out),
    .sel(decoder_2_out2[13]), .en(Power));
  Multiplexer #(.width(24)) multiplexer_120 (
    .in0(counter_1_q), .in1(\Сomand_Number_When_Loading_RAM ), .out(multiplexer_120_out),
    .sel(decoder_2_out2[13]), .en(Power));
  Multiplexer #(.width(24)) multiplexer_121 (
    .in0(counter_1_q), .in1(\Сomand_Number_When_Loading_RAM ), .out(multiplexer_121_out),
    .sel(decoder_2_out2[13]), .en(Power));
  Multiplexer #(.width(24)) multiplexer_122 (
    .in0(counter_1_q), .in1(\Сomand_Number_When_Loading_RAM ), .out(multiplexer_122_out),
    .sel(decoder_2_out2[13]), .en(Power));
  Multiplexer #(.width(24)) multiplexer_123 (
    .in0(counter_1_q), .in1(\Сomand_Number_When_Loading_RAM ), .out(multiplexer_123_out),
    .sel(decoder_4_out2[13]), .en(Power));
  Multiplexer #(.width(24)) multiplexer_124 (
    .in0(counter_1_q), .in1(\Сomand_Number_When_Loading_RAM ), .out(multiplexer_124_out),
    .sel(decoder_4_out2[13]), .en(Power));
  Multiplexer #(.width(24)) multiplexer_125 (
    .in0(counter_1_q), .in1(\Сomand_Number_When_Loading_RAM ), .out(multiplexer_125_out),
    .sel(decoder_4_out2[13]), .en(Power));
  Multiplexer #(.width(24)) multiplexer_126 (
    .in0(counter_1_q), .in1(\Сomand_Number_When_Loading_RAM ), .out(multiplexer_126_out),
    .sel(decoder_4_out2[13]), .en(Power));
  not not_109 (not_109_out, decoder_2_out2[13]);
  not not_110 (not_110_out, decoder_2_out2[13]);
  not not_111 (not_111_out, decoder_2_out2[13]);
  not not_112 (not_112_out, decoder_2_out2[13]);
  not not_113 (not_113_out, decoder_4_out2[13]);
  not not_114 (not_114_out, decoder_4_out2[13]);
  not not_115 (not_115_out, decoder_4_out2[13]);
  not not_116 (not_116_out, decoder_4_out2[13]);
  RAM #(.addrWidth(24), .dataWidth(32), .bus("separate")) ram_105 (
    .addr(multiplexer_119_out), .din(Data_in_to_Ram_0_31), .data(ram_105_data), .str(decoder_2_out2[13]),
    .sel(Power), .clk(Clk), .ld(not_109_out), .clr(or_1_out[3]));
  RAM #(.addrWidth(24), .dataWidth(32), .bus("separate")) ram_106 (
    .addr(multiplexer_120_out), .din(Data_in_to_Ram_32_63), .data(ram_106_data), .str(decoder_2_out2[13]),
    .sel(Power), .clk(Clk), .ld(not_110_out), .clr(or_1_out[3]));
  RAM #(.addrWidth(24), .dataWidth(32), .bus("separate")) ram_107 (
    .addr(multiplexer_121_out), .din(Data_in_to_Ram_64_95), .data(ram_107_data), .str(decoder_2_out2[13]),
    .sel(Power), .clk(Clk), .ld(not_111_out), .clr(or_1_out[3]));
  RAM #(.addrWidth(24), .dataWidth(32), .bus("separate")) ram_108 (
    .addr(multiplexer_122_out), .din(Data_in_to_Ram_96_127), .data(ram_108_data), .str(decoder_2_out2[13]),
    .sel(Power), .clk(Clk), .ld(not_112_out), .clr(or_1_out[3]));
  RAM #(.addrWidth(24), .dataWidth(32), .bus("separate")) ram_109 (
    .addr(multiplexer_123_out), .din(Data_in_to_Ram_0_31), .data(ram_109_data), .str(decoder_4_out2[13]),
    .sel(Power), .clk(not_3_out), .ld(not_113_out), .clr(or_1_out[3]));
  RAM #(.addrWidth(24), .dataWidth(32), .bus("separate")) ram_110 (
    .addr(multiplexer_124_out), .din(Data_in_to_Ram_32_63), .data(ram_110_data), .str(decoder_4_out2[13]),
    .sel(Power), .clk(not_3_out), .ld(not_114_out), .clr(or_1_out[3]));
  RAM #(.addrWidth(24), .dataWidth(32), .bus("separate")) ram_111 (
    .addr(multiplexer_125_out), .din(Data_in_to_Ram_64_95), .data(ram_111_data), .str(decoder_4_out2[13]),
    .sel(Power), .clk(not_3_out), .ld(not_115_out), .clr(or_1_out[3]));
  RAM #(.addrWidth(24), .dataWidth(32), .bus("separate")) ram_112 (
    .addr(multiplexer_126_out), .din(Data_in_to_Ram_96_127), .data(ram_112_data), .str(decoder_4_out2[13]),
    .sel(Power), .clk(not_3_out), .ld(not_116_out), .clr(or_1_out[3]));
  Register #(.width(1)) register_30 (
    .D(Power), .en(Power), .Q(register_2_q[14]), .clk(decoder_3_out2[14]), .clr(or_5_out[0]));
  Register #(.width(1)) register_31 (
    .D(Power), .en(Power), .Q(register_3_q[14]), .clk(decoder_3_out2[14]), .clr(or_5_out[0]));
  Multiplexer #(.width(24)) multiplexer_127 (
    .in0(counter_1_q), .in1(\Сomand_Number_When_Loading_RAM ), .out(multiplexer_127_out),
    .sel(decoder_2_out2[14]), .en(Power));
  Multiplexer #(.width(24)) multiplexer_128 (
    .in0(counter_1_q), .in1(\Сomand_Number_When_Loading_RAM ), .out(multiplexer_128_out),
    .sel(decoder_2_out2[14]), .en(Power));
  Multiplexer #(.width(24)) multiplexer_129 (
    .in0(counter_1_q), .in1(\Сomand_Number_When_Loading_RAM ), .out(multiplexer_129_out),
    .sel(decoder_2_out2[14]), .en(Power));
  Multiplexer #(.width(24)) multiplexer_130 (
    .in0(counter_1_q), .in1(\Сomand_Number_When_Loading_RAM ), .out(multiplexer_130_out),
    .sel(decoder_2_out2[14]), .en(Power));
  Multiplexer #(.width(24)) multiplexer_131 (
    .in0(counter_1_q), .in1(\Сomand_Number_When_Loading_RAM ), .out(multiplexer_131_out),
    .sel(decoder_4_out2[14]), .en(Power));
  Multiplexer #(.width(24)) multiplexer_132 (
    .in0(counter_1_q), .in1(\Сomand_Number_When_Loading_RAM ), .out(multiplexer_132_out),
    .sel(decoder_4_out2[14]), .en(Power));
  Multiplexer #(.width(24)) multiplexer_133 (
    .in0(counter_1_q), .in1(\Сomand_Number_When_Loading_RAM ), .out(multiplexer_133_out),
    .sel(decoder_4_out2[14]), .en(Power));
  Multiplexer #(.width(24)) multiplexer_134 (
    .in0(counter_1_q), .in1(\Сomand_Number_When_Loading_RAM ), .out(multiplexer_134_out),
    .sel(decoder_4_out2[14]), .en(Power));
  RAM #(.addrWidth(24), .dataWidth(32), .bus("separate")) ram_113 (
    .addr(multiplexer_127_out), .din(Data_in_to_Ram_0_31), .data(ram_113_data), .str(decoder_2_out2[14]),
    .sel(Power), .clk(Clk), .ld(not_117_out), .clr(or_5_out[0]));
  not not_117 (not_117_out, decoder_2_out2[14]);
  RAM #(.addrWidth(24), .dataWidth(32), .bus("separate")) ram_114 (
    .addr(multiplexer_128_out), .din(Data_in_to_Ram_32_63), .data(ram_114_data), .str(decoder_2_out2[14]),
    .sel(Power), .clk(Clk), .ld(not_118_out), .clr(or_5_out[0]));
  not not_118 (not_118_out, decoder_2_out2[14]);
  RAM #(.addrWidth(24), .dataWidth(32), .bus("separate")) ram_115 (
    .addr(multiplexer_129_out), .din(Data_in_to_Ram_64_95), .data(ram_115_data), .str(decoder_2_out2[14]),
    .sel(Power), .clk(Clk), .ld(not_119_out), .clr(or_5_out[0]));
  not not_119 (not_119_out, decoder_2_out2[14]);
  RAM #(.addrWidth(24), .dataWidth(32), .bus("separate")) ram_116 (
    .addr(multiplexer_130_out), .din(Data_in_to_Ram_96_127), .data(ram_116_data), .str(decoder_2_out2[14]),
    .sel(Power), .clk(Clk), .ld(not_120_out), .clr(or_5_out[0]));
  not not_120 (not_120_out, decoder_2_out2[14]);
  RAM #(.addrWidth(24), .dataWidth(32), .bus("separate")) ram_117 (
    .addr(multiplexer_131_out), .din(Data_in_to_Ram_0_31), .data(ram_117_data), .str(decoder_4_out2[14]),
    .sel(Power), .clk(not_3_out), .ld(not_121_out), .clr(or_5_out[0]));
  not not_121 (not_121_out, decoder_4_out2[14]);
  RAM #(.addrWidth(24), .dataWidth(32), .bus("separate")) ram_118 (
    .addr(multiplexer_132_out), .din(Data_in_to_Ram_32_63), .data(ram_118_data), .str(decoder_4_out2[14]),
    .sel(Power), .clk(not_3_out), .ld(not_122_out), .clr(or_5_out[0]));
  not not_122 (not_122_out, decoder_4_out2[14]);
  RAM #(.addrWidth(24), .dataWidth(32), .bus("separate")) ram_119 (
    .addr(multiplexer_133_out), .din(Data_in_to_Ram_64_95), .data(ram_119_data), .str(decoder_4_out2[14]),
    .sel(Power), .clk(not_3_out), .ld(not_123_out), .clr(or_5_out[0]));
  not not_123 (not_123_out, decoder_4_out2[14]);
  RAM #(.addrWidth(24), .dataWidth(32), .bus("separate")) ram_120 (
    .addr(multiplexer_134_out), .din(Data_in_to_Ram_96_127), .data(ram_120_data), .str(decoder_4_out2[14]),
    .sel(Power), .clk(not_3_out), .ld(not_124_out), .clr(or_5_out[0]));
  not not_124 (not_124_out, decoder_4_out2[14]);
  Register #(.width(1)) register_32 (
    .D(Power), .en(Power), .Q(register_2_q[15]), .clk(decoder_3_out2[15]), .clr(or_5_out[1]));
  Register #(.width(1)) register_33 (
    .D(Power), .en(Power), .Q(register_3_q[15]), .clk(decoder_3_out2[15]), .clr(or_5_out[1]));
  Multiplexer #(.width(24)) multiplexer_135 (
    .in0(counter_1_q), .in1(\Сomand_Number_When_Loading_RAM ), .out(multiplexer_135_out),
    .sel(decoder_2_out2[15]), .en(Power));
  Multiplexer #(.width(24)) multiplexer_136 (
    .in0(counter_1_q), .in1(\Сomand_Number_When_Loading_RAM ), .out(multiplexer_136_out),
    .sel(decoder_2_out2[15]), .en(Power));
  Multiplexer #(.width(24)) multiplexer_137 (
    .in0(counter_1_q), .in1(\Сomand_Number_When_Loading_RAM ), .out(multiplexer_137_out),
    .sel(decoder_2_out2[15]), .en(Power));
  Multiplexer #(.width(24)) multiplexer_138 (
    .in0(counter_1_q), .in1(\Сomand_Number_When_Loading_RAM ), .out(multiplexer_138_out),
    .sel(decoder_2_out2[15]), .en(Power));
  Multiplexer #(.width(24)) multiplexer_139 (
    .in0(counter_1_q), .in1(\Сomand_Number_When_Loading_RAM ), .out(multiplexer_139_out),
    .sel(decoder_4_out2[15]), .en(Power));
  Multiplexer #(.width(24)) multiplexer_140 (
    .in0(counter_1_q), .in1(\Сomand_Number_When_Loading_RAM ), .out(multiplexer_140_out),
    .sel(decoder_4_out2[15]), .en(Power));
  Multiplexer #(.width(24)) multiplexer_141 (
    .in0(counter_1_q), .in1(\Сomand_Number_When_Loading_RAM ), .out(multiplexer_141_out),
    .sel(decoder_4_out2[15]), .en(Power));
  Multiplexer #(.width(24)) multiplexer_142 (
    .in0(counter_1_q), .in1(\Сomand_Number_When_Loading_RAM ), .out(multiplexer_142_out),
    .sel(decoder_4_out2[15]), .en(Power));
  RAM #(.addrWidth(24), .dataWidth(32), .bus("separate")) ram_121 (
    .addr(multiplexer_135_out), .din(Data_in_to_Ram_0_31), .data(ram_121_data), .str(decoder_2_out2[15]),
    .sel(Power), .clk(Clk), .ld(not_125_out), .clr(or_5_out[1]));
  not not_125 (not_125_out, decoder_2_out2[15]);
  RAM #(.addrWidth(24), .dataWidth(32), .bus("separate")) ram_122 (
    .addr(multiplexer_136_out), .din(Data_in_to_Ram_32_63), .data(ram_122_data), .str(decoder_2_out2[15]),
    .sel(Power), .clk(Clk), .ld(not_126_out), .clr(or_5_out[1]));
  not not_126 (not_126_out, decoder_2_out2[15]);
  RAM #(.addrWidth(24), .dataWidth(32), .bus("separate")) ram_123 (
    .addr(multiplexer_137_out), .din(Data_in_to_Ram_64_95), .data(ram_123_data), .str(decoder_2_out2[15]),
    .sel(Power), .clk(Clk), .ld(not_127_out), .clr(or_5_out[1]));
  not not_127 (not_127_out, decoder_2_out2[15]);
  RAM #(.addrWidth(24), .dataWidth(32), .bus("separate")) ram_124 (
    .addr(multiplexer_138_out), .din(Data_in_to_Ram_96_127), .data(ram_124_data), .str(decoder_2_out2[15]),
    .sel(Power), .clk(Clk), .ld(not_128_out), .clr(or_5_out[1]));
  not not_128 (not_128_out, decoder_2_out2[15]);
  RAM #(.addrWidth(24), .dataWidth(32), .bus("separate")) ram_125 (
    .addr(multiplexer_139_out), .din(Data_in_to_Ram_0_31), .data(ram_125_data), .str(decoder_4_out2[15]),
    .sel(Power), .clk(not_3_out), .ld(not_129_out), .clr(or_5_out[1]));
  not not_129 (not_129_out, decoder_4_out2[15]);
  RAM #(.addrWidth(24), .dataWidth(32), .bus("separate")) ram_126 (
    .addr(multiplexer_140_out), .din(Data_in_to_Ram_32_63), .data(ram_126_data), .str(decoder_4_out2[15]),
    .sel(Power), .clk(not_3_out), .ld(not_130_out), .clr(or_5_out[1]));
  not not_130 (not_130_out, decoder_4_out2[15]);
  RAM #(.addrWidth(24), .dataWidth(32), .bus("separate")) ram_127 (
    .addr(multiplexer_141_out), .din(Data_in_to_Ram_64_95), .data(ram_127_data), .str(decoder_4_out2[15]),
    .sel(Power), .clk(not_3_out), .ld(not_131_out), .clr(or_5_out[1]));
  not not_131 (not_131_out, decoder_4_out2[15]);
  RAM #(.addrWidth(24), .dataWidth(32), .bus("separate")) ram_128 (
    .addr(multiplexer_142_out), .din(Data_in_to_Ram_96_127), .data(ram_128_data), .str(decoder_4_out2[15]),
    .sel(Power), .clk(not_3_out), .ld(not_132_out), .clr(or_5_out[1]));
  not not_132 (not_132_out, decoder_4_out2[15]);
  Register #(.width(1)) register_34 (
    .D(Power), .en(Power), .Q(register_34_q[0]), .clk(decoder_3_out2[16]), .clr(or_7_out[0]));
  Register #(.width(1)) register_35 (
    .D(Power), .en(Power), .Q(register_35_q[0]), .clk(decoder_3_out2[16]), .clr(or_7_out[0]));
  Multiplexer #(.width(24)) multiplexer_143 (
    .in0(counter_1_q), .in1(\Сomand_Number_When_Loading_RAM ), .out(multiplexer_143_out),
    .sel(decoder_2_out18[0]), .en(Power));
  Multiplexer #(.width(24)) multiplexer_144 (
    .in0(counter_1_q), .in1(\Сomand_Number_When_Loading_RAM ), .out(multiplexer_144_out),
    .sel(decoder_2_out18[0]), .en(Power));
  Multiplexer #(.width(24)) multiplexer_145 (
    .in0(counter_1_q), .in1(\Сomand_Number_When_Loading_RAM ), .out(multiplexer_145_out),
    .sel(decoder_2_out18[0]), .en(Power));
  Multiplexer #(.width(24)) multiplexer_146 (
    .in0(counter_1_q), .in1(\Сomand_Number_When_Loading_RAM ), .out(multiplexer_146_out),
    .sel(decoder_2_out18[0]), .en(Power));
  Multiplexer #(.width(24)) multiplexer_147 (
    .in0(counter_1_q), .in1(\Сomand_Number_When_Loading_RAM ), .out(multiplexer_147_out),
    .sel(decoder_4_out18[0]), .en(Power));
  Multiplexer #(.width(24)) multiplexer_148 (
    .in0(counter_1_q), .in1(\Сomand_Number_When_Loading_RAM ), .out(multiplexer_148_out),
    .sel(decoder_4_out18[0]), .en(Power));
  Multiplexer #(.width(24)) multiplexer_149 (
    .in0(counter_1_q), .in1(\Сomand_Number_When_Loading_RAM ), .out(multiplexer_149_out),
    .sel(decoder_4_out18[0]), .en(Power));
  Multiplexer #(.width(24)) multiplexer_150 (
    .in0(counter_1_q), .in1(\Сomand_Number_When_Loading_RAM ), .out(multiplexer_150_out),
    .sel(decoder_4_out18[0]), .en(Power));
  not not_133 (not_133_out, decoder_2_out18[0]);
  not not_134 (not_134_out, decoder_2_out18[0]);
  not not_135 (not_135_out, decoder_2_out18[0]);
  not not_136 (not_136_out, decoder_2_out18[0]);
  not not_137 (not_137_out, decoder_4_out18[0]);
  not not_138 (not_138_out, decoder_4_out18[0]);
  not not_139 (not_139_out, decoder_4_out18[0]);
  not not_140 (not_140_out, decoder_4_out18[0]);
  RAM #(.addrWidth(24), .dataWidth(32), .bus("separate")) ram_129 (
    .addr(multiplexer_143_out), .din(Data_in_to_Ram_0_31), .data(ram_129_data), .str(decoder_2_out18[0]),
    .sel(Power), .clk(Clk), .ld(not_133_out), .clr(or_7_out[0]));
  RAM #(.addrWidth(24), .dataWidth(32), .bus("separate")) ram_130 (
    .addr(multiplexer_144_out), .din(Data_in_to_Ram_32_63), .data(ram_130_data), .str(decoder_2_out18[0]),
    .sel(Power), .clk(Clk), .ld(not_134_out), .clr(or_7_out[0]));
  RAM #(.addrWidth(24), .dataWidth(32), .bus("separate")) ram_131 (
    .addr(multiplexer_145_out), .din(Data_in_to_Ram_64_95), .data(ram_131_data), .str(decoder_2_out18[0]),
    .sel(Power), .clk(Clk), .ld(not_135_out), .clr(or_7_out[0]));
  RAM #(.addrWidth(24), .dataWidth(32), .bus("separate")) ram_132 (
    .addr(multiplexer_146_out), .din(Data_in_to_Ram_96_127), .data(ram_132_data), .str(decoder_2_out18[0]),
    .sel(Power), .clk(Clk), .ld(not_136_out), .clr(or_7_out[0]));
  RAM #(.addrWidth(24), .dataWidth(32), .bus("separate")) ram_133 (
    .addr(multiplexer_147_out), .din(Data_in_to_Ram_0_31), .data(ram_133_data), .str(decoder_4_out18[0]),
    .sel(Power), .clk(not_3_out), .ld(not_137_out), .clr(or_7_out[0]));
  RAM #(.addrWidth(24), .dataWidth(32), .bus("separate")) ram_134 (
    .addr(multiplexer_148_out), .din(Data_in_to_Ram_32_63), .data(ram_134_data), .str(decoder_4_out18[0]),
    .sel(Power), .clk(not_3_out), .ld(not_138_out), .clr(or_7_out[0]));
  RAM #(.addrWidth(24), .dataWidth(32), .bus("separate")) ram_135 (
    .addr(multiplexer_149_out), .din(Data_in_to_Ram_64_95), .data(ram_135_data), .str(decoder_4_out18[0]),
    .sel(Power), .clk(not_3_out), .ld(not_139_out), .clr(or_7_out[0]));
  RAM #(.addrWidth(24), .dataWidth(32), .bus("separate")) ram_136 (
    .addr(multiplexer_150_out), .din(Data_in_to_Ram_96_127), .data(ram_136_data), .str(decoder_4_out18[0]),
    .sel(Power), .clk(not_3_out), .ld(not_140_out), .clr(or_7_out[0]));
  Register #(.width(1)) register_36 (
    .D(Power), .en(Power), .Q(register_34_q[1]), .clk(decoder_3_out19[0]), .clr(or_7_out[1]));
  Register #(.width(1)) register_37 (
    .D(Power), .en(Power), .Q(register_35_q[1]), .clk(decoder_3_out19[0]), .clr(or_7_out[1]));
  Multiplexer #(.width(24)) multiplexer_151 (
    .in0(counter_1_q), .in1(\Сomand_Number_When_Loading_RAM ), .out(multiplexer_151_out),
    .sel(decoder_2_out18[1]), .en(Power));
  Multiplexer #(.width(24)) multiplexer_152 (
    .in0(counter_1_q), .in1(\Сomand_Number_When_Loading_RAM ), .out(multiplexer_152_out),
    .sel(decoder_2_out18[1]), .en(Power));
  Multiplexer #(.width(24)) multiplexer_153 (
    .in0(counter_1_q), .in1(\Сomand_Number_When_Loading_RAM ), .out(multiplexer_153_out),
    .sel(decoder_2_out18[1]), .en(Power));
  Multiplexer #(.width(24)) multiplexer_154 (
    .in0(counter_1_q), .in1(\Сomand_Number_When_Loading_RAM ), .out(multiplexer_154_out),
    .sel(decoder_2_out18[1]), .en(Power));
  Multiplexer #(.width(24)) multiplexer_155 (
    .in0(counter_1_q), .in1(\Сomand_Number_When_Loading_RAM ), .out(multiplexer_155_out),
    .sel(decoder_4_out18[1]), .en(Power));
  Multiplexer #(.width(24)) multiplexer_156 (
    .in0(counter_1_q), .in1(\Сomand_Number_When_Loading_RAM ), .out(multiplexer_156_out),
    .sel(decoder_4_out18[1]), .en(Power));
  Multiplexer #(.width(24)) multiplexer_157 (
    .in0(counter_1_q), .in1(\Сomand_Number_When_Loading_RAM ), .out(multiplexer_157_out),
    .sel(decoder_4_out18[1]), .en(Power));
  Multiplexer #(.width(24)) multiplexer_158 (
    .in0(counter_1_q), .in1(\Сomand_Number_When_Loading_RAM ), .out(multiplexer_158_out),
    .sel(decoder_4_out18[1]), .en(Power));
  not not_141 (not_141_out, decoder_2_out18[1]);
  not not_142 (not_142_out, decoder_2_out18[1]);
  not not_143 (not_143_out, decoder_2_out18[1]);
  not not_144 (not_144_out, decoder_2_out18[1]);
  not not_145 (not_145_out, decoder_4_out18[1]);
  not not_146 (not_146_out, decoder_4_out18[1]);
  not not_147 (not_147_out, decoder_4_out18[1]);
  not not_148 (not_148_out, decoder_4_out18[1]);
  RAM #(.addrWidth(24), .dataWidth(32), .bus("separate")) ram_137 (
    .addr(multiplexer_151_out), .din(Data_in_to_Ram_0_31), .data(ram_137_data), .str(decoder_2_out18[1]),
    .sel(Power), .clk(Clk), .ld(not_141_out), .clr(or_7_out[1]));
  RAM #(.addrWidth(24), .dataWidth(32), .bus("separate")) ram_138 (
    .addr(multiplexer_152_out), .din(Data_in_to_Ram_32_63), .data(ram_138_data), .str(decoder_2_out18[1]),
    .sel(Power), .clk(Clk), .ld(not_142_out), .clr(or_7_out[1]));
  RAM #(.addrWidth(24), .dataWidth(32), .bus("separate")) ram_139 (
    .addr(multiplexer_153_out), .din(Data_in_to_Ram_64_95), .data(ram_139_data), .str(decoder_2_out18[1]),
    .sel(Power), .clk(Clk), .ld(not_143_out), .clr(or_7_out[1]));
  RAM #(.addrWidth(24), .dataWidth(32), .bus("separate")) ram_140 (
    .addr(multiplexer_154_out), .din(Data_in_to_Ram_96_127), .data(ram_140_data), .str(decoder_2_out18[1]),
    .sel(Power), .clk(Clk), .ld(not_144_out), .clr(or_7_out[1]));
  RAM #(.addrWidth(24), .dataWidth(32), .bus("separate")) ram_141 (
    .addr(multiplexer_155_out), .din(Data_in_to_Ram_0_31), .data(ram_141_data), .str(decoder_4_out18[1]),
    .sel(Power), .clk(not_3_out), .ld(not_145_out), .clr(or_7_out[1]));
  RAM #(.addrWidth(24), .dataWidth(32), .bus("separate")) ram_142 (
    .addr(multiplexer_156_out), .din(Data_in_to_Ram_32_63), .data(ram_142_data), .str(decoder_4_out18[1]),
    .sel(Power), .clk(not_3_out), .ld(not_146_out), .clr(or_7_out[1]));
  RAM #(.addrWidth(24), .dataWidth(32), .bus("separate")) ram_143 (
    .addr(multiplexer_157_out), .din(Data_in_to_Ram_64_95), .data(ram_143_data), .str(decoder_4_out18[1]),
    .sel(Power), .clk(not_3_out), .ld(not_147_out), .clr(or_7_out[1]));
  RAM #(.addrWidth(24), .dataWidth(32), .bus("separate")) ram_144 (
    .addr(multiplexer_158_out), .din(Data_in_to_Ram_96_127), .data(ram_144_data), .str(decoder_4_out18[1]),
    .sel(Power), .clk(not_3_out), .ld(not_148_out), .clr(or_7_out[1]));
  Register #(.width(1)) register_38 (
    .D(Power), .en(Power), .Q(register_34_q[2]), .clk(decoder_3_out19[1]), .clr(or_7_out[2]));
  Register #(.width(1)) register_39 (
    .D(Power), .en(Power), .Q(register_35_q[2]), .clk(decoder_3_out19[1]), .clr(or_7_out[2]));
  Multiplexer #(.width(24)) multiplexer_159 (
    .in0(counter_1_q), .in1(\Сomand_Number_When_Loading_RAM ), .out(multiplexer_159_out),
    .sel(decoder_2_out18[2]), .en(Power));
  Multiplexer #(.width(24)) multiplexer_160 (
    .in0(counter_1_q), .in1(\Сomand_Number_When_Loading_RAM ), .out(multiplexer_160_out),
    .sel(decoder_2_out18[2]), .en(Power));
  Multiplexer #(.width(24)) multiplexer_161 (
    .in0(counter_1_q), .in1(\Сomand_Number_When_Loading_RAM ), .out(multiplexer_161_out),
    .sel(decoder_2_out18[2]), .en(Power));
  Multiplexer #(.width(24)) multiplexer_162 (
    .in0(counter_1_q), .in1(\Сomand_Number_When_Loading_RAM ), .out(multiplexer_162_out),
    .sel(decoder_2_out18[2]), .en(Power));
  Multiplexer #(.width(24)) multiplexer_163 (
    .in0(counter_1_q), .in1(\Сomand_Number_When_Loading_RAM ), .out(multiplexer_163_out),
    .sel(decoder_4_out18[2]), .en(Power));
  Multiplexer #(.width(24)) multiplexer_164 (
    .in0(counter_1_q), .in1(\Сomand_Number_When_Loading_RAM ), .out(multiplexer_164_out),
    .sel(decoder_4_out18[2]), .en(Power));
  Multiplexer #(.width(24)) multiplexer_165 (
    .in0(counter_1_q), .in1(\Сomand_Number_When_Loading_RAM ), .out(multiplexer_165_out),
    .sel(decoder_4_out18[2]), .en(Power));
  Multiplexer #(.width(24)) multiplexer_166 (
    .in0(counter_1_q), .in1(\Сomand_Number_When_Loading_RAM ), .out(multiplexer_166_out),
    .sel(decoder_4_out18[2]), .en(Power));
  RAM #(.addrWidth(24), .dataWidth(32), .bus("separate")) ram_145 (
    .addr(multiplexer_159_out), .din(Data_in_to_Ram_0_31), .data(ram_145_data), .str(decoder_2_out18[2]),
    .sel(Power), .clk(Clk), .ld(not_149_out), .clr(or_7_out[2]));
  not not_149 (not_149_out, decoder_2_out18[2]);
  RAM #(.addrWidth(24), .dataWidth(32), .bus("separate")) ram_146 (
    .addr(multiplexer_160_out), .din(Data_in_to_Ram_32_63), .data(ram_146_data), .str(decoder_2_out18[2]),
    .sel(Power), .clk(Clk), .ld(not_150_out), .clr(or_7_out[2]));
  not not_150 (not_150_out, decoder_2_out18[2]);
  RAM #(.addrWidth(24), .dataWidth(32), .bus("separate")) ram_147 (
    .addr(multiplexer_161_out), .din(Data_in_to_Ram_64_95), .data(ram_147_data), .str(decoder_2_out18[2]),
    .sel(Power), .clk(Clk), .ld(not_151_out), .clr(or_7_out[2]));
  not not_151 (not_151_out, decoder_2_out18[2]);
  RAM #(.addrWidth(24), .dataWidth(32), .bus("separate")) ram_148 (
    .addr(multiplexer_162_out), .din(Data_in_to_Ram_96_127), .data(ram_148_data), .str(decoder_2_out18[2]),
    .sel(Power), .clk(Clk), .ld(not_152_out), .clr(or_7_out[2]));
  not not_152 (not_152_out, decoder_2_out18[2]);
  RAM #(.addrWidth(24), .dataWidth(32), .bus("separate")) ram_149 (
    .addr(multiplexer_163_out), .din(Data_in_to_Ram_0_31), .data(ram_149_data), .str(decoder_4_out18[2]),
    .sel(Power), .clk(not_3_out), .ld(not_153_out), .clr(or_7_out[2]));
  not not_153 (not_153_out, decoder_4_out18[2]);
  RAM #(.addrWidth(24), .dataWidth(32), .bus("separate")) ram_150 (
    .addr(multiplexer_164_out), .din(Data_in_to_Ram_32_63), .data(ram_150_data), .str(decoder_4_out18[2]),
    .sel(Power), .clk(not_3_out), .ld(not_154_out), .clr(or_7_out[2]));
  not not_154 (not_154_out, decoder_4_out18[2]);
  RAM #(.addrWidth(24), .dataWidth(32), .bus("separate")) ram_151 (
    .addr(multiplexer_165_out), .din(Data_in_to_Ram_64_95), .data(ram_151_data), .str(decoder_4_out18[2]),
    .sel(Power), .clk(not_3_out), .ld(not_155_out), .clr(or_7_out[2]));
  not not_155 (not_155_out, decoder_4_out18[2]);
  RAM #(.addrWidth(24), .dataWidth(32), .bus("separate")) ram_152 (
    .addr(multiplexer_166_out), .din(Data_in_to_Ram_96_127), .data(ram_152_data), .str(decoder_4_out18[2]),
    .sel(Power), .clk(not_3_out), .ld(not_156_out), .clr(or_7_out[2]));
  not not_156 (not_156_out, decoder_4_out18[2]);
  Register #(.width(1)) register_40 (
    .D(Power), .en(Power), .Q(register_34_q[3]), .clk(decoder_3_out19[2]), .clr(or_7_out[3]));
  Register #(.width(1)) register_41 (
    .D(Power), .en(Power), .Q(register_35_q[3]), .clk(decoder_3_out19[2]), .clr(or_7_out[3]));
  Multiplexer #(.width(24)) multiplexer_167 (
    .in0(counter_1_q), .in1(\Сomand_Number_When_Loading_RAM ), .out(multiplexer_167_out),
    .sel(decoder_2_out18[3]), .en(Power));
  Multiplexer #(.width(24)) multiplexer_168 (
    .in0(counter_1_q), .in1(\Сomand_Number_When_Loading_RAM ), .out(multiplexer_168_out),
    .sel(decoder_2_out18[3]), .en(Power));
  Multiplexer #(.width(24)) multiplexer_169 (
    .in0(counter_1_q), .in1(\Сomand_Number_When_Loading_RAM ), .out(multiplexer_169_out),
    .sel(decoder_2_out18[3]), .en(Power));
  Multiplexer #(.width(24)) multiplexer_170 (
    .in0(counter_1_q), .in1(\Сomand_Number_When_Loading_RAM ), .out(multiplexer_170_out),
    .sel(decoder_2_out18[3]), .en(Power));
  Multiplexer #(.width(24)) multiplexer_171 (
    .in0(counter_1_q), .in1(\Сomand_Number_When_Loading_RAM ), .out(multiplexer_171_out),
    .sel(decoder_4_out18[3]), .en(Power));
  Multiplexer #(.width(24)) multiplexer_172 (
    .in0(counter_1_q), .in1(\Сomand_Number_When_Loading_RAM ), .out(multiplexer_172_out),
    .sel(decoder_4_out18[3]), .en(Power));
  Multiplexer #(.width(24)) multiplexer_173 (
    .in0(counter_1_q), .in1(\Сomand_Number_When_Loading_RAM ), .out(multiplexer_173_out),
    .sel(decoder_4_out18[3]), .en(Power));
  Multiplexer #(.width(24)) multiplexer_174 (
    .in0(counter_1_q), .in1(\Сomand_Number_When_Loading_RAM ), .out(multiplexer_174_out),
    .sel(decoder_4_out18[3]), .en(Power));
  RAM #(.addrWidth(24), .dataWidth(32), .bus("separate")) ram_153 (
    .addr(multiplexer_167_out), .din(Data_in_to_Ram_0_31), .data(ram_153_data), .str(decoder_2_out18[3]),
    .sel(Power), .clk(Clk), .ld(not_157_out), .clr(or_7_out[3]));
  not not_157 (not_157_out, decoder_2_out18[3]);
  RAM #(.addrWidth(24), .dataWidth(32), .bus("separate")) ram_154 (
    .addr(multiplexer_168_out), .din(Data_in_to_Ram_32_63), .data(ram_154_data), .str(decoder_2_out18[3]),
    .sel(Power), .clk(Clk), .ld(not_158_out), .clr(or_7_out[3]));
  not not_158 (not_158_out, decoder_2_out18[3]);
  RAM #(.addrWidth(24), .dataWidth(32), .bus("separate")) ram_155 (
    .addr(multiplexer_169_out), .din(Data_in_to_Ram_64_95), .data(ram_155_data), .str(decoder_2_out18[3]),
    .sel(Power), .clk(Clk), .ld(not_159_out), .clr(or_7_out[3]));
  not not_159 (not_159_out, decoder_2_out18[3]);
  RAM #(.addrWidth(24), .dataWidth(32), .bus("separate")) ram_156 (
    .addr(multiplexer_170_out), .din(Data_in_to_Ram_96_127), .data(ram_156_data), .str(decoder_2_out18[3]),
    .sel(Power), .clk(Clk), .ld(not_160_out), .clr(or_7_out[3]));
  not not_160 (not_160_out, decoder_2_out18[3]);
  RAM #(.addrWidth(24), .dataWidth(32), .bus("separate")) ram_157 (
    .addr(multiplexer_171_out), .din(Data_in_to_Ram_0_31), .data(ram_157_data), .str(decoder_4_out18[3]),
    .sel(Power), .clk(not_3_out), .ld(not_161_out), .clr(or_7_out[3]));
  not not_161 (not_161_out, decoder_4_out18[3]);
  RAM #(.addrWidth(24), .dataWidth(32), .bus("separate")) ram_158 (
    .addr(multiplexer_172_out), .din(Data_in_to_Ram_32_63), .data(ram_158_data), .str(decoder_4_out18[3]),
    .sel(Power), .clk(not_3_out), .ld(not_162_out), .clr(or_7_out[3]));
  not not_162 (not_162_out, decoder_4_out18[3]);
  RAM #(.addrWidth(24), .dataWidth(32), .bus("separate")) ram_159 (
    .addr(multiplexer_173_out), .din(Data_in_to_Ram_64_95), .data(ram_159_data), .str(decoder_4_out18[3]),
    .sel(Power), .clk(not_3_out), .ld(not_163_out), .clr(or_7_out[3]));
  not not_163 (not_163_out, decoder_4_out18[3]);
  RAM #(.addrWidth(24), .dataWidth(32), .bus("separate")) ram_160 (
    .addr(multiplexer_174_out), .din(Data_in_to_Ram_96_127), .data(ram_160_data), .str(decoder_4_out18[3]),
    .sel(Power), .clk(not_3_out), .ld(not_164_out), .clr(or_7_out[3]));
  not not_164 (not_164_out, decoder_4_out18[3]);
  Register #(.width(1)) register_42 (
    .D(Power), .en(Power), .Q(register_34_q[4]), .clk(decoder_3_out19[3]), .clr(or_7_out[4]));
  Register #(.width(1)) register_43 (
    .D(Power), .en(Power), .Q(register_35_q[4]), .clk(decoder_3_out19[3]), .clr(or_7_out[4]));
  Multiplexer #(.width(24)) multiplexer_175 (
    .in0(counter_1_q), .in1(\Сomand_Number_When_Loading_RAM ), .out(multiplexer_175_out),
    .sel(decoder_2_out18[4]), .en(Power));
  Multiplexer #(.width(24)) multiplexer_176 (
    .in0(counter_1_q), .in1(\Сomand_Number_When_Loading_RAM ), .out(multiplexer_176_out),
    .sel(decoder_2_out18[4]), .en(Power));
  Multiplexer #(.width(24)) multiplexer_177 (
    .in0(counter_1_q), .in1(\Сomand_Number_When_Loading_RAM ), .out(multiplexer_177_out),
    .sel(decoder_2_out18[4]), .en(Power));
  Multiplexer #(.width(24)) multiplexer_178 (
    .in0(counter_1_q), .in1(\Сomand_Number_When_Loading_RAM ), .out(multiplexer_178_out),
    .sel(decoder_2_out18[4]), .en(Power));
  Multiplexer #(.width(24)) multiplexer_179 (
    .in0(counter_1_q), .in1(\Сomand_Number_When_Loading_RAM ), .out(multiplexer_179_out),
    .sel(decoder_4_out18[4]), .en(Power));
  Multiplexer #(.width(24)) multiplexer_180 (
    .in0(counter_1_q), .in1(\Сomand_Number_When_Loading_RAM ), .out(multiplexer_180_out),
    .sel(decoder_4_out18[4]), .en(Power));
  Multiplexer #(.width(24)) multiplexer_181 (
    .in0(counter_1_q), .in1(\Сomand_Number_When_Loading_RAM ), .out(multiplexer_181_out),
    .sel(decoder_4_out18[4]), .en(Power));
  Multiplexer #(.width(24)) multiplexer_182 (
    .in0(counter_1_q), .in1(\Сomand_Number_When_Loading_RAM ), .out(multiplexer_182_out),
    .sel(decoder_4_out18[4]), .en(Power));
  not not_165 (not_165_out, decoder_2_out18[4]);
  not not_166 (not_166_out, decoder_2_out18[4]);
  not not_167 (not_167_out, decoder_2_out18[4]);
  not not_168 (not_168_out, decoder_2_out18[4]);
  not not_169 (not_169_out, decoder_4_out18[4]);
  not not_170 (not_170_out, decoder_4_out18[4]);
  not not_171 (not_171_out, decoder_4_out18[4]);
  not not_172 (not_172_out, decoder_4_out18[4]);
  RAM #(.addrWidth(24), .dataWidth(32), .bus("separate")) ram_161 (
    .addr(multiplexer_175_out), .din(Data_in_to_Ram_0_31), .data(ram_161_data), .str(decoder_2_out18[4]),
    .sel(Power), .clk(Clk), .ld(not_165_out), .clr(or_7_out[4]));
  RAM #(.addrWidth(24), .dataWidth(32), .bus("separate")) ram_162 (
    .addr(multiplexer_176_out), .din(Data_in_to_Ram_32_63), .data(ram_162_data), .str(decoder_2_out18[4]),
    .sel(Power), .clk(Clk), .ld(not_166_out), .clr(or_7_out[4]));
  RAM #(.addrWidth(24), .dataWidth(32), .bus("separate")) ram_163 (
    .addr(multiplexer_177_out), .din(Data_in_to_Ram_64_95), .data(ram_163_data), .str(decoder_2_out18[4]),
    .sel(Power), .clk(Clk), .ld(not_167_out), .clr(or_7_out[4]));
  RAM #(.addrWidth(24), .dataWidth(32), .bus("separate")) ram_164 (
    .addr(multiplexer_178_out), .din(Data_in_to_Ram_96_127), .data(ram_164_data), .str(decoder_2_out18[4]),
    .sel(Power), .clk(Clk), .ld(not_168_out), .clr(or_7_out[4]));
  RAM #(.addrWidth(24), .dataWidth(32), .bus("separate")) ram_165 (
    .addr(multiplexer_179_out), .din(Data_in_to_Ram_0_31), .data(ram_165_data), .str(decoder_4_out18[4]),
    .sel(Power), .clk(not_3_out), .ld(not_169_out), .clr(or_7_out[4]));
  RAM #(.addrWidth(24), .dataWidth(32), .bus("separate")) ram_166 (
    .addr(multiplexer_180_out), .din(Data_in_to_Ram_32_63), .data(ram_166_data), .str(decoder_4_out18[4]),
    .sel(Power), .clk(not_3_out), .ld(not_170_out), .clr(or_7_out[4]));
  RAM #(.addrWidth(24), .dataWidth(32), .bus("separate")) ram_167 (
    .addr(multiplexer_181_out), .din(Data_in_to_Ram_64_95), .data(ram_167_data), .str(decoder_4_out18[4]),
    .sel(Power), .clk(not_3_out), .ld(not_171_out), .clr(or_7_out[4]));
  RAM #(.addrWidth(24), .dataWidth(32), .bus("separate")) ram_168 (
    .addr(multiplexer_182_out), .din(Data_in_to_Ram_96_127), .data(ram_168_data), .str(decoder_4_out18[4]),
    .sel(Power), .clk(not_3_out), .ld(not_172_out), .clr(or_7_out[4]));
  Register #(.width(1)) register_44 (
    .D(Power), .en(Power), .Q(register_34_q[5]), .clk(decoder_3_out19[4]), .clr(or_7_out[5]));
  Register #(.width(1)) register_45 (
    .D(Power), .en(Power), .Q(register_35_q[5]), .clk(decoder_3_out19[4]), .clr(or_7_out[5]));
  Multiplexer #(.width(24)) multiplexer_183 (
    .in0(counter_1_q), .in1(\Сomand_Number_When_Loading_RAM ), .out(multiplexer_183_out),
    .sel(decoder_2_out18[5]), .en(Power));
  Multiplexer #(.width(24)) multiplexer_184 (
    .in0(counter_1_q), .in1(\Сomand_Number_When_Loading_RAM ), .out(multiplexer_184_out),
    .sel(decoder_2_out18[5]), .en(Power));
  Multiplexer #(.width(24)) multiplexer_185 (
    .in0(counter_1_q), .in1(\Сomand_Number_When_Loading_RAM ), .out(multiplexer_185_out),
    .sel(decoder_2_out18[5]), .en(Power));
  Multiplexer #(.width(24)) multiplexer_186 (
    .in0(counter_1_q), .in1(\Сomand_Number_When_Loading_RAM ), .out(multiplexer_186_out),
    .sel(decoder_2_out18[5]), .en(Power));
  Multiplexer #(.width(24)) multiplexer_187 (
    .in0(counter_1_q), .in1(\Сomand_Number_When_Loading_RAM ), .out(multiplexer_187_out),
    .sel(decoder_4_out18[5]), .en(Power));
  Multiplexer #(.width(24)) multiplexer_188 (
    .in0(counter_1_q), .in1(\Сomand_Number_When_Loading_RAM ), .out(multiplexer_188_out),
    .sel(decoder_4_out18[5]), .en(Power));
  Multiplexer #(.width(24)) multiplexer_189 (
    .in0(counter_1_q), .in1(\Сomand_Number_When_Loading_RAM ), .out(multiplexer_189_out),
    .sel(decoder_4_out18[5]), .en(Power));
  Multiplexer #(.width(24)) multiplexer_190 (
    .in0(counter_1_q), .in1(\Сomand_Number_When_Loading_RAM ), .out(multiplexer_190_out),
    .sel(decoder_4_out18[5]), .en(Power));
  not not_173 (not_173_out, decoder_2_out18[5]);
  not not_174 (not_174_out, decoder_2_out18[5]);
  not not_175 (not_175_out, decoder_2_out18[5]);
  not not_176 (not_176_out, decoder_2_out18[5]);
  not not_177 (not_177_out, decoder_4_out18[5]);
  not not_178 (not_178_out, decoder_4_out18[5]);
  not not_179 (not_179_out, decoder_4_out18[5]);
  not not_180 (not_180_out, decoder_4_out18[5]);
  RAM #(.addrWidth(24), .dataWidth(32), .bus("separate")) ram_169 (
    .addr(multiplexer_183_out), .din(Data_in_to_Ram_0_31), .data(ram_169_data), .str(decoder_2_out18[5]),
    .sel(Power), .clk(Clk), .ld(not_173_out), .clr(or_7_out[5]));
  RAM #(.addrWidth(24), .dataWidth(32), .bus("separate")) ram_170 (
    .addr(multiplexer_184_out), .din(Data_in_to_Ram_32_63), .data(ram_170_data), .str(decoder_2_out18[5]),
    .sel(Power), .clk(Clk), .ld(not_174_out), .clr(or_7_out[5]));
  RAM #(.addrWidth(24), .dataWidth(32), .bus("separate")) ram_171 (
    .addr(multiplexer_185_out), .din(Data_in_to_Ram_64_95), .data(ram_171_data), .str(decoder_2_out18[5]),
    .sel(Power), .clk(Clk), .ld(not_175_out), .clr(or_7_out[5]));
  RAM #(.addrWidth(24), .dataWidth(32), .bus("separate")) ram_172 (
    .addr(multiplexer_186_out), .din(Data_in_to_Ram_96_127), .data(ram_172_data), .str(decoder_2_out18[5]),
    .sel(Power), .clk(Clk), .ld(not_176_out), .clr(or_7_out[5]));
  RAM #(.addrWidth(24), .dataWidth(32), .bus("separate")) ram_173 (
    .addr(multiplexer_187_out), .din(Data_in_to_Ram_0_31), .data(ram_173_data), .str(decoder_4_out18[5]),
    .sel(Power), .clk(not_3_out), .ld(not_177_out), .clr(or_7_out[5]));
  RAM #(.addrWidth(24), .dataWidth(32), .bus("separate")) ram_174 (
    .addr(multiplexer_188_out), .din(Data_in_to_Ram_32_63), .data(ram_174_data), .str(decoder_4_out18[5]),
    .sel(Power), .clk(not_3_out), .ld(not_178_out), .clr(or_7_out[5]));
  RAM #(.addrWidth(24), .dataWidth(32), .bus("separate")) ram_175 (
    .addr(multiplexer_189_out), .din(Data_in_to_Ram_64_95), .data(ram_175_data), .str(decoder_4_out18[5]),
    .sel(Power), .clk(not_3_out), .ld(not_179_out), .clr(or_7_out[5]));
  RAM #(.addrWidth(24), .dataWidth(32), .bus("separate")) ram_176 (
    .addr(multiplexer_190_out), .din(Data_in_to_Ram_96_127), .data(ram_176_data), .str(decoder_4_out18[5]),
    .sel(Power), .clk(not_3_out), .ld(not_180_out), .clr(or_7_out[5]));
  Register #(.width(1)) register_46 (
    .D(Power), .en(Power), .Q(register_34_q[6]), .clk(decoder_3_out19[5]), .clr(or_7_out[6]));
  Register #(.width(1)) register_47 (
    .D(Power), .en(Power), .Q(register_35_q[6]), .clk(decoder_3_out19[5]), .clr(or_7_out[6]));
  Multiplexer #(.width(24)) multiplexer_191 (
    .in0(counter_1_q), .in1(\Сomand_Number_When_Loading_RAM ), .out(multiplexer_191_out),
    .sel(decoder_2_out18[6]), .en(Power));
  Multiplexer #(.width(24)) multiplexer_192 (
    .in0(counter_1_q), .in1(\Сomand_Number_When_Loading_RAM ), .out(multiplexer_192_out),
    .sel(decoder_2_out18[6]), .en(Power));
  Multiplexer #(.width(24)) multiplexer_193 (
    .in0(counter_1_q), .in1(\Сomand_Number_When_Loading_RAM ), .out(multiplexer_193_out),
    .sel(decoder_2_out18[6]), .en(Power));
  Multiplexer #(.width(24)) multiplexer_194 (
    .in0(counter_1_q), .in1(\Сomand_Number_When_Loading_RAM ), .out(multiplexer_194_out),
    .sel(decoder_2_out18[6]), .en(Power));
  Multiplexer #(.width(24)) multiplexer_195 (
    .in0(counter_1_q), .in1(\Сomand_Number_When_Loading_RAM ), .out(multiplexer_195_out),
    .sel(decoder_4_out18[6]), .en(Power));
  Multiplexer #(.width(24)) multiplexer_196 (
    .in0(counter_1_q), .in1(\Сomand_Number_When_Loading_RAM ), .out(multiplexer_196_out),
    .sel(decoder_4_out18[6]), .en(Power));
  Multiplexer #(.width(24)) multiplexer_197 (
    .in0(counter_1_q), .in1(\Сomand_Number_When_Loading_RAM ), .out(multiplexer_197_out),
    .sel(decoder_4_out18[6]), .en(Power));
  Multiplexer #(.width(24)) multiplexer_198 (
    .in0(counter_1_q), .in1(\Сomand_Number_When_Loading_RAM ), .out(multiplexer_198_out),
    .sel(decoder_4_out18[6]), .en(Power));
  RAM #(.addrWidth(24), .dataWidth(32), .bus("separate")) ram_177 (
    .addr(multiplexer_191_out), .din(Data_in_to_Ram_0_31), .data(ram_177_data), .str(decoder_2_out18[6]),
    .sel(Power), .clk(Clk), .ld(not_181_out), .clr(or_7_out[6]));
  not not_181 (not_181_out, decoder_2_out18[6]);
  RAM #(.addrWidth(24), .dataWidth(32), .bus("separate")) ram_178 (
    .addr(multiplexer_192_out), .din(Data_in_to_Ram_32_63), .data(ram_178_data), .str(decoder_2_out18[6]),
    .sel(Power), .clk(Clk), .ld(not_182_out), .clr(or_7_out[6]));
  not not_182 (not_182_out, decoder_2_out18[6]);
  RAM #(.addrWidth(24), .dataWidth(32), .bus("separate")) ram_179 (
    .addr(multiplexer_193_out), .din(Data_in_to_Ram_64_95), .data(ram_179_data), .str(decoder_2_out18[6]),
    .sel(Power), .clk(Clk), .ld(not_183_out), .clr(or_7_out[6]));
  not not_183 (not_183_out, decoder_2_out18[6]);
  RAM #(.addrWidth(24), .dataWidth(32), .bus("separate")) ram_180 (
    .addr(multiplexer_194_out), .din(Data_in_to_Ram_96_127), .data(ram_180_data), .str(decoder_2_out18[6]),
    .sel(Power), .clk(Clk), .ld(not_184_out), .clr(or_7_out[6]));
  not not_184 (not_184_out, decoder_2_out18[6]);
  RAM #(.addrWidth(24), .dataWidth(32), .bus("separate")) ram_181 (
    .addr(multiplexer_195_out), .din(Data_in_to_Ram_0_31), .data(ram_181_data), .str(decoder_4_out18[6]),
    .sel(Power), .clk(not_3_out), .ld(not_185_out), .clr(or_7_out[6]));
  not not_185 (not_185_out, decoder_4_out18[6]);
  RAM #(.addrWidth(24), .dataWidth(32), .bus("separate")) ram_182 (
    .addr(multiplexer_196_out), .din(Data_in_to_Ram_32_63), .data(ram_182_data), .str(decoder_4_out18[6]),
    .sel(Power), .clk(not_3_out), .ld(not_186_out), .clr(or_7_out[6]));
  not not_186 (not_186_out, decoder_4_out18[6]);
  RAM #(.addrWidth(24), .dataWidth(32), .bus("separate")) ram_183 (
    .addr(multiplexer_197_out), .din(Data_in_to_Ram_64_95), .data(ram_183_data), .str(decoder_4_out18[6]),
    .sel(Power), .clk(not_3_out), .ld(not_187_out), .clr(or_7_out[6]));
  not not_187 (not_187_out, decoder_4_out18[6]);
  RAM #(.addrWidth(24), .dataWidth(32), .bus("separate")) ram_184 (
    .addr(multiplexer_198_out), .din(Data_in_to_Ram_96_127), .data(ram_184_data), .str(decoder_4_out18[6]),
    .sel(Power), .clk(not_3_out), .ld(not_188_out), .clr(or_7_out[6]));
  not not_188 (not_188_out, decoder_4_out18[6]);
  Register #(.width(1)) register_48 (
    .D(Power), .en(Power), .Q(register_34_q[7]), .clk(decoder_3_out19[6]), .clr(or_7_out[7]));
  Register #(.width(1)) register_49 (
    .D(Power), .en(Power), .Q(register_35_q[7]), .clk(decoder_3_out19[6]), .clr(or_7_out[7]));
  Multiplexer #(.width(24)) multiplexer_199 (
    .in0(counter_1_q), .in1(\Сomand_Number_When_Loading_RAM ), .out(multiplexer_199_out),
    .sel(decoder_2_out18[7]), .en(Power));
  Multiplexer #(.width(24)) multiplexer_200 (
    .in0(counter_1_q), .in1(\Сomand_Number_When_Loading_RAM ), .out(multiplexer_200_out),
    .sel(decoder_2_out18[7]), .en(Power));
  Multiplexer #(.width(24)) multiplexer_201 (
    .in0(counter_1_q), .in1(\Сomand_Number_When_Loading_RAM ), .out(multiplexer_201_out),
    .sel(decoder_2_out18[7]), .en(Power));
  Multiplexer #(.width(24)) multiplexer_202 (
    .in0(counter_1_q), .in1(\Сomand_Number_When_Loading_RAM ), .out(multiplexer_202_out),
    .sel(decoder_2_out18[7]), .en(Power));
  Multiplexer #(.width(24)) multiplexer_203 (
    .in0(counter_1_q), .in1(\Сomand_Number_When_Loading_RAM ), .out(multiplexer_203_out),
    .sel(decoder_4_out18[7]), .en(Power));
  Multiplexer #(.width(24)) multiplexer_204 (
    .in0(counter_1_q), .in1(\Сomand_Number_When_Loading_RAM ), .out(multiplexer_204_out),
    .sel(decoder_4_out18[7]), .en(Power));
  Multiplexer #(.width(24)) multiplexer_205 (
    .in0(counter_1_q), .in1(\Сomand_Number_When_Loading_RAM ), .out(multiplexer_205_out),
    .sel(decoder_4_out18[7]), .en(Power));
  Multiplexer #(.width(24)) multiplexer_206 (
    .in0(counter_1_q), .in1(\Сomand_Number_When_Loading_RAM ), .out(multiplexer_206_out),
    .sel(decoder_4_out18[7]), .en(Power));
  RAM #(.addrWidth(24), .dataWidth(32), .bus("separate")) ram_185 (
    .addr(multiplexer_199_out), .din(Data_in_to_Ram_0_31), .data(ram_185_data), .str(decoder_2_out18[7]),
    .sel(Power), .clk(Clk), .ld(not_189_out), .clr(or_7_out[7]));
  not not_189 (not_189_out, decoder_2_out18[7]);
  RAM #(.addrWidth(24), .dataWidth(32), .bus("separate")) ram_186 (
    .addr(multiplexer_200_out), .din(Data_in_to_Ram_32_63), .data(ram_186_data), .str(decoder_2_out18[7]),
    .sel(Power), .clk(Clk), .ld(not_190_out), .clr(or_7_out[7]));
  not not_190 (not_190_out, decoder_2_out18[7]);
  RAM #(.addrWidth(24), .dataWidth(32), .bus("separate")) ram_187 (
    .addr(multiplexer_201_out), .din(Data_in_to_Ram_64_95), .data(ram_187_data), .str(decoder_2_out18[7]),
    .sel(Power), .clk(Clk), .ld(not_191_out), .clr(or_7_out[7]));
  not not_191 (not_191_out, decoder_2_out18[7]);
  RAM #(.addrWidth(24), .dataWidth(32), .bus("separate")) ram_188 (
    .addr(multiplexer_202_out), .din(Data_in_to_Ram_96_127), .data(ram_188_data), .str(decoder_2_out18[7]),
    .sel(Power), .clk(Clk), .ld(not_192_out), .clr(or_7_out[7]));
  not not_192 (not_192_out, decoder_2_out18[7]);
  RAM #(.addrWidth(24), .dataWidth(32), .bus("separate")) ram_189 (
    .addr(multiplexer_203_out), .din(Data_in_to_Ram_0_31), .data(ram_189_data), .str(decoder_4_out18[7]),
    .sel(Power), .clk(not_3_out), .ld(not_193_out), .clr(or_7_out[7]));
  not not_193 (not_193_out, decoder_4_out18[7]);
  RAM #(.addrWidth(24), .dataWidth(32), .bus("separate")) ram_190 (
    .addr(multiplexer_204_out), .din(Data_in_to_Ram_32_63), .data(ram_190_data), .str(decoder_4_out18[7]),
    .sel(Power), .clk(not_3_out), .ld(not_194_out), .clr(or_7_out[7]));
  not not_194 (not_194_out, decoder_4_out18[7]);
  RAM #(.addrWidth(24), .dataWidth(32), .bus("separate")) ram_191 (
    .addr(multiplexer_205_out), .din(Data_in_to_Ram_64_95), .data(ram_191_data), .str(decoder_4_out18[7]),
    .sel(Power), .clk(not_3_out), .ld(not_195_out), .clr(or_7_out[7]));
  not not_195 (not_195_out, decoder_4_out18[7]);
  RAM #(.addrWidth(24), .dataWidth(32), .bus("separate")) ram_192 (
    .addr(multiplexer_206_out), .din(Data_in_to_Ram_96_127), .data(ram_192_data), .str(decoder_4_out18[7]),
    .sel(Power), .clk(not_3_out), .ld(not_196_out), .clr(or_7_out[7]));
  not not_196 (not_196_out, decoder_4_out18[7]);
  Register #(.width(1)) register_50 (
    .D(Power), .en(Power), .Q(register_34_q[8]), .clk(decoder_3_out19[7]), .clr(or_7_out[8]));
  Register #(.width(1)) register_51 (
    .D(Power), .en(Power), .Q(register_35_q[8]), .clk(decoder_3_out19[7]), .clr(or_7_out[8]));
  Multiplexer #(.width(24)) multiplexer_207 (
    .in0(counter_1_q), .in1(\Сomand_Number_When_Loading_RAM ), .out(multiplexer_207_out),
    .sel(decoder_2_out18[8]), .en(Power));
  Multiplexer #(.width(24)) multiplexer_208 (
    .in0(counter_1_q), .in1(\Сomand_Number_When_Loading_RAM ), .out(multiplexer_208_out),
    .sel(decoder_2_out18[8]), .en(Power));
  Multiplexer #(.width(24)) multiplexer_209 (
    .in0(counter_1_q), .in1(\Сomand_Number_When_Loading_RAM ), .out(multiplexer_209_out),
    .sel(decoder_2_out18[8]), .en(Power));
  Multiplexer #(.width(24)) multiplexer_210 (
    .in0(counter_1_q), .in1(\Сomand_Number_When_Loading_RAM ), .out(multiplexer_210_out),
    .sel(decoder_2_out18[8]), .en(Power));
  Multiplexer #(.width(24)) multiplexer_211 (
    .in0(counter_1_q), .in1(\Сomand_Number_When_Loading_RAM ), .out(multiplexer_211_out),
    .sel(decoder_4_out18[8]), .en(Power));
  Multiplexer #(.width(24)) multiplexer_212 (
    .in0(counter_1_q), .in1(\Сomand_Number_When_Loading_RAM ), .out(multiplexer_212_out),
    .sel(decoder_4_out18[8]), .en(Power));
  Multiplexer #(.width(24)) multiplexer_213 (
    .in0(counter_1_q), .in1(\Сomand_Number_When_Loading_RAM ), .out(multiplexer_213_out),
    .sel(decoder_4_out18[8]), .en(Power));
  Multiplexer #(.width(24)) multiplexer_214 (
    .in0(counter_1_q), .in1(\Сomand_Number_When_Loading_RAM ), .out(multiplexer_214_out),
    .sel(decoder_4_out18[8]), .en(Power));
  not not_197 (not_197_out, decoder_2_out18[8]);
  not not_198 (not_198_out, decoder_2_out18[8]);
  not not_199 (not_199_out, decoder_2_out18[8]);
  not not_200 (not_200_out, decoder_2_out18[8]);
  not not_201 (not_201_out, decoder_4_out18[8]);
  not not_202 (not_202_out, decoder_4_out18[8]);
  not not_203 (not_203_out, decoder_4_out18[8]);
  not not_204 (not_204_out, decoder_4_out18[8]);
  RAM #(.addrWidth(24), .dataWidth(32), .bus("separate")) ram_193 (
    .addr(multiplexer_207_out), .din(Data_in_to_Ram_0_31), .data(ram_193_data), .str(decoder_2_out18[8]),
    .sel(Power), .clk(Clk), .ld(not_197_out), .clr(or_7_out[8]));
  RAM #(.addrWidth(24), .dataWidth(32), .bus("separate")) ram_194 (
    .addr(multiplexer_208_out), .din(Data_in_to_Ram_32_63), .data(ram_194_data), .str(decoder_2_out18[8]),
    .sel(Power), .clk(Clk), .ld(not_198_out), .clr(or_7_out[8]));
  RAM #(.addrWidth(24), .dataWidth(32), .bus("separate")) ram_195 (
    .addr(multiplexer_209_out), .din(Data_in_to_Ram_64_95), .data(ram_195_data), .str(decoder_2_out18[8]),
    .sel(Power), .clk(Clk), .ld(not_199_out), .clr(or_7_out[8]));
  RAM #(.addrWidth(24), .dataWidth(32), .bus("separate")) ram_196 (
    .addr(multiplexer_210_out), .din(Data_in_to_Ram_96_127), .data(ram_196_data), .str(decoder_2_out18[8]),
    .sel(Power), .clk(Clk), .ld(not_200_out), .clr(or_7_out[8]));
  RAM #(.addrWidth(24), .dataWidth(32), .bus("separate")) ram_197 (
    .addr(multiplexer_211_out), .din(Data_in_to_Ram_0_31), .data(ram_197_data), .str(decoder_4_out18[8]),
    .sel(Power), .clk(not_3_out), .ld(not_201_out), .clr(or_7_out[8]));
  RAM #(.addrWidth(24), .dataWidth(32), .bus("separate")) ram_198 (
    .addr(multiplexer_212_out), .din(Data_in_to_Ram_32_63), .data(ram_198_data), .str(decoder_4_out18[8]),
    .sel(Power), .clk(not_3_out), .ld(not_202_out), .clr(or_7_out[8]));
  RAM #(.addrWidth(24), .dataWidth(32), .bus("separate")) ram_199 (
    .addr(multiplexer_213_out), .din(Data_in_to_Ram_64_95), .data(ram_199_data), .str(decoder_4_out18[8]),
    .sel(Power), .clk(not_3_out), .ld(not_203_out), .clr(or_7_out[8]));
  RAM #(.addrWidth(24), .dataWidth(32), .bus("separate")) ram_200 (
    .addr(multiplexer_214_out), .din(Data_in_to_Ram_96_127), .data(ram_200_data), .str(decoder_4_out18[8]),
    .sel(Power), .clk(not_3_out), .ld(not_204_out), .clr(or_7_out[8]));
  Register #(.width(1)) register_52 (
    .D(Power), .en(Power), .Q(register_34_q[9]), .clk(decoder_3_out19[8]), .clr(or_7_out[9]));
  Register #(.width(1)) register_53 (
    .D(Power), .en(Power), .Q(register_35_q[9]), .clk(decoder_3_out19[8]), .clr(or_7_out[9]));
  Multiplexer #(.width(24)) multiplexer_215 (
    .in0(counter_1_q), .in1(\Сomand_Number_When_Loading_RAM ), .out(multiplexer_215_out),
    .sel(decoder_2_out18[9]), .en(Power));
  Multiplexer #(.width(24)) multiplexer_216 (
    .in0(counter_1_q), .in1(\Сomand_Number_When_Loading_RAM ), .out(multiplexer_216_out),
    .sel(decoder_2_out18[9]), .en(Power));
  Multiplexer #(.width(24)) multiplexer_217 (
    .in0(counter_1_q), .in1(\Сomand_Number_When_Loading_RAM ), .out(multiplexer_217_out),
    .sel(decoder_2_out18[9]), .en(Power));
  Multiplexer #(.width(24)) multiplexer_218 (
    .in0(counter_1_q), .in1(\Сomand_Number_When_Loading_RAM ), .out(multiplexer_218_out),
    .sel(decoder_2_out18[9]), .en(Power));
  Multiplexer #(.width(24)) multiplexer_219 (
    .in0(counter_1_q), .in1(\Сomand_Number_When_Loading_RAM ), .out(multiplexer_219_out),
    .sel(decoder_4_out18[9]), .en(Power));
  Multiplexer #(.width(24)) multiplexer_220 (
    .in0(counter_1_q), .in1(\Сomand_Number_When_Loading_RAM ), .out(multiplexer_220_out),
    .sel(decoder_4_out18[9]), .en(Power));
  Multiplexer #(.width(24)) multiplexer_221 (
    .in0(counter_1_q), .in1(\Сomand_Number_When_Loading_RAM ), .out(multiplexer_221_out),
    .sel(decoder_4_out18[9]), .en(Power));
  Multiplexer #(.width(24)) multiplexer_222 (
    .in0(counter_1_q), .in1(\Сomand_Number_When_Loading_RAM ), .out(multiplexer_222_out),
    .sel(decoder_4_out18[9]), .en(Power));
  not not_205 (not_205_out, decoder_2_out18[9]);
  not not_206 (not_206_out, decoder_2_out18[9]);
  not not_207 (not_207_out, decoder_2_out18[9]);
  not not_208 (not_208_out, decoder_2_out18[9]);
  not not_209 (not_209_out, decoder_4_out18[9]);
  not not_210 (not_210_out, decoder_4_out18[9]);
  not not_211 (not_211_out, decoder_4_out18[9]);
  not not_212 (not_212_out, decoder_4_out18[9]);
  RAM #(.addrWidth(24), .dataWidth(32), .bus("separate")) ram_201 (
    .addr(multiplexer_215_out), .din(Data_in_to_Ram_0_31), .data(ram_201_data), .str(decoder_2_out18[9]),
    .sel(Power), .clk(Clk), .ld(not_205_out), .clr(or_7_out[9]));
  RAM #(.addrWidth(24), .dataWidth(32), .bus("separate")) ram_202 (
    .addr(multiplexer_216_out), .din(Data_in_to_Ram_32_63), .data(ram_202_data), .str(decoder_2_out18[9]),
    .sel(Power), .clk(Clk), .ld(not_206_out), .clr(or_7_out[9]));
  RAM #(.addrWidth(24), .dataWidth(32), .bus("separate")) ram_203 (
    .addr(multiplexer_217_out), .din(Data_in_to_Ram_64_95), .data(ram_203_data), .str(decoder_2_out18[9]),
    .sel(Power), .clk(Clk), .ld(not_207_out), .clr(or_7_out[9]));
  RAM #(.addrWidth(24), .dataWidth(32), .bus("separate")) ram_204 (
    .addr(multiplexer_218_out), .din(Data_in_to_Ram_96_127), .data(ram_204_data), .str(decoder_2_out18[9]),
    .sel(Power), .clk(Clk), .ld(not_208_out), .clr(or_7_out[9]));
  RAM #(.addrWidth(24), .dataWidth(32), .bus("separate")) ram_205 (
    .addr(multiplexer_219_out), .din(Data_in_to_Ram_0_31), .data(ram_205_data), .str(decoder_4_out18[9]),
    .sel(Power), .clk(not_3_out), .ld(not_209_out), .clr(or_7_out[9]));
  RAM #(.addrWidth(24), .dataWidth(32), .bus("separate")) ram_206 (
    .addr(multiplexer_220_out), .din(Data_in_to_Ram_32_63), .data(ram_206_data), .str(decoder_4_out18[9]),
    .sel(Power), .clk(not_3_out), .ld(not_210_out), .clr(or_7_out[9]));
  RAM #(.addrWidth(24), .dataWidth(32), .bus("separate")) ram_207 (
    .addr(multiplexer_221_out), .din(Data_in_to_Ram_64_95), .data(ram_207_data), .str(decoder_4_out18[9]),
    .sel(Power), .clk(not_3_out), .ld(not_211_out), .clr(or_7_out[9]));
  RAM #(.addrWidth(24), .dataWidth(32), .bus("separate")) ram_208 (
    .addr(multiplexer_222_out), .din(Data_in_to_Ram_96_127), .data(ram_208_data), .str(decoder_4_out18[9]),
    .sel(Power), .clk(not_3_out), .ld(not_212_out), .clr(or_7_out[9]));
  Register #(.width(1)) register_54 (
    .D(Power), .en(Power), .Q(register_34_q[10]), .clk(decoder_3_out19[9]), .clr(or_7_out[10]));
  Register #(.width(1)) register_55 (
    .D(Power), .en(Power), .Q(register_35_q[10]), .clk(decoder_3_out19[9]), .clr(or_7_out[10]));
  Multiplexer #(.width(24)) multiplexer_223 (
    .in0(counter_1_q), .in1(\Сomand_Number_When_Loading_RAM ), .out(multiplexer_223_out),
    .sel(decoder_2_out18[10]), .en(Power));
  Multiplexer #(.width(24)) multiplexer_224 (
    .in0(counter_1_q), .in1(\Сomand_Number_When_Loading_RAM ), .out(multiplexer_224_out),
    .sel(decoder_2_out18[10]), .en(Power));
  Multiplexer #(.width(24)) multiplexer_225 (
    .in0(counter_1_q), .in1(\Сomand_Number_When_Loading_RAM ), .out(multiplexer_225_out),
    .sel(decoder_2_out18[10]), .en(Power));
  Multiplexer #(.width(24)) multiplexer_226 (
    .in0(counter_1_q), .in1(\Сomand_Number_When_Loading_RAM ), .out(multiplexer_226_out),
    .sel(decoder_2_out18[10]), .en(Power));
  Multiplexer #(.width(24)) multiplexer_227 (
    .in0(counter_1_q), .in1(\Сomand_Number_When_Loading_RAM ), .out(multiplexer_227_out),
    .sel(decoder_4_out18[10]), .en(Power));
  Multiplexer #(.width(24)) multiplexer_228 (
    .in0(counter_1_q), .in1(\Сomand_Number_When_Loading_RAM ), .out(multiplexer_228_out),
    .sel(decoder_4_out18[10]), .en(Power));
  Multiplexer #(.width(24)) multiplexer_229 (
    .in0(counter_1_q), .in1(\Сomand_Number_When_Loading_RAM ), .out(multiplexer_229_out),
    .sel(decoder_4_out18[10]), .en(Power));
  Multiplexer #(.width(24)) multiplexer_230 (
    .in0(counter_1_q), .in1(\Сomand_Number_When_Loading_RAM ), .out(multiplexer_230_out),
    .sel(decoder_4_out18[10]), .en(Power));
  RAM #(.addrWidth(24), .dataWidth(32), .bus("separate")) ram_209 (
    .addr(multiplexer_223_out), .din(Data_in_to_Ram_0_31), .data(ram_209_data), .str(decoder_2_out18[10]),
    .sel(Power), .clk(Clk), .ld(not_213_out), .clr(or_7_out[10]));
  not not_213 (not_213_out, decoder_2_out18[10]);
  RAM #(.addrWidth(24), .dataWidth(32), .bus("separate")) ram_210 (
    .addr(multiplexer_224_out), .din(Data_in_to_Ram_32_63), .data(ram_210_data), .str(decoder_2_out18[10]),
    .sel(Power), .clk(Clk), .ld(not_214_out), .clr(or_7_out[10]));
  not not_214 (not_214_out, decoder_2_out18[10]);
  RAM #(.addrWidth(24), .dataWidth(32), .bus("separate")) ram_211 (
    .addr(multiplexer_225_out), .din(Data_in_to_Ram_64_95), .data(ram_211_data), .str(decoder_2_out18[10]),
    .sel(Power), .clk(Clk), .ld(not_215_out), .clr(or_7_out[10]));
  not not_215 (not_215_out, decoder_2_out18[10]);
  RAM #(.addrWidth(24), .dataWidth(32), .bus("separate")) ram_212 (
    .addr(multiplexer_226_out), .din(Data_in_to_Ram_96_127), .data(ram_212_data), .str(decoder_2_out18[10]),
    .sel(Power), .clk(Clk), .ld(not_216_out), .clr(or_7_out[10]));
  not not_216 (not_216_out, decoder_2_out18[10]);
  RAM #(.addrWidth(24), .dataWidth(32), .bus("separate")) ram_213 (
    .addr(multiplexer_227_out), .din(Data_in_to_Ram_0_31), .data(ram_213_data), .str(decoder_4_out18[10]),
    .sel(Power), .clk(not_3_out), .ld(not_217_out), .clr(or_7_out[10]));
  not not_217 (not_217_out, decoder_4_out18[10]);
  RAM #(.addrWidth(24), .dataWidth(32), .bus("separate")) ram_214 (
    .addr(multiplexer_228_out), .din(Data_in_to_Ram_32_63), .data(ram_214_data), .str(decoder_4_out18[10]),
    .sel(Power), .clk(not_3_out), .ld(not_218_out), .clr(or_7_out[10]));
  not not_218 (not_218_out, decoder_4_out18[10]);
  RAM #(.addrWidth(24), .dataWidth(32), .bus("separate")) ram_215 (
    .addr(multiplexer_229_out), .din(Data_in_to_Ram_64_95), .data(ram_215_data), .str(decoder_4_out18[10]),
    .sel(Power), .clk(not_3_out), .ld(not_219_out), .clr(or_7_out[10]));
  not not_219 (not_219_out, decoder_4_out18[10]);
  RAM #(.addrWidth(24), .dataWidth(32), .bus("separate")) ram_216 (
    .addr(multiplexer_230_out), .din(Data_in_to_Ram_96_127), .data(ram_216_data), .str(decoder_4_out18[10]),
    .sel(Power), .clk(not_3_out), .ld(not_220_out), .clr(or_7_out[10]));
  not not_220 (not_220_out, decoder_4_out18[10]);
  Register #(.width(1)) register_56 (
    .D(Power), .en(Power), .Q(register_34_q[11]), .clk(decoder_3_out19[10]), .clr(or_7_out[11]));
  Register #(.width(1)) register_57 (
    .D(Power), .en(Power), .Q(register_35_q[11]), .clk(decoder_3_out19[10]), .clr(or_7_out[11]));
  Multiplexer #(.width(24)) multiplexer_231 (
    .in0(counter_1_q), .in1(\Сomand_Number_When_Loading_RAM ), .out(multiplexer_231_out),
    .sel(decoder_2_out18[11]), .en(Power));
  Multiplexer #(.width(24)) multiplexer_232 (
    .in0(counter_1_q), .in1(\Сomand_Number_When_Loading_RAM ), .out(multiplexer_232_out),
    .sel(decoder_2_out18[11]), .en(Power));
  Multiplexer #(.width(24)) multiplexer_233 (
    .in0(counter_1_q), .in1(\Сomand_Number_When_Loading_RAM ), .out(multiplexer_233_out),
    .sel(decoder_2_out18[11]), .en(Power));
  Multiplexer #(.width(24)) multiplexer_234 (
    .in0(counter_1_q), .in1(\Сomand_Number_When_Loading_RAM ), .out(multiplexer_234_out),
    .sel(decoder_2_out18[11]), .en(Power));
  Multiplexer #(.width(24)) multiplexer_235 (
    .in0(counter_1_q), .in1(\Сomand_Number_When_Loading_RAM ), .out(multiplexer_235_out),
    .sel(decoder_4_out18[11]), .en(Power));
  Multiplexer #(.width(24)) multiplexer_236 (
    .in0(counter_1_q), .in1(\Сomand_Number_When_Loading_RAM ), .out(multiplexer_236_out),
    .sel(decoder_4_out18[11]), .en(Power));
  Multiplexer #(.width(24)) multiplexer_237 (
    .in0(counter_1_q), .in1(\Сomand_Number_When_Loading_RAM ), .out(multiplexer_237_out),
    .sel(decoder_4_out18[11]), .en(Power));
  Multiplexer #(.width(24)) multiplexer_238 (
    .in0(counter_1_q), .in1(\Сomand_Number_When_Loading_RAM ), .out(multiplexer_238_out),
    .sel(decoder_4_out18[11]), .en(Power));
  RAM #(.addrWidth(24), .dataWidth(32), .bus("separate")) ram_217 (
    .addr(multiplexer_231_out), .din(Data_in_to_Ram_0_31), .data(ram_217_data), .str(decoder_2_out18[11]),
    .sel(Power), .clk(Clk), .ld(not_221_out), .clr(or_7_out[11]));
  not not_221 (not_221_out, decoder_2_out18[11]);
  RAM #(.addrWidth(24), .dataWidth(32), .bus("separate")) ram_218 (
    .addr(multiplexer_232_out), .din(Data_in_to_Ram_32_63), .data(ram_218_data), .str(decoder_2_out18[11]),
    .sel(Power), .clk(Clk), .ld(not_222_out), .clr(or_7_out[11]));
  not not_222 (not_222_out, decoder_2_out18[11]);
  RAM #(.addrWidth(24), .dataWidth(32), .bus("separate")) ram_219 (
    .addr(multiplexer_233_out), .din(Data_in_to_Ram_64_95), .data(ram_219_data), .str(decoder_2_out18[11]),
    .sel(Power), .clk(Clk), .ld(not_223_out), .clr(or_7_out[11]));
  not not_223 (not_223_out, decoder_2_out18[11]);
  RAM #(.addrWidth(24), .dataWidth(32), .bus("separate")) ram_220 (
    .addr(multiplexer_234_out), .din(Data_in_to_Ram_96_127), .data(ram_220_data), .str(decoder_2_out18[11]),
    .sel(Power), .clk(Clk), .ld(not_224_out), .clr(or_7_out[11]));
  not not_224 (not_224_out, decoder_2_out18[11]);
  RAM #(.addrWidth(24), .dataWidth(32), .bus("separate")) ram_221 (
    .addr(multiplexer_235_out), .din(Data_in_to_Ram_0_31), .data(ram_221_data), .str(decoder_4_out18[11]),
    .sel(Power), .clk(not_3_out), .ld(not_225_out), .clr(or_7_out[11]));
  not not_225 (not_225_out, decoder_4_out18[11]);
  RAM #(.addrWidth(24), .dataWidth(32), .bus("separate")) ram_222 (
    .addr(multiplexer_236_out), .din(Data_in_to_Ram_32_63), .data(ram_222_data), .str(decoder_4_out18[11]),
    .sel(Power), .clk(not_3_out), .ld(not_226_out), .clr(or_7_out[11]));
  not not_226 (not_226_out, decoder_4_out18[11]);
  RAM #(.addrWidth(24), .dataWidth(32), .bus("separate")) ram_223 (
    .addr(multiplexer_237_out), .din(Data_in_to_Ram_64_95), .data(ram_223_data), .str(decoder_4_out18[11]),
    .sel(Power), .clk(not_3_out), .ld(not_227_out), .clr(or_7_out[11]));
  not not_227 (not_227_out, decoder_4_out18[11]);
  RAM #(.addrWidth(24), .dataWidth(32), .bus("separate")) ram_224 (
    .addr(multiplexer_238_out), .din(Data_in_to_Ram_96_127), .data(ram_224_data), .str(decoder_4_out18[11]),
    .sel(Power), .clk(not_3_out), .ld(not_228_out), .clr(or_7_out[11]));
  not not_228 (not_228_out, decoder_4_out18[11]);
  Register #(.width(1)) register_58 (
    .D(Power), .en(Power), .Q(register_34_q[12]), .clk(decoder_3_out19[11]), .clr(or_7_out[12]));
  Register #(.width(1)) register_59 (
    .D(Power), .en(Power), .Q(register_35_q[12]), .clk(decoder_3_out19[11]), .clr(or_7_out[12]));
  Multiplexer #(.width(24)) multiplexer_239 (
    .in0(counter_1_q), .in1(\Сomand_Number_When_Loading_RAM ), .out(multiplexer_239_out),
    .sel(decoder_2_out18[12]), .en(Power));
  Multiplexer #(.width(24)) multiplexer_240 (
    .in0(counter_1_q), .in1(\Сomand_Number_When_Loading_RAM ), .out(multiplexer_240_out),
    .sel(decoder_2_out18[12]), .en(Power));
  Multiplexer #(.width(24)) multiplexer_241 (
    .in0(counter_1_q), .in1(\Сomand_Number_When_Loading_RAM ), .out(multiplexer_241_out),
    .sel(decoder_2_out18[12]), .en(Power));
  Multiplexer #(.width(24)) multiplexer_242 (
    .in0(counter_1_q), .in1(\Сomand_Number_When_Loading_RAM ), .out(multiplexer_242_out),
    .sel(decoder_2_out18[12]), .en(Power));
  Multiplexer #(.width(24)) multiplexer_243 (
    .in0(counter_1_q), .in1(\Сomand_Number_When_Loading_RAM ), .out(multiplexer_243_out),
    .sel(decoder_4_out18[12]), .en(Power));
  Multiplexer #(.width(24)) multiplexer_244 (
    .in0(counter_1_q), .in1(\Сomand_Number_When_Loading_RAM ), .out(multiplexer_244_out),
    .sel(decoder_4_out18[12]), .en(Power));
  Multiplexer #(.width(24)) multiplexer_245 (
    .in0(counter_1_q), .in1(\Сomand_Number_When_Loading_RAM ), .out(multiplexer_245_out),
    .sel(decoder_4_out18[12]), .en(Power));
  Multiplexer #(.width(24)) multiplexer_246 (
    .in0(counter_1_q), .in1(\Сomand_Number_When_Loading_RAM ), .out(multiplexer_246_out),
    .sel(decoder_4_out18[12]), .en(Power));
  not not_229 (not_229_out, decoder_2_out18[12]);
  not not_230 (not_230_out, decoder_2_out18[12]);
  not not_231 (not_231_out, decoder_2_out18[12]);
  not not_232 (not_232_out, decoder_2_out18[12]);
  not not_233 (not_233_out, decoder_4_out18[12]);
  not not_234 (not_234_out, decoder_4_out18[12]);
  not not_235 (not_235_out, decoder_4_out18[12]);
  not not_236 (not_236_out, decoder_4_out18[12]);
  RAM #(.addrWidth(24), .dataWidth(32), .bus("separate")) ram_225 (
    .addr(multiplexer_239_out), .din(Data_in_to_Ram_0_31), .data(ram_225_data), .str(decoder_2_out18[12]),
    .sel(Power), .clk(Clk), .ld(not_229_out), .clr(or_7_out[12]));
  RAM #(.addrWidth(24), .dataWidth(32), .bus("separate")) ram_226 (
    .addr(multiplexer_240_out), .din(Data_in_to_Ram_32_63), .data(ram_226_data), .str(decoder_2_out18[12]),
    .sel(Power), .clk(Clk), .ld(not_230_out), .clr(or_7_out[12]));
  RAM #(.addrWidth(24), .dataWidth(32), .bus("separate")) ram_227 (
    .addr(multiplexer_241_out), .din(Data_in_to_Ram_64_95), .data(ram_227_data), .str(decoder_2_out18[12]),
    .sel(Power), .clk(Clk), .ld(not_231_out), .clr(or_7_out[12]));
  RAM #(.addrWidth(24), .dataWidth(32), .bus("separate")) ram_228 (
    .addr(multiplexer_242_out), .din(Data_in_to_Ram_96_127), .data(ram_228_data), .str(decoder_2_out18[12]),
    .sel(Power), .clk(Clk), .ld(not_232_out), .clr(or_7_out[12]));
  RAM #(.addrWidth(24), .dataWidth(32), .bus("separate")) ram_229 (
    .addr(multiplexer_243_out), .din(Data_in_to_Ram_0_31), .data(ram_229_data), .str(decoder_4_out18[12]),
    .sel(Power), .clk(not_3_out), .ld(not_233_out), .clr(or_7_out[12]));
  RAM #(.addrWidth(24), .dataWidth(32), .bus("separate")) ram_230 (
    .addr(multiplexer_244_out), .din(Data_in_to_Ram_32_63), .data(ram_230_data), .str(decoder_4_out18[12]),
    .sel(Power), .clk(not_3_out), .ld(not_234_out), .clr(or_7_out[12]));
  RAM #(.addrWidth(24), .dataWidth(32), .bus("separate")) ram_231 (
    .addr(multiplexer_245_out), .din(Data_in_to_Ram_64_95), .data(ram_231_data), .str(decoder_4_out18[12]),
    .sel(Power), .clk(not_3_out), .ld(not_235_out), .clr(or_7_out[12]));
  RAM #(.addrWidth(24), .dataWidth(32), .bus("separate")) ram_232 (
    .addr(multiplexer_246_out), .din(Data_in_to_Ram_96_127), .data(ram_232_data), .str(decoder_4_out18[12]),
    .sel(Power), .clk(not_3_out), .ld(not_236_out), .clr(or_7_out[12]));
  Register #(.width(1)) register_60 (
    .D(Power), .en(Power), .Q(register_34_q[13]), .clk(decoder_3_out19[12]), .clr(or_7_out[13]));
  Register #(.width(1)) register_61 (
    .D(Power), .en(Power), .Q(register_35_q[13]), .clk(decoder_3_out19[12]), .clr(or_7_out[13]));
  Multiplexer #(.width(24)) multiplexer_247 (
    .in0(counter_1_q), .in1(\Сomand_Number_When_Loading_RAM ), .out(multiplexer_247_out),
    .sel(decoder_2_out18[13]), .en(Power));
  Multiplexer #(.width(24)) multiplexer_248 (
    .in0(counter_1_q), .in1(\Сomand_Number_When_Loading_RAM ), .out(multiplexer_248_out),
    .sel(decoder_2_out18[13]), .en(Power));
  Multiplexer #(.width(24)) multiplexer_249 (
    .in0(counter_1_q), .in1(\Сomand_Number_When_Loading_RAM ), .out(multiplexer_249_out),
    .sel(decoder_2_out18[13]), .en(Power));
  Multiplexer #(.width(24)) multiplexer_250 (
    .in0(counter_1_q), .in1(\Сomand_Number_When_Loading_RAM ), .out(multiplexer_250_out),
    .sel(decoder_2_out18[13]), .en(Power));
  Multiplexer #(.width(24)) multiplexer_251 (
    .in0(counter_1_q), .in1(\Сomand_Number_When_Loading_RAM ), .out(multiplexer_251_out),
    .sel(decoder_4_out18[13]), .en(Power));
  Multiplexer #(.width(24)) multiplexer_252 (
    .in0(counter_1_q), .in1(\Сomand_Number_When_Loading_RAM ), .out(multiplexer_252_out),
    .sel(decoder_4_out18[13]), .en(Power));
  Multiplexer #(.width(24)) multiplexer_253 (
    .in0(counter_1_q), .in1(\Сomand_Number_When_Loading_RAM ), .out(multiplexer_253_out),
    .sel(decoder_4_out18[13]), .en(Power));
  Multiplexer #(.width(24)) multiplexer_254 (
    .in0(counter_1_q), .in1(\Сomand_Number_When_Loading_RAM ), .out(multiplexer_254_out),
    .sel(decoder_4_out18[13]), .en(Power));
  not not_237 (not_237_out, decoder_2_out18[13]);
  not not_238 (not_238_out, decoder_2_out18[13]);
  not not_239 (not_239_out, decoder_2_out18[13]);
  not not_240 (not_240_out, decoder_2_out18[13]);
  not not_241 (not_241_out, decoder_4_out18[13]);
  not not_242 (not_242_out, decoder_4_out18[13]);
  not not_243 (not_243_out, decoder_4_out18[13]);
  not not_244 (not_244_out, decoder_4_out18[13]);
  RAM #(.addrWidth(24), .dataWidth(32), .bus("separate")) ram_233 (
    .addr(multiplexer_247_out), .din(Data_in_to_Ram_0_31), .data(ram_233_data), .str(decoder_2_out18[13]),
    .sel(Power), .clk(Clk), .ld(not_237_out), .clr(or_7_out[13]));
  RAM #(.addrWidth(24), .dataWidth(32), .bus("separate")) ram_234 (
    .addr(multiplexer_248_out), .din(Data_in_to_Ram_32_63), .data(ram_234_data), .str(decoder_2_out18[13]),
    .sel(Power), .clk(Clk), .ld(not_238_out), .clr(or_7_out[13]));
  RAM #(.addrWidth(24), .dataWidth(32), .bus("separate")) ram_235 (
    .addr(multiplexer_249_out), .din(Data_in_to_Ram_64_95), .data(ram_235_data), .str(decoder_2_out18[13]),
    .sel(Power), .clk(Clk), .ld(not_239_out), .clr(or_7_out[13]));
  RAM #(.addrWidth(24), .dataWidth(32), .bus("separate")) ram_236 (
    .addr(multiplexer_250_out), .din(Data_in_to_Ram_96_127), .data(ram_236_data), .str(decoder_2_out18[13]),
    .sel(Power), .clk(Clk), .ld(not_240_out), .clr(or_7_out[13]));
  RAM #(.addrWidth(24), .dataWidth(32), .bus("separate")) ram_237 (
    .addr(multiplexer_251_out), .din(Data_in_to_Ram_0_31), .data(ram_237_data), .str(decoder_4_out18[13]),
    .sel(Power), .clk(not_3_out), .ld(not_241_out), .clr(or_7_out[13]));
  RAM #(.addrWidth(24), .dataWidth(32), .bus("separate")) ram_238 (
    .addr(multiplexer_252_out), .din(Data_in_to_Ram_32_63), .data(ram_238_data), .str(decoder_4_out18[13]),
    .sel(Power), .clk(not_3_out), .ld(not_242_out), .clr(or_7_out[13]));
  RAM #(.addrWidth(24), .dataWidth(32), .bus("separate")) ram_239 (
    .addr(multiplexer_253_out), .din(Data_in_to_Ram_64_95), .data(ram_239_data), .str(decoder_4_out18[13]),
    .sel(Power), .clk(not_3_out), .ld(not_243_out), .clr(or_7_out[13]));
  RAM #(.addrWidth(24), .dataWidth(32), .bus("separate")) ram_240 (
    .addr(multiplexer_254_out), .din(Data_in_to_Ram_96_127), .data(ram_240_data), .str(decoder_4_out18[13]),
    .sel(Power), .clk(not_3_out), .ld(not_244_out), .clr(or_7_out[13]));

  // Notes on the sheet:
  //   comand_64_95bit: pull=up
  //   comand_32_63bit: pull=up
  //   comand_0_31bit: pull=up
  //   comand_96_127bit: pull=up
  //   contents of rom_1 (hex, n*v repeats v):
  //   1 124
  //   contents of rom_2 (hex, n*v repeats v):
  //   1 1235
  //   contents of rom_3 (hex, n*v repeats v):
  //   1
  //   contents of rom_4 (hex, n*v repeats v):
  //   1345
  //   contents of rom_5 (hex, n*v repeats v):
  //   2345 235
  //   contents of rom_6 (hex, n*v repeats v):
  //   0 2345
endmodule

module increesor (
  input  [31:0] in,
  output [31:0] out_2
);

  Pull_Resistor pull_resistor_1 (.node(in));
  Pull_Resistor pull_resistor_2 (.node(out_2));
  Adder #(.width(32)) adder_1 (.a(in), .b(32'h1), .out(out_2));  // open: cin, cout
endmodule

module PC (
  input  [31:0] sRam,
  input  [31:0] Stack_Pointer__in,
  input  [31:0] Z,
  input  Power,
  input  Reset,
  input  Clk,
  input  Load_PC_Pointer,
  input  Load_Stack_Pointer,
  input  Push,
  input  Pop,
  input  UP_0__DOWN_1,
  input  Load_Select,
  output [31:0] Data_out
);

  wire and_1_out, and_2_out, not_1_out, or_1_out, or_2_out, or_3_out, or_4_out, or_5_out;
  wire [23:0] bit_extender_1_out, Stack_Pointer_q;
  wire [31:0] multiplexer_1_out, ram_1_data;

  Pull_Resistor pull_resistor_1 (.node(Load_Stack_Pointer));
  Pull_Resistor pull_resistor_2 (.node(Reset));
  Pull_Resistor pull_resistor_3 (.node(Power));
  Pull_Resistor pull_resistor_4 (.node(Load_PC_Pointer));
  Pull_Resistor pull_resistor_5 (.node(sRam));
  Pull_Resistor pull_resistor_6 (.node(Z));
  Pull_Resistor pull_resistor_7 (.node(Clk));
  Pull_Resistor pull_resistor_8 (.node(Stack_Pointer__in));
  Pull_Resistor pull_resistor_9 (.node(UP_0__DOWN_1));
  Pull_Resistor pull_resistor_10 (.node(Push));
  Pull_Resistor pull_resistor_11 (.node(Pop));
  Pull_Resistor pull_resistor_12 (.node(Load_Select));
  Bit_Extender #(.in_width(32), .out_width(24)) bit_extender_1 (.in(Stack_Pointer__in), .out(bit_extender_1_out));
  Multiplexer #(.select(2), .width(32)) multiplexer_1 (
    .in0(sRam), .in1(Stack_Pointer__in), .in2(Z), .in3(ram_1_data), .out(multiplexer_1_out),
    .sel({Pop, Load_Select}), .en(Power));
  or or_1 (or_1_out, Push, Pop);
  or or_2 (or_2_out, UP_0__DOWN_1, Load_PC_Pointer);
  or or_3 (or_3_out, UP_0__DOWN_1, Load_Stack_Pointer);
  or or_4 (or_4_out, UP_0__DOWN_1, and_1_out);
  and and_1 (and_1_out, ~Load_Stack_Pointer, ~UP_0__DOWN_1);  // AND_Gate
  and and_2 (and_2_out, ~UP_0__DOWN_1, ~Load_PC_Pointer);  // AND_Gate
  or or_5 (or_5_out, and_2_out, UP_0__DOWN_1);
  Counter #(.width(32), .max('hffffffff)) PC_Pointer (
    .load(or_2_out), .D(multiplexer_1_out), .count(or_5_out), .Q(Data_out), .clk(Clk), .clr(Reset));  // open: carry
  Counter #(.width(24), .max('hffffff)) Stack_Pointer (
    .load(or_3_out), .D(bit_extender_1_out), .count(or_4_out), .Q(Stack_Pointer_q), .clk(or_1_out),
    .clr(Reset));  // open: carry
  RAM #(.addrWidth(24), .dataWidth(32), .bus("separate")) ram_1 (
    .addr(Stack_Pointer_q), .din(Data_out), .data(ram_1_data), .str(Push), .sel(Power), .clk(Clk),
    .ld(not_1_out), .clr(Reset));
  not not_1 (not_1_out, Push);
  Pull_Resistor pull_resistor_13 (.node(Data_out));
endmodule

module Loading_proqrams_device__LPD (
  input  [31:0] Data_in,
  input  Clk,
  input  Reset_Stop_loading,
  input  Power,
  input  Load__Access_to_Load,
  input  [31:0] \Сдвиг_Адреса_загрузки__Диск ,
  output [31:0] _1,
  output [31:0] _2,
  output [31:0] _3,
  output [31:0] _4,
  output Loading_Complete,
  output Load_RAM,
  output [23:0] Adress_for_loading_to_Comand_Protocol,
  output Loading,
  output [31:0] Adress_for_loading__for_Disk,
  output RAM_TYPE_LOADING
);

  wire adder_1_cout, and_2_out, and_3_out, and_4_out, and_5_out, and_6_out, and_7_out, and_8_out,
       comparator_1_eq, comparator_2_eq, comparator_3_eq, comparator_4_eq, comparator_5_eq, comparator_6_eq,
       comparator_7_eq, comparator_8_eq, counter_1_carry, counter_2_carry, or_1_out, or_2_out, or_3_out,
       pull_resistor_3_node;
  wire [2:0] counter_1_q;
  wire [31:0] counter_3_q, register_2_q;

  Pull_Resistor pull_resistor_1 (.node(\Сдвиг_Адреса_загрузки__Диск ));
  Pull_Resistor pull_resistor_2 (.node(Reset_Stop_loading));
  Pull_Resistor pull_resistor_3 (.node(pull_resistor_3_node));
  Pull_Resistor pull_resistor_4 (.node(Data_in));
  Pull_Resistor pull_resistor_5 (.node(Clk));
  Pull_Resistor pull_resistor_6 (.node(Power));
  and and_1 (pull_resistor_3_node, Load__Access_to_Load, ~Loading);  // AND_Gate
  or or_1 (or_1_out, and_8_out, Reset_Stop_loading, adder_1_cout, ~Power, counter_2_carry);  // OR_Gate
  Counter #(.width(3), .max('h7)) counter_1 (
    .load(1'b0), .D(3'b000), .count(Loading), .Q(counter_1_q), .carry(counter_1_carry), .clk(Clk),
    .clr(or_1_out));
  Register #(.width(1)) register_1 (
    .D(pull_resistor_3_node), .en(pull_resistor_3_node), .Q(Loading), .clk(pull_resistor_3_node),
    .clr(or_1_out));
  Counter #(.width(24), .max('hffffff)) counter_2 (
    .load(1'b0), .D({24{1'b0}}), .count(Loading), .Q(Adress_for_loading_to_Comand_Protocol),
    .carry(counter_2_carry), .clk(counter_1_carry), .clr(or_1_out));
  Counter #(.width(32), .max('hffffffff)) counter_3 (
    .load(1'b0), .D({32{1'b0}}), .count(Loading), .Q(counter_3_q), .clk(Clk), .clr(or_1_out));  // open: carry
  Register #(.width(32)) register_2 (
    .D(\Сдвиг_Адреса_загрузки__Диск ), .en(pull_resistor_3_node), .Q(register_2_q),
    .clk(pull_resistor_3_node), .clr(or_1_out));
  or or_2 (or_2_out, pull_resistor_3_node, comparator_1_eq);
  Comparator #(.width(2)) comparator_1 (.a(counter_1_q[1:0]), .b(2'b00), .eq(comparator_1_eq));  // open: gt, lt
  Comparator #(.width(2)) comparator_2 (.a(counter_1_q[1:0]), .b(2'b01), .eq(comparator_2_eq));  // open: gt, lt
  and and_2 (and_2_out, comparator_2_eq, Loading);
  Comparator #(.width(2)) comparator_3 (.a(counter_1_q[1:0]), .b(2'b10), .eq(comparator_3_eq));  // open: gt, lt
  and and_3 (and_3_out, comparator_3_eq, Loading);
  Comparator #(.width(2)) comparator_4 (.a(counter_1_q[1:0]), .b(2'b11), .eq(comparator_4_eq));  // open: gt, lt
  and and_4 (and_4_out, comparator_4_eq, Loading);
  or or_3 (or_3_out, counter_2_carry, adder_1_cout, and_8_out);
  or or_4 (Load_RAM, comparator_4_eq, counter_1_carry);
  Adder #(.width(32)) adder_1 (
    .a(counter_3_q), .b(register_2_q), .out(Adress_for_loading__for_Disk), .cout(adder_1_cout));  // open: cin
  Register #(.width(1)) register_3 (.D(or_3_out), .en(or_3_out), .Q(Loading_Complete), .clk(or_3_out), .clr(and_5_out));
  and and_5 (and_5_out, ~Clk, Loading_Complete);  // AND_Gate
  Register #(.width(32)) register_4 (.D(Data_in), .en(and_6_out), .Q(_1), .clk(Clk), .clr(or_1_out));
  and and_6 (and_6_out, or_2_out, Loading);
  Register #(.width(32)) register_5 (.D(Data_in), .en(and_2_out), .Q(_2), .clk(Clk), .clr(or_1_out));
  Register #(.width(32)) register_6 (.D(Data_in), .en(and_3_out), .Q(_3), .clk(Clk), .clr(or_1_out));
  Register #(.width(32)) register_7 (.D(Data_in), .en(and_4_out), .Q(_4), .clk(Clk), .clr(or_1_out));
  Comparator #(.width(32)) comparator_5 (.a(_1), .b({32{1'b0}}), .eq(comparator_5_eq));  // open: gt, lt
  Comparator #(.width(32)) comparator_6 (.a(_2), .b({32{1'b0}}), .eq(comparator_6_eq));  // open: gt, lt
  Comparator #(.width(32)) comparator_7 (.a(_3), .b({32{1'b0}}), .eq(comparator_7_eq));  // open: gt, lt
  Comparator #(.width(32)) comparator_8 (.a(_4), .b({32{1'b0}}), .eq(comparator_8_eq));  // open: gt, lt
  Pull_Resistor pull_resistor_7 (.node(Loading_Complete));
  Pull_Resistor pull_resistor_8 (.node(Adress_for_loading_to_Comand_Protocol));
  Pull_Resistor pull_resistor_9 (.node(Adress_for_loading__for_Disk));
  Pull_Resistor pull_resistor_10 (.node(Loading));
  and and_7 (and_7_out, comparator_5_eq, comparator_6_eq, comparator_7_eq, comparator_8_eq);
  Pull_Resistor pull_resistor_11 (.node(_2));
  Pull_Resistor pull_resistor_12 (.node(_3));
  Pull_Resistor pull_resistor_13 (.node(Load_RAM));
  Pull_Resistor pull_resistor_14 (.node(_1));
  Pull_Resistor pull_resistor_15 (.node(_4));
  and and_8 (and_8_out, Load_RAM, Loading, and_7_out);
  not not_1 (RAM_TYPE_LOADING, counter_1_carry);
endmodule

module \строение_логических_элементов  (
  input  in_1,
  input  in_2,
  input  Reset,
  input  Clk,
  input  in_5,
  input  in_6,
  input  Load,
  input  Count,
  input  [3:0] Data_in,
  input  in_10,
  input  in_11,
  input  in_12,
  input  in_13,
  input  in_14,
  input  in_15,
  input  in_16,
  input  in_17,
  input  in_18,
  input  in_19,
  input  in_20,
  input  in_21,
  input  in_22,
  input  in_23,
  input  in_24,
  input  in_25,
  input  in_26,
  input  in_27,
  input  in_28,
  input  in_29,
  input  in_30,
  input  in_31,
  input  in_32,
  input  in_33,
  input  Clk_2,
  input  En,
  input  in_36,
  input  in_37,
  input  In,
  input  in_39,
  input  in_40,
  input  Reset_2,
  input  in_42,
  input  in_43,
  input  in_44,
  input  in_45,
  input  in_46,
  input  in_47,
  input  in_48,
  input  in_49,
  input  in_50,
  input  in_51,
  input  in_52,
  input  in_53,
  output out_54,
  output out_55,
  output out_56,
  output out_57,
  output out_58,
  output out_59,
  output [3:0] Data_out,
  output out_61,
  output out_62,
  output out_63,
  output out_64,
  output out_65,
  output out_66,
  output out_67,
  output out_68,
  output out_69,
  output out_70,
  output out_71,
  output out_72,
  output out_73,
  output out_74,
  output out_75,
  output out_76,
  output out_77,
  output out_78,
  output out_79,
  output out_80,
  output out_81,
  output out_82
);

  wire and_2_out, and_4_out, and_5_out, and_6_out, and_7_out, and_8_out, and_9_out, and_10_out, and_11_out,
       and_12_out, and_13_out, and_14_out, and_15_out, and_16_out, d_ff_2_qn, d_ff_3_qn, d_ff_4_qn,
       d_ff_5_qn, multiplexer_2_out, multiplexer_3_out, multiplexer_4_out, multiplexer_5_out, nand_1_out,
       not_2_out, not_3_out, not_4_out, or_2_out, or_4_out, or_5_out, or_6_out, or_7_out, or_8_out, or_9_out,
       transistor_5_out, transistor_8_out, transistor_10_out, transistor_12_out, transistor_13_out,
       xor_2_out, xor_4_out, xor_5_out, xor_6_out, xor_7_out;

  not not_1 (out_54, in_1);
  buf buffer_1 (out_56, in_5);
  and and_1 (out_58, in_10, in_12);
  or or_1 (out_61, in_14, in_16);
  xor xor_1 (out_63, in_18, in_20);
  assign out_65 = in_24 ? in_22 : 1'bz;  // Controlled_Buffer controlled_buffer_1
  Multiplexer multiplexer_1 (.in0(in_26), .in1(in_28), .out(out_67), .sel(in_30), .en(in_32));
  Demultiplexer demultiplexer_1 (.out0(out_71), .out1(out_73), .in(in_36), .sel(in_42), .en(in_39));
  Decoder decoder_1 (.out0(out_75), .out1(out_77), .sel(in_46), .en(in_44));
  Adder #(.width(1)) adder_1 (.a(in_50), .b(in_52), .out(out_80), .cin(in_48), .cout(out_81));
  Transistor transistor_1 (.in(1'b1), .out(out_55), .gate(in_2));
  Transistor #(.\type ("n"), .gate("br")) transistor_2 (.in(1'b0), .out(out_55), .gate(in_2));
  Transistor transistor_3 (.in(1'b0), .out(out_57), .gate(in_6));
  Transistor #(.\type ("n"), .gate("br")) transistor_4 (.in(1'b1), .out(out_57), .gate(in_6));
  Transistor #(.\type ("n")) transistor_5 (.in(1'b1), .out(transistor_5_out), .gate(in_11));
  Transistor transistor_6 (.in(1'b0), .out(out_59), .gate(in_13));
  Transistor #(.gate("br")) transistor_7 (.in(1'b0), .out(out_59), .gate(in_11));
  Transistor transistor_8 (.in(1'b0), .out(transistor_8_out), .gate(in_17));
  or or_2 (or_2_out, in_19, in_21);
  nand nand_1 (nand_1_out, in_21, in_19);
  Transistor #(.\type ("n"), .gate("br")) transistor_9 (.in(in_23), .out(out_66), .gate(in_25));
  Transistor transistor_10 (.in(in_27), .out(transistor_10_out), .gate(in_31));
  Transistor #(.\type ("n"), .gate("br")) transistor_11 (.in(in_29), .out(transistor_10_out), .gate(in_31));
  Transistor transistor_12 (.in(in_37), .out(transistor_12_out), .gate(in_43));
  Pull_Resistor pull_resistor_1 (.node(transistor_12_out));
  Transistor #(.\type ("n"), .gate("br")) transistor_13 (.in(in_37), .out(transistor_13_out), .gate(in_43));
  Pull_Resistor pull_resistor_2 (.node(transistor_13_out));
  Demultiplexer demultiplexer_2 (.out0(out_76), .out1(out_78), .in(1'b1), .sel(in_47), .en(in_45));
  xor xor_2 (xor_2_out, in_51, in_53);
  and and_2 (and_2_out, in_51, in_53);
  Transistor #(.\type ("n")) transistor_14 (.in(transistor_5_out), .out(out_59), .gate(in_13));
  Transistor #(.\type ("n")) transistor_15 (.in(1'b1), .out(out_62), .gate(in_15));
  Transistor #(.\type ("n"), .gate("br")) transistor_16 (.in(1'b1), .out(out_62), .gate(in_17));
  Transistor transistor_17 (.in(transistor_8_out), .out(out_62), .gate(in_15));
  and and_3 (out_64, or_2_out, nand_1_out);
  Transistor #(.\type ("n"), .gate("br")) transistor_18 (.in(transistor_10_out), .out(out_68), .gate(in_33));
  Transistor #(.\type ("n")) transistor_19 (.in(transistor_12_out), .out(out_72), .gate(in_40));
  Transistor #(.\type ("n"), .gate("br")) transistor_20 (.in(transistor_13_out), .out(out_74), .gate(in_40));
  xor xor_3 (out_79, in_49, xor_2_out);
  and and_4 (and_4_out, in_49, xor_2_out);
  or or_3 (out_82, and_4_out, and_2_out);
  Counter #(.width(4), .max('hf)) counter_1 ();  // open: load, D, count, Q, carry, clk, clr
  D_Flip_Flop d_ff_1 ();  // open: clk, D, Q, Qn, preset, en, reset
  and and_5 (and_5_out, Load, Count);
  or or_4 (or_4_out, Load, Count);
  and and_6 (and_6_out, Load, ~Count);  // AND_Gate
  not not_2 (not_2_out, and_5_out);
  and and_7 (and_7_out, or_4_out, Clk);
  not not_3 (not_3_out, not_2_out);
  and and_8 (and_8_out, not_3_out, d_ff_2_qn);
  and and_9 (and_9_out, and_8_out, d_ff_3_qn);
  not not_4 (not_4_out, In);
  and and_10 (and_10_out, Clk_2, En);
  and and_11 (and_11_out, not_2_out, Data_out[0]);
  and and_12 (and_12_out, and_11_out, Data_out[1]);
  and and_13 (and_13_out, and_12_out, Data_out[2]);
  and and_14 (and_14_out, and_9_out, d_ff_4_qn);
  and and_15 (and_15_out, not_4_out, and_10_out);
  and and_16 (and_16_out, and_10_out, In);
  or or_5 (or_5_out, and_16_out, Reset_2);
  xor xor_4 (xor_4_out, Data_out[0], or_6_out);
  or or_6 (or_6_out, not_2_out, not_3_out);
  xor xor_5 (xor_5_out, Data_out[1], or_7_out);
  or or_7 (or_7_out, and_11_out, and_8_out);
  xor xor_6 (xor_6_out, Data_out[2], or_8_out);
  or or_8 (or_8_out, and_12_out, and_9_out);
  xor xor_7 (xor_7_out, Data_out[3], or_9_out);
  or or_9 (or_9_out, and_13_out, and_14_out);
  nor nor_1 (out_69, and_15_out, out_70);
  nor nor_2 (out_70, out_69, or_5_out);
  Multiplexer #(.disabled(0)) multiplexer_2 (
    .in0(xor_4_out), .in1(Data_in[0]), .out(multiplexer_2_out), .sel(and_6_out), .en(1'b1));
  Multiplexer #(.disabled(0)) multiplexer_3 (
    .in0(xor_5_out), .in1(Data_in[1]), .out(multiplexer_3_out), .sel(and_6_out), .en(1'b1));
  Multiplexer #(.disabled(0)) multiplexer_4 (
    .in0(xor_6_out), .in1(Data_in[2]), .out(multiplexer_4_out), .sel(and_6_out), .en(1'b1));
  Multiplexer #(.disabled(0)) multiplexer_5 (
    .in0(xor_7_out), .in1(Data_in[3]), .out(multiplexer_5_out), .sel(and_6_out), .en(1'b1));
  D_Flip_Flop d_ff_2 (
    .clk(and_7_out), .D(multiplexer_2_out), .Q(Data_out[0]), .Qn(d_ff_2_qn), .preset(1'b0), .en(or_4_out),
    .reset(Reset));
  D_Flip_Flop d_ff_3 (
    .clk(and_7_out), .D(multiplexer_3_out), .Q(Data_out[1]), .Qn(d_ff_3_qn), .preset(1'b0), .en(or_4_out),
    .reset(Reset));
  D_Flip_Flop d_ff_4 (
    .clk(and_7_out), .D(multiplexer_4_out), .Q(Data_out[2]), .Qn(d_ff_4_qn), .preset(1'b0), .en(or_4_out),
    .reset(Reset));
  D_Flip_Flop d_ff_5 (
    .clk(and_7_out), .D(multiplexer_5_out), .Q(Data_out[3]), .Qn(d_ff_5_qn), .preset(1'b0), .en(or_4_out),
    .reset(Reset));
endmodule

module Shader_Unit (
  input  [31:0] Operation,
  input  [31:0] Data_in,
  input  Load,
  input  Power,
  input  Clk,
  input  Reset,
  output Loaded_successfully,
  output Occured,
  output [3:0] Shader_Counter_condition,
  output [3:0] \priority 
);

  wire \alu_сpu_gpu_1_error , \alu_сpu_gpu_2_error , \alu_сpu_gpu_3_error , decoder_1_out0, decoder_1_out1,
       decoder_1_out2, decoder_1_out3, decoder_1_out4, decoder_1_out5, decoder_1_out6, decoder_1_out7,
       decoder_1_out15, not_1_out, or_1_out, or_2_out, or_3_out, or_4_out;
  wire [3:0] bit_extender_1_out;
  wire [5:0] decoder_1_out8;
  wire [22:0] register_2_q, register_4_q, register_6_q;
  wire [23:0] bit_extender_2_out;
  wire [31:0] _1_X_q, _1_Y_q, _2_X_q, _2Y_q, _3X_q, _3Y_q, \alu_сpu_gpu_1_c , \alu_сpu_gpu_2_c ,
       \alu_сpu_gpu_3_c , register_3_q, register_5_q, register_7_q, \Сolor_q ;
  wire [31:8] undriven, undriven_2, undriven_3;

  Counter #(.width(4), .max('hf)) counter_1 (
    .load(1'b0), .D(4'b0000), .count(or_1_out), .Q(Shader_Counter_condition), .clk(Clk), .clr(or_3_out));  // open: carry
  or or_1 (or_1_out, Load, Loaded_successfully);
  or or_2 (or_2_out, ~Power, Reset);  // OR_Gate
  Decoder #(.select(4), .disabled(0)) decoder_1 (
    .out0(decoder_1_out0), .out1(decoder_1_out1), .out2(decoder_1_out2), .out3(decoder_1_out3),
    .out4(decoder_1_out4), .out5(decoder_1_out5), .out6(decoder_1_out6), .out7(decoder_1_out7),
    .out8(decoder_1_out8[0]), .out9(decoder_1_out8[1]), .out10(decoder_1_out8[2]), .out11(decoder_1_out8[3]),
    .out12(decoder_1_out8[4]), .out13(decoder_1_out8[5]), .out14(Loaded_successfully),
    .out15(decoder_1_out15), .sel(Shader_Counter_condition), .en(Load));
  or or_3 (or_3_out, decoder_1_out15, or_2_out);
  not not_1 (not_1_out, Clk);
  Register #(.width(1)) register_1 (
    .D(Loaded_successfully), .en(not_1_out), .Q(Occured), .clk(not_1_out), .clr(or_2_out));
  Register #(.width(32)) _1_X (.D(Data_in), .en(decoder_1_out0), .Q(_1_X_q), .clk(Clk), .clr(or_2_out));
  Register #(.width(32)) _1_Y (.D(Data_in), .en(decoder_1_out1), .Q(_1_Y_q), .clk(Clk), .clr(or_2_out));
  Register #(.width(32)) \u_Сolor  (.D(Data_in), .en(decoder_1_out6), .Q(\Сolor_q ), .clk(Clk), .clr(or_2_out));
  Register #(.width(32)) _2_X (.D(Data_in), .en(decoder_1_out2), .Q(_2_X_q), .clk(Clk), .clr(or_2_out));
  Register #(.width(32)) _2Y (.D(Data_in), .en(decoder_1_out3), .Q(_2Y_q), .clk(Clk), .clr(or_2_out));
  Bit_Extender #(.in_width(32), .out_width(4)) bit_extender_1 (.in(Data_in), .out(bit_extender_1_out));
  Register #(.width(4)) u_priority (
    .D(bit_extender_1_out), .en(decoder_1_out7), .Q(\priority ), .clk(Clk), .clr(or_2_out));
  Bit_Extender #(.in_width(32), .out_width(24)) bit_extender_2 (.in(\Сolor_q ), .out(bit_extender_2_out));
  Register #(.width(32)) _3X (.D(Data_in), .en(decoder_1_out4), .Q(_3X_q), .clk(Clk), .clr(or_2_out));
  Register #(.width(32)) _3Y (.D(Data_in), .en(decoder_1_out5), .Q(_3Y_q), .clk(Clk), .clr(or_2_out));
  Register #(.width(23)) register_2 (
    .D(Data_in[22:0]), .en(decoder_1_out8[0]), .Q(register_2_q), .clk(Clk), .clr(or_2_out));
  \ALU__СPU_GPU  \alu_сpu_gpu_1  (
    .Power(Power), .Operation(register_2_q), .A({undriven_3, bit_extender_2_out[7:0]}), .B(register_3_q),
    .C(\alu_сpu_gpu_1_c ), .Error(\alu_сpu_gpu_1_error ));  // open: compare, Error_type
  Register #(.width(32)) register_3 (.D(Data_in), .en(decoder_1_out8[1]), .Q(register_3_q), .clk(Clk), .clr(or_2_out));
  Register #(.width(23)) register_4 (
    .D(Data_in[22:0]), .en(decoder_1_out8[2]), .Q(register_4_q), .clk(Clk), .clr(or_2_out));
  \ALU__СPU_GPU  \alu_сpu_gpu_2  (
    .Power(Power), .Operation(register_4_q), .A({undriven, bit_extender_2_out[15:8]}), .B(register_5_q),
    .C(\alu_сpu_gpu_2_c ), .Error(\alu_сpu_gpu_2_error ));  // open: compare, Error_type
  Register #(.width(32)) register_5 (.D(Data_in), .en(decoder_1_out8[3]), .Q(register_5_q), .clk(Clk), .clr(or_2_out));
  Register #(.width(23)) register_6 (
    .D(Data_in[22:0]), .en(decoder_1_out8[4]), .Q(register_6_q), .clk(Clk), .clr(or_2_out));
  \ALU__СPU_GPU  \alu_сpu_gpu_3  (
    .Power(Power), .Operation(register_6_q), .A({undriven_2, bit_extender_2_out[23:16]}), .B(register_7_q),
    .C(\alu_сpu_gpu_3_c ), .Error(\alu_сpu_gpu_3_error ));  // open: compare, Error_type
  Register #(.width(32)) register_7 (.D(Data_in), .en(decoder_1_out8[5]), .Q(register_7_q), .clk(Clk), .clr(or_2_out));
  or or_4 (or_4_out, \alu_сpu_gpu_1_error , \alu_сpu_gpu_2_error , \alu_сpu_gpu_3_error );
  Multiplexer #(.width(24), .disabled(0)) multiplexer_1 (
    .in0({\alu_сpu_gpu_3_c [7:0], \alu_сpu_gpu_2_c [7:0], \alu_сpu_gpu_1_c [7:0]}), .in1({24{1'b0}}),
    .sel(or_4_out), .en(Power));  // open: out
endmodule

module Shared_Registers (
  input  [31:0] Data_in,
  input  Power,
  input  [4:0] Choose_Register,
  input  Load,
  input  Reset_choosed_register,
  input  Reset_all,
  input  Clk,
  input  [4:0] \С1 ,
  input  [4:0] \С2 ,
  input  [4:0] \С3 ,
  output [31:0] Data_out__1,
  output [31:0] Data_out__2,
  output [31:0] Data_out__3
);

  wire and_1_out, and_2_out, and_3_out, and_4_out, and_5_out, and_6_out, and_7_out, and_8_out, and_9_out,
       and_10_out, and_11_out, and_12_out, and_13_out, and_14_out, and_15_out, and_16_out, and_17_out,
       and_18_out, and_19_out, and_20_out, and_21_out, and_22_out, and_23_out, and_24_out, and_25_out,
       and_26_out, and_27_out, and_28_out, and_29_out, and_30_out, and_31_out, and_32_out, and_33_out,
       and_34_out, and_35_out, and_36_out, and_37_out, and_38_out, and_39_out, and_40_out, and_41_out,
       and_42_out, and_43_out, and_44_out, and_45_out, and_46_out, and_47_out, and_48_out, and_49_out,
       and_50_out, and_51_out, and_52_out, and_53_out, and_54_out, and_55_out, and_56_out, and_57_out,
       and_58_out, and_59_out, and_60_out, and_61_out, and_62_out, and_63_out, and_64_out, decoder_1_out0,
       decoder_1_out1, decoder_1_out2, decoder_1_out3, decoder_1_out4, decoder_1_out5, decoder_1_out6,
       decoder_1_out7, decoder_1_out8, decoder_1_out9, decoder_1_out10, decoder_1_out11, decoder_1_out12,
       decoder_1_out13, decoder_1_out14, decoder_1_out15, decoder_1_out16, decoder_1_out17, decoder_1_out18,
       decoder_1_out19, decoder_1_out20, decoder_1_out21, decoder_1_out22, decoder_1_out23, decoder_1_out24,
       decoder_1_out25, decoder_1_out26, decoder_1_out27, decoder_1_out28, decoder_1_out29, decoder_1_out30,
       decoder_1_out31, or_1_out, or_2_out, or_3_out, or_4_out, or_5_out, or_6_out, or_7_out, or_8_out,
       or_9_out, or_10_out, or_11_out, or_12_out, or_13_out, or_14_out, or_15_out, or_16_out, or_17_out,
       or_18_out, or_19_out, or_20_out, or_21_out, or_22_out, or_23_out, or_24_out, or_25_out, or_26_out,
       or_27_out, or_28_out, or_29_out, or_30_out, or_31_out, or_32_out;
  wire [31:0] register_1_q, register_2_q, register_3_q, register_4_q, register_5_q, register_6_q,
       register_7_q, register_8_q, register_9_q, register_10_q, register_11_q, register_12_q, register_13_q,
       register_14_q, register_15_q, register_16_q, register_17_q, register_18_q, register_19_q,
       register_20_q, register_21_q, register_22_q, register_23_q, register_24_q, register_25_q,
       register_26_q, register_27_q, register_28_q, register_29_q, register_30_q, register_31_q,
       register_32_q, undriven;

  Pull_Resistor pull_resistor_1 (.node(Data_in));
  Pull_Resistor pull_resistor_2 (.node(Choose_Register));
  Pull_Resistor pull_resistor_3 (.node(Power));
  Pull_Resistor pull_resistor_4 (.node(Clk));
  Pull_Resistor pull_resistor_5 (.node(Reset_all));
  Pull_Resistor pull_resistor_6 (.node(\С1 ));
  Pull_Resistor pull_resistor_7 (.node(Reset_choosed_register));
  Pull_Resistor pull_resistor_8 (.node(\С2 ));
  Pull_Resistor pull_resistor_9 (.node(\С3 ));
  Pull_Resistor pull_resistor_10 (.node(Load));
  Decoder #(.select(5), .disabled(0)) decoder_1 (
    .out0(decoder_1_out0), .out1(decoder_1_out1), .out2(decoder_1_out2), .out3(decoder_1_out3),
    .out4(decoder_1_out4), .out5(decoder_1_out5), .out6(decoder_1_out6), .out7(decoder_1_out7),
    .out8(decoder_1_out8), .out9(decoder_1_out9), .out10(decoder_1_out10), .out11(decoder_1_out11),
    .out12(decoder_1_out12), .out13(decoder_1_out13), .out14(decoder_1_out14), .out15(decoder_1_out15),
    .out16(decoder_1_out16), .out17(decoder_1_out17), .out18(decoder_1_out18), .out19(decoder_1_out19),
    .out20(decoder_1_out20), .out21(decoder_1_out21), .out22(decoder_1_out22), .out23(decoder_1_out23),
    .out24(decoder_1_out24), .out25(decoder_1_out25), .out26(decoder_1_out26), .out27(decoder_1_out27),
    .out28(decoder_1_out28), .out29(decoder_1_out29), .out30(decoder_1_out30), .out31(decoder_1_out31),
    .sel(Choose_Register), .en(Power));
  and and_1 (and_1_out, Load, decoder_1_out0);
  and and_2 (and_2_out, decoder_1_out0, Reset_choosed_register);
  or or_1 (or_1_out, and_2_out, Reset_all);
  and and_3 (and_3_out, Load, decoder_1_out1);
  and and_4 (and_4_out, decoder_1_out1, Reset_choosed_register);
  or or_2 (or_2_out, and_4_out, Reset_all);
  and and_5 (and_5_out, Load, decoder_1_out2);
  and and_6 (and_6_out, decoder_1_out2, Reset_choosed_register);
  or or_3 (or_3_out, and_6_out, Reset_all);
  and and_7 (and_7_out, Load, decoder_1_out3);
  and and_8 (and_8_out, decoder_1_out3, Reset_choosed_register);
  or or_4 (or_4_out, and_8_out, Reset_all);
  and and_9 (and_9_out, Load, decoder_1_out4);
  and and_10 (and_10_out, decoder_1_out4, Reset_choosed_register);
  or or_5 (or_5_out, and_10_out, Reset_all);
  and and_11 (and_11_out, Load, decoder_1_out5);
  and and_12 (and_12_out, decoder_1_out5, Reset_choosed_register);
  or or_6 (or_6_out, and_12_out, Reset_all);
  and and_13 (and_13_out, Load, decoder_1_out6);
  and and_14 (and_14_out, decoder_1_out6, Reset_choosed_register);
  or or_7 (or_7_out, and_14_out, Reset_all);
  and and_15 (and_15_out, Load, decoder_1_out7);
  and and_16 (and_16_out, decoder_1_out7, Reset_choosed_register);
  or or_8 (or_8_out, and_16_out, Reset_all);
  and and_17 (and_17_out, Load, decoder_1_out8);
  and and_18 (and_18_out, decoder_1_out8, Reset_choosed_register);
  or or_9 (or_9_out, and_18_out, Reset_all);
  and and_19 (and_19_out, Load, decoder_1_out9);
  and and_20 (and_20_out, decoder_1_out9, Reset_choosed_register);
  or or_10 (or_10_out, and_20_out, Reset_all);
  and and_21 (and_21_out, Load, decoder_1_out10);
  and and_22 (and_22_out, decoder_1_out10, Reset_choosed_register);
  or or_11 (or_11_out, and_22_out, Reset_all);
  and and_23 (and_23_out, Load, decoder_1_out11);
  and and_24 (and_24_out, decoder_1_out11, Reset_choosed_register);
  or or_12 (or_12_out, and_24_out, Reset_all);
  and and_25 (and_25_out, Load, decoder_1_out12);
  and and_26 (and_26_out, decoder_1_out12, Reset_choosed_register);
  or or_13 (or_13_out, and_26_out, Reset_all);
  and and_27 (and_27_out, Load, decoder_1_out13);
  and and_28 (and_28_out, decoder_1_out13, Reset_choosed_register);
  or or_14 (or_14_out, and_28_out, Reset_all);
  and and_29 (and_29_out, Load, decoder_1_out14);
  and and_30 (and_30_out, decoder_1_out14, Reset_choosed_register);
  or or_15 (or_15_out, and_30_out, Reset_all);
  and and_31 (and_31_out, Load, decoder_1_out15);
  and and_32 (and_32_out, decoder_1_out15, Reset_choosed_register);
  or or_16 (or_16_out, and_32_out, Reset_all);
  and and_33 (and_33_out, Load, decoder_1_out16);
  and and_34 (and_34_out, decoder_1_out16, Reset_choosed_register);
  or or_17 (or_17_out, and_34_out, Reset_all);
  and and_35 (and_35_out, Load, decoder_1_out17);
  and and_36 (and_36_out, decoder_1_out17, Reset_choosed_register);
  or or_18 (or_18_out, and_36_out, Reset_all);
  and and_37 (and_37_out, Load, decoder_1_out18);
  and and_38 (and_38_out, decoder_1_out18, Reset_choosed_register);
  or or_19 (or_19_out, and_38_out, Reset_all);
  and and_39 (and_39_out, Load, decoder_1_out19);
  and and_40 (and_40_out, decoder_1_out19, Reset_choosed_register);
  or or_20 (or_20_out, and_40_out, Reset_all);
  and and_41 (and_41_out, Load, decoder_1_out20);
  and and_42 (and_42_out, decoder_1_out20, Reset_choosed_register);
  or or_21 (or_21_out, and_42_out, Reset_all);
  and and_43 (and_43_out, Load, decoder_1_out21);
  and and_44 (and_44_out, decoder_1_out21, Reset_choosed_register);
  or or_22 (or_22_out, and_44_out, Reset_all);
  and and_45 (and_45_out, Load, decoder_1_out22);
  and and_46 (and_46_out, decoder_1_out22, Reset_choosed_register);
  or or_23 (or_23_out, and_46_out, Reset_all);
  and and_47 (and_47_out, Load, decoder_1_out23);
  and and_48 (and_48_out, decoder_1_out23, Reset_choosed_register);
  or or_24 (or_24_out, and_48_out, Reset_all);
  and and_49 (and_49_out, Load, decoder_1_out24);
  and and_50 (and_50_out, decoder_1_out24, Reset_choosed_register);
  or or_25 (or_25_out, and_50_out, Reset_all);
  and and_51 (and_51_out, Load, decoder_1_out25);
  and and_52 (and_52_out, decoder_1_out25, Reset_choosed_register);
  or or_26 (or_26_out, and_52_out, Reset_all);
  and and_53 (and_53_out, Load, decoder_1_out26);
  and and_54 (and_54_out, decoder_1_out26, Reset_choosed_register);
  or or_27 (or_27_out, and_54_out, Reset_all);
  and and_55 (and_55_out, Load, decoder_1_out27);
  and and_56 (and_56_out, decoder_1_out27, Reset_choosed_register);
  or or_28 (or_28_out, and_56_out, Reset_all);
  and and_57 (and_57_out, Load, decoder_1_out28);
  and and_58 (and_58_out, decoder_1_out28, Reset_choosed_register);
  or or_29 (or_29_out, and_58_out, Reset_all);
  and and_59 (and_59_out, Load, decoder_1_out29);
  and and_60 (and_60_out, decoder_1_out29, Reset_choosed_register);
  or or_30 (or_30_out, and_60_out, Reset_all);
  and and_61 (and_61_out, Load, decoder_1_out30);
  and and_62 (and_62_out, decoder_1_out30, Reset_choosed_register);
  or or_31 (or_31_out, and_62_out, Reset_all);
  and and_63 (and_63_out, Load, decoder_1_out31);
  and and_64 (and_64_out, decoder_1_out31, Reset_choosed_register);
  or or_32 (or_32_out, and_64_out, Reset_all);
  Register #(.width(32)) register_1 (.D(Data_in), .en(and_1_out), .Q(register_1_q), .clk(Clk), .clr(or_1_out));
  Register #(.width(32)) register_2 (.D(Data_in), .en(and_3_out), .Q(register_2_q), .clk(Clk), .clr(or_2_out));
  Register #(.width(32)) register_3 (.D(Data_in), .en(and_5_out), .Q(register_3_q), .clk(Clk), .clr(or_3_out));
  Register #(.width(32)) register_4 (.D(Data_in), .en(and_7_out), .Q(register_4_q), .clk(Clk), .clr(or_4_out));
  Register #(.width(32)) register_5 (.D(Data_in), .en(and_9_out), .Q(register_5_q), .clk(Clk), .clr(or_5_out));
  Register #(.width(32)) register_6 (.D(Data_in), .en(and_11_out), .Q(register_6_q), .clk(Clk), .clr(or_6_out));
  Register #(.width(32)) register_7 (.D(Data_in), .en(and_13_out), .Q(register_7_q), .clk(Clk), .clr(or_7_out));
  Register #(.width(32)) register_8 (.D(Data_in), .en(and_15_out), .Q(register_8_q), .clk(Clk), .clr(or_8_out));
  Register #(.width(32)) register_9 (.D(undriven), .en(and_17_out), .Q(register_9_q), .clk(Clk), .clr(or_9_out));
  Register #(.width(32)) register_10 (.D(undriven), .en(and_19_out), .Q(register_10_q), .clk(Clk), .clr(or_10_out));
  Register #(.width(32)) register_11 (.D(undriven), .en(and_21_out), .Q(register_11_q), .clk(Clk), .clr(or_11_out));
  Register #(.width(32)) register_12 (.D(undriven), .en(and_23_out), .Q(register_12_q), .clk(Clk), .clr(or_12_out));
  Register #(.width(32)) register_13 (.D(undriven), .en(and_25_out), .Q(register_13_q), .clk(Clk), .clr(or_13_out));
  Register #(.width(32)) register_14 (.D(undriven), .en(and_27_out), .Q(register_14_q), .clk(Clk), .clr(or_14_out));
  Register #(.width(32)) register_15 (.D(undriven), .en(and_29_out), .Q(register_15_q), .clk(Clk), .clr(or_15_out));
  Register #(.width(32)) register_16 (.D(undriven), .en(and_31_out), .Q(register_16_q), .clk(Clk), .clr(or_16_out));
  Register #(.width(32)) register_17 (.D(Data_in), .en(and_33_out), .Q(register_17_q), .clk(Clk), .clr(or_17_out));
  Register #(.width(32)) register_18 (.D(Data_in), .en(and_35_out), .Q(register_18_q), .clk(Clk), .clr(or_18_out));
  Register #(.width(32)) register_19 (.D(Data_in), .en(and_37_out), .Q(register_19_q), .clk(Clk), .clr(or_19_out));
  Register #(.width(32)) register_20 (.D(Data_in), .en(and_39_out), .Q(register_20_q), .clk(Clk), .clr(or_20_out));
  Register #(.width(32)) register_21 (.D(Data_in), .en(and_41_out), .Q(register_21_q), .clk(Clk), .clr(or_21_out));
  Register #(.width(32)) register_22 (.D(Data_in), .en(and_43_out), .Q(register_22_q), .clk(Clk), .clr(or_22_out));
  Register #(.width(32)) register_23 (.D(Data_in), .en(and_45_out), .Q(register_23_q), .clk(Clk), .clr(or_23_out));
  Register #(.width(32)) register_24 (.D(Data_in), .en(and_47_out), .Q(register_24_q), .clk(Clk), .clr(or_24_out));
  Register #(.width(32)) register_25 (.D(Data_in), .en(and_49_out), .Q(register_25_q), .clk(Clk), .clr(or_25_out));
  Register #(.width(32)) register_26 (.D(Data_in), .en(and_51_out), .Q(register_26_q), .clk(Clk), .clr(or_26_out));
  Register #(.width(32)) register_27 (.D(Data_in), .en(and_53_out), .Q(register_27_q), .clk(Clk), .clr(or_27_out));
  Register #(.width(32)) register_28 (.D(Data_in), .en(and_55_out), .Q(register_28_q), .clk(Clk), .clr(or_28_out));
  Register #(.width(32)) register_29 (.D(Data_in), .en(and_57_out), .Q(register_29_q), .clk(Clk), .clr(or_29_out));
  Register #(.width(32)) register_30 (.D(Data_in), .en(and_59_out), .Q(register_30_q), .clk(Clk), .clr(or_30_out));
  Register #(.width(32)) register_31 (.D(Data_in), .en(and_61_out), .Q(register_31_q), .clk(Clk), .clr(or_31_out));
  Register #(.width(32)) register_32 (.D(Data_in), .en(and_63_out), .Q(register_32_q), .clk(Clk), .clr(or_32_out));
  Pull_Resistor pull_resistor_11 (.node(Data_out__1));
  Multiplexer #(.select(5), .width(32), .disabled(0), .enable("false")) multiplexer_1 (
    .in0(register_1_q), .in1(register_2_q), .in2(register_3_q), .in3(register_4_q), .in4(register_5_q),
    .in5(register_6_q), .in6(register_7_q), .in7(register_8_q), .in8(register_9_q), .in9(register_10_q),
    .in10(register_11_q), .in11(register_12_q), .in12(register_13_q), .in13(register_14_q),
    .in14(register_15_q), .in15(register_16_q), .in16(register_17_q), .in17(register_18_q),
    .in18(register_19_q), .in19(register_20_q), .in20(register_21_q), .in21(register_22_q),
    .in22(register_23_q), .in23(register_24_q), .in24(register_25_q), .in25(register_26_q),
    .in26(register_27_q), .in27(register_28_q), .in28(register_29_q), .in29(register_30_q),
    .in30(register_31_q), .in31(register_32_q), .out(Data_out__1), .sel(\С1 ));
  Pull_Resistor pull_resistor_12 (.node(Data_out__2));
  Multiplexer #(.select(5), .width(32), .disabled(0), .enable("false")) multiplexer_2 (
    .in0(register_1_q), .in1(register_2_q), .in2(register_3_q), .in3(register_4_q), .in4(register_5_q),
    .in5(register_6_q), .in6(register_7_q), .in7(register_8_q), .in8(register_9_q), .in9(register_10_q),
    .in10(register_11_q), .in11(register_12_q), .in12(register_13_q), .in13(register_14_q),
    .in14(register_15_q), .in15(register_16_q), .in16(register_17_q), .in17(register_18_q),
    .in18(register_19_q), .in19(register_20_q), .in20(register_21_q), .in21(register_22_q),
    .in22(register_23_q), .in23(register_24_q), .in24(register_25_q), .in25(register_26_q),
    .in26(register_27_q), .in27(register_28_q), .in28(register_29_q), .in29(register_30_q),
    .in30(register_31_q), .in31(register_32_q), .out(Data_out__2), .sel(\С2 ));
  Multiplexer #(.select(5), .width(32), .disabled(0), .enable("false")) multiplexer_3 (
    .in0(register_1_q), .in1(register_2_q), .in2(register_3_q), .in3(register_4_q), .in4(register_5_q),
    .in5(register_6_q), .in6(register_7_q), .in7(register_8_q), .in8(register_9_q), .in9(register_10_q),
    .in10(register_11_q), .in11(register_12_q), .in12(register_13_q), .in13(register_14_q),
    .in14(register_15_q), .in15(register_16_q), .in16(register_17_q), .in17(register_18_q),
    .in18(register_19_q), .in19(register_20_q), .in20(register_21_q), .in21(register_22_q),
    .in22(register_23_q), .in23(register_24_q), .in24(register_25_q), .in25(register_26_q),
    .in26(register_27_q), .in27(register_28_q), .in28(register_29_q), .in29(register_30_q),
    .in30(register_31_q), .in31(register_32_q), .out(Data_out__3), .sel(\С3 ));
  Pull_Resistor pull_resistor_13 (.node(Data_out__3));
endmodule

module Shader_Control_Unit (
  input  [31:0] Value,
  input  [31:0] Operatoin,
  input  Power,
  input  [5:0] Shader_Program,
  input  Clk,
  input  Reset,
  input  Eranch,
  input  Start,
  output Push,
  output Pop,
  output Reset_2,
  output [4:0] REG_1__SR,
  output [4:0] REG_2__SR,
  output [4:0] REG_3__SR,
  output [22:0] ALU_Control,
  output [15:0] PA,
  output [31:0] Value_2,
  output EN_REG,
  output Bisy,
  output Clk_2,
  output Power_2
);

  wire and_1_out, and_2_out, or_1_out, or_2_out, or_3_out, or_4_out, PC_carry, s_r_ff_1_qn;
  wire [9:0] bit_extender_2_out;
  wire [14:0] bit_extender_1_out;

  Pull_Resistor pull_resistor_1 (.node(Reset));
  Pull_Resistor pull_resistor_2 (.node(Clk));
  Pull_Resistor pull_resistor_3 (.node(Operatoin));
  Pull_Resistor pull_resistor_4 (.node(Shader_Program));
  Pull_Resistor pull_resistor_5 (.node(Eranch));
  Pull_Resistor pull_resistor_6 (.node(Power));
  Pull_Resistor pull_resistor_7 (.node(Value));
  Bit_Extender #(.in_width(32), .out_width(15)) bit_extender_1 (.in(Value), .out(bit_extender_1_out));
  Pull_Resistor pull_resistor_8 (.node(Start));
  Bit_Extender #(.in_width(32), .out_width(10)) bit_extender_2 (.in(Value), .out(bit_extender_2_out));
  or or_1 (or_1_out, Operatoin[31], Reset);
  and and_1 (and_1_out, Start, ~Bisy);  // AND_Gate
  S_R_Flip_Flop s_r_ff_1 (.Q(Bisy), .Qn(s_r_ff_1_qn), .preset(Start), .reset(or_2_out));  // open: S, clk, R, en
  or or_2 (or_2_out, or_1_out, ~Power, PC_carry);  // OR_Gate
  and and_2 (and_2_out, ~Eranch, Bisy);  // AND_Gate
  or or_3 (or_3_out, or_1_out, ~Power, and_1_out, PC_carry);  // OR_Gate
  Register #(.width(6)) u_Shader_Program (
    .D(Shader_Program), .en(and_1_out), .Q(PA[5:0]), .clk(and_1_out), .clr(or_1_out));
  Counter #(.width(10), .max('h3ff)) PC (
    .load(Eranch), .D(bit_extender_2_out), .count(and_2_out), .Q(PA[15:6]), .carry(PC_carry), .clk(Clk),
    .clr(or_3_out));
  Register #(.width(15)) register_1 (
    .D(bit_extender_1_out), .en(Operatoin[26]), .Q({REG_3__SR, REG_2__SR, REG_1__SR}), .clk(Operatoin[26]),
    .clr(or_4_out));
  or or_4 (or_4_out, Operatoin[27], s_r_ff_1_qn);

  assign ALU_Control = Operatoin[22:0];
  assign Clk_2 = Clk;
  assign EN_REG = Operatoin[25];
  assign Pop = Operatoin[24];
  assign Power_2 = Power;
  assign Push = Operatoin[23];
  assign Reset_2 = Operatoin[31];
  assign Value_2 = Value;
endmodule
module Shader_Program_Cashe (
  input  [31:0] Data_in,
  input  [31:0] Operation_in,
  input  [15:0] PA,
  input  [15:0] Adress,
  input  Clk,
  input  Reading,
  input  WR,
  input  Reset,
  input  Power,
  output [31:0] Data_out,
  output [31:0] Operation_out
);

  wire and_1_out, and_2_out, and_3_out, and_4_out, and_5_out, and_6_out, and_7_out, and_8_out, and_9_out,
       and_10_out, and_11_out, and_12_out, and_13_out, and_14_out, and_15_out, and_16_out, and_17_out,
       and_18_out, and_19_out, and_20_out, and_21_out, and_22_out, and_23_out, and_24_out, and_25_out,
       and_26_out, and_27_out, and_28_out, and_29_out, and_30_out, and_31_out, and_32_out, and_33_out,
       and_34_out, comparator_1_eq, comparator_2_eq, comparator_3_eq, comparator_4_eq, comparator_5_eq,
       comparator_6_eq, comparator_7_eq, comparator_8_eq, comparator_9_eq, comparator_10_eq,
       comparator_11_eq, comparator_12_eq, comparator_13_eq, comparator_14_eq, comparator_15_eq,
       comparator_16_eq, comparator_17_eq, comparator_18_eq, comparator_19_eq, comparator_20_eq,
       comparator_21_eq, comparator_22_eq, comparator_23_eq, comparator_24_eq, comparator_25_eq,
       comparator_26_eq, comparator_27_eq, comparator_28_eq, comparator_29_eq, comparator_30_eq,
       comparator_31_eq, comparator_32_eq, comparator_33_eq, comparator_34_eq, not_1_out, not_2_out,
       not_3_out, not_4_out, not_5_out, not_6_out, not_7_out, not_8_out, not_9_out, not_10_out, not_11_out,
       not_12_out, not_13_out, not_14_out, not_15_out, not_16_out, not_17_out, not_18_out, not_19_out,
       not_20_out, not_21_out, not_22_out, not_23_out, not_24_out, not_25_out, not_26_out, not_27_out,
       not_28_out, not_29_out, not_30_out, not_31_out, not_32_out, not_33_out, not_34_out, undriven_2,
       undriven_3, undriven_10, undriven_11, undriven_12;
  wire [3:0] undriven, undriven_4, undriven_6;
  wire [11:0] multiplexer_1_out, multiplexer_2_out, multiplexer_3_out, multiplexer_4_out, multiplexer_5_out,
       multiplexer_6_out, multiplexer_7_out, multiplexer_8_out, multiplexer_9_out, multiplexer_10_out,
       multiplexer_11_out, multiplexer_12_out, multiplexer_13_out, multiplexer_14_out, multiplexer_15_out,
       multiplexer_16_out, multiplexer_17_out, undriven_5, undriven_7;
  wire [31:0] controlled_buffer_33_out, controlled_buffer_34_out, ram_1_data, ram_2_data, ram_3_data,
       ram_4_data, ram_5_data, ram_6_data, ram_7_data, ram_8_data, ram_9_data, ram_10_data, ram_11_data,
       ram_12_data, ram_13_data, ram_14_data, ram_15_data, ram_16_data, ram_17_data, ram_18_data,
       ram_19_data, ram_20_data, ram_21_data, ram_22_data, ram_23_data, ram_24_data, ram_25_data,
       ram_26_data, ram_27_data, ram_28_data, ram_29_data, ram_30_data, ram_31_data, ram_32_data,
       ram_33_data, ram_34_data, undriven_8, undriven_9;

  Pull_Resistor pull_resistor_1 (.node(PA));
  Pull_Resistor pull_resistor_2 (.node(Clk));
  Pull_Resistor pull_resistor_3 (.node(Adress));
  Pull_Resistor pull_resistor_4 (.node(Power));
  Pull_Resistor pull_resistor_5 (.node(Reset));
  Pull_Resistor pull_resistor_6 (.node(Operation_in));
  Pull_Resistor pull_resistor_7 (.node(Reading));
  Pull_Resistor pull_resistor_8 (.node(WR));
  Pull_Resistor pull_resistor_9 (.node(Data_in));
  Comparator #(.width(4)) comparator_1 (.a(4'b0000), .b(PA[15:12]), .eq(comparator_1_eq));  // open: gt, lt
  Comparator #(.width(4)) comparator_2 (.a(4'b0000), .b(Adress[15:12]), .eq(comparator_2_eq));  // open: gt, lt
  Comparator #(.width(4)) comparator_3 (.a(4'b0001), .b(PA[15:12]), .eq(comparator_3_eq));  // open: gt, lt
  Comparator #(.width(4)) comparator_4 (.a(4'b0001), .b(Adress[15:12]), .eq(comparator_4_eq));  // open: gt, lt
  Comparator #(.width(4)) comparator_5 (.a(4'b0010), .b(PA[15:12]), .eq(comparator_5_eq));  // open: gt, lt
  Comparator #(.width(4)) comparator_6 (.a(4'b0010), .b(Adress[15:12]), .eq(comparator_6_eq));  // open: gt, lt
  Comparator #(.width(4)) comparator_7 (.a(4'b0011), .b(PA[15:12]), .eq(comparator_7_eq));  // open: gt, lt
  Comparator #(.width(4)) comparator_8 (.a(4'b0011), .b(Adress[15:12]), .eq(comparator_8_eq));  // open: gt, lt
  Comparator #(.width(4)) comparator_9 (.a(4'b0100), .b(PA[15:12]), .eq(comparator_9_eq));  // open: gt, lt
  Comparator #(.width(4)) comparator_10 (.a(4'b0100), .b(Adress[15:12]), .eq(comparator_10_eq));  // open: gt, lt
  Comparator #(.width(4)) comparator_11 (.a(4'b0101), .b(PA[15:12]), .eq(comparator_11_eq));  // open: gt, lt
  Comparator #(.width(4)) comparator_12 (.a(4'b0101), .b(Adress[15:12]), .eq(comparator_12_eq));  // open: gt, lt
  Comparator #(.width(4)) comparator_13 (.a(4'b0110), .b(PA[15:12]), .eq(comparator_13_eq));  // open: gt, lt
  Comparator #(.width(4)) comparator_14 (.a(4'b0110), .b(Adress[15:12]), .eq(comparator_14_eq));  // open: gt, lt
  Comparator #(.width(4)) comparator_15 (.a(4'b0111), .b(PA[15:12]), .eq(comparator_15_eq));  // open: gt, lt
  Comparator #(.width(4)) comparator_16 (.a(4'b0111), .b(Adress[15:12]), .eq(comparator_16_eq));  // open: gt, lt
  Comparator #(.width(4)) comparator_17 (.a(4'b1000), .b(PA[15:12]), .eq(comparator_17_eq));  // open: gt, lt
  Comparator #(.width(4)) comparator_18 (.a(4'b1000), .b(Adress[15:12]), .eq(comparator_18_eq));  // open: gt, lt
  Comparator #(.width(4)) comparator_19 (.a(4'b1001), .b(PA[15:12]), .eq(comparator_19_eq));  // open: gt, lt
  Comparator #(.width(4)) comparator_20 (.a(4'b1001), .b(Adress[15:12]), .eq(comparator_20_eq));  // open: gt, lt
  Comparator #(.width(4)) comparator_21 (.a(4'b1010), .b(PA[15:12]), .eq(comparator_21_eq));  // open: gt, lt
  Comparator #(.width(4)) comparator_22 (.a(4'b1010), .b(Adress[15:12]), .eq(comparator_22_eq));  // open: gt, lt
  Comparator #(.width(4)) comparator_23 (.a(4'b1011), .b(PA[15:12]), .eq(comparator_23_eq));  // open: gt, lt
  Comparator #(.width(4)) comparator_24 (.a(4'b1011), .b(Adress[15:12]), .eq(comparator_24_eq));  // open: gt, lt
  Comparator #(.width(4)) comparator_25 (.a(4'b1100), .b(PA[15:12]), .eq(comparator_25_eq));  // open: gt, lt
  Comparator #(.width(4)) comparator_26 (.a(4'b1100), .b(Adress[15:12]), .eq(comparator_26_eq));  // open: gt, lt
  Comparator #(.width(4)) comparator_27 (.a(4'b1101), .b(PA[15:12]), .eq(comparator_27_eq));  // open: gt, lt
  Comparator #(.width(4)) comparator_28 (.a(4'b1101), .b(Adress[15:12]), .eq(comparator_28_eq));  // open: gt, lt
  Comparator #(.width(4)) comparator_29 (.a(4'b1110), .b(PA[15:12]), .eq(comparator_29_eq));  // open: gt, lt
  Comparator #(.width(4)) comparator_30 (.a(4'b1110), .b(Adress[15:12]), .eq(comparator_30_eq));  // open: gt, lt
  Comparator #(.width(4)) comparator_31 (.a(4'b1111), .b(PA[15:12]), .eq(comparator_31_eq));  // open: gt, lt
  Comparator #(.width(4)) comparator_32 (.a(4'b1111), .b(Adress[15:12]), .eq(comparator_32_eq));  // open: gt, lt
  and and_1 (and_1_out, comparator_1_eq, Reading);
  and and_2 (and_2_out, WR, comparator_2_eq);
  and and_3 (and_3_out, comparator_3_eq, Reading);
  and and_4 (and_4_out, WR, comparator_4_eq);
  and and_5 (and_5_out, comparator_5_eq, Reading);
  and and_6 (and_6_out, WR, comparator_6_eq);
  and and_7 (and_7_out, comparator_7_eq, Reading);
  and and_8 (and_8_out, WR, comparator_8_eq);
  and and_9 (and_9_out, comparator_9_eq, Reading);
  and and_10 (and_10_out, WR, comparator_10_eq);
  and and_11 (and_11_out, comparator_11_eq, Reading);
  and and_12 (and_12_out, WR, comparator_12_eq);
  and and_13 (and_13_out, comparator_13_eq, Reading);
  and and_14 (and_14_out, WR, comparator_14_eq);
  and and_15 (and_15_out, comparator_15_eq, Reading);
  and and_16 (and_16_out, WR, comparator_16_eq);
  and and_17 (and_17_out, comparator_17_eq, Reading);
  and and_18 (and_18_out, WR, comparator_18_eq);
  and and_19 (and_19_out, comparator_19_eq, Reading);
  and and_20 (and_20_out, WR, comparator_20_eq);
  and and_21 (and_21_out, comparator_21_eq, Reading);
  and and_22 (and_22_out, WR, comparator_22_eq);
  and and_23 (and_23_out, comparator_23_eq, Reading);
  and and_24 (and_24_out, WR, comparator_24_eq);
  and and_25 (and_25_out, comparator_25_eq, Reading);
  and and_26 (and_26_out, WR, comparator_26_eq);
  and and_27 (and_27_out, comparator_27_eq, Reading);
  and and_28 (and_28_out, WR, comparator_28_eq);
  and and_29 (and_29_out, comparator_29_eq, Reading);
  and and_30 (and_30_out, WR, comparator_30_eq);
  and and_31 (and_31_out, comparator_31_eq, Reading);
  and and_32 (and_32_out, WR, comparator_32_eq);
  Multiplexer #(.width(12), .disabled(0), .enable("false")) multiplexer_1 (
    .in0(Adress[11:0]), .in1(PA[11:0]), .out(multiplexer_1_out), .sel(and_1_out));
  Multiplexer #(.width(12), .disabled(0), .enable("false")) multiplexer_2 (
    .in0(Adress[11:0]), .in1(PA[11:0]), .out(multiplexer_2_out), .sel(and_3_out));
  Multiplexer #(.width(12), .disabled(0), .enable("false")) multiplexer_3 (
    .in0(Adress[11:0]), .in1(PA[11:0]), .out(multiplexer_3_out), .sel(and_5_out));
  Multiplexer #(.width(12), .disabled(0), .enable("false")) multiplexer_4 (
    .in0(Adress[11:0]), .in1(PA[11:0]), .out(multiplexer_4_out), .sel(and_7_out));
  Multiplexer #(.width(12), .disabled(0), .enable("false")) multiplexer_5 (
    .in0(Adress[11:0]), .in1(PA[11:0]), .out(multiplexer_5_out), .sel(and_9_out));
  Multiplexer #(.width(12), .disabled(0), .enable("false")) multiplexer_6 (
    .in0(Adress[11:0]), .in1(PA[11:0]), .out(multiplexer_6_out), .sel(and_11_out));
  Multiplexer #(.width(12), .disabled(0), .enable("false")) multiplexer_7 (
    .in0(Adress[11:0]), .in1(PA[11:0]), .out(multiplexer_7_out), .sel(and_13_out));
  Multiplexer #(.width(12), .disabled(0), .enable("false")) multiplexer_8 (
    .in0(Adress[11:0]), .in1(PA[11:0]), .out(multiplexer_8_out), .sel(and_15_out));
  Multiplexer #(.width(12), .disabled(0), .enable("false")) multiplexer_9 (
    .in0(Adress[11:0]), .in1(PA[11:0]), .out(multiplexer_9_out), .sel(and_17_out));
  Multiplexer #(.width(12), .disabled(0), .enable("false")) multiplexer_10 (
    .in0(Adress[11:0]), .in1(PA[11:0]), .out(multiplexer_10_out), .sel(and_19_out));
  Multiplexer #(.width(12), .disabled(0), .enable("false")) multiplexer_11 (
    .in0(Adress[11:0]), .in1(PA[11:0]), .out(multiplexer_11_out), .sel(and_21_out));
  Multiplexer #(.width(12), .disabled(0), .enable("false")) multiplexer_12 (
    .in0(Adress[11:0]), .in1(PA[11:0]), .out(multiplexer_12_out), .sel(and_23_out));
  Multiplexer #(.width(12), .disabled(0), .enable("false")) multiplexer_13 (
    .in0(Adress[11:0]), .in1(PA[11:0]), .out(multiplexer_13_out), .sel(and_25_out));
  Multiplexer #(.width(12), .disabled(0), .enable("false")) multiplexer_14 (
    .in0(Adress[11:0]), .in1(PA[11:0]), .out(multiplexer_14_out), .sel(and_27_out));
  Multiplexer #(.width(12), .disabled(0), .enable("false")) multiplexer_15 (
    .in0(Adress[11:0]), .in1(PA[11:0]), .out(multiplexer_15_out), .sel(and_29_out));
  Multiplexer #(.width(12), .disabled(0), .enable("false")) multiplexer_16 (
    .in0(Adress[11:0]), .in1(PA[11:0]), .out(multiplexer_16_out), .sel(and_31_out));
  not not_1 (not_1_out, and_2_out);
  not not_2 (not_2_out, and_4_out);
  not not_3 (not_3_out, and_6_out);
  not not_4 (not_4_out, and_8_out);
  not not_5 (not_5_out, and_10_out);
  not not_6 (not_6_out, and_12_out);
  not not_7 (not_7_out, and_14_out);
  not not_8 (not_8_out, and_16_out);
  not not_9 (not_9_out, and_18_out);
  not not_10 (not_10_out, and_20_out);
  not not_11 (not_11_out, and_22_out);
  not not_12 (not_12_out, and_24_out);
  not not_13 (not_13_out, and_26_out);
  not not_14 (not_14_out, and_28_out);
  not not_15 (not_15_out, and_30_out);
  not not_16 (not_16_out, and_32_out);
  RAM #(.addrWidth(12), .dataWidth(32), .bus("separate")) ram_1 (
    .addr(multiplexer_1_out), .din(Data_in), .data(ram_1_data), .str(and_2_out), .sel(Power), .clk(Clk),
    .ld(not_1_out), .clr(Reset));
  RAM #(.addrWidth(12), .dataWidth(32), .bus("separate")) ram_2 (
    .addr(multiplexer_2_out), .din(Data_in), .data(ram_2_data), .str(and_4_out), .sel(Power), .clk(Clk),
    .ld(not_2_out), .clr(Reset));
  RAM #(.addrWidth(12), .dataWidth(32), .bus("separate")) ram_3 (
    .addr(multiplexer_3_out), .din(Data_in), .data(ram_3_data), .str(and_6_out), .sel(Power), .clk(Clk),
    .ld(not_3_out), .clr(Reset));
  RAM #(.addrWidth(12), .dataWidth(32), .bus("separate")) ram_4 (
    .addr(multiplexer_4_out), .din(Data_in), .data(ram_4_data), .str(and_8_out), .sel(Power), .clk(Clk),
    .ld(not_4_out), .clr(Reset));
  RAM #(.addrWidth(12), .dataWidth(32), .bus("separate")) ram_5 (
    .addr(multiplexer_5_out), .din(Data_in), .data(ram_5_data), .str(and_10_out), .sel(Power), .clk(Clk),
    .ld(not_5_out), .clr(Reset));
  RAM #(.addrWidth(12), .dataWidth(32), .bus("separate")) ram_6 (
    .addr(multiplexer_6_out), .din(Data_in), .data(ram_6_data), .str(and_12_out), .sel(Power), .clk(Clk),
    .ld(not_6_out), .clr(Reset));
  RAM #(.addrWidth(12), .dataWidth(32), .bus("separate")) ram_7 (
    .addr(multiplexer_7_out), .din(Data_in), .data(ram_7_data), .str(and_14_out), .sel(Power), .clk(Clk),
    .ld(not_7_out), .clr(Reset));
  RAM #(.addrWidth(12), .dataWidth(32), .bus("separate")) ram_8 (
    .addr(multiplexer_8_out), .din(Data_in), .data(ram_8_data), .str(and_16_out), .sel(Power), .clk(Clk),
    .ld(not_8_out), .clr(Reset));
  RAM #(.addrWidth(12), .dataWidth(32), .bus("separate")) ram_9 (
    .addr(multiplexer_9_out), .din(Data_in), .data(ram_9_data), .str(and_18_out), .sel(Power), .clk(Clk),
    .ld(not_9_out), .clr(Reset));
  RAM #(.addrWidth(12), .dataWidth(32), .bus("separate")) ram_10 (
    .addr(multiplexer_10_out), .din(Data_in), .data(ram_10_data), .str(and_20_out), .sel(Power), .clk(Clk),
    .ld(not_10_out), .clr(Reset));
  RAM #(.addrWidth(12), .dataWidth(32), .bus("separate")) ram_11 (
    .addr(multiplexer_11_out), .din(Data_in), .data(ram_11_data), .str(and_22_out), .sel(Power), .clk(Clk),
    .ld(not_11_out), .clr(Reset));
  RAM #(.addrWidth(12), .dataWidth(32), .bus("separate")) ram_12 (
    .addr(multiplexer_12_out), .din(Data_in), .data(ram_12_data), .str(and_24_out), .sel(Power), .clk(Clk),
    .ld(not_12_out), .clr(Reset));
  RAM #(.addrWidth(12), .dataWidth(32), .bus("separate")) ram_13 (
    .addr(multiplexer_13_out), .din(Data_in), .data(ram_13_data), .str(and_26_out), .sel(Power), .clk(Clk),
    .ld(not_13_out), .clr(Reset));
  RAM #(.addrWidth(12), .dataWidth(32), .bus("separate")) ram_14 (
    .addr(multiplexer_14_out), .din(Data_in), .data(ram_14_data), .str(and_28_out), .sel(Power), .clk(Clk),
    .ld(not_14_out), .clr(Reset));
  RAM #(.addrWidth(12), .dataWidth(32), .bus("separate")) ram_15 (
    .addr(multiplexer_15_out), .din(Data_in), .data(ram_15_data), .str(and_30_out), .sel(Power), .clk(Clk),
    .ld(not_15_out), .clr(Reset));
  RAM #(.addrWidth(12), .dataWidth(32), .bus("separate")) ram_16 (
    .addr(multiplexer_16_out), .din(Data_in), .data(ram_16_data), .str(and_32_out), .sel(Power), .clk(Clk),
    .ld(not_16_out), .clr(Reset));
  not not_17 (not_17_out, and_2_out);
  not not_18 (not_18_out, and_4_out);
  not not_19 (not_19_out, and_6_out);
  not not_20 (not_20_out, and_8_out);
  not not_21 (not_21_out, and_10_out);
  not not_22 (not_22_out, and_12_out);
  not not_23 (not_23_out, and_14_out);
  not not_24 (not_24_out, and_16_out);
  not not_25 (not_25_out, and_18_out);
  not not_26 (not_26_out, and_20_out);
  not not_27 (not_27_out, and_22_out);
  not not_28 (not_28_out, and_24_out);
  not not_29 (not_29_out, and_26_out);
  not not_30 (not_30_out, and_28_out);
  not not_31 (not_31_out, and_30_out);
  not not_32 (not_32_out, and_32_out);
  assign Data_out = and_1_out ? ram_1_data : 32'bz;  // Controlled_Buffer controlled_buffer_1
  RAM #(.addrWidth(12), .dataWidth(32), .bus("separate")) ram_17 (
    .din(Operation_in), .data(ram_17_data), .str(and_2_out), .sel(Power), .clk(Clk), .ld(not_17_out),
    .clr(Reset));  // open: addr
  assign Operation_out = and_1_out ? ram_17_data : 32'bz;  // Controlled_Buffer controlled_buffer_2
  assign Data_out = and_3_out ? ram_2_data : 32'bz;  // Controlled_Buffer controlled_buffer_3
  assign Operation_out = and_3_out ? ram_18_data : 32'bz;  // Controlled_Buffer controlled_buffer_4
  RAM #(.addrWidth(12), .dataWidth(32), .bus("separate")) ram_18 (
    .din(Operation_in), .data(ram_18_data), .str(and_4_out), .sel(Power), .clk(Clk), .ld(not_18_out),
    .clr(Reset));  // open: addr
  assign Data_out = and_5_out ? ram_3_data : 32'bz;  // Controlled_Buffer controlled_buffer_5
  RAM #(.addrWidth(12), .dataWidth(32), .bus("separate")) ram_19 (
    .din(Operation_in), .data(ram_19_data), .str(and_6_out), .sel(Power), .clk(Clk), .ld(not_19_out),
    .clr(Reset));  // open: addr
  assign Operation_out = and_5_out ? ram_19_data : 32'bz;  // Controlled_Buffer controlled_buffer_6
  assign Data_out = and_7_out ? ram_4_data : 32'bz;  // Controlled_Buffer controlled_buffer_7
  RAM #(.addrWidth(12), .dataWidth(32), .bus("separate")) ram_20 (
    .din(Operation_in), .data(ram_20_data), .str(and_8_out), .sel(Power), .clk(Clk), .ld(not_20_out),
    .clr(Reset));  // open: addr
  assign Operation_out = and_7_out ? ram_20_data : 32'bz;  // Controlled_Buffer controlled_buffer_8
  assign Data_out = and_9_out ? ram_5_data : 32'bz;  // Controlled_Buffer controlled_buffer_9
  RAM #(.addrWidth(12), .dataWidth(32), .bus("separate")) ram_21 (
    .din(Operation_in), .data(ram_21_data), .str(and_10_out), .sel(Power), .clk(Clk), .ld(not_21_out),
    .clr(Reset));  // open: addr
  assign Operation_out = and_9_out ? ram_21_data : 32'bz;  // Controlled_Buffer controlled_buffer_10
  assign Data_out = and_11_out ? ram_6_data : 32'bz;  // Controlled_Buffer controlled_buffer_11
  assign Operation_out = and_11_out ? ram_22_data : 32'bz;  // Controlled_Buffer controlled_buffer_12
  RAM #(.addrWidth(12), .dataWidth(32), .bus("separate")) ram_22 (
    .din(Operation_in), .data(ram_22_data), .str(and_12_out), .sel(Power), .clk(Clk), .ld(not_22_out),
    .clr(Reset));  // open: addr
  assign Data_out = and_13_out ? ram_7_data : 32'bz;  // Controlled_Buffer controlled_buffer_13
  RAM #(.addrWidth(12), .dataWidth(32), .bus("separate")) ram_23 (
    .din(Operation_in), .data(ram_23_data), .str(and_14_out), .sel(Power), .clk(Clk), .ld(not_23_out),
    .clr(Reset));  // open: addr
  assign Operation_out = and_13_out ? ram_23_data : 32'bz;  // Controlled_Buffer controlled_buffer_14
  assign Data_out = and_15_out ? ram_8_data : 32'bz;  // Controlled_Buffer controlled_buffer_15
  assign Operation_out = and_15_out ? ram_24_data : 32'bz;  // Controlled_Buffer controlled_buffer_16
  RAM #(.addrWidth(12), .dataWidth(32), .bus("separate")) ram_24 (
    .din(Operation_in), .data(ram_24_data), .str(and_16_out), .sel(Power), .clk(Clk), .ld(not_24_out),
    .clr(Reset));  // open: addr
  assign Data_out = and_17_out ? ram_9_data : 32'bz;  // Controlled_Buffer controlled_buffer_17
  assign Operation_out = and_17_out ? ram_25_data : 32'bz;  // Controlled_Buffer controlled_buffer_18
  RAM #(.addrWidth(12), .dataWidth(32), .bus("separate")) ram_25 (
    .din(Operation_in), .data(ram_25_data), .str(and_18_out), .sel(Power), .clk(Clk), .ld(not_25_out),
    .clr(Reset));  // open: addr
  assign Data_out = and_19_out ? ram_10_data : 32'bz;  // Controlled_Buffer controlled_buffer_19
  RAM #(.addrWidth(12), .dataWidth(32), .bus("separate")) ram_26 (
    .din(Operation_in), .data(ram_26_data), .str(and_20_out), .sel(Power), .clk(Clk), .ld(not_26_out),
    .clr(Reset));  // open: addr
  assign Operation_out = and_19_out ? ram_26_data : 32'bz;  // Controlled_Buffer controlled_buffer_20
  assign Data_out = and_21_out ? ram_11_data : 32'bz;  // Controlled_Buffer controlled_buffer_21
  assign Operation_out = and_21_out ? ram_27_data : 32'bz;  // Controlled_Buffer controlled_buffer_22
  RAM #(.addrWidth(12), .dataWidth(32), .bus("separate")) ram_27 (
    .din(Operation_in), .data(ram_27_data), .str(and_22_out), .sel(Power), .clk(Clk), .ld(not_27_out),
    .clr(Reset));  // open: addr
  assign Data_out = and_23_out ? ram_12_data : 32'bz;  // Controlled_Buffer controlled_buffer_23
  assign Operation_out = and_23_out ? ram_28_data : 32'bz;  // Controlled_Buffer controlled_buffer_24
  RAM #(.addrWidth(12), .dataWidth(32), .bus("separate")) ram_28 (
    .din(Operation_in), .data(ram_28_data), .str(and_24_out), .sel(Power), .clk(Clk), .ld(not_28_out),
    .clr(Reset));  // open: addr
  assign Data_out = and_25_out ? ram_13_data : 32'bz;  // Controlled_Buffer controlled_buffer_25
  assign Operation_out = and_25_out ? ram_29_data : 32'bz;  // Controlled_Buffer controlled_buffer_26
  RAM #(.addrWidth(12), .dataWidth(32), .bus("separate")) ram_29 (
    .din(Operation_in), .data(ram_29_data), .str(and_26_out), .sel(Power), .clk(Clk), .ld(not_29_out),
    .clr(Reset));  // open: addr
  assign Data_out = and_27_out ? ram_14_data : 32'bz;  // Controlled_Buffer controlled_buffer_27
  assign Operation_out = and_27_out ? ram_30_data : 32'bz;  // Controlled_Buffer controlled_buffer_28
  RAM #(.addrWidth(12), .dataWidth(32), .bus("separate")) ram_30 (
    .din(Operation_in), .data(ram_30_data), .str(and_28_out), .sel(Power), .clk(Clk), .ld(not_30_out),
    .clr(Reset));  // open: addr
  assign Data_out = and_29_out ? ram_15_data : 32'bz;  // Controlled_Buffer controlled_buffer_29
  RAM #(.addrWidth(12), .dataWidth(32), .bus("separate")) ram_31 (
    .din(Operation_in), .data(ram_31_data), .str(and_30_out), .sel(Power), .clk(Clk), .ld(not_31_out),
    .clr(Reset));  // open: addr
  assign Operation_out = and_29_out ? ram_31_data : 32'bz;  // Controlled_Buffer controlled_buffer_30
  assign Data_out = and_31_out ? ram_16_data : 32'bz;  // Controlled_Buffer controlled_buffer_31
  assign Operation_out = and_31_out ? ram_32_data : 32'bz;  // Controlled_Buffer controlled_buffer_32
  RAM #(.addrWidth(12), .dataWidth(32), .bus("separate")) ram_32 (
    .din(Operation_in), .data(ram_32_data), .str(and_32_out), .sel(Power), .clk(Clk), .ld(not_32_out),
    .clr(Reset));  // open: addr
  Pull_Resistor pull_resistor_10 (.node(Operation_out));
  Pull_Resistor pull_resistor_11 (.node(Data_out));
  Comparator #(.width(4)) comparator_33 (.a(undriven), .b(undriven_6), .eq(comparator_33_eq));  // open: gt, lt
  Comparator #(.width(4)) comparator_34 (.a(undriven), .b(undriven_4), .eq(comparator_34_eq));  // open: gt, lt
  Multiplexer #(.width(12), .disabled(0), .enable("false")) multiplexer_17 (
    .in0(undriven_5), .in1(undriven_7), .out(multiplexer_17_out), .sel(and_33_out));
  and and_33 (and_33_out, comparator_33_eq, undriven_3);
  and and_34 (and_34_out, undriven_2, comparator_34_eq);
  RAM #(.addrWidth(12), .dataWidth(32), .bus("separate")) ram_33 (
    .addr(multiplexer_17_out), .din(undriven_9), .data(ram_33_data), .str(and_34_out), .sel(undriven_10),
    .clk(undriven_11), .ld(not_33_out), .clr(undriven_12));
  not not_33 (not_33_out, and_34_out);
  not not_34 (not_34_out, and_34_out);
  assign controlled_buffer_33_out = and_33_out ? ram_33_data : 32'bz;  // Controlled_Buffer controlled_buffer_33
  RAM #(.addrWidth(12), .dataWidth(32), .bus("separate")) ram_34 (
    .din(undriven_8), .data(ram_34_data), .str(and_34_out), .sel(undriven_10), .clk(undriven_11),
    .ld(not_34_out), .clr(undriven_12));  // open: addr
  assign controlled_buffer_34_out = and_33_out ? ram_34_data : 32'bz;  // Controlled_Buffer controlled_buffer_34

  // Notes on the sheet:
  //   Data
  //   Operation
endmodule

module DDR_Shader_Register (
  input  [4:0] Adress_1,
  input  [4:0] Adress_2,
  input  Power,
  input  Reset,
  input  Clk,
  input  WE_1,
  input  WE_2,
  input  [31:0] Data_in_1,
  input  [31:0] Data_in_2,
  output [31:0] Data_out
);

  wire and_1_out, and_2_out, not_1_out, or_1_out;
  wire [4:0] multiplexer_1_out;
  wire [31:0] controlled_buffer_1_out, ram_1_data;

  and and_1 (and_1_out, Clk, WE_1);
  and and_2 (and_2_out, ~Clk, WE_2);  // AND_Gate
  assign controlled_buffer_1_out = and_1_out ? Data_in_1 : 32'bz;  // Controlled_Buffer controlled_buffer_1
  assign controlled_buffer_1_out = and_2_out ? Data_in_2 : 32'bz;  // Controlled_Buffer controlled_buffer_2
  Multiplexer #(.width(5)) multiplexer_1 (
    .in0(Adress_1), .in1(Adress_2), .out(multiplexer_1_out), .sel(Clk), .en(Power));
  or or_1 (or_1_out, and_1_out, and_2_out);
  not not_1 (not_1_out, and_2_out);
  RAM #(.addrWidth(5), .dataWidth(32), .bus("separate")) ram_1 (
    .addr(multiplexer_1_out), .din(controlled_buffer_1_out), .data(ram_1_data), .str(or_1_out), .sel(Power),
    .clk(or_1_out), .ld(not_1_out), .clr(Reset));
  Register #(.width(32)) register_1 (.D(ram_1_data), .en(Power), .Q(Data_out), .clk(Clk), .clr(Reset));
  Pull_Resistor pull_resistor_1 (.node(Data_out));
endmodule

module File_Register__Cash (
  input  Load_Reg,
  input  [31:0] Data_in,
  input  Clk,
  input  Reset,
  input  Power,
  output [31:0] Data_out
);

  wire not_1_out;
  wire [31:0] multiplexer_1_out, multiplexer_2_out, register_1_q, register_2_q;

  Pull_Resistor pull_resistor_1 (.node(Load_Reg));
  Pull_Resistor pull_resistor_2 (.node(Reset));
  Pull_Resistor pull_resistor_3 (.node(Power));
  Pull_Resistor pull_resistor_4 (.node(Data_in));
  Pull_Resistor pull_resistor_5 (.node(Clk));
  Multiplexer #(.width(32), .disabled(0)) multiplexer_1 (
    .in0(register_2_q), .in1(Data_in), .out(multiplexer_1_out), .sel(Load_Reg), .en(Power));
  not not_1 (not_1_out, Clk);
  Multiplexer #(.width(32), .disabled(0)) multiplexer_2 (
    .in0(Data_in), .in1(register_1_q), .out(multiplexer_2_out), .sel(Load_Reg), .en(Power));
  Register #(.width(32)) register_1 (.D(multiplexer_1_out), .en(Power), .Q(register_1_q), .clk(not_1_out), .clr(Reset));
  Multiplexer #(.width(32), .disabled(0)) multiplexer_3 (
    .in0(register_1_q), .in1(register_2_q), .out(Data_out), .sel(Clk), .en(Power));
  Register #(.width(32)) register_2 (.D(multiplexer_2_out), .en(Power), .Q(register_2_q), .clk(Clk), .clr(Reset));
endmodule

module empty_spaces_counter__ESC (
  input  [31:0] in_1,
  input  [4:0] Counter_in,
  input  Load,
  output [4:0] Counter_out,
  output Count,
  output Load_2
);

  wire and_1_out, and_2_out, and_3_out, and_4_out, and_5_out, and_6_out, and_7_out, and_8_out, and_9_out,
       and_10_out, and_11_out, and_12_out, and_13_out, and_14_out, and_15_out, and_16_out, and_17_out,
       and_18_out, and_19_out, and_20_out, and_21_out, and_22_out, and_23_out, and_24_out, and_25_out,
       and_26_out, and_27_out, and_28_out, and_29_out, and_30_out, and_31_out, and_32_out, and_33_out,
       and_34_out, and_35_out, and_36_out, and_37_out, and_38_out, and_39_out, and_40_out, and_41_out,
       and_42_out, and_43_out, and_44_out, and_45_out, and_46_out, and_47_out, and_48_out, and_49_out,
       and_50_out, and_51_out, and_52_out, and_53_out, and_54_out, and_55_out, and_56_out, and_57_out,
       and_58_out, and_59_out, and_60_out, bitselector_2_out, bitselector_3_out, bitselector_4_out,
       bitselector_5_out, bitselector_6_out, bitselector_7_out, bitselector_8_out, bitselector_9_out,
       bitselector_10_out, bitselector_11_out, bitselector_12_out, bitselector_13_out, bitselector_14_out,
       bitselector_15_out, bitselector_16_out, bitselector_17_out, bitselector_18_out, bitselector_19_out,
       bitselector_20_out, bitselector_21_out, bitselector_22_out, bitselector_23_out, bitselector_24_out,
       bitselector_25_out, bitselector_26_out, bitselector_27_out, bitselector_28_out, bitselector_29_out,
       bitselector_30_out, bitselector_31_out, bitselector_32_out, comparator_1_lt, comparator_2_lt,
       comparator_3_lt, comparator_4_lt, comparator_5_lt, comparator_6_lt, comparator_7_lt, comparator_8_lt,
       comparator_9_lt, comparator_10_lt, comparator_11_lt, comparator_12_lt, comparator_13_lt,
       comparator_14_lt, comparator_15_lt, comparator_16_lt, comparator_17_lt, comparator_18_lt,
       comparator_19_lt, comparator_20_lt, comparator_21_lt, comparator_22_lt, comparator_23_lt,
       comparator_24_lt, comparator_25_lt, comparator_26_lt, comparator_27_lt, comparator_28_lt,
       comparator_29_lt, comparator_30_lt, comparator_31_lt, not_1_out;
  wire [4:0] adder_1_out, adder_2_out, adder_3_out, adder_4_out, adder_5_out, adder_6_out, adder_7_out,
       adder_8_out, adder_9_out, adder_10_out, adder_11_out, adder_12_out, adder_13_out, adder_14_out,
       adder_15_out, adder_16_out, adder_17_out, adder_18_out, adder_19_out, adder_20_out, adder_21_out,
       adder_22_out, adder_23_out, adder_24_out, adder_25_out, adder_26_out, adder_27_out, adder_28_out,
       adder_29_out, adder_30_out, adder_31_out, adder_32_out, adder_33_out, bitadder_1_out;
  wire [31:0] multiplexer_1_out, multiplexer_2_out, multiplexer_3_out, multiplexer_4_out, multiplexer_5_out,
       multiplexer_6_out, multiplexer_7_out, multiplexer_8_out, multiplexer_9_out, multiplexer_10_out,
       multiplexer_11_out, multiplexer_12_out, multiplexer_13_out, multiplexer_14_out, multiplexer_15_out,
       multiplexer_16_out, multiplexer_17_out, multiplexer_18_out, multiplexer_19_out, multiplexer_20_out,
       multiplexer_21_out, multiplexer_22_out, multiplexer_23_out, multiplexer_24_out, multiplexer_25_out,
       multiplexer_26_out, multiplexer_27_out, multiplexer_28_out, multiplexer_29_out, multiplexer_30_out;

  Pull_Resistor pull_resistor_1 (.node(in_1));
  Pull_Resistor pull_resistor_2 (.node(Counter_in));
  BitSelector #(.width(32)) bitselector_1 (.in(in_1), .out(Count), .sel(adder_1_out));
  Adder #(.width(5)) adder_1 (.a(Counter_in), .b(5'b00001), .out(adder_1_out));  // open: cin, cout
  Comparator #(.width(5), .mode("unsigned")) comparator_1 (
    .a(Counter_in), .b({5{1'b1}}), .lt(comparator_1_lt));  // open: gt, eq
  Adder #(.width(5)) adder_2 (.a(Counter_in), .b(5'b00001), .out(adder_2_out));  // open: cin, cout
  Comparator #(.width(5), .mode("unsigned")) comparator_2 (
    .a(Counter_in), .b(5'b11110), .lt(comparator_2_lt));  // open: gt, eq
  Multiplexer #(.width(32), .disabled(0), .enable("false")) multiplexer_1 (
    .in0({32{1'b1}}), .in1(in_1), .out(multiplexer_1_out), .sel(and_1_out));
  Adder #(.width(5)) adder_3 (.a(Counter_in), .b(5'b00010), .out(adder_3_out));  // open: cin, cout
  Comparator #(.width(5), .mode("unsigned")) comparator_3 (
    .a(Counter_in), .b(5'b11101), .lt(comparator_3_lt));  // open: gt, eq
  Multiplexer #(.width(32), .disabled(0), .enable("false")) multiplexer_2 (
    .in0({32{1'b1}}), .in1(in_1), .out(multiplexer_2_out), .sel(and_4_out));
  Adder #(.width(5)) adder_4 (.a(Counter_in), .b(5'b00011), .out(adder_4_out));  // open: cin, cout
  Comparator #(.width(5), .mode("unsigned")) comparator_4 (
    .a(Counter_in), .b(5'b11100), .lt(comparator_4_lt));  // open: gt, eq
  Multiplexer #(.width(32), .disabled(0), .enable("false")) multiplexer_3 (
    .in0({32{1'b1}}), .in1(in_1), .out(multiplexer_3_out), .sel(and_6_out));
  Adder #(.width(5)) adder_5 (.a(Counter_in), .b(5'b00100), .out(adder_5_out));  // open: cin, cout
  Comparator #(.width(5), .mode("unsigned")) comparator_5 (
    .a(Counter_in), .b(5'b11011), .lt(comparator_5_lt));  // open: gt, eq
  Multiplexer #(.width(32), .disabled(0), .enable("false")) multiplexer_4 (
    .in0({32{1'b1}}), .in1(in_1), .out(multiplexer_4_out), .sel(and_8_out));
  Adder #(.width(5)) adder_6 (.a(Counter_in), .b(5'b00101), .out(adder_6_out));  // open: cin, cout
  Comparator #(.width(5), .mode("unsigned")) comparator_6 (
    .a(Counter_in), .b(5'b11010), .lt(comparator_6_lt));  // open: gt, eq
  Multiplexer #(.width(32), .disabled(0), .enable("false")) multiplexer_5 (
    .in0({32{1'b1}}), .in1(in_1), .out(multiplexer_5_out), .sel(and_10_out));
  Adder #(.width(5)) adder_7 (.a(Counter_in), .b(5'b00110), .out(adder_7_out));  // open: cin, cout
  Comparator #(.width(5), .mode("unsigned")) comparator_7 (
    .a(Counter_in), .b(5'b11001), .lt(comparator_7_lt));  // open: gt, eq
  Multiplexer #(.width(32), .disabled(0), .enable("false")) multiplexer_6 (
    .in0({32{1'b1}}), .in1(in_1), .out(multiplexer_6_out), .sel(and_12_out));
  Adder #(.width(5)) adder_8 (.a(Counter_in), .b(5'b00111), .out(adder_8_out));  // open: cin, cout
  Comparator #(.width(5), .mode("unsigned")) comparator_8 (
    .a(Counter_in), .b(5'b11000), .lt(comparator_8_lt));  // open: gt, eq
  Multiplexer #(.width(32), .disabled(0), .enable("false")) multiplexer_7 (
    .in0({32{1'b1}}), .in1(in_1), .out(multiplexer_7_out), .sel(and_14_out));
  Adder #(.width(5)) adder_9 (.a(Counter_in), .b(5'b01000), .out(adder_9_out));  // open: cin, cout
  Comparator #(.width(5), .mode("unsigned")) comparator_9 (
    .a(Counter_in), .b(5'b10111), .lt(comparator_9_lt));  // open: gt, eq
  Multiplexer #(.width(32), .disabled(0), .enable("false")) multiplexer_8 (
    .in0({32{1'b1}}), .in1(in_1), .out(multiplexer_8_out), .sel(and_16_out));
  Adder #(.width(5)) adder_10 (.a(Counter_in), .b(5'b01001), .out(adder_10_out));  // open: cin, cout
  Comparator #(.width(5), .mode("unsigned")) comparator_10 (
    .a(Counter_in), .b(5'b10110), .lt(comparator_10_lt));  // open: gt, eq
  Multiplexer #(.width(32), .disabled(0), .enable("false")) multiplexer_9 (
    .in0({32{1'b1}}), .in1(in_1), .out(multiplexer_9_out), .sel(and_18_out));
  Adder #(.width(5)) adder_11 (.a(Counter_in), .b(5'b01010), .out(adder_11_out));  // open: cin, cout
  Comparator #(.width(5), .mode("unsigned")) comparator_11 (
    .a(Counter_in), .b(5'b10101), .lt(comparator_11_lt));  // open: gt, eq
  Multiplexer #(.width(32), .disabled(0), .enable("false")) multiplexer_10 (
    .in0({32{1'b1}}), .in1(in_1), .out(multiplexer_10_out), .sel(and_20_out));
  Adder #(.width(5)) adder_12 (.a(Counter_in), .b(5'b01011), .out(adder_12_out));  // open: cin, cout
  Comparator #(.width(5), .mode("unsigned")) comparator_12 (
    .a(Counter_in), .b(5'b10100), .lt(comparator_12_lt));  // open: gt, eq
  Multiplexer #(.width(32), .disabled(0), .enable("false")) multiplexer_11 (
    .in0({32{1'b1}}), .in1(in_1), .out(multiplexer_11_out), .sel(and_22_out));
  Adder #(.width(5)) adder_13 (.a(Counter_in), .b(5'b01100), .out(adder_13_out));  // open: cin, cout
  Comparator #(.width(5), .mode("unsigned")) comparator_13 (
    .a(Counter_in), .b(5'b10011), .lt(comparator_13_lt));  // open: gt, eq
  Multiplexer #(.width(32), .disabled(0), .enable("false")) multiplexer_12 (
    .in0({32{1'b1}}), .in1(in_1), .out(multiplexer_12_out), .sel(and_24_out));
  Adder #(.width(5)) adder_14 (.a(Counter_in), .b(5'b01101), .out(adder_14_out));  // open: cin, cout
  Comparator #(.width(5), .mode("unsigned")) comparator_14 (
    .a(Counter_in), .b(5'b10010), .lt(comparator_14_lt));  // open: gt, eq
  Multiplexer #(.width(32), .disabled(0), .enable("false")) multiplexer_13 (
    .in0({32{1'b1}}), .in1(in_1), .out(multiplexer_13_out), .sel(and_26_out));
  Adder #(.width(5)) adder_15 (.a(Counter_in), .b(5'b01110), .out(adder_15_out));  // open: cin, cout
  Comparator #(.width(5), .mode("unsigned")) comparator_15 (
    .a(Counter_in), .b(5'b10001), .lt(comparator_15_lt));  // open: gt, eq
  Multiplexer #(.width(32), .disabled(0), .enable("false")) multiplexer_14 (
    .in0({32{1'b1}}), .in1(in_1), .out(multiplexer_14_out), .sel(and_28_out));
  Adder #(.width(5)) adder_16 (.a(Counter_in), .b(5'b01111), .out(adder_16_out));  // open: cin, cout
  Comparator #(.width(5), .mode("unsigned")) comparator_16 (
    .a(Counter_in), .b(5'b10000), .lt(comparator_16_lt));  // open: gt, eq
  Multiplexer #(.width(32), .disabled(0), .enable("false")) multiplexer_15 (
    .in0({32{1'b1}}), .in1(in_1), .out(multiplexer_15_out), .sel(and_30_out));
  Adder #(.width(5)) adder_17 (.a(Counter_in), .b(5'b10000), .out(adder_17_out));  // open: cin, cout
  Comparator #(.width(5), .mode("unsigned")) comparator_17 (
    .a(Counter_in), .b(5'b01111), .lt(comparator_17_lt));  // open: gt, eq
  Multiplexer #(.width(32), .disabled(0), .enable("false")) multiplexer_16 (
    .in0({32{1'b1}}), .in1(in_1), .out(multiplexer_16_out), .sel(and_32_out));
  Adder #(.width(5)) adder_18 (.a(Counter_in), .b(5'b10001), .out(adder_18_out));  // open: cin, cout
  Comparator #(.width(5), .mode("unsigned")) comparator_18 (
    .a(Counter_in), .b(5'b01110), .lt(comparator_18_lt));  // open: gt, eq
  Multiplexer #(.width(32), .disabled(0), .enable("false")) multiplexer_17 (
    .in0({32{1'b1}}), .in1(in_1), .out(multiplexer_17_out), .sel(and_34_out));
  Adder #(.width(5)) adder_19 (.a(Counter_in), .b(5'b10010), .out(adder_19_out));  // open: cin, cout
  Comparator #(.width(5), .mode("unsigned")) comparator_19 (
    .a(Counter_in), .b(5'b01101), .lt(comparator_19_lt));  // open: gt, eq
  Multiplexer #(.width(32), .disabled(0), .enable("false")) multiplexer_18 (
    .in0({32{1'b1}}), .in1(in_1), .out(multiplexer_18_out), .sel(and_36_out));
  Adder #(.width(5)) adder_20 (.a(Counter_in), .b(5'b10011), .out(adder_20_out));  // open: cin, cout
  Comparator #(.width(5), .mode("unsigned")) comparator_20 (
    .a(Counter_in), .b(5'b01100), .lt(comparator_20_lt));  // open: gt, eq
  Multiplexer #(.width(32), .disabled(0), .enable("false")) multiplexer_19 (
    .in0({32{1'b1}}), .in1(in_1), .out(multiplexer_19_out), .sel(and_38_out));
  Adder #(.width(5)) adder_21 (.a(Counter_in), .b(5'b10100), .out(adder_21_out));  // open: cin, cout
  Comparator #(.width(5), .mode("unsigned")) comparator_21 (
    .a(Counter_in), .b(5'b01011), .lt(comparator_21_lt));  // open: gt, eq
  Multiplexer #(.width(32), .disabled(0), .enable("false")) multiplexer_20 (
    .in0({32{1'b1}}), .in1(in_1), .out(multiplexer_20_out), .sel(and_40_out));
  Adder #(.width(5)) adder_22 (.a(Counter_in), .b(5'b10101), .out(adder_22_out));  // open: cin, cout
  Comparator #(.width(5), .mode("unsigned")) comparator_22 (
    .a(Counter_in), .b(5'b01010), .lt(comparator_22_lt));  // open: gt, eq
  Multiplexer #(.width(32), .disabled(0), .enable("false")) multiplexer_21 (
    .in0({32{1'b1}}), .in1(in_1), .out(multiplexer_21_out), .sel(and_42_out));
  Adder #(.width(5)) adder_23 (.a(Counter_in), .b(5'b10110), .out(adder_23_out));  // open: cin, cout
  Comparator #(.width(5), .mode("unsigned")) comparator_23 (
    .a(Counter_in), .b(5'b01001), .lt(comparator_23_lt));  // open: gt, eq
  Multiplexer #(.width(32), .disabled(0), .enable("false")) multiplexer_22 (
    .in0({32{1'b1}}), .in1(in_1), .out(multiplexer_22_out), .sel(and_44_out));
  Adder #(.width(5)) adder_24 (.a(Counter_in), .b(5'b10111), .out(adder_24_out));  // open: cin, cout
  Comparator #(.width(5), .mode("unsigned")) comparator_24 (
    .a(Counter_in), .b(5'b01000), .lt(comparator_24_lt));  // open: gt, eq
  Multiplexer #(.width(32), .disabled(0), .enable("false")) multiplexer_23 (
    .in0({32{1'b1}}), .in1(in_1), .out(multiplexer_23_out), .sel(and_46_out));
  Adder #(.width(5)) adder_25 (.a(Counter_in), .b(5'b11000), .out(adder_25_out));  // open: cin, cout
  Comparator #(.width(5), .mode("unsigned")) comparator_25 (
    .a(Counter_in), .b(5'b00111), .lt(comparator_25_lt));  // open: gt, eq
  Multiplexer #(.width(32), .disabled(0), .enable("false")) multiplexer_24 (
    .in0({32{1'b1}}), .in1(in_1), .out(multiplexer_24_out), .sel(and_48_out));
  Adder #(.width(5)) adder_26 (.a(Counter_in), .b(5'b11001), .out(adder_26_out));  // open: cin, cout
  Comparator #(.width(5), .mode("unsigned")) comparator_26 (
    .a(Counter_in), .b(5'b00110), .lt(comparator_26_lt));  // open: gt, eq
  Multiplexer #(.width(32), .disabled(0), .enable("false")) multiplexer_25 (
    .in0({32{1'b1}}), .in1(in_1), .out(multiplexer_25_out), .sel(and_50_out));
  Adder #(.width(5)) adder_27 (.a(Counter_in), .b(5'b11010), .out(adder_27_out));  // open: cin, cout
  Comparator #(.width(5), .mode("unsigned")) comparator_27 (
    .a(Counter_in), .b(5'b00101), .lt(comparator_27_lt));  // open: gt, eq
  Multiplexer #(.width(32), .disabled(0), .enable("false")) multiplexer_26 (
    .in0({32{1'b1}}), .in1(in_1), .out(multiplexer_26_out), .sel(and_52_out));
  Adder #(.width(5)) adder_28 (.a(Counter_in), .b(5'b11011), .out(adder_28_out));  // open: cin, cout
  Comparator #(.width(5), .mode("unsigned")) comparator_28 (
    .a(Counter_in), .b(5'b00100), .lt(comparator_28_lt));  // open: gt, eq
  Multiplexer #(.width(32), .disabled(0), .enable("false")) multiplexer_27 (
    .in0({32{1'b1}}), .in1(in_1), .out(multiplexer_27_out), .sel(and_54_out));
  Adder #(.width(5)) adder_29 (.a(Counter_in), .b(5'b11100), .out(adder_29_out));  // open: cin, cout
  Comparator #(.width(5), .mode("unsigned")) comparator_29 (
    .a(Counter_in), .b(5'b00011), .lt(comparator_29_lt));  // open: gt, eq
  Multiplexer #(.width(32), .disabled(0), .enable("false")) multiplexer_28 (
    .in0({32{1'b1}}), .in1(in_1), .out(multiplexer_28_out), .sel(and_56_out));
  Adder #(.width(5)) adder_30 (.a(Counter_in), .b(5'b11101), .out(adder_30_out));  // open: cin, cout
  Comparator #(.width(5), .mode("unsigned")) comparator_30 (
    .a(Counter_in), .b(5'b00010), .lt(comparator_30_lt));  // open: gt, eq
  Multiplexer #(.width(32), .disabled(0), .enable("false")) multiplexer_29 (
    .in0({32{1'b1}}), .in1(in_1), .out(multiplexer_29_out), .sel(and_58_out));
  Adder #(.width(5)) adder_31 (.a(Counter_in), .b(5'b11110), .out(adder_31_out));  // open: cin, cout
  Comparator #(.width(5), .mode("unsigned")) comparator_31 (
    .a(Counter_in), .b(5'b00001), .lt(comparator_31_lt));  // open: gt, eq
  Multiplexer #(.width(32), .disabled(0), .enable("false")) multiplexer_30 (
    .in0({32{1'b1}}), .in1(in_1), .out(multiplexer_30_out), .sel(and_60_out));
  Adder #(.width(5)) adder_32 (.a(Counter_in), .b({5{1'b1}}), .out(adder_32_out));  // open: cin, cout
  and and_1 (and_1_out, comparator_1_lt, ~bitselector_2_out);  // AND_Gate
  BitSelector #(.width(32)) bitselector_2 (.in(in_1), .out(bitselector_2_out), .sel(adder_2_out));
  and and_2 (and_2_out, comparator_2_lt, ~bitselector_3_out);  // AND_Gate
  BitSelector #(.width(32)) bitselector_3 (.in(multiplexer_1_out), .out(bitselector_3_out), .sel(adder_3_out));
  and and_3 (and_3_out, comparator_3_lt, ~bitselector_4_out);  // AND_Gate
  BitSelector #(.width(32)) bitselector_4 (.in(multiplexer_2_out), .out(bitselector_4_out), .sel(adder_4_out));
  and and_4 (and_4_out, and_1_out, and_2_out);
  and and_5 (and_5_out, comparator_4_lt, ~bitselector_5_out);  // AND_Gate
  BitSelector #(.width(32)) bitselector_5 (.in(multiplexer_3_out), .out(bitselector_5_out), .sel(adder_5_out));
  and and_6 (and_6_out, and_4_out, and_3_out);
  and and_7 (and_7_out, comparator_5_lt, ~bitselector_6_out);  // AND_Gate
  BitSelector #(.width(32)) bitselector_6 (.in(multiplexer_4_out), .out(bitselector_6_out), .sel(adder_6_out));
  and and_8 (and_8_out, and_6_out, and_5_out);
  and and_9 (and_9_out, comparator_6_lt, ~bitselector_7_out);  // AND_Gate
  BitSelector #(.width(32)) bitselector_7 (.in(multiplexer_5_out), .out(bitselector_7_out), .sel(adder_7_out));
  and and_10 (and_10_out, and_8_out, and_7_out);
  and and_11 (and_11_out, comparator_7_lt, ~bitselector_8_out);  // AND_Gate
  BitSelector #(.width(32)) bitselector_8 (.in(multiplexer_6_out), .out(bitselector_8_out), .sel(adder_8_out));
  and and_12 (and_12_out, and_10_out, and_9_out);
  and and_13 (and_13_out, comparator_8_lt, ~bitselector_9_out);  // AND_Gate
  BitSelector #(.width(32)) bitselector_9 (.in(multiplexer_7_out), .out(bitselector_9_out), .sel(adder_9_out));
  and and_14 (and_14_out, and_12_out, and_11_out);
  and and_15 (and_15_out, comparator_9_lt, ~bitselector_10_out);  // AND_Gate
  BitSelector #(.width(32)) bitselector_10 (.in(multiplexer_8_out), .out(bitselector_10_out), .sel(adder_10_out));
  and and_16 (and_16_out, and_14_out, and_13_out);
  and and_17 (and_17_out, comparator_10_lt, ~bitselector_11_out);  // AND_Gate
  BitSelector #(.width(32)) bitselector_11 (.in(multiplexer_9_out), .out(bitselector_11_out), .sel(adder_11_out));
  and and_18 (and_18_out, and_16_out, and_15_out);
  and and_19 (and_19_out, comparator_11_lt, ~bitselector_12_out);  // AND_Gate
  BitSelector #(.width(32)) bitselector_12 (.in(multiplexer_10_out), .out(bitselector_12_out), .sel(adder_12_out));
  and and_20 (and_20_out, and_18_out, and_17_out);
  and and_21 (and_21_out, comparator_12_lt, ~bitselector_13_out);  // AND_Gate
  BitSelector #(.width(32)) bitselector_13 (.in(multiplexer_11_out), .out(bitselector_13_out), .sel(adder_13_out));
  and and_22 (and_22_out, and_20_out, and_19_out);
  and and_23 (and_23_out, comparator_13_lt, ~bitselector_14_out);  // AND_Gate
  BitSelector #(.width(32)) bitselector_14 (.in(multiplexer_12_out), .out(bitselector_14_out), .sel(adder_14_out));
  and and_24 (and_24_out, and_22_out, and_21_out);
  and and_25 (and_25_out, comparator_14_lt, ~bitselector_15_out);  // AND_Gate
  BitSelector #(.width(32)) bitselector_15 (.in(multiplexer_13_out), .out(bitselector_15_out), .sel(adder_15_out));
  and and_26 (and_26_out, and_24_out, and_23_out);
  and and_27 (and_27_out, comparator_15_lt, ~bitselector_16_out);  // AND_Gate
  BitSelector #(.width(32)) bitselector_16 (.in(multiplexer_14_out), .out(bitselector_16_out), .sel(adder_16_out));
  and and_28 (and_28_out, and_26_out, and_25_out);
  and and_29 (and_29_out, comparator_16_lt, ~bitselector_17_out);  // AND_Gate
  BitSelector #(.width(32)) bitselector_17 (.in(multiplexer_15_out), .out(bitselector_17_out), .sel(adder_17_out));
  and and_30 (and_30_out, and_28_out, and_27_out);
  and and_31 (and_31_out, comparator_17_lt, ~bitselector_18_out);  // AND_Gate
  BitSelector #(.width(32)) bitselector_18 (.in(multiplexer_16_out), .out(bitselector_18_out), .sel(adder_18_out));
  and and_32 (and_32_out, and_30_out, and_29_out);
  and and_33 (and_33_out, comparator_18_lt, ~bitselector_19_out);  // AND_Gate
  BitSelector #(.width(32)) bitselector_19 (.in(multiplexer_17_out), .out(bitselector_19_out), .sel(adder_19_out));
  and and_34 (and_34_out, and_32_out, and_31_out);
  and and_35 (and_35_out, comparator_19_lt, ~bitselector_20_out);  // AND_Gate
  BitSelector #(.width(32)) bitselector_20 (.in(multiplexer_18_out), .out(bitselector_20_out), .sel(adder_20_out));
  and and_36 (and_36_out, and_34_out, and_33_out);
  and and_37 (and_37_out, comparator_20_lt, ~bitselector_21_out);  // AND_Gate
  BitSelector #(.width(32)) bitselector_21 (.in(multiplexer_19_out), .out(bitselector_21_out), .sel(adder_21_out));
  and and_38 (and_38_out, and_36_out, and_35_out);
  and and_39 (and_39_out, comparator_21_lt, ~bitselector_22_out);  // AND_Gate
  BitSelector #(.width(32)) bitselector_22 (.in(multiplexer_20_out), .out(bitselector_22_out), .sel(adder_22_out));
  and and_40 (and_40_out, and_38_out, and_37_out);
  and and_41 (and_41_out, comparator_22_lt, ~bitselector_23_out);  // AND_Gate
  BitSelector #(.width(32)) bitselector_23 (.in(multiplexer_21_out), .out(bitselector_23_out), .sel(adder_23_out));
  and and_42 (and_42_out, and_40_out, and_39_out);
  and and_43 (and_43_out, comparator_23_lt, ~bitselector_24_out);  // AND_Gate
  BitSelector #(.width(32)) bitselector_24 (.in(multiplexer_22_out), .out(bitselector_24_out), .sel(adder_24_out));
  and and_44 (and_44_out, and_42_out, and_41_out);
  and and_45 (and_45_out, comparator_24_lt, ~bitselector_25_out);  // AND_Gate
  BitSelector #(.width(32)) bitselector_25 (.in(multiplexer_23_out), .out(bitselector_25_out), .sel(adder_25_out));
  and and_46 (and_46_out, and_44_out, and_43_out);
  and and_47 (and_47_out, comparator_25_lt, ~bitselector_26_out);  // AND_Gate
  BitSelector #(.width(32)) bitselector_26 (.in(multiplexer_24_out), .out(bitselector_26_out), .sel(adder_26_out));
  and and_48 (and_48_out, and_46_out, and_45_out);
  and and_49 (and_49_out, comparator_26_lt, ~bitselector_27_out);  // AND_Gate
  BitSelector #(.width(32)) bitselector_27 (.in(multiplexer_25_out), .out(bitselector_27_out), .sel(adder_27_out));
  and and_50 (and_50_out, and_48_out, and_47_out);
  and and_51 (and_51_out, comparator_27_lt, ~bitselector_28_out);  // AND_Gate
  BitSelector #(.width(32)) bitselector_28 (.in(multiplexer_26_out), .out(bitselector_28_out), .sel(adder_28_out));
  and and_52 (and_52_out, and_50_out, and_49_out);
  and and_53 (and_53_out, comparator_28_lt, ~bitselector_29_out);  // AND_Gate
  BitSelector #(.width(32)) bitselector_29 (.in(multiplexer_27_out), .out(bitselector_29_out), .sel(adder_29_out));
  and and_54 (and_54_out, and_52_out, and_51_out);
  and and_55 (and_55_out, comparator_29_lt, ~bitselector_30_out);  // AND_Gate
  BitSelector #(.width(32)) bitselector_30 (.in(multiplexer_28_out), .out(bitselector_30_out), .sel(adder_30_out));
  and and_56 (and_56_out, and_54_out, and_53_out);
  and and_57 (and_57_out, comparator_30_lt, ~bitselector_31_out);  // AND_Gate
  BitSelector #(.width(32)) bitselector_31 (.in(multiplexer_29_out), .out(bitselector_31_out), .sel(adder_31_out));
  and and_58 (and_58_out, and_56_out, and_55_out);
  and and_59 (and_59_out, comparator_31_lt, ~bitselector_32_out);  // AND_Gate
  BitSelector #(.width(32)) bitselector_32 (.in(multiplexer_30_out), .out(bitselector_32_out), .sel(adder_32_out));
  and and_60 (and_60_out, and_58_out, and_57_out);
  Adder #(.width(5)) adder_33 (.a(bitadder_1_out), .b(5'b00001), .out(adder_33_out));  // open: cin, cout
  Adder #(.width(5)) adder_34 (.a(Counter_in), .b(adder_33_out), .out(Counter_out));  // open: cin, cout
  not not_1 (not_1_out, Count);
  or or_1 (Load_2, not_1_out, Load);
  BitAdder #(.width(1)) bitadder_1 (
    .in0(and_1_out), .in1(and_2_out), .in2(and_3_out), .in3(and_5_out), .in4(and_7_out), .in5(and_9_out),
    .in6(and_11_out), .in7(and_13_out), .in8(and_15_out), .in9(and_17_out), .in10(and_19_out),
    .in11(and_21_out), .in12(and_23_out), .in13(and_25_out), .in14(and_27_out), .in15(and_29_out),
    .in16(and_31_out), .in17(and_33_out), .in18(and_35_out), .in19(and_37_out), .in20(and_39_out),
    .in21(and_41_out), .in22(and_43_out), .in23(and_45_out), .in24(and_47_out), .in25(and_49_out),
    .in26(and_51_out), .in27(and_53_out), .in28(and_55_out), .in29(and_57_out), .in30(and_59_out),
    .out(bitadder_1_out));
endmodule

module Computer (
);

  RAM_for_computer ram_for_computer_1 ();  // open: in_1, power, Clk, Reset, in_5, in_6, in_7, in_8, in_9, in_10, in_11, in_12, in_13, in_14, in_15, in_16, in_17, in_18, in_19, in_20, in_21, in_22, in_23, in_24, in_25, in_26, in_27, in_28, in_29, in_30, in_31, in_32, in_33, in_34, in_35, in_36, out_37, out_38, out_39, out_40, out_41, out_42, out_43, out_44, out_45, out_46, out_47, out_48, out_49, out_50, out_51, out_52
endmodule

module Timer (
  input  Reset,
  input  Power,
  input  Load_speed_clock,
  input  Reset_speed_clock,
  input  Clk,
  input  Clk__one_per_second,
  input  [31:0] Data_in,
  output [31:0] Time_FP,
  output [31:0] Porsion_of_time
);

  wire and_1_out, and_2_out, and_3_out, comparator_1_eq, comparator_1_gt, comparator_1_lt, comparator_2_gt,
       comparator_3_eq, comparator_4_eq, counter_2_q, counter_3_carry, decoder_1_out0, decoder_1_out1,
       fp_probe_1_p1, int_to_fp_2_p1, not_1_out, not_2_out, or_1_out, or_2_out, or_3_out, or_4_out,
       register_1_q;
  wire [31:0] adder_1_p2, counter_1_q, counter_3_q, divider_1_p2, multiplexer_1_out, multiplexer_2_out,
       multiplexer_3_out, register_2_q, register_3_q, subtractor_1_out;

  Register #(.width(1)) register_1 (
    .D(Load_speed_clock), .en(Power), .Q(register_1_q), .clk(Load_speed_clock), .clr(or_1_out));
  not not_1 (not_1_out, register_1_q);
  or or_1 (or_1_out, Reset_speed_clock, Reset);
  Counter #(.width(32), .max('hffffffff)) counter_1 (
    .load(register_1_q), .D(Data_in), .count(not_1_out), .Q(counter_1_q), .clk(Clk), .clr(or_2_out));  // open: carry
  Decoder #(.disabled(0)) decoder_1 (
    .out0(decoder_1_out0), .out1(decoder_1_out1), .sel(counter_2_q), .en(Clk__one_per_second));
  Register #(.width(32)) register_2 (.D(counter_1_q), .en(Power), .Q(register_2_q), .clk(decoder_1_out1), .clr(Reset));
  Counter #(.width(1), .max('h1)) counter_2 (
    .load(1'b0), .D(1'b0), .count(Clk__one_per_second), .Q(counter_2_q), .clk(Clk__one_per_second),
    .clr(Reset));  // open: carry
  or or_2 (or_2_out, decoder_1_out1, or_1_out, decoder_1_out0);
  not not_2 (not_2_out, and_1_out);
  and and_1 (and_1_out, ~comparator_1_gt, comparator_1_lt);  // AND_Gate
  Comparator #(.width(32), .mode("unsigned")) comparator_1 (
    .a(register_3_q), .b(register_2_q), .gt(comparator_1_gt), .eq(comparator_1_eq), .lt(comparator_1_lt));
  Counter #(.width(32), .max('hffffffff)) counter_3 (
    .load(1'b0), .D({32{1'b0}}), .count(Power), .Q(counter_3_q), .carry(counter_3_carry), .clk(Clk),
    .clr(or_3_out));
  Multiplier #(.width(32)) multiplier_1 (.a(multiplexer_1_out), .b(32'h2));  // open: out, cin, cout
  Register #(.width(32)) register_3 (.D(register_2_q), .en(Power), .Q(register_3_q), .clk(decoder_1_out0), .clr(Reset));
  Multiplexer #(.width(32), .disabled(0)) multiplexer_1 (
    .in0(register_3_q), .in1(register_2_q), .out(multiplexer_1_out), .sel(counter_2_q), .en(Power));
  Multiplexer #(.width(32), .disabled(0)) multiplexer_2 (
    .in0(register_2_q), .in1(register_3_q), .out(multiplexer_2_out), .sel(not_2_out), .en(Power));
  Subtractor #(.width(32)) subtractor_1 (
    .a(multiplexer_2_out), .b(multiplexer_3_out), .out(subtractor_1_out));  // open: bin, bout
  Multiplexer #(.width(32), .disabled(0)) multiplexer_3 (
    .in0(register_3_q), .in1(register_2_q), .out(multiplexer_3_out), .sel(not_2_out), .en(Power));
  // FP_Probe fp_probe_1: pin names not known; wires that end beside it: fp_probe_1_p1
  // Int_To_FP int_to_fp_1: pin names not known; wires that end beside it: counter_3_q, fp_probe_1_p1
  // Divider divider_1: pin names not known; wires that end beside it: fp_probe_1_p1, divider_1_p2
  // Int_To_FP int_to_fp_2: pin names not known; wires that end beside it: int_to_fp_2_p1, int_to_fp_2_p1
  // FP_Probe fp_probe_2: pin names not known; wires that end beside it: int_to_fp_2_p1
  Counter #(.width(32), .max('hffffffff)) counter_4 (
    .load(1'b0), .D({32{1'b0}}), .count(Power), .Q(Porsion_of_time), .clk(counter_3_carry), .clr(Reset));  // open: carry
  or or_3 (or_3_out, Reset, and_2_out);
  and and_2 (and_2_out, Clk__one_per_second, and_3_out);
  // Adder adder_1: pin names not known; wires that end beside it: divider_1_p2, adder_1_p2, Time_FP, Time_FP
  Register #(.width(32)) register_4 (.D(divider_1_p2), .en(Power), .Q(adder_1_p2), .clk(and_3_out), .clr(Reset));
  Comparator #(.width(32)) comparator_2 (.a(subtractor_1_out), .b(32'h5), .gt(comparator_2_gt));  // open: eq, lt
  Comparator #(.width(32)) comparator_3 (.a(register_3_q), .b({32{1'b0}}), .eq(comparator_3_eq));  // open: gt, lt
  Comparator #(.width(32)) comparator_4 (.a(register_2_q), .b({32{1'b0}}), .eq(comparator_4_eq));  // open: gt, lt
  // FP_Probe fp_probe_3: pin names not known; wires that end beside it: adder_1_p2
  and and_3 (and_3_out, comparator_2_gt, ~or_4_out, ~comparator_1_eq);  // AND_Gate
  or or_4 (or_4_out, comparator_3_eq, comparator_4_eq);
  // FP_Probe fp_probe_4: pin names not known; wires that end beside it: divider_1_p2
  // FP_Probe fp_probe_5: pin names not known
endmodule

module Clock__Time (
  input  Reset_timer,
  input  Power,
  input  Load_timer,
  input  Reset_speed_clock,
  input  Clk,
  input  Clk__one_per_second,
  input  [31:0] Data_in,
  input  En_Reg,
  input  Reset_reg,
  input  Access_to_reg,
  input  Reset_time_memory,
  input  [4:0] Comand,
  input  [3:0] Time_memory_adress,
  output [31:0] Timer_time,
  output [31:0] Porsion_of_time,
  output [31:0] Date,
  output Over_time,
  output [31:0] TM_value
);

  wire [31:0] int_to_fp_1_p2, register_1_q;

  Timer timer_1 (
    .Reset(Reset_timer), .Power(Power), .Load_speed_clock(Load_timer), .Reset_speed_clock(Reset_speed_clock),
    .Clk(Clk), .Clk__one_per_second(Clk__one_per_second), .Data_in(Data_in), .Time_FP(Timer_time),
    .Porsion_of_time(Porsion_of_time));
  // Int_To_FP int_to_fp_1: pin names not known; wires that end beside it: Data_in, int_to_fp_1_p2
  Register #(.width(32)) register_1 (.D(int_to_fp_1_p2), .en(En_Reg), .Q(register_1_q), .clk(Clk), .clr(Reset_reg));
  Time_memory__TM time_memory_tm_1 (
    .Power(Power), .Clk(Clk), .Access_to_Reg(Access_to_reg), .Reset_all(Reset_time_memory), .Comand(Comand),
    .Data_in(Data_in), .Time_memory_adress(Time_memory_adress), .OVER_TIME(Over_time), .Data_out(TM_value));
  // Adder adder_1: pin names not known; wires that end beside it: Timer_time, register_1_q, Date
endmodule

module Time_memory__TM (
  input  Power,
  input  Clk,
  input  Access_to_Reg,
  input  Reset_all,
  input  [4:0] Comand,
  input  [31:0] Data_in,
  input  [3:0] Time_memory_adress,
  output OVER_TIME,
  output [31:0] Data_out
);

  wire and_1_out, and_2_out, and_3_out, and_4_out, and_5_out, and_6_out, and_7_out, and_8_out,
       comparator_1_p3, comparator_1_p4, comparator_3_p3, comparator_3_p4, comparator_5_p3, comparator_5_p4,
       comparator_7_p3, comparator_7_p4, comparator_9_p3, comparator_9_p4, comparator_11_p3,
       comparator_11_p4, comparator_13_p3, comparator_13_p4, comparator_15_p3, comparator_15_p4,
       decoder_1_out0, decoder_1_out1, decoder_1_out2, decoder_1_out3, decoder_1_out4, decoder_1_out5,
       decoder_1_out6, decoder_1_out7, decoder_1_out8, decoder_1_out16, decoder_1_out17, decoder_1_out18,
       decoder_1_out19, decoder_1_out20, decoder_1_out21, decoder_1_out22, decoder_1_out23, decoder_1_out24,
       not_1_out, not_2_out, not_3_out, not_4_out, not_5_out, not_6_out, not_7_out, not_8_out, not_9_out,
       or_1_out, or_2_out, or_3_out, or_4_out, or_5_out, or_6_out, or_7_out, or_8_out, or_9_out, or_10_out,
       or_11_out, or_12_out, or_13_out, or_14_out, or_15_out, or_16_out, or_17_out, or_18_out, or_19_out,
       or_20_out, or_21_out, or_22_out, or_23_out, or_24_out, or_25_out;
  wire [14:0] register_20_q, register_24_q;
  wire [31:0] register_1_q, register_2_q, register_3_q, register_4_q, register_5_q, register_6_q,
       register_7_q, register_8_q, register_9_q, register_10_q, register_11_q, register_12_q, register_13_q,
       register_14_q, register_15_q, register_16_q;

  Decoder #(.select(5), .disabled(0)) decoder_1 (
    .out0(decoder_1_out0), .out1(decoder_1_out1), .out2(decoder_1_out2), .out3(decoder_1_out3),
    .out4(decoder_1_out4), .out5(decoder_1_out5), .out6(decoder_1_out6), .out7(decoder_1_out7),
    .out8(decoder_1_out8), .out9(register_20_q[14]), .out10(register_20_q[11]), .out11(register_20_q[10]),
    .out12(register_20_q[7]), .out13(register_20_q[6]), .out14(register_20_q[3]), .out15(register_20_q[1]),
    .out16(decoder_1_out16), .out17(decoder_1_out17), .out18(decoder_1_out18), .out19(decoder_1_out19),
    .out20(decoder_1_out20), .out21(decoder_1_out21), .out22(decoder_1_out22), .out23(decoder_1_out23),
    .out24(decoder_1_out24), .out25(register_24_q[14]), .out26(register_24_q[11]), .out27(register_24_q[10]),
    .out28(register_24_q[7]), .out29(register_24_q[6]), .out30(register_24_q[3]), .out31(register_24_q[2]),
    .sel(Comand), .en(Access_to_Reg));
  or or_1 (or_1_out, decoder_1_out1, Reset_all, register_20_q[12]);
  or or_2 (or_2_out, decoder_1_out3, Reset_all, register_20_q[8]);
  or or_3 (or_3_out, decoder_1_out5, Reset_all, register_20_q[4]);
  or or_4 (or_4_out, decoder_1_out7, Reset_all, register_20_q[0]);
  or or_5 (or_5_out, decoder_1_out17, Reset_all, register_24_q[12]);
  or or_6 (or_6_out, decoder_1_out19, Reset_all, register_24_q[8]);
  or or_7 (or_7_out, decoder_1_out21, Reset_all, register_24_q[4]);
  or or_8 (or_8_out, decoder_1_out23, Reset_all, register_24_q[0]);
  Register #(.width(32)) register_1 (.D(Data_in), .en(decoder_1_out0), .Q(register_1_q), .clk(Clk), .clr(or_1_out));
  Register #(.width(32)) register_2 (.D(Data_in), .en(decoder_1_out2), .Q(register_2_q), .clk(Clk), .clr(or_2_out));
  Register #(.width(32)) register_3 (.D(Data_in), .en(decoder_1_out4), .Q(register_3_q), .clk(Clk), .clr(or_3_out));
  Register #(.width(32)) register_4 (.D(Data_in), .en(decoder_1_out6), .Q(register_4_q), .clk(Clk), .clr(or_4_out));
  Register #(.width(32)) register_5 (.D(Data_in), .en(decoder_1_out16), .Q(register_5_q), .clk(Clk), .clr(or_5_out));
  Register #(.width(32)) register_6 (.D(Data_in), .en(decoder_1_out18), .Q(register_6_q), .clk(Clk), .clr(or_6_out));
  Register #(.width(32)) register_7 (.D(Data_in), .en(decoder_1_out20), .Q(register_7_q), .clk(Clk), .clr(or_7_out));
  Register #(.width(32)) register_8 (.D(Data_in), .en(decoder_1_out22), .Q(register_8_q), .clk(Clk), .clr(or_8_out));
  or or_9 (or_9_out, register_20_q[14], Reset_all, register_20_q[12]);
  or or_10 (or_10_out, register_20_q[10], Reset_all, register_20_q[8]);
  or or_11 (or_11_out, register_20_q[6], Reset_all, register_20_q[4]);
  or or_12 (or_12_out, Reset_all, register_20_q[1], register_20_q[0]);
  or or_13 (or_13_out, register_24_q[14], Reset_all, register_24_q[12]);
  or or_14 (or_14_out, register_24_q[10], Reset_all, register_24_q[8]);
  or or_15 (or_15_out, register_24_q[6], Reset_all, register_24_q[4]);
  or or_16 (or_16_out, register_24_q[2], Reset_all, register_24_q[0]);
  Register #(.width(32)) register_9 (.D(Data_in), .en(decoder_1_out8), .Q(register_9_q), .clk(Clk), .clr(or_9_out));
  Register #(.width(32)) register_10 (
    .D(Data_in), .en(register_20_q[11]), .Q(register_10_q), .clk(Clk), .clr(or_10_out));
  Register #(.width(32)) register_11 (
    .D(Data_in), .en(register_20_q[7]), .Q(register_11_q), .clk(Clk), .clr(or_11_out));
  Register #(.width(32)) register_12 (
    .D(Data_in), .en(register_20_q[3]), .Q(register_12_q), .clk(Clk), .clr(or_12_out));
  Register #(.width(32)) register_13 (.D(Data_in), .en(decoder_1_out24), .Q(register_13_q), .clk(Clk), .clr(or_13_out));
  Register #(.width(32)) register_14 (
    .D(Data_in), .en(register_24_q[11]), .Q(register_14_q), .clk(Clk), .clr(or_14_out));
  Register #(.width(32)) register_15 (
    .D(Data_in), .en(register_24_q[7]), .Q(register_15_q), .clk(Clk), .clr(or_15_out));
  Register #(.width(32)) register_16 (
    .D(Data_in), .en(register_24_q[3]), .Q(register_16_q), .clk(Clk), .clr(or_16_out));
  Multiplexer #(.select(4), .width(32)) multiplexer_1 (
    .in1(register_4_q), .in2(register_3_q), .in3(register_2_q), .in4(register_1_q), .in5(register_12_q),
    .in6(register_11_q), .in7(register_10_q), .in8(register_9_q), .in9(register_16_q), .in10(register_15_q),
    .in11(register_14_q), .in12(register_13_q), .in13(register_8_q), .in14(register_7_q),
    .in15(register_6_q), .out(Data_out), .sel(Time_memory_adress), .en(Power));  // open: in0
  Pull_Resistor pull_resistor_1 (.node(Data_out));
  or or_17 (or_17_out, comparator_1_p3, comparator_1_p4);
  // Comparator comparator_1: pin names not known; wires that end beside it: register_1_q, register_9_q, comparator_1_p3, comparator_1_p4
  // NOT_Gate not_1 has open pins: in=open, out=not_1_out
  // Comparator comparator_2: pin names not known; wires that end beside it: register_9_q, {32{1'b0}}
  // Comparator comparator_3: pin names not known; wires that end beside it: register_2_q, register_10_q, comparator_3_p3, comparator_3_p4
  or or_18 (or_18_out, comparator_3_p3, comparator_3_p4);
  // NOT_Gate not_2 has open pins: in=open, out=not_2_out
  // Comparator comparator_4: pin names not known; wires that end beside it: register_10_q, {32{1'b0}}
  or or_19 (or_19_out, comparator_5_p3, comparator_5_p4);
  // Comparator comparator_5: pin names not known; wires that end beside it: register_3_q, register_11_q, comparator_5_p3, comparator_5_p4
  // NOT_Gate not_3 has open pins: in=open, out=not_3_out
  // Comparator comparator_6: pin names not known; wires that end beside it: register_11_q, {32{1'b0}}
  // Comparator comparator_7: pin names not known; wires that end beside it: register_4_q, register_12_q, comparator_7_p3, comparator_7_p4
  or or_20 (or_20_out, comparator_7_p3, comparator_7_p4);
  // Comparator comparator_8: pin names not known; wires that end beside it: register_12_q, {32{1'b0}}
  // NOT_Gate not_4 has open pins: in=open, out=not_4_out
  // Comparator comparator_9: pin names not known; wires that end beside it: register_5_q, register_13_q, comparator_9_p3, comparator_9_p4
  or or_21 (or_21_out, comparator_9_p3, comparator_9_p4);
  // NOT_Gate not_5 has open pins: in=open, out=not_5_out
  // Comparator comparator_10: pin names not known; wires that end beside it: register_13_q, {32{1'b0}}
  // Comparator comparator_11: pin names not known; wires that end beside it: register_6_q, register_14_q, comparator_11_p3, comparator_11_p4
  or or_22 (or_22_out, comparator_11_p3, comparator_11_p4);
  // NOT_Gate not_6 has open pins: in=open, out=not_6_out
  // Comparator comparator_12: pin names not known; wires that end beside it: register_14_q, {32{1'b0}}
  // Comparator comparator_13: pin names not known; wires that end beside it: register_7_q, register_15_q, comparator_13_p3, comparator_13_p4
  or or_23 (or_23_out, comparator_13_p3, comparator_13_p4);
  // NOT_Gate not_7 has open pins: in=open, out=not_7_out
  // Comparator comparator_14: pin names not known; wires that end beside it: register_15_q, {32{1'b0}}
  // Comparator comparator_15: pin names not known; wires that end beside it: register_8_q, register_16_q, comparator_15_p3, comparator_15_p4
  or or_24 (or_24_out, comparator_15_p3, comparator_15_p4);
  // NOT_Gate not_8 has open pins: in=open, out=not_8_out
  // Comparator comparator_16: pin names not known; wires that end beside it: register_5_q, register_16_q, {32{1'b0}}
  and and_1 (and_1_out, or_17_out, not_1_out);
  and and_2 (and_2_out, or_18_out, not_2_out);
  and and_3 (and_3_out, or_19_out, not_3_out);
  and and_4 (and_4_out, or_20_out, not_4_out);
  and and_5 (and_5_out, or_21_out, not_5_out);
  and and_6 (and_6_out, or_22_out, not_6_out);
  and and_7 (and_7_out, or_23_out, not_7_out);
  and and_8 (and_8_out, or_24_out, not_8_out);
  or or_25 (or_25_out, ~Power, Reset_all);  // OR_Gate
  Register #(.width(1)) register_17 (
    .D(and_1_out), .en(Power), .Q(register_20_q[12]), .clk(not_9_out), .clr(or_25_out));
  Register #(.width(1)) register_18 (.D(and_2_out), .en(Power), .Q(register_20_q[8]), .clk(not_9_out), .clr(or_25_out));
  Register #(.width(1)) register_19 (.D(and_3_out), .en(Power), .Q(register_20_q[4]), .clk(not_9_out), .clr(or_25_out));
  Register #(.width(1)) register_20 (.D(and_4_out), .en(Power), .Q(register_20_q[0]), .clk(not_9_out), .clr(or_25_out));
  Register #(.width(1)) register_21 (
    .D(and_5_out), .en(Power), .Q(register_24_q[12]), .clk(not_9_out), .clr(or_25_out));
  Register #(.width(1)) register_22 (.D(and_6_out), .en(Power), .Q(register_24_q[8]), .clk(not_9_out), .clr(or_25_out));
  Register #(.width(1)) register_23 (.D(and_7_out), .en(Power), .Q(register_24_q[4]), .clk(not_9_out), .clr(or_25_out));
  Register #(.width(1)) register_24 (.D(and_8_out), .en(Power), .Q(register_24_q[0]), .clk(not_9_out), .clr(or_25_out));
  not not_9 (not_9_out, Clk);
  or or_26 (OVER_TIME, register_20_q[12], register_20_q[8], register_20_q[0], register_24_q[12], register_24_q[8], register_24_q[4], register_24_q[0], register_20_q[4]);
endmodule

module Specialised_program_loader__SPL_____program_loads_program (
  input  Reset,
  input  Clk,
  input  Load,
  input  RAM_indicator,
  input  [1:0] Reg_number,
  input  [31:0] Data_in,
  input  Load_ram,
  output [31:0] Data_out_1,
  output [31:0] Data_out_2,
  output [31:0] Data_out_3,
  output [31:0] Data_out_4,
  output [23:0] Load_adress
);

  wire and_1_out, and_2_out, decoder_1_out0, decoder_1_out1, decoder_1_out2, decoder_1_out3, decoder_2_out0,
       decoder_2_out1, decoder_2_out2, decoder_2_out3, not_1_out;
  wire [31:0] register_1_q, register_2_q, register_3_q, register_4_q, register_5_q, register_6_q,
       register_7_q, register_8_q;

  and and_1 (and_1_out, Load, RAM_indicator);
  and and_2 (and_2_out, ~RAM_indicator, Load);  // AND_Gate
  Decoder #(.select(2), .disabled(0)) decoder_1 (
    .out0(decoder_1_out0), .out1(decoder_1_out1), .out2(decoder_1_out2), .out3(decoder_1_out3),
    .sel(Reg_number), .en(and_1_out));
  Decoder #(.select(2), .disabled(0)) decoder_2 (
    .out0(decoder_2_out0), .out1(decoder_2_out1), .out2(decoder_2_out2), .out3(decoder_2_out3),
    .sel(Reg_number), .en(and_2_out));
  Register #(.width(32)) register_1 (.D(Data_in), .en(decoder_1_out0), .Q(register_1_q), .clk(Clk), .clr(Reset));
  Register #(.width(32)) register_2 (.D(Data_in), .en(decoder_1_out1), .Q(register_2_q), .clk(Clk), .clr(Reset));
  Register #(.width(32)) register_3 (.D(Data_in), .en(decoder_1_out2), .Q(register_3_q), .clk(Clk), .clr(Reset));
  Register #(.width(32)) register_4 (.D(Data_in), .en(decoder_1_out3), .Q(register_4_q), .clk(Clk), .clr(Reset));
  not not_1 (not_1_out, Clk);
  Register #(.width(32)) register_5 (.D(Data_in), .en(decoder_2_out0), .Q(register_5_q), .clk(not_1_out), .clr(Reset));
  Register #(.width(32)) register_6 (.D(Data_in), .en(decoder_2_out1), .Q(register_6_q), .clk(not_1_out), .clr(Reset));
  Register #(.width(32)) register_7 (.D(Data_in), .en(decoder_2_out2), .Q(register_7_q), .clk(not_1_out), .clr(Reset));
  Register #(.width(32)) register_8 (.D(Data_in), .en(decoder_2_out3), .Q(register_8_q), .clk(not_1_out), .clr(Reset));
  Counter #(.width(24), .max('hffffff)) counter_1 (
    .load(1'b0), .D({24{1'b0}}), .count(Load_ram), .Q(Load_adress), .clk(Load_ram), .clr(Reset));  // open: carry
  Pull_Resistor pull_resistor_1 (.node(Data_out_1));
  Multiplexer #(.width(32), .disabled(0), .enable("false")) multiplexer_1 (
    .in0(register_5_q), .in1(register_1_q), .out(Data_out_1), .sel(RAM_indicator));
  Pull_Resistor pull_resistor_2 (.node(Data_out_2));
  Multiplexer #(.width(32), .disabled(0), .enable("false")) multiplexer_2 (
    .in0(register_6_q), .in1(register_2_q), .out(Data_out_2), .sel(RAM_indicator));
  Pull_Resistor pull_resistor_3 (.node(Data_out_3));
  Multiplexer #(.width(32), .disabled(0), .enable("false")) multiplexer_3 (
    .in0(register_7_q), .in1(register_3_q), .out(Data_out_3), .sel(RAM_indicator));
  Pull_Resistor pull_resistor_4 (.node(Data_out_4));
  Multiplexer #(.width(32), .disabled(0), .enable("false")) multiplexer_4 (
    .in0(register_8_q), .in1(register_4_q), .out(Data_out_4), .sel(RAM_indicator));
endmodule

module Simplified_CPP__SCPP (
  input  Power,
  input  \Сlk ,
  input  Load,
  input  Load_completed,
  input  Reset,
  input  [23:0] adress,
  input  [31:0] Data_in,
  input  [1:0] RAM_number,
  output Occured,
  output [31:0] _0_31,
  output [31:0] _32_63,
  output [31:0] _64_95,
  output [31:0] _96_127
);

  wire and_1_out, and_2_out, and_3_out, and_4_out, decoder_1_out0, decoder_1_out1, decoder_1_out2,
       decoder_1_out3, not_1_out, not_2_out, not_3_out, not_4_out;
  wire [31:0] pull_resistor_2_node;

  Pull_Resistor pull_resistor_1 (.node(adress));
  Decoder #(.select(2), .disabled(0)) decoder_1 (
    .out0(decoder_1_out0), .out1(decoder_1_out1), .out2(decoder_1_out2), .out3(decoder_1_out3),
    .sel(RAM_number), .en(Load));
  Pull_Resistor pull_resistor_2 (.node(pull_resistor_2_node));
  // Probe on pull_resistor_2_node
  Register #(.width(1)) register_1 (.D(Load_completed), .en(Power), .Q(Occured), .clk(Load_completed), .clr(Reset));
  and and_1 (and_1_out, Load, decoder_1_out0);
  and and_2 (and_2_out, Load, decoder_1_out1);
  and and_3 (and_3_out, Load, decoder_1_out2);
  and and_4 (and_4_out, Load, decoder_1_out3);
  not not_1 (not_1_out, and_1_out);
  not not_2 (not_2_out, and_2_out);
  not not_3 (not_3_out, and_3_out);
  not not_4 (not_4_out, and_4_out);
  RAM #(.addrWidth(24), .dataWidth(32), .bus("separate")) ram_1 (
    .addr(adress), .din(Data_in), .data(_0_31), .str(and_1_out), .sel(Power), .clk(\Сlk ), .ld(not_1_out),
    .clr(Reset));
  RAM #(.addrWidth(24), .dataWidth(32), .bus("separate")) ram_2 (
    .addr(adress), .din(Data_in), .data(_32_63), .str(and_2_out), .sel(Power), .clk(\Сlk ), .ld(not_2_out),
    .clr(Reset));
  RAM #(.addrWidth(24), .dataWidth(32), .bus("separate")) ram_3 (
    .addr(adress), .din(Data_in), .data(_64_95), .str(and_3_out), .sel(Power), .clk(\Сlk ), .ld(not_3_out),
    .clr(Reset));
  RAM #(.addrWidth(24), .dataWidth(32), .bus("separate")) ram_4 (
    .addr(adress), .din(Data_in), .data(_96_127), .str(and_4_out), .sel(Power), .clk(\Сlk ), .ld(not_4_out),
    .clr(Reset));
  Pull_Resistor pull_resistor_3 (.node(_0_31));
  Pull_Resistor pull_resistor_4 (.node(_32_63));
  Pull_Resistor pull_resistor_5 (.node(_64_95));
  Pull_Resistor pull_resistor_6 (.node(_96_127));
  // also tied to VCC on the sheet: pull_resistor_2_node[15]
endmodule

module CPU (
  input  in_1,
  input  in_2
);

  wire Access_to_RAM__US, and_1_out, and_2_out, and_3_out, and_4_out, and_5_out, and_6_out, and_7_out, Clk,
       clock_1_out, Comparation, \cpu_сore_cpuc_1_compare , \cpu_сore_cpuc_1_error ,
       \cpu_сore_cpuc_1_occured , \cpu_сore_cpuc_2_compare , \cpu_сore_cpuc_2_error ,
       \cpu_сore_cpuc_2_occured , \cpu_сore_cpuc_3_compare , \cpu_сore_cpuc_3_error ,
       \cpu_сore_cpuc_3_occured , \cpu_сore_cpuc_4_compare , \cpu_сore_cpuc_4_error ,
       \cpu_сore_cpuc_4_occured , \cpu_сore_cpuc_5_compare , \cpu_сore_cpuc_5_error ,
       \cpu_сore_cpuc_5_occured , \cpu_сore_cpuc_6_compare , \cpu_сore_cpuc_6_error ,
       \cpu_сore_cpuc_6_occured , \cpu_сore_cpuc_7_compare , \cpu_сore_cpuc_7_error ,
       \cpu_сore_cpuc_7_occured , \cpu_сore_cpuc_8_compare , \cpu_сore_cpuc_8_error ,
       \cpu_сore_cpuc_8_occured , \cpu_сore_cpuc_9_compare , \cpu_сore_cpuc_9_error ,
       \cpu_сore_cpuc_9_occured , \cpu_сore_cpuc_10_compare , \cpu_сore_cpuc_10_error ,
       \cpu_сore_cpuc_10_occured , \cpu_сore_cpuc_11_compare , \cpu_сore_cpuc_11_error ,
       \cpu_сore_cpuc_11_occured , \cpu_сore_cpuc_12_compare , \cpu_сore_cpuc_12_error ,
       \cpu_сore_cpuc_12_occured , \cpu_сore_cpuc_13_compare , \cpu_сore_cpuc_13_error ,
       \cpu_сore_cpuc_13_occured , \cpu_сore_cpuc_14_compare , \cpu_сore_cpuc_14_error ,
       \cpu_сore_cpuc_14_occured , \cpu_сore_cpuc_15_compare , \cpu_сore_cpuc_15_error ,
       \cpu_сore_cpuc_15_occured , \cpu_сore_cpuc_16_compare , \cpu_сore_cpuc_16_error ,
       \cpu_сore_cpuc_16_occured , Enable_Date_reg, Enable_operation_with_TM, Load_timer, Load_USP,
       main_cpu_core_mcpuc_1_p35, main_cpu_core_mcpuc_1_p36, main_cpu_core_mcpuc_1_p37,
       main_cpu_core_mcpuc_1_p38, main_cpu_core_mcpuc_1_p39, main_cpu_core_mcpuc_1_p40,
       main_cpu_core_mcpuc_1_p41, main_cpu_core_mcpuc_1_p42, main_cpu_core_mcpuc_1_p43,
       main_cpu_core_mcpuc_1_p44, main_cpu_core_mcpuc_1_p45, main_cpu_core_mcpuc_1_p46,
       main_cpu_core_mcpuc_1_p47, main_cpu_core_mcpuc_1_p48, main_cpu_core_mcpuc_1_p49,
       main_cpu_core_mcpuc_1_p50, or_1_out, or_2_out, or_3_out, or_4_out, Power, Reset, Reset_clk_reg,
       Reset_speed_clk, Reset_timer, Reset_TM, undriven_5, undriven_10, undriven_11, undriven_12,
       undriven_13, undriven_14, undriven_15, undriven_16, undriven_17, undriven_18, undriven_19,
       undriven_20, undriven_33, undriven_38, undriven_39, undriven_40, undriven_41, undriven_42,
       undriven_43, undriven_44, undriven_45, undriven_46, undriven_47, undriven_48, undriven_61,
       undriven_66, undriven_67, undriven_68, undriven_69, undriven_70, undriven_71, undriven_72,
       undriven_73, undriven_74, undriven_75, undriven_76, undriven_89, undriven_94, undriven_95,
       undriven_96, undriven_97, undriven_98, undriven_99, undriven_100, undriven_101, undriven_102,
       undriven_103, undriven_104, UP_DOWN__US, UPop, UPush;
  wire [1:0] \Сlock_load_control ;
  wire [2:0] main_cpu_core_mcpuc_1_p3, main_cpu_core_mcpuc_1_p4, main_cpu_core_mcpuc_1_p5,
       main_cpu_core_mcpuc_1_p6, main_cpu_core_mcpuc_1_p7, main_cpu_core_mcpuc_1_p8,
       main_cpu_core_mcpuc_1_p9, main_cpu_core_mcpuc_1_p10, main_cpu_core_mcpuc_1_p11,
       main_cpu_core_mcpuc_1_p12, main_cpu_core_mcpuc_1_p13, main_cpu_core_mcpuc_1_p14,
       main_cpu_core_mcpuc_1_p15, main_cpu_core_mcpuc_1_p16, main_cpu_core_mcpuc_1_p17,
       main_cpu_core_mcpuc_1_p18;
  wire [3:0] TM_adress;
  wire [4:0] TM_COMAND;
  wire [31:0] A, C, \cpu_сore_cpuc_1_data_adress_out , \cpu_сore_cpuc_1_data_out , \cpu_сore_cpuc_1_etype ,
       \cpu_сore_cpuc_2_data_adress_out , \cpu_сore_cpuc_2_data_out , \cpu_сore_cpuc_2_etype ,
       \cpu_сore_cpuc_3_data_adress_out , \cpu_сore_cpuc_3_data_out , \cpu_сore_cpuc_3_etype ,
       \cpu_сore_cpuc_4_data_adress_out , \cpu_сore_cpuc_4_data_out , \cpu_сore_cpuc_4_etype ,
       \cpu_сore_cpuc_5_data_adress_out , \cpu_сore_cpuc_5_data_out , \cpu_сore_cpuc_5_etype ,
       \cpu_сore_cpuc_6_data_adress_out , \cpu_сore_cpuc_6_data_out , \cpu_сore_cpuc_6_etype ,
       \cpu_сore_cpuc_7_data_adress_out , \cpu_сore_cpuc_7_data_out , \cpu_сore_cpuc_7_etype ,
       \cpu_сore_cpuc_8_data_adress_out , \cpu_сore_cpuc_8_data_out , \cpu_сore_cpuc_8_etype ,
       \cpu_сore_cpuc_9_data_adress_out , \cpu_сore_cpuc_9_data_out , \cpu_сore_cpuc_9_etype ,
       \cpu_сore_cpuc_10_data_adress_out , \cpu_сore_cpuc_10_data_out , \cpu_сore_cpuc_10_etype ,
       \cpu_сore_cpuc_11_data_adress_out , \cpu_сore_cpuc_11_data_out , \cpu_сore_cpuc_11_etype ,
       \cpu_сore_cpuc_12_data_adress_out , \cpu_сore_cpuc_12_data_out , \cpu_сore_cpuc_12_etype ,
       \cpu_сore_cpuc_13_data_adress_out , \cpu_сore_cpuc_13_data_out , \cpu_сore_cpuc_13_etype ,
       \cpu_сore_cpuc_14_data_adress_out , \cpu_сore_cpuc_14_data_out , \cpu_сore_cpuc_14_etype ,
       \cpu_сore_cpuc_15_data_adress_out , \cpu_сore_cpuc_15_data_out , \cpu_сore_cpuc_15_etype ,
       \cpu_сore_cpuc_16_data_adress_out , \cpu_сore_cpuc_16_data_out , \cpu_сore_cpuc_16_etype , D, Data_in,
       main_cpu_core_mcpuc_1_p19, main_cpu_core_mcpuc_1_p20, main_cpu_core_mcpuc_1_p21,
       main_cpu_core_mcpuc_1_p22, main_cpu_core_mcpuc_1_p23, main_cpu_core_mcpuc_1_p24,
       main_cpu_core_mcpuc_1_p25, main_cpu_core_mcpuc_1_p26, main_cpu_core_mcpuc_1_p27,
       main_cpu_core_mcpuc_1_p28, main_cpu_core_mcpuc_1_p29, main_cpu_core_mcpuc_1_p30,
       main_cpu_core_mcpuc_1_p31, main_cpu_core_mcpuc_1_p32, main_cpu_core_mcpuc_1_p33,
       main_cpu_core_mcpuc_1_p34, multiplexer_1_out, Timer_time, undriven, undriven_2, undriven_3,
       undriven_4, undriven_6, undriven_7, undriven_8, undriven_9, undriven_21, undriven_22, undriven_23,
       undriven_24, undriven_25, undriven_26, undriven_27, undriven_28, undriven_29, undriven_30,
       undriven_31, undriven_32, undriven_34, undriven_35, undriven_36, undriven_37, undriven_49,
       undriven_50, undriven_51, undriven_52, undriven_53, undriven_54, undriven_55, undriven_56,
       undriven_57, undriven_58, undriven_59, undriven_60, undriven_62, undriven_63, undriven_64,
       undriven_65, undriven_77, undriven_78, undriven_79, undriven_80, undriven_81, undriven_82,
       undriven_83, undriven_84, undriven_85, undriven_86, undriven_87, undriven_88, undriven_90,
       undriven_91, undriven_92, undriven_93, undriven_105, undriven_106, undriven_107, undriven_108,
       undriven_109, undriven_110, undriven_111, undriven_112, UStack_out, Z;

  User_Stack__US user_stack_us_1 (
    .Z_Access_to_memory(Z), .Load_US_Pointer(C), .Data_in(Data_in), .Power(Power), .Clk(Clk), .Reset(Reset),
    .Load_US(Load_USP), .UP_0__DOWN_1(UP_DOWN__US), .Access(Access_to_RAM__US), .UPush(UPush), .UPop(UPop),
    .Data_out(UStack_out));
  and and_1 (and_1_out, Reset_clk_reg, Comparation);
  and and_2 (and_2_out, Reset_TM, Comparation);
  and and_3 (and_3_out, Reset_timer, Comparation);
  and and_4 (and_4_out, Reset_speed_clk, Comparation);
  or or_1 (or_1_out, and_1_out, Reset);
  or or_2 (or_2_out, and_2_out, Reset);
  or or_3 (or_3_out, and_3_out, Reset);
  or or_4 (or_4_out, and_4_out, Reset);
  Clock #(.highDuration(2050), .lowDuration(2050)) clock_1 (.out(clock_1_out));
  Multiplexer #(.select(2), .width(32), .disabled(0)) multiplexer_1 (
    .in0(A), .in1(Z), .in2(D), .in3(C), .out(multiplexer_1_out), .sel(\Сlock_load_control ), .en(Power));
  and and_5 (and_5_out, Comparation, Enable_Date_reg);
  and and_6 (and_6_out, Comparation, Enable_operation_with_TM);
  and and_7 (and_7_out, Comparation, Load_timer);
  Clock__Time clock_time_1 (
    .Reset_timer(or_3_out), .Power(Power), .Load_timer(and_7_out), .Reset_speed_clock(or_4_out), .Clk(Clk),
    .Clk__one_per_second(clock_1_out), .Data_in(multiplexer_1_out), .En_Reg(and_5_out), .Reset_reg(or_1_out),
    .Access_to_reg(and_6_out), .Reset_time_memory(or_2_out), .Comand(TM_COMAND),
    .Time_memory_adress(TM_adress), .Timer_time(Timer_time));  // open: Porsion_of_time, Date, Over_time, TM_value
  // Main_CPU_Core_MCPUC main_cpu_core_mcpuc_1: pin names not known; wires that end beside it: in_1, in_2, main_cpu_core_mcpuc_1_p3, main_cpu_core_mcpuc_1_p4, main_cpu_core_mcpuc_1_p5, main_cpu_core_mcpuc_1_p6, main_cpu_core_mcpuc_1_p7, main_cpu_core_mcpuc_1_p8, main_cpu_core_mcpuc_1_p9, main_cpu_core_mcpuc_1_p10, main_cpu_core_mcpuc_1_p11, main_cpu_core_mcpuc_1_p12, main_cpu_core_mcpuc_1_p13, main_cpu_core_mcpuc_1_p14, main_cpu_core_mcpuc_1_p15, main_cpu_core_mcpuc_1_p16, main_cpu_core_mcpuc_1_p17, main_cpu_core_mcpuc_1_p18, main_cpu_core_mcpuc_1_p19, main_cpu_core_mcpuc_1_p20, main_cpu_core_mcpuc_1_p21, main_cpu_core_mcpuc_1_p22, main_cpu_core_mcpuc_1_p23, main_cpu_core_mcpuc_1_p24, main_cpu_core_mcpuc_1_p25, main_cpu_core_mcpuc_1_p26, main_cpu_core_mcpuc_1_p27, main_cpu_core_mcpuc_1_p28, main_cpu_core_mcpuc_1_p29, main_cpu_core_mcpuc_1_p30, main_cpu_core_mcpuc_1_p31, main_cpu_core_mcpuc_1_p32, main_cpu_core_mcpuc_1_p33, main_cpu_core_mcpuc_1_p34, main_cpu_core_mcpuc_1_p35, main_cpu_core_mcpuc_1_p36, main_cpu_core_mcpuc_1_p37, main_cpu_core_mcpuc_1_p38, main_cpu_core_mcpuc_1_p39, main_cpu_core_mcpuc_1_p40, main_cpu_core_mcpuc_1_p41, main_cpu_core_mcpuc_1_p42, main_cpu_core_mcpuc_1_p43, main_cpu_core_mcpuc_1_p44, main_cpu_core_mcpuc_1_p45, main_cpu_core_mcpuc_1_p46, main_cpu_core_mcpuc_1_p47, main_cpu_core_mcpuc_1_p48, main_cpu_core_mcpuc_1_p49, main_cpu_core_mcpuc_1_p50
  \CPU_Сore__CPUC  \cpu_сore_cpuc_1  (
    .Data_adress_out(\cpu_сore_cpuc_1_data_adress_out ), .Data_in_2(undriven_25),
    .Data_out(\cpu_сore_cpuc_1_data_out ), .Main_core_comand(undriven_21), .Power(in_2), .Clk(undriven_17),
    .Start_CPU_Core(main_cpu_core_mcpuc_1_p35), .CPU_Core_condition(main_cpu_core_mcpuc_1_p3),
    .Execute_Device(undriven_6), .Data_in__U(undriven), .Occured(\cpu_сore_cpuc_1_occured ),
    .compare(\cpu_сore_cpuc_1_compare ), .Error(\cpu_сore_cpuc_1_error ), .Data_in(undriven_12),
    .ETYPE(\cpu_сore_cpuc_1_etype ), .Data_in_3(main_cpu_core_mcpuc_1_p19), .Overtimed(undriven_5));
  \CPU_Сore__CPUC  \cpu_сore_cpuc_2  (
    .Data_adress_out(\cpu_сore_cpuc_2_data_adress_out ), .Data_in_2(undriven_26),
    .Data_out(\cpu_сore_cpuc_2_data_out ), .Main_core_comand(undriven_22), .Power(in_2), .Clk(undriven_18),
    .Start_CPU_Core(main_cpu_core_mcpuc_1_p36), .CPU_Core_condition(main_cpu_core_mcpuc_1_p4),
    .Execute_Device(undriven_7), .Data_in__U(undriven_2), .Occured(\cpu_сore_cpuc_2_occured ),
    .compare(\cpu_сore_cpuc_2_compare ), .Error(\cpu_сore_cpuc_2_error ), .Data_in(undriven_13),
    .ETYPE(\cpu_сore_cpuc_2_etype ), .Data_in_3(main_cpu_core_mcpuc_1_p20), .Overtimed(undriven_10));
  \CPU_Сore__CPUC  \cpu_сore_cpuc_3  (
    .Data_adress_out(\cpu_сore_cpuc_3_data_adress_out ), .Data_in_2(undriven_27),
    .Data_out(\cpu_сore_cpuc_3_data_out ), .Main_core_comand(undriven_23), .Power(in_2), .Clk(undriven_19),
    .Start_CPU_Core(main_cpu_core_mcpuc_1_p37), .CPU_Core_condition(main_cpu_core_mcpuc_1_p5),
    .Execute_Device(undriven_8), .Data_in__U(undriven_3), .Occured(\cpu_сore_cpuc_3_occured ),
    .compare(\cpu_сore_cpuc_3_compare ), .Error(\cpu_сore_cpuc_3_error ), .Data_in(undriven_14),
    .ETYPE(\cpu_сore_cpuc_3_etype ), .Data_in_3(main_cpu_core_mcpuc_1_p21), .Overtimed(undriven_11));
  \CPU_Сore__CPUC  \cpu_сore_cpuc_4  (
    .Data_adress_out(\cpu_сore_cpuc_4_data_adress_out ), .Data_in_2(undriven_28),
    .Data_out(\cpu_сore_cpuc_4_data_out ), .Main_core_comand(undriven_24), .Power(in_2), .Clk(undriven_20),
    .Start_CPU_Core(main_cpu_core_mcpuc_1_p38), .CPU_Core_condition(main_cpu_core_mcpuc_1_p6),
    .Execute_Device(undriven_9), .Data_in__U(undriven_4), .Occured(\cpu_сore_cpuc_4_occured ),
    .compare(\cpu_сore_cpuc_4_compare ), .Error(\cpu_сore_cpuc_4_error ), .Data_in(undriven_15),
    .ETYPE(\cpu_сore_cpuc_4_etype ), .Data_in_3(main_cpu_core_mcpuc_1_p22), .Overtimed(undriven_16));
  \CPU_Сore__CPUC  \cpu_сore_cpuc_5  (
    .Data_adress_out(\cpu_сore_cpuc_5_data_adress_out ), .Data_in_2(undriven_53),
    .Data_out(\cpu_сore_cpuc_5_data_out ), .Main_core_comand(undriven_49), .Power(in_2), .Clk(undriven_45),
    .Start_CPU_Core(main_cpu_core_mcpuc_1_p39), .CPU_Core_condition(main_cpu_core_mcpuc_1_p7),
    .Execute_Device(undriven_34), .Data_in__U(undriven_29), .Occured(\cpu_сore_cpuc_5_occured ),
    .compare(\cpu_сore_cpuc_5_compare ), .Error(\cpu_сore_cpuc_5_error ), .Data_in(undriven_40),
    .ETYPE(\cpu_сore_cpuc_5_etype ), .Data_in_3(main_cpu_core_mcpuc_1_p23), .Overtimed(undriven_33));
  \CPU_Сore__CPUC  \cpu_сore_cpuc_6  (
    .Data_adress_out(\cpu_сore_cpuc_6_data_adress_out ), .Data_in_2(undriven_54),
    .Data_out(\cpu_сore_cpuc_6_data_out ), .Main_core_comand(undriven_50), .Power(in_2), .Clk(undriven_46),
    .Start_CPU_Core(main_cpu_core_mcpuc_1_p40), .CPU_Core_condition(main_cpu_core_mcpuc_1_p8),
    .Execute_Device(undriven_35), .Data_in__U(undriven_30), .Occured(\cpu_сore_cpuc_6_occured ),
    .compare(\cpu_сore_cpuc_6_compare ), .Error(\cpu_сore_cpuc_6_error ), .Data_in(undriven_41),
    .ETYPE(\cpu_сore_cpuc_6_etype ), .Data_in_3(main_cpu_core_mcpuc_1_p26), .Overtimed(undriven_38));
  \CPU_Сore__CPUC  \cpu_сore_cpuc_7  (
    .Data_adress_out(\cpu_сore_cpuc_7_data_adress_out ), .Data_in_2(undriven_55),
    .Data_out(\cpu_сore_cpuc_7_data_out ), .Main_core_comand(undriven_51), .Power(in_2), .Clk(undriven_47),
    .Start_CPU_Core(main_cpu_core_mcpuc_1_p41), .CPU_Core_condition(main_cpu_core_mcpuc_1_p9),
    .Execute_Device(undriven_36), .Data_in__U(undriven_31), .Occured(\cpu_сore_cpuc_7_occured ),
    .compare(\cpu_сore_cpuc_7_compare ), .Error(\cpu_сore_cpuc_7_error ), .Data_in(undriven_42),
    .ETYPE(\cpu_сore_cpuc_7_etype ), .Data_in_3(main_cpu_core_mcpuc_1_p25), .Overtimed(undriven_39));
  \CPU_Сore__CPUC  \cpu_сore_cpuc_8  (
    .Data_adress_out(\cpu_сore_cpuc_8_data_adress_out ), .Data_in_2(undriven_56),
    .Data_out(\cpu_сore_cpuc_8_data_out ), .Main_core_comand(undriven_52), .Power(in_2), .Clk(undriven_48),
    .Start_CPU_Core(main_cpu_core_mcpuc_1_p42), .CPU_Core_condition(main_cpu_core_mcpuc_1_p10),
    .Execute_Device(undriven_37), .Data_in__U(undriven_32), .Occured(\cpu_сore_cpuc_8_occured ),
    .compare(\cpu_сore_cpuc_8_compare ), .Error(\cpu_сore_cpuc_8_error ), .Data_in(undriven_43),
    .ETYPE(\cpu_сore_cpuc_8_etype ), .Data_in_3(main_cpu_core_mcpuc_1_p24), .Overtimed(undriven_44));
  \CPU_Сore__CPUC  \cpu_сore_cpuc_9  (
    .Data_adress_out(\cpu_сore_cpuc_9_data_adress_out ), .Data_in_2(undriven_81),
    .Data_out(\cpu_сore_cpuc_9_data_out ), .Main_core_comand(undriven_77), .Power(in_2), .Clk(undriven_73),
    .Start_CPU_Core(main_cpu_core_mcpuc_1_p43), .CPU_Core_condition(main_cpu_core_mcpuc_1_p11),
    .Execute_Device(undriven_62), .Data_in__U(undriven_57), .Occured(\cpu_сore_cpuc_9_occured ),
    .compare(\cpu_сore_cpuc_9_compare ), .Error(\cpu_сore_cpuc_9_error ), .Data_in(undriven_68),
    .ETYPE(\cpu_сore_cpuc_9_etype ), .Data_in_3(main_cpu_core_mcpuc_1_p27), .Overtimed(undriven_61));
  \CPU_Сore__CPUC  \cpu_сore_cpuc_10  (
    .Data_adress_out(\cpu_сore_cpuc_10_data_adress_out ), .Data_in_2(undriven_82),
    .Data_out(\cpu_сore_cpuc_10_data_out ), .Main_core_comand(undriven_78), .Power(in_2), .Clk(undriven_74),
    .Start_CPU_Core(main_cpu_core_mcpuc_1_p44), .CPU_Core_condition(main_cpu_core_mcpuc_1_p12),
    .Execute_Device(undriven_63), .Data_in__U(undriven_58), .Occured(\cpu_сore_cpuc_10_occured ),
    .compare(\cpu_сore_cpuc_10_compare ), .Error(\cpu_сore_cpuc_10_error ), .Data_in(undriven_69),
    .ETYPE(\cpu_сore_cpuc_10_etype ), .Data_in_3(main_cpu_core_mcpuc_1_p28), .Overtimed(undriven_66));
  \CPU_Сore__CPUC  \cpu_сore_cpuc_11  (
    .Data_adress_out(\cpu_сore_cpuc_11_data_adress_out ), .Data_in_2(undriven_83),
    .Data_out(\cpu_сore_cpuc_11_data_out ), .Main_core_comand(undriven_79), .Power(in_2), .Clk(undriven_75),
    .Start_CPU_Core(main_cpu_core_mcpuc_1_p45), .CPU_Core_condition(main_cpu_core_mcpuc_1_p13),
    .Execute_Device(undriven_64), .Data_in__U(undriven_59), .Occured(\cpu_сore_cpuc_11_occured ),
    .compare(\cpu_сore_cpuc_11_compare ), .Error(\cpu_сore_cpuc_11_error ), .Data_in(undriven_70),
    .ETYPE(\cpu_сore_cpuc_11_etype ), .Data_in_3(main_cpu_core_mcpuc_1_p29), .Overtimed(undriven_67));
  \CPU_Сore__CPUC  \cpu_сore_cpuc_12  (
    .Data_adress_out(\cpu_сore_cpuc_12_data_adress_out ), .Data_in_2(undriven_84),
    .Data_out(\cpu_сore_cpuc_12_data_out ), .Main_core_comand(undriven_80), .Power(in_2), .Clk(undriven_76),
    .Start_CPU_Core(main_cpu_core_mcpuc_1_p46), .CPU_Core_condition(main_cpu_core_mcpuc_1_p14),
    .Execute_Device(undriven_65), .Data_in__U(undriven_60), .Occured(\cpu_сore_cpuc_12_occured ),
    .compare(\cpu_сore_cpuc_12_compare ), .Error(\cpu_сore_cpuc_12_error ), .Data_in(undriven_71),
    .ETYPE(\cpu_сore_cpuc_12_etype ), .Data_in_3(main_cpu_core_mcpuc_1_p30), .Overtimed(undriven_72));
  \CPU_Сore__CPUC  \cpu_сore_cpuc_13  (
    .Data_adress_out(\cpu_сore_cpuc_13_data_adress_out ), .Data_in_2(undriven_109),
    .Data_out(\cpu_сore_cpuc_13_data_out ), .Main_core_comand(undriven_105), .Power(in_2),
    .Clk(undriven_101), .Start_CPU_Core(main_cpu_core_mcpuc_1_p47),
    .CPU_Core_condition(main_cpu_core_mcpuc_1_p15), .Execute_Device(undriven_90), .Data_in__U(undriven_85),
    .Occured(\cpu_сore_cpuc_13_occured ), .compare(\cpu_сore_cpuc_13_compare ),
    .Error(\cpu_сore_cpuc_13_error ), .Data_in(undriven_96), .ETYPE(\cpu_сore_cpuc_13_etype ),
    .Data_in_3(main_cpu_core_mcpuc_1_p31), .Overtimed(undriven_89));
  \CPU_Сore__CPUC  \cpu_сore_cpuc_14  (
    .Data_adress_out(\cpu_сore_cpuc_14_data_adress_out ), .Data_in_2(undriven_110),
    .Data_out(\cpu_сore_cpuc_14_data_out ), .Main_core_comand(undriven_106), .Power(in_2),
    .Clk(undriven_102), .Start_CPU_Core(main_cpu_core_mcpuc_1_p48),
    .CPU_Core_condition(main_cpu_core_mcpuc_1_p16), .Execute_Device(undriven_91), .Data_in__U(undriven_86),
    .Occured(\cpu_сore_cpuc_14_occured ), .compare(\cpu_сore_cpuc_14_compare ),
    .Error(\cpu_сore_cpuc_14_error ), .Data_in(undriven_97), .ETYPE(\cpu_сore_cpuc_14_etype ),
    .Data_in_3(main_cpu_core_mcpuc_1_p32), .Overtimed(undriven_94));
  \CPU_Сore__CPUC  \cpu_сore_cpuc_15  (
    .Data_adress_out(\cpu_сore_cpuc_15_data_adress_out ), .Data_in_2(undriven_111),
    .Data_out(\cpu_сore_cpuc_15_data_out ), .Main_core_comand(undriven_107), .Power(in_2),
    .Clk(undriven_103), .Start_CPU_Core(main_cpu_core_mcpuc_1_p49),
    .CPU_Core_condition(main_cpu_core_mcpuc_1_p17), .Execute_Device(undriven_92), .Data_in__U(undriven_87),
    .Occured(\cpu_сore_cpuc_15_occured ), .compare(\cpu_сore_cpuc_15_compare ),
    .Error(\cpu_сore_cpuc_15_error ), .Data_in(undriven_98), .ETYPE(\cpu_сore_cpuc_15_etype ),
    .Data_in_3(main_cpu_core_mcpuc_1_p33), .Overtimed(undriven_95));
  \CPU_Сore__CPUC  \cpu_сore_cpuc_16  (
    .Data_adress_out(\cpu_сore_cpuc_16_data_adress_out ), .Data_in_2(undriven_112),
    .Data_out(\cpu_сore_cpuc_16_data_out ), .Main_core_comand(undriven_108), .Power(in_2),
    .Clk(undriven_104), .Start_CPU_Core(main_cpu_core_mcpuc_1_p50),
    .CPU_Core_condition(main_cpu_core_mcpuc_1_p18), .Execute_Device(undriven_93), .Data_in__U(undriven_88),
    .Occured(\cpu_сore_cpuc_16_occured ), .compare(\cpu_сore_cpuc_16_compare ),
    .Error(\cpu_сore_cpuc_16_error ), .Data_in(undriven_99), .ETYPE(\cpu_сore_cpuc_16_etype ),
    .Data_in_3(main_cpu_core_mcpuc_1_p34), .Overtimed(undriven_100));
endmodule

module RAM_for_computer (
  input  [15:0] in_1,
  input  power,
  input  Clk,
  input  Reset,
  input  [31:0] in_5,
  input  [23:0] in_6,
  input  [31:0] in_7,
  input  [23:0] in_8,
  input  [31:0] in_9,
  input  [23:0] in_10,
  input  [31:0] in_11,
  input  [23:0] in_12,
  input  [31:0] in_13,
  input  [31:0] in_14,
  input  [23:0] in_15,
  input  [23:0] in_16,
  input  [31:0] in_17,
  input  [23:0] in_18,
  input  [31:0] in_19,
  input  [23:0] in_20,
  input  [31:0] in_21,
  input  [23:0] in_22,
  input  [31:0] in_23,
  input  [23:0] in_24,
  input  [31:0] in_25,
  input  [31:0] in_26,
  input  [23:0] in_27,
  input  [23:0] in_28,
  input  [31:0] in_29,
  input  [31:0] in_30,
  input  [23:0] in_31,
  input  [23:0] in_32,
  input  [31:0] in_33,
  input  [23:0] in_34,
  input  [31:0] in_35,
  input  [23:0] in_36,
  output [31:0] out_37,
  output [31:0] out_38,
  output [31:0] out_39,
  output [31:0] out_40,
  output [31:0] out_41,
  output [31:0] out_42,
  output [31:0] out_43,
  output [31:0] out_44,
  output [31:0] out_45,
  output [31:0] out_46,
  output [31:0] out_47,
  output [31:0] out_48,
  output [31:0] out_49,
  output [31:0] out_50,
  output [31:0] out_51,
  output [31:0] out_52
);

  wire not_1_out, not_2_out, not_3_out, not_4_out, not_5_out, not_6_out, not_7_out, not_8_out, not_9_out,
       not_10_out, not_11_out, not_12_out, not_13_out, not_14_out, not_15_out, not_16_out;

  Pull_Resistor pull_resistor_1 (.node(power));
  Pull_Resistor pull_resistor_2 (.node(Reset));
  Pull_Resistor pull_resistor_3 (.node(in_1));
  Pull_Resistor pull_resistor_4 (.node(Clk));
  Pull_Resistor pull_resistor_5 (.node(in_5));
  Pull_Resistor pull_resistor_6 (.node(in_6));
  Pull_Resistor pull_resistor_7 (.node(in_8));
  Pull_Resistor pull_resistor_8 (.node(in_7));
  Pull_Resistor pull_resistor_9 (.node(in_9));
  Pull_Resistor pull_resistor_10 (.node(in_10));
  Pull_Resistor pull_resistor_11 (.node(in_12));
  Pull_Resistor pull_resistor_12 (.node(in_11));
  Pull_Resistor pull_resistor_13 (.node(in_13));
  Pull_Resistor pull_resistor_14 (.node(in_15));
  Pull_Resistor pull_resistor_15 (.node(in_16));
  Pull_Resistor pull_resistor_16 (.node(in_14));
  Pull_Resistor pull_resistor_17 (.node(in_19));
  Pull_Resistor pull_resistor_18 (.node(in_20));
  Pull_Resistor pull_resistor_19 (.node(in_22));
  Pull_Resistor pull_resistor_20 (.node(in_21));
  Pull_Resistor pull_resistor_21 (.node(in_23));
  Pull_Resistor pull_resistor_22 (.node(in_24));
  Pull_Resistor pull_resistor_23 (.node(in_28));
  Pull_Resistor pull_resistor_24 (.node(in_32));
  Pull_Resistor pull_resistor_25 (.node(in_27));
  Pull_Resistor pull_resistor_26 (.node(in_31));
  Pull_Resistor pull_resistor_27 (.node(in_34));
  Pull_Resistor pull_resistor_28 (.node(in_36));
  Pull_Resistor pull_resistor_29 (.node(in_18));
  Pull_Resistor pull_resistor_30 (.node(in_17));
  Pull_Resistor pull_resistor_31 (.node(in_26));
  Pull_Resistor pull_resistor_32 (.node(in_30));
  Pull_Resistor pull_resistor_33 (.node(in_25));
  Pull_Resistor pull_resistor_34 (.node(in_29));
  Pull_Resistor pull_resistor_35 (.node(in_33));
  Pull_Resistor pull_resistor_36 (.node(in_35));
  not not_1 (not_1_out, in_1[0]);
  not not_2 (not_2_out, in_1[1]);
  not not_3 (not_3_out, in_1[2]);
  not not_4 (not_4_out, in_1[3]);
  not not_5 (not_5_out, in_1[4]);
  not not_6 (not_6_out, in_1[5]);
  not not_7 (not_7_out, in_1[6]);
  not not_8 (not_8_out, in_1[7]);
  not not_9 (not_9_out, in_1[8]);
  not not_10 (not_10_out, in_1[9]);
  not not_11 (not_11_out, in_1[10]);
  not not_12 (not_12_out, in_1[11]);
  not not_13 (not_13_out, in_1[12]);
  not not_14 (not_14_out, in_1[13]);
  not not_15 (not_15_out, in_1[14]);
  not not_16 (not_16_out, in_1[15]);
  Pull_Resistor pull_resistor_37 (.node(out_37));
  RAM #(.addrWidth(24), .dataWidth(32), .bus("separate")) ram_1 (
    .addr(in_6), .din(in_5), .data(out_37), .str(in_1[0]), .sel(power), .clk(Clk), .ld(not_1_out), .clr(Reset));
  Pull_Resistor pull_resistor_38 (.node(out_38));
  RAM #(.addrWidth(24), .dataWidth(32), .bus("separate")) ram_2 (
    .addr(in_8), .din(in_7), .data(out_38), .str(in_1[1]), .sel(power), .clk(Clk), .ld(not_2_out), .clr(Reset));
  Pull_Resistor pull_resistor_39 (.node(out_39));
  RAM #(.addrWidth(24), .dataWidth(32), .bus("separate")) ram_3 (
    .addr(in_10), .din(in_9), .data(out_39), .str(in_1[2]), .sel(power), .clk(Clk), .ld(not_3_out),
    .clr(Reset));
  RAM #(.addrWidth(24), .dataWidth(32), .bus("separate")) ram_4 (
    .addr(in_12), .din(in_11), .data(out_40), .str(in_1[3]), .sel(power), .clk(Clk), .ld(not_4_out),
    .clr(Reset));
  Pull_Resistor pull_resistor_40 (.node(out_40));
  RAM #(.addrWidth(24), .dataWidth(32), .bus("separate")) ram_5 (
    .addr(in_15), .din(in_13), .data(out_41), .str(in_1[4]), .sel(power), .clk(Clk), .ld(not_5_out),
    .clr(Reset));
  Pull_Resistor pull_resistor_41 (.node(out_41));
  Pull_Resistor pull_resistor_42 (.node(out_42));
  RAM #(.addrWidth(24), .dataWidth(32), .bus("separate")) ram_6 (
    .addr(in_16), .din(in_14), .data(out_42), .str(in_1[5]), .sel(power), .clk(Clk), .ld(not_6_out),
    .clr(Reset));
  Pull_Resistor pull_resistor_43 (.node(out_43));
  RAM #(.addrWidth(24), .dataWidth(32), .bus("separate")) ram_7 (
    .addr(in_18), .din(in_17), .data(out_43), .str(in_1[6]), .sel(power), .clk(Clk), .ld(not_7_out),
    .clr(Reset));
  RAM #(.addrWidth(24), .dataWidth(32), .bus("separate")) ram_8 (
    .addr(in_20), .din(in_19), .data(out_44), .str(in_1[7]), .sel(power), .clk(Clk), .ld(not_8_out),
    .clr(Reset));
  Pull_Resistor pull_resistor_44 (.node(out_44));
  Pull_Resistor pull_resistor_45 (.node(out_45));
  RAM #(.addrWidth(24), .dataWidth(32), .bus("separate")) ram_9 (
    .addr(in_22), .din(in_21), .data(out_45), .str(in_1[8]), .sel(power), .clk(Clk), .ld(not_9_out),
    .clr(Reset));
  RAM #(.addrWidth(24), .dataWidth(32), .bus("separate")) ram_10 (
    .addr(in_24), .din(in_23), .data(out_46), .str(in_1[9]), .sel(power), .clk(Clk), .ld(not_10_out),
    .clr(Reset));
  Pull_Resistor pull_resistor_46 (.node(out_46));
  RAM #(.addrWidth(24), .dataWidth(32), .bus("separate")) ram_11 (
    .addr(in_28), .din(in_26), .data(out_47), .str(in_1[10]), .sel(power), .clk(Clk), .ld(not_11_out),
    .clr(Reset));
  Pull_Resistor pull_resistor_47 (.node(out_47));
  Pull_Resistor pull_resistor_48 (.node(out_48));
  RAM #(.addrWidth(24), .dataWidth(32), .bus("separate")) ram_12 (
    .addr(in_32), .din(in_30), .data(out_48), .str(in_1[11]), .sel(power), .clk(Clk), .ld(not_12_out),
    .clr(Reset));
  RAM #(.addrWidth(24), .dataWidth(32), .bus("separate")) ram_13 (
    .addr(in_27), .din(in_25), .data(out_49), .str(in_1[12]), .sel(power), .clk(Clk), .ld(not_13_out),
    .clr(Reset));
  Pull_Resistor pull_resistor_49 (.node(out_49));
  Pull_Resistor pull_resistor_50 (.node(out_50));
  RAM #(.addrWidth(24), .dataWidth(32), .bus("separate")) ram_14 (
    .addr(in_31), .din(in_29), .data(out_50), .str(in_1[13]), .sel(power), .clk(Clk), .ld(not_14_out),
    .clr(Reset));
  Pull_Resistor pull_resistor_51 (.node(out_51));
  RAM #(.addrWidth(24), .dataWidth(32), .bus("separate")) ram_15 (
    .addr(in_34), .din(in_33), .data(out_51), .str(in_1[14]), .sel(power), .clk(Clk), .ld(not_15_out),
    .clr(Reset));
  Pull_Resistor pull_resistor_52 (.node(out_52));
  RAM #(.addrWidth(24), .dataWidth(32), .bus("separate")) ram_16 (
    .addr(in_36), .din(in_35), .data(out_52), .str(in_1[15]), .sel(power), .clk(Clk), .ld(not_16_out),
    .clr(Reset));
endmodule
module Main_CPU_Core_MCPUC (
  input  [31:0] Adress_in_0,
  input  [31:0] Adress_in_1,
  input  [31:0] Adress_in_2,
  input  [31:0] Adress_in_3,
  input  [31:0] Adress_in_4,
  input  [31:0] Adress_in_5,
  input  [31:0] Adress_in_6,
  input  [31:0] Adress_in_7,
  input  [31:0] Adress_in_8,
  input  [31:0] Adress_in_9,
  input  [31:0] Adress_in_10,
  input  [31:0] Adress_in_11,
  input  [31:0] Adress_in_12,
  input  [31:0] Adress_in_13,
  input  [31:0] Adress_in_14,
  input  [31:0] Adress_in_15,
  input  Occured__0,
  input  Occured__1,
  input  Occured__2,
  input  Occured__3,
  input  Occured__4,
  input  Occured__5,
  input  Occured__6,
  input  Occured__7,
  input  Occured__8,
  input  Occured__9,
  input  Occured__10,
  input  Occured__11,
  input  Occured__12,
  input  Occured__13,
  input  Occured__14,
  input  Occured__15,
  input  Clk,
  input  Power,
  input  [2:0] condition_0,
  input  [2:0] condition_1,
  input  [2:0] condition_2,
  input  [2:0] condition_3,
  input  [2:0] condition_4,
  input  [2:0] condition_5,
  input  [2:0] condition_6,
  input  [2:0] condition_7,
  input  [2:0] condition_8,
  input  [2:0] condition_9,
  input  [2:0] condition_10,
  input  [2:0] condition_11,
  input  [2:0] condition_12,
  input  [2:0] condition_13,
  input  [2:0] condition_14,
  input  [2:0] condition_15,
  input  in_51,
  output [31:0] Adress_out,
  output [31:0] CPU_Core_comand,
  output [31:0] Adress_out_2,
  output [31:0] CPU_Core_comand_2,
  output [31:0] Adress_out_3,
  output [31:0] CPU_Core_comand_3,
  output [31:0] Adress_out_4,
  output [31:0] CPU_Core_comand_4,
  output [31:0] Adress_out_5,
  output [31:0] CPU_Core_comand_5,
  output [31:0] Adress_out_6,
  output [31:0] CPU_Core_comand_6,
  output [31:0] Adress_out_7,
  output [31:0] CPU_Core_comand_7,
  output [31:0] Adress_out_8,
  output [31:0] CPU_Core_comand_8,
  output [31:0] Adress_out_9,
  output [31:0] CPU_Core_comand_9,
  output [31:0] Adress_out_10,
  output [31:0] CPU_Core_comand_10,
  output [31:0] Adress_out_11,
  output [31:0] CPU_Core_comand_11,
  output [31:0] Adress_out_12,
  output [31:0] CPU_Core_comand_12,
  output [31:0] Adress_out_13,
  output [31:0] CPU_Core_comand_13,
  output [31:0] Adress_out_14,
  output [31:0] CPU_Core_comand_14,
  output [31:0] Adress_out_15,
  output [31:0] CPU_Core_comand_15,
  output [31:0] Adress_out_16,
  output [31:0] CPU_Core_comand_16,
  output Start_CPU_Core_0,
  output Start_CPU_Core_1,
  output Start_CPU_Core_2,
  output Start_CPU_Core_3,
  output Start_CPU_Core_4,
  output Start_CPU_Core_5,
  output Start_CPU_Core_6,
  output Start_CPU_Core_7,
  output Start_CPU_Core_8,
  output Start_CPU_Core_9,
  output Start_CPU_Core_10,
  output Start_CPU_Core_11,
  output Start_CPU_Core_12,
  output Start_CPU_Core_13,
  output Start_CPU_Core_14,
  output Start_CPU_Core_15
);

  wire and_17_out, and_18_out, and_19_out, and_20_out, and_21_out, and_22_out, and_23_out, and_24_out,
       and_25_out, and_26_out, and_27_out, and_28_out, and_29_out, and_30_out, and_31_out, and_32_out,
       and_33_out, and_34_out, and_35_out, and_36_out, and_37_out, and_38_out, and_39_out, and_40_out,
       and_41_out, and_42_out, and_43_out, and_44_out, and_45_out, and_46_out, and_47_out, and_48_out,
       and_49_out, and_50_out, and_51_out, and_52_out, and_53_out, and_54_out, and_55_out, and_56_out,
       and_57_out, and_58_out, and_59_out, and_60_out, and_61_out, and_62_out, and_63_out, and_64_out,
       and_65_out, and_66_out, and_67_out, and_68_out, and_69_out, and_70_out, and_71_out, and_72_out,
       and_73_out, and_74_out, and_75_out, and_76_out, and_77_out, and_78_out, and_79_out, and_80_out,
       and_81_out, and_82_out, and_83_out, clock_1_out, comparator_1_eq, comparator_1_lt, comparator_2_eq,
       comparator_3_eq, comparator_4_eq, comparator_4_lt, comparator_5_eq, comparator_6_eq, comparator_7_eq,
       comparator_7_lt, comparator_8_eq, comparator_9_eq, comparator_10_eq, comparator_10_lt,
       comparator_11_eq, comparator_12_eq, comparator_13_eq, comparator_13_lt, comparator_14_eq,
       comparator_15_eq, comparator_16_eq, comparator_16_lt, comparator_17_eq, comparator_18_eq,
       comparator_19_eq, comparator_19_lt, comparator_20_eq, comparator_21_eq, comparator_22_eq,
       comparator_22_lt, comparator_23_eq, comparator_24_eq, comparator_25_eq, comparator_25_lt,
       comparator_26_eq, comparator_27_eq, comparator_28_eq, comparator_28_lt, comparator_29_eq,
       comparator_30_eq, comparator_31_eq, comparator_31_lt, comparator_32_eq, comparator_33_eq,
       comparator_34_eq, comparator_34_lt, comparator_35_eq, comparator_36_eq, comparator_37_eq,
       comparator_37_lt, comparator_38_eq, comparator_39_eq, comparator_40_eq, comparator_40_lt,
       comparator_41_eq, comparator_42_eq, comparator_43_eq, comparator_43_lt, comparator_44_eq,
       comparator_45_eq, comparator_46_eq, comparator_46_lt, comparator_47_eq, comparator_48_eq,
       comparator_49_eq, comparator_49_lt, comparator_50_eq, comparator_51_eq, counter_1_carry,
       counter_2_carry, counter_3_carry, counter_4_carry, counter_5_carry, counter_6_carry, counter_7_carry,
       counter_8_carry, counter_9_carry, counter_10_carry, counter_11_carry, counter_12_carry,
       counter_13_carry, counter_14_carry, counter_15_carry, counter_16_carry, counter_17_carry,
       cpu_core_loader_cpucl_1_load_0, cpu_core_loader_cpucl_1_load_1, cpu_core_loader_cpucl_1_load_2,
       cpu_core_loader_cpucl_1_load_3, decoder_1_out0, decoder_1_out1, decoder_1_out2, decoder_1_out3,
       decoder_2_out0, decoder_2_out1, decoder_2_out2, decoder_2_out3, decoder_3_out0, decoder_3_out1,
       decoder_3_out2, decoder_3_out3, decoder_4_out0, decoder_4_out1, decoder_4_out2, decoder_4_out3,
       or_1_out, or_2_out, or_3_out, or_4_out, or_5_out, or_6_out, or_7_out, or_8_out, or_13_out, or_14_out,
       or_15_out, or_16_out, or_17_out, or_18_out, or_23_out, or_24_out, or_25_out, or_26_out, or_27_out,
       or_28_out, or_29_out, or_30_out, or_35_out, or_36_out, or_37_out, or_38_out, or_39_out, or_40_out,
       or_41_out, or_42_out, or_43_out, or_44_out, or_45_out, or_46_out, or_47_out, or_48_out, or_49_out,
       or_50_out, register_6_q, register_7_q, register_8_q, register_9_q, register_10_q, undriven_2,
       undriven_5, undriven_6, undriven_7, undriven_8, undriven_11, undriven_12, undriven_13, undriven_14,
       undriven_15, undriven_20, undriven_21, undriven_22, undriven_23, undriven_28, undriven_29,
       undriven_30, undriven_31, undriven_36, undriven_37, undriven_38, undriven_39, undriven_44,
       undriven_45, undriven_46, undriven_47, undriven_48, undriven_49, undriven_50, undriven_51,
       undriven_52, undriven_53, undriven_54, undriven_55, undriven_56, undriven_57, undriven_58,
       undriven_59, undriven_60, undriven_61, undriven_63, undriven_64, undriven_66, undriven_69;
  wire [1:0] undriven, undriven_9, undriven_65, undriven_68;
  wire [3:0] cpu_core_loader_cpucl_2_load_0, cpu_core_loader_cpucl_3_load_0, cpu_core_loader_cpucl_4_load_0,
       or_9_out, or_19_out, or_31_out, register_15_q, register_19_q, register_20_q, register_21_q,
       register_22_q, register_23_q, register_24_q, register_25_q, register_26_q, register_27_q,
       register_28_q, register_29_q, register_30_q, register_31_q, register_32_q, register_33_q,
       register_34_q, register_39_q, register_47_q, undriven_16, undriven_17, undriven_18, undriven_19,
       undriven_24, undriven_25, undriven_26, undriven_27, undriven_32, undriven_33, undriven_34,
       undriven_35, undriven_40, undriven_41, undriven_42, undriven_43;
  wire [15:0] counter_1_q, counter_2_q, counter_3_q, counter_4_q, counter_5_q, counter_6_q, counter_7_q,
       counter_8_q, counter_9_q, counter_10_q, counter_11_q, counter_12_q, counter_13_q, counter_14_q,
       counter_15_q, counter_16_q, counter_17_q, cpu_core_loader_cpucl_3_data_out,
       cpu_core_loader_cpucl_3_data_out_2, register_1_q, register_2_q, register_3_q, register_4_q,
       register_5_q, register_11_q, register_12_q, register_13_q, register_14_q, register_35_q,
       register_36_q, register_37_q, register_38_q, register_43_q, register_44_q, register_45_q,
       register_46_q;
  wire [31:0] bit_extender_1_out, bit_extender_2_out, bit_extender_3_out, bit_extender_4_out,
       bit_extender_5_out, bit_extender_6_out, bit_extender_7_out, bit_extender_8_out, bit_extender_9_out,
       bit_extender_10_out, bit_extender_11_out, bit_extender_12_out, bit_extender_13_out,
       bit_extender_14_out, bit_extender_15_out, bit_extender_16_out, cpu_core_loader_cpucl_1_data_out,
       cpu_core_loader_cpucl_2_data_out, cpu_core_loader_cpucl_4_data_out, undriven_3, undriven_4,
       undriven_10, undriven_62, undriven_67;

  Clock clock_1 (.out(clock_1_out));
  Multiplexer #(.width(32), .disabled(0)) multiplexer_1 (
    .in0(bit_extender_1_out), .in1(Adress_in_0), .out(Adress_out), .sel(Occured__0), .en(Power));
  Multiplexer #(.width(32), .disabled(0)) multiplexer_2 (
    .in0(bit_extender_2_out), .in1(Adress_in_1), .out(Adress_out_2), .sel(Occured__1), .en(Power));
  Multiplexer #(.width(32), .disabled(0)) multiplexer_3 (
    .in0(bit_extender_3_out), .in1(Adress_in_2), .out(Adress_out_3), .sel(Occured__2), .en(Power));
  Multiplexer #(.width(32), .disabled(0)) multiplexer_4 (
    .in0(bit_extender_4_out), .in1(Adress_in_3), .out(Adress_out_4), .sel(Occured__3), .en(Power));
  Multiplexer #(.width(32), .disabled(0)) multiplexer_5 (
    .in0(bit_extender_5_out), .in1(Adress_in_4), .out(Adress_out_5), .sel(Occured__4), .en(Power));
  Multiplexer #(.width(32), .disabled(0)) multiplexer_6 (
    .in0(bit_extender_6_out), .in1(Adress_in_5), .out(Adress_out_6), .sel(Occured__5), .en(Power));
  Multiplexer #(.width(32), .disabled(0)) multiplexer_7 (
    .in0(bit_extender_7_out), .in1(Adress_in_6), .out(Adress_out_7), .sel(Occured__6), .en(Power));
  Multiplexer #(.width(32), .disabled(0)) multiplexer_8 (
    .in0(bit_extender_8_out), .in1(Adress_in_7), .out(Adress_out_8), .sel(Occured__7), .en(Power));
  Multiplexer #(.width(32), .disabled(0)) multiplexer_9 (
    .in0(bit_extender_9_out), .in1(Adress_in_8), .out(Adress_out_9), .sel(Occured__8), .en(Power));
  Multiplexer #(.width(32), .disabled(0)) multiplexer_10 (
    .in0(bit_extender_10_out), .in1(Adress_in_9), .out(Adress_out_10), .sel(Occured__9), .en(Power));
  Multiplexer #(.width(32), .disabled(0)) multiplexer_11 (
    .in0(bit_extender_11_out), .in1(Adress_in_10), .out(Adress_out_11), .sel(Occured__10), .en(Power));
  Multiplexer #(.width(32), .disabled(0)) multiplexer_12 (
    .in0(bit_extender_12_out), .in1(Adress_in_11), .out(Adress_out_12), .sel(Occured__11), .en(Power));
  Multiplexer #(.width(32), .disabled(0)) multiplexer_13 (
    .in0(bit_extender_13_out), .in1(Adress_in_12), .out(Adress_out_13), .sel(Occured__12), .en(Power));
  Multiplexer #(.width(32), .disabled(0)) multiplexer_14 (
    .in0(bit_extender_14_out), .in1(Adress_in_13), .out(Adress_out_14), .sel(Occured__13), .en(Power));
  Multiplexer #(.width(32), .disabled(0)) multiplexer_15 (
    .in0(bit_extender_15_out), .in1(Adress_in_14), .out(Adress_out_15), .sel(Occured__14), .en(Power));
  Multiplexer #(.width(32), .disabled(0)) multiplexer_16 (
    .in0(bit_extender_16_out), .in1(Adress_in_15), .out(Adress_out_16), .sel(Occured__15), .en(Power));
  and and_1 (Start_CPU_Core_0, ~condition_0[0], clock_1_out);  // AND_Gate
  and and_2 (Start_CPU_Core_1, ~condition_1[0], clock_1_out);  // AND_Gate
  and and_3 (Start_CPU_Core_2, ~condition_2[0], clock_1_out);  // AND_Gate
  and and_4 (Start_CPU_Core_3, ~condition_3[0], clock_1_out);  // AND_Gate
  and and_5 (Start_CPU_Core_4, ~condition_4[0], clock_1_out);  // AND_Gate
  and and_6 (Start_CPU_Core_5, ~condition_5[0], clock_1_out);  // AND_Gate
  and and_7 (Start_CPU_Core_6, ~condition_6[0], clock_1_out);  // AND_Gate
  and and_8 (Start_CPU_Core_7, ~condition_7[0], clock_1_out);  // AND_Gate
  and and_9 (Start_CPU_Core_8, ~condition_8[0], clock_1_out);  // AND_Gate
  and and_10 (Start_CPU_Core_9, ~condition_9[0], clock_1_out);  // AND_Gate
  and and_11 (Start_CPU_Core_10, ~condition_10[0], clock_1_out);  // AND_Gate
  and and_12 (Start_CPU_Core_11, ~condition_11[0], clock_1_out);  // AND_Gate
  and and_13 (Start_CPU_Core_12, ~condition_12[0], clock_1_out);  // AND_Gate
  and and_14 (Start_CPU_Core_13, ~condition_13[0], clock_1_out);  // AND_Gate
  and and_15 (Start_CPU_Core_14, ~condition_14[0], clock_1_out);  // AND_Gate
  and and_16 (Start_CPU_Core_15, ~condition_15[0], clock_1_out);  // AND_Gate
  Decoder #(.select(2), .disabled(0)) decoder_1 (
    .out0(decoder_1_out0), .out1(decoder_1_out1), .out2(decoder_1_out2), .out3(decoder_1_out3), .en(1'b0));  // open: sel
  or or_1 (or_1_out, decoder_1_out0, 1'b0);
  or or_2 (or_2_out, decoder_1_out1, 1'b0);
  or or_3 (or_3_out, decoder_1_out2, 1'b0);
  or or_4 (or_4_out, decoder_1_out3, 1'b0);
  CPU_Core_Loader__CPUCL cpu_core_loader_cpucl_1 (
    .Clk(clock_1_out), .Cond_0(Occured__0), .Cond_1(Occured__1), .Cond_2(Occured__2), .Cond_3(Occured__3),
    .Load(undriven_2), .in_7(undriven), .Power(Power), .Load_cond_0(register_6_q),
    .Load_cond_1(register_7_q), .Load_cond_2(register_8_q), .Load_cond_3(register_9_q), .Data_in(undriven_3),
    .Load_0(cpu_core_loader_cpucl_1_load_0), .Load_1(cpu_core_loader_cpucl_1_load_1),
    .Load_2(cpu_core_loader_cpucl_1_load_2), .Load_3(cpu_core_loader_cpucl_1_load_3),
    .Data_out(cpu_core_loader_cpucl_1_data_out));
  Decoder #(.select(2), .disabled(0)) decoder_2 (
    .out0(decoder_2_out0), .out1(decoder_2_out1), .out2(decoder_2_out2), .out3(decoder_2_out3), .en(1'b0));  // open: sel
  Counter #(.width(16), .max('hffff)) counter_1 (
    .load(cpu_core_loader_cpucl_1_load_0), .D(cpu_core_loader_cpucl_1_data_out[15:0]), .count(and_17_out),
    .Q(counter_1_q), .carry(counter_1_carry), .clk(clock_1_out), .clr(or_13_out));
  and and_17 (and_17_out, ~cpu_core_loader_cpucl_1_load_0, register_6_q);  // AND_Gate
  Register #(.width(16)) register_1 (
    .D(cpu_core_loader_cpucl_1_data_out[31:16]), .en(cpu_core_loader_cpucl_1_load_0), .Q(register_1_q),
    .clk(clock_1_out), .clr(or_13_out));
  Counter #(.width(16), .max('hffff)) counter_2 (
    .load(cpu_core_loader_cpucl_1_load_1), .D(cpu_core_loader_cpucl_1_data_out[15:0]), .count(and_18_out),
    .Q(counter_2_q), .carry(counter_2_carry), .clk(clock_1_out), .clr(or_14_out));
  and and_18 (and_18_out, ~cpu_core_loader_cpucl_1_load_1, register_7_q);  // AND_Gate
  Register #(.width(16)) register_2 (
    .D(cpu_core_loader_cpucl_1_data_out[31:16]), .en(cpu_core_loader_cpucl_1_load_1), .Q(register_2_q),
    .clk(clock_1_out), .clr(or_14_out));
  Counter #(.width(16), .max('hffff)) counter_3 (
    .load(cpu_core_loader_cpucl_1_load_2), .D(cpu_core_loader_cpucl_1_data_out[15:0]), .count(and_19_out),
    .Q(counter_3_q), .carry(counter_3_carry), .clk(clock_1_out), .clr(or_15_out));
  and and_19 (and_19_out, ~cpu_core_loader_cpucl_1_load_2, register_8_q);  // AND_Gate
  Register #(.width(16)) register_3 (
    .D(cpu_core_loader_cpucl_1_data_out[31:16]), .en(cpu_core_loader_cpucl_1_load_2), .Q(register_3_q),
    .clk(clock_1_out), .clr(or_15_out));
  Counter #(.width(16), .max('hffff)) counter_4 (
    .load(cpu_core_loader_cpucl_1_load_3), .D(cpu_core_loader_cpucl_1_data_out[15:0]), .count(and_20_out),
    .Q(counter_4_q), .carry(counter_4_carry), .clk(clock_1_out), .clr(or_16_out));
  and and_20 (and_20_out, ~cpu_core_loader_cpucl_1_load_3, register_9_q);  // AND_Gate
  Register #(.width(16)) register_4 (
    .D(cpu_core_loader_cpucl_1_data_out[31:16]), .en(cpu_core_loader_cpucl_1_load_3), .Q(register_4_q),
    .clk(clock_1_out), .clr(or_16_out));
  and and_21 (and_21_out, ~undriven_7, register_10_q);  // AND_Gate
  Register #(.width(16)) register_5 (
    .D(undriven_4[31:16]), .en(undriven_7), .Q(register_5_q), .clk(undriven_6), .clr(or_18_out));
  Register #(.width(1)) register_6 (.D(Power), .en(and_22_out), .Q(register_6_q), .clk(clock_1_out), .clr(or_13_out));
  or or_5 (or_5_out, counter_1_carry, comparator_1_eq, comparator_1_lt);
  Comparator #(.width(16), .mode("unsigned")) comparator_1 (
    .a(register_1_q), .b(counter_1_q), .eq(comparator_1_eq), .lt(comparator_1_lt));  // open: gt
  Comparator #(.width(16), .mode("unsigned")) comparator_2 (
    .a(counter_1_q), .b({16{1'b0}}), .eq(comparator_2_eq));  // open: gt, lt
  and and_22 (and_22_out, comparator_2_eq, cpu_core_loader_cpucl_1_load_0);
  Comparator #(.width(16), .mode("unsigned")) comparator_3 (
    .a(register_1_q), .b({16{1'b0}}), .eq(comparator_3_eq));  // open: gt, lt
  Register #(.width(1)) register_7 (.D(Power), .en(and_23_out), .Q(register_7_q), .clk(clock_1_out), .clr(or_14_out));
  Comparator #(.width(16), .mode("unsigned")) comparator_4 (
    .a(register_2_q), .b(counter_2_q), .eq(comparator_4_eq), .lt(comparator_4_lt));  // open: gt
  or or_6 (or_6_out, counter_2_carry, comparator_4_eq, comparator_4_lt);
  Comparator #(.width(16), .mode("unsigned")) comparator_5 (
    .a(counter_2_q), .b({16{1'b0}}), .eq(comparator_5_eq));  // open: gt, lt
  and and_23 (and_23_out, comparator_5_eq, cpu_core_loader_cpucl_1_load_1);
  Comparator #(.width(16), .mode("unsigned")) comparator_6 (
    .a(register_2_q), .b({16{1'b0}}), .eq(comparator_6_eq));  // open: gt, lt
  Register #(.width(1)) register_8 (.D(Power), .en(and_24_out), .Q(register_8_q), .clk(clock_1_out), .clr(or_15_out));
  or or_7 (or_7_out, counter_3_carry, comparator_7_eq, comparator_7_lt);
  Comparator #(.width(16), .mode("unsigned")) comparator_7 (
    .a(register_3_q), .b(counter_3_q), .eq(comparator_7_eq), .lt(comparator_7_lt));  // open: gt
  Comparator #(.width(16), .mode("unsigned")) comparator_8 (
    .a(counter_3_q), .b({16{1'b0}}), .eq(comparator_8_eq));  // open: gt, lt
  and and_24 (and_24_out, comparator_8_eq, cpu_core_loader_cpucl_1_load_2);
  Comparator #(.width(16), .mode("unsigned")) comparator_9 (
    .a(register_3_q), .b({16{1'b0}}), .eq(comparator_9_eq));  // open: gt, lt
  Register #(.width(1)) register_9 (.D(Power), .en(and_25_out), .Q(register_9_q), .clk(clock_1_out), .clr(or_16_out));
  or or_8 (or_8_out, counter_4_carry, comparator_10_eq, comparator_10_lt);
  Comparator #(.width(16), .mode("unsigned")) comparator_10 (
    .a(register_4_q), .b(counter_4_q), .eq(comparator_10_eq), .lt(comparator_10_lt));  // open: gt
  Comparator #(.width(16), .mode("unsigned")) comparator_11 (
    .a(counter_4_q), .b({16{1'b0}}), .eq(comparator_11_eq));  // open: gt, lt
  and and_25 (and_25_out, comparator_11_eq, cpu_core_loader_cpucl_1_load_3);
  Comparator #(.width(16), .mode("unsigned")) comparator_12 (
    .a(register_4_q), .b({16{1'b0}}), .eq(comparator_12_eq));  // open: gt, lt
  Counter #(.width(16), .max('hffff)) counter_5 (
    .load(undriven_7), .D(undriven_4[15:0]), .count(and_21_out), .Q(counter_5_q), .carry(counter_5_carry),
    .clk(undriven_6), .clr(or_18_out));
  Comparator #(.width(16), .mode("unsigned")) comparator_13 (
    .a(register_5_q), .b(counter_5_q), .eq(comparator_13_eq), .lt(comparator_13_lt));  // open: gt
  Comparator #(.width(16), .mode("unsigned")) comparator_14 (
    .a(counter_5_q), .b({16{1'b0}}), .eq(comparator_14_eq));  // open: gt, lt
  Comparator #(.width(16), .mode("unsigned")) comparator_15 (
    .a(register_5_q), .b({16{1'b0}}), .eq(comparator_15_eq));  // open: gt, lt
  or or_9 (or_9_out[0], decoder_2_out0, 1'b0);
  or or_10 (or_9_out[1], decoder_2_out1, 1'b0);
  or or_11 (or_9_out[2], decoder_2_out2, 1'b0);
  or or_12 (or_9_out[3], decoder_2_out3, 1'b0);
  or or_13 (or_13_out, and_26_out, and_27_out, or_1_out);
  and and_26 (and_26_out, or_5_out, ~comparator_2_eq, ~comparator_3_eq, ~cpu_core_loader_cpucl_1_load_0);  // AND_Gate
  and and_27 (and_27_out, ~comparator_2_eq, comparator_3_eq);  // AND_Gate
  or or_14 (or_14_out, and_28_out, and_29_out, or_2_out);
  and and_28 (and_28_out, or_6_out, ~comparator_5_eq, ~comparator_6_eq, ~cpu_core_loader_cpucl_1_load_1);  // AND_Gate
  and and_29 (and_29_out, ~comparator_5_eq, comparator_6_eq);  // AND_Gate
  or or_15 (or_15_out, and_30_out, and_31_out, or_3_out);
  and and_30 (and_30_out, or_7_out, ~comparator_8_eq, ~comparator_9_eq, ~cpu_core_loader_cpucl_1_load_2);  // AND_Gate
  and and_31 (and_31_out, ~comparator_8_eq, comparator_9_eq);  // AND_Gate
  or or_16 (or_16_out, and_32_out, and_33_out, or_4_out);
  and and_32 (and_32_out, or_8_out, ~comparator_11_eq, ~comparator_12_eq, ~cpu_core_loader_cpucl_1_load_3);  // AND_Gate
  and and_33 (and_33_out, ~comparator_11_eq, comparator_12_eq);  // AND_Gate
  Register #(.width(1)) register_10 (
    .D(undriven_5), .en(and_35_out), .Q(register_10_q), .clk(undriven_6), .clr(or_18_out));
  or or_17 (or_17_out, counter_5_carry, comparator_13_eq, comparator_13_lt);
  and and_34 (and_34_out, or_17_out, ~comparator_14_eq, ~comparator_15_eq, ~undriven_7);  // AND_Gate
  and and_35 (and_35_out, comparator_14_eq, undriven_7);
  or or_18 (or_18_out, and_34_out, undriven_8);
  assign bit_extender_1_out = {{16{1'b0}}, counter_1_q};  // Bit_Extender bit_extender_1
  assign bit_extender_2_out = {{16{1'b0}}, counter_2_q};  // Bit_Extender bit_extender_2
  assign bit_extender_3_out = {{16{1'b0}}, counter_3_q};  // Bit_Extender bit_extender_3
  assign bit_extender_4_out = {{16{1'b0}}, counter_4_q};  // Bit_Extender bit_extender_4
  CPU_Core_Loader__CPUCL cpu_core_loader_cpucl_2 (
    .Clk(clock_1_out), .Cond_0(Occured__4), .Cond_1(Occured__5), .Cond_2(Occured__6), .Cond_3(Occured__7),
    .Load(undriven_11), .in_7(undriven_9), .Power(Power), .Load_cond_0(register_15_q[0]),
    .Load_cond_1(register_15_q[1]), .Load_cond_2(register_15_q[2]), .Load_cond_3(register_15_q[3]),
    .Data_in(undriven_10), .Load_0(cpu_core_loader_cpucl_2_load_0[0]),
    .Load_1(cpu_core_loader_cpucl_2_load_0[1]), .Load_2(cpu_core_loader_cpucl_2_load_0[2]),
    .Load_3(cpu_core_loader_cpucl_2_load_0[3]), .Data_out(cpu_core_loader_cpucl_2_data_out));
  and and_36 (and_36_out, ~cpu_core_loader_cpucl_2_load_0[0], register_15_q[0]);  // AND_Gate
  Register #(.width(16)) register_11 (
    .D(cpu_core_loader_cpucl_2_data_out[31:16]), .en(cpu_core_loader_cpucl_2_load_0[0]), .Q(register_11_q),
    .clk(clock_1_out), .clr(or_27_out));
  and and_37 (and_37_out, ~cpu_core_loader_cpucl_2_load_0[1], register_15_q[1]);  // AND_Gate
  Register #(.width(16)) register_12 (
    .D(cpu_core_loader_cpucl_2_data_out[31:16]), .en(cpu_core_loader_cpucl_2_load_0[1]), .Q(register_12_q),
    .clk(clock_1_out), .clr(or_28_out));
  and and_38 (and_38_out, ~cpu_core_loader_cpucl_2_load_0[2], register_15_q[2]);  // AND_Gate
  Register #(.width(16)) register_13 (
    .D(cpu_core_loader_cpucl_2_data_out[31:16]), .en(cpu_core_loader_cpucl_2_load_0[2]), .Q(register_13_q),
    .clk(clock_1_out), .clr(or_29_out));
  and and_39 (and_39_out, ~cpu_core_loader_cpucl_2_load_0[3], register_15_q[3]);  // AND_Gate
  Register #(.width(16)) register_14 (
    .D(cpu_core_loader_cpucl_2_data_out[31:16]), .en(cpu_core_loader_cpucl_2_load_0[3]), .Q(register_14_q),
    .clk(clock_1_out), .clr(or_30_out));
  Decoder #(.select(2), .disabled(0)) decoder_3 (
    .out0(decoder_3_out0), .out1(decoder_3_out1), .out2(decoder_3_out2), .out3(decoder_3_out3), .en(1'b0));  // open: sel
  Counter #(.width(16), .max('hffff)) counter_6 (
    .load(cpu_core_loader_cpucl_2_load_0[0]), .D(cpu_core_loader_cpucl_2_data_out[15:0]), .count(and_36_out),
    .Q(counter_6_q), .carry(counter_6_carry), .clk(clock_1_out), .clr(or_27_out));
  Comparator #(.width(16), .mode("unsigned")) comparator_16 (
    .a(register_11_q), .b(counter_6_q), .eq(comparator_16_eq), .lt(comparator_16_lt));  // open: gt
  Comparator #(.width(16), .mode("unsigned")) comparator_17 (
    .a(counter_6_q), .b({16{1'b0}}), .eq(comparator_17_eq));  // open: gt, lt
  Comparator #(.width(16), .mode("unsigned")) comparator_18 (
    .a(register_11_q), .b({16{1'b0}}), .eq(comparator_18_eq));  // open: gt, lt
  Counter #(.width(16), .max('hffff)) counter_7 (
    .load(cpu_core_loader_cpucl_2_load_0[1]), .D(cpu_core_loader_cpucl_2_data_out[15:0]), .count(and_37_out),
    .Q(counter_7_q), .carry(counter_7_carry), .clk(clock_1_out), .clr(or_28_out));
  Comparator #(.width(16), .mode("unsigned")) comparator_19 (
    .a(register_12_q), .b(counter_7_q), .eq(comparator_19_eq), .lt(comparator_19_lt));  // open: gt
  Comparator #(.width(16), .mode("unsigned")) comparator_20 (
    .a(counter_7_q), .b({16{1'b0}}), .eq(comparator_20_eq));  // open: gt, lt
  Comparator #(.width(16), .mode("unsigned")) comparator_21 (
    .a(register_12_q), .b({16{1'b0}}), .eq(comparator_21_eq));  // open: gt, lt
  Counter #(.width(16), .max('hffff)) counter_8 (
    .load(cpu_core_loader_cpucl_2_load_0[2]), .D(cpu_core_loader_cpucl_2_data_out[15:0]), .count(and_38_out),
    .Q(counter_8_q), .carry(counter_8_carry), .clk(clock_1_out), .clr(or_29_out));
  Comparator #(.width(16), .mode("unsigned")) comparator_22 (
    .a(register_13_q), .b(counter_8_q), .eq(comparator_22_eq), .lt(comparator_22_lt));  // open: gt
  Comparator #(.width(16), .mode("unsigned")) comparator_23 (
    .a(counter_8_q), .b({16{1'b0}}), .eq(comparator_23_eq));  // open: gt, lt
  Comparator #(.width(16), .mode("unsigned")) comparator_24 (
    .a(register_13_q), .b({16{1'b0}}), .eq(comparator_24_eq));  // open: gt, lt
  Counter #(.width(16), .max('hffff)) counter_9 (
    .load(cpu_core_loader_cpucl_2_load_0[3]), .D(cpu_core_loader_cpucl_2_data_out[15:0]), .count(and_39_out),
    .Q(counter_9_q), .carry(counter_9_carry), .clk(clock_1_out), .clr(or_30_out));
  Comparator #(.width(16), .mode("unsigned")) comparator_25 (
    .a(register_14_q), .b(counter_9_q), .eq(comparator_25_eq), .lt(comparator_25_lt));  // open: gt
  Comparator #(.width(16), .mode("unsigned")) comparator_26 (
    .a(counter_9_q), .b({16{1'b0}}), .eq(comparator_26_eq));  // open: gt, lt
  Comparator #(.width(16), .mode("unsigned")) comparator_27 (
    .a(register_14_q), .b({16{1'b0}}), .eq(comparator_27_eq));  // open: gt, lt
  or or_19 (or_19_out[0], decoder_3_out0, 1'b0);
  or or_20 (or_19_out[1], decoder_3_out1, 1'b0);
  or or_21 (or_19_out[2], decoder_3_out2, 1'b0);
  or or_22 (or_19_out[3], decoder_3_out3, 1'b0);
  Register #(.width(1)) register_15 (
    .D(Power), .en(and_41_out), .Q(register_15_q[0]), .clk(clock_1_out), .clr(or_27_out));
  or or_23 (or_23_out, counter_6_carry, comparator_16_eq, comparator_16_lt);
  and and_40 (and_40_out, or_23_out, ~comparator_17_eq, ~comparator_18_eq, ~cpu_core_loader_cpucl_2_load_0[0]);  // AND_Gate
  and and_41 (and_41_out, comparator_17_eq, cpu_core_loader_cpucl_2_load_0[0]);
  Register #(.width(1)) register_16 (
    .D(Power), .en(and_43_out), .Q(register_15_q[1]), .clk(clock_1_out), .clr(or_28_out));
  or or_24 (or_24_out, counter_7_carry, comparator_19_eq, comparator_19_lt);
  and and_42 (and_42_out, or_24_out, ~comparator_20_eq, ~comparator_21_eq, ~cpu_core_loader_cpucl_2_load_0[1]);  // AND_Gate
  and and_43 (and_43_out, comparator_20_eq, cpu_core_loader_cpucl_2_load_0[1]);
  Register #(.width(1)) register_17 (
    .D(Power), .en(and_45_out), .Q(register_15_q[2]), .clk(clock_1_out), .clr(or_29_out));
  or or_25 (or_25_out, counter_8_carry, comparator_22_eq, comparator_22_lt);
  and and_44 (and_44_out, or_25_out, ~comparator_23_eq, ~comparator_24_eq, ~cpu_core_loader_cpucl_2_load_0[2]);  // AND_Gate
  and and_45 (and_45_out, comparator_23_eq, cpu_core_loader_cpucl_2_load_0[2]);
  Register #(.width(1)) register_18 (
    .D(Power), .en(and_47_out), .Q(register_15_q[3]), .clk(clock_1_out), .clr(or_30_out));
  or or_26 (or_26_out, counter_9_carry, comparator_25_eq, comparator_25_lt);
  and and_46 (and_46_out, or_26_out, ~comparator_26_eq, ~comparator_27_eq, ~cpu_core_loader_cpucl_2_load_0[3]);  // AND_Gate
  and and_47 (and_47_out, comparator_26_eq, cpu_core_loader_cpucl_2_load_0[3]);
  Register #(.width(4)) register_19 (
    .D(undriven_19), .en(undriven_15), .Q(register_19_q), .clk(undriven_56), .clr(undriven_44));
  Register #(.width(4)) register_20 (
    .D(undriven_27), .en(undriven_23), .Q(register_20_q), .clk(undriven_57), .clr(undriven_60));
  Register #(.width(4)) register_21 (
    .D(undriven_35), .en(undriven_31), .Q(register_21_q), .clk(undriven_58), .clr(undriven_50));
  Register #(.width(4)) register_22 (
    .D(undriven_43), .en(undriven_39), .Q(register_22_q), .clk(undriven_59), .clr(undriven_61));
  or or_27 (or_27_out, and_40_out, and_48_out, or_9_out[0]);
  and and_48 (and_48_out, ~comparator_17_eq, comparator_18_eq);  // AND_Gate
  or or_28 (or_28_out, and_42_out, and_49_out, or_9_out[1]);
  and and_49 (and_49_out, ~comparator_20_eq, comparator_21_eq);  // AND_Gate
  or or_29 (or_29_out, and_44_out, and_50_out, or_9_out[2]);
  and and_50 (and_50_out, ~comparator_23_eq, comparator_24_eq);  // AND_Gate
  or or_30 (or_30_out, and_46_out, and_51_out, or_9_out[3]);
  and and_51 (and_51_out, ~comparator_26_eq, comparator_27_eq);  // AND_Gate
  Register #(.width(4)) register_23 (
    .D(undriven_18), .en(undriven_14), .Q(register_23_q), .clk(undriven_56), .clr(undriven_45));
  Register #(.width(4)) register_24 (
    .D(undriven_26), .en(undriven_22), .Q(register_24_q), .clk(undriven_57), .clr(undriven_48));
  Register #(.width(4)) register_25 (
    .D(undriven_34), .en(undriven_30), .Q(register_25_q), .clk(undriven_58), .clr(undriven_51));
  Register #(.width(4)) register_26 (
    .D(undriven_42), .en(undriven_38), .Q(register_26_q), .clk(undriven_59), .clr(undriven_54));
  Register #(.width(4)) register_27 (
    .D(undriven_17), .en(undriven_13), .Q(register_27_q), .clk(undriven_56), .clr(undriven_46));
  Register #(.width(4)) register_28 (
    .D(undriven_25), .en(undriven_21), .Q(register_28_q), .clk(undriven_57), .clr(undriven_63));
  Register #(.width(4)) register_29 (
    .D(undriven_33), .en(undriven_29), .Q(register_29_q), .clk(undriven_58), .clr(undriven_52));
  Register #(.width(4)) register_30 (
    .D(undriven_41), .en(undriven_37), .Q(register_30_q), .clk(undriven_59), .clr(undriven_64));
  assign bit_extender_5_out = {{16{1'b0}}, counter_6_q};  // Bit_Extender bit_extender_5
  assign bit_extender_6_out = {{16{1'b0}}, counter_7_q};  // Bit_Extender bit_extender_6
  assign bit_extender_7_out = {{16{1'b0}}, counter_8_q};  // Bit_Extender bit_extender_7
  assign bit_extender_8_out = {{16{1'b0}}, counter_9_q};  // Bit_Extender bit_extender_8
  Register #(.width(4)) register_31 (
    .D(undriven_16), .en(undriven_12), .Q(register_31_q), .clk(undriven_56), .clr(undriven_47));
  Register #(.width(4)) register_32 (
    .D(undriven_24), .en(undriven_20), .Q(register_32_q), .clk(undriven_57), .clr(undriven_49));
  Register #(.width(4)) register_33 (
    .D(undriven_32), .en(undriven_28), .Q(register_33_q), .clk(undriven_58), .clr(undriven_53));
  Register #(.width(4)) register_34 (
    .D(undriven_40), .en(undriven_36), .Q(register_34_q), .clk(undriven_59), .clr(undriven_55));
  CPU_Core_Loader__CPUCL cpu_core_loader_cpucl_3 (
    .Clk(clock_1_out), .Cond_0(Occured__8), .Cond_1(Occured__9), .Cond_2(Occured__10), .Cond_3(Occured__11),
    .Load(undriven_66), .in_7(undriven_65), .Power(Power), .Load_cond_0(register_39_q[0]),
    .Load_cond_1(register_39_q[1]), .Load_cond_2(register_39_q[2]), .Load_cond_3(register_39_q[3]),
    .Data_in(undriven_62), .Load_0(cpu_core_loader_cpucl_3_load_0[0]),
    .Load_1(cpu_core_loader_cpucl_3_load_0[1]), .Load_2(cpu_core_loader_cpucl_3_load_0[2]),
    .Load_3(cpu_core_loader_cpucl_3_load_0[3]),
    .Data_out({cpu_core_loader_cpucl_3_data_out_2, cpu_core_loader_cpucl_3_data_out}));
  and and_52 (and_52_out, ~cpu_core_loader_cpucl_3_load_0[0], register_39_q[0]);  // AND_Gate
  Register #(.width(16)) register_35 (
    .D(cpu_core_loader_cpucl_3_data_out_2), .en(cpu_core_loader_cpucl_3_load_0[0]), .Q(register_35_q),
    .clk(clock_1_out), .clr(or_39_out));
  and and_53 (and_53_out, ~cpu_core_loader_cpucl_3_load_0[1], register_39_q[1]);  // AND_Gate
  Register #(.width(16)) register_36 (
    .D(cpu_core_loader_cpucl_3_data_out_2), .en(cpu_core_loader_cpucl_3_load_0[1]), .Q(register_36_q),
    .clk(clock_1_out), .clr(or_40_out));
  and and_54 (and_54_out, ~cpu_core_loader_cpucl_3_load_0[2], register_39_q[2]);  // AND_Gate
  Register #(.width(16)) register_37 (
    .D(cpu_core_loader_cpucl_3_data_out_2), .en(cpu_core_loader_cpucl_3_load_0[2]), .Q(register_37_q),
    .clk(clock_1_out), .clr(or_41_out));
  and and_55 (and_55_out, ~cpu_core_loader_cpucl_3_load_0[3], register_39_q[3]);  // AND_Gate
  Register #(.width(16)) register_38 (
    .D(cpu_core_loader_cpucl_3_data_out_2), .en(cpu_core_loader_cpucl_3_load_0[3]), .Q(register_38_q),
    .clk(clock_1_out), .clr(or_42_out));
  Decoder #(.select(2), .disabled(0)) decoder_4 (
    .out0(decoder_4_out0), .out1(decoder_4_out1), .out2(decoder_4_out2), .out3(decoder_4_out3), .en(1'b0));  // open: sel
  Counter #(.width(16), .max('hffff)) counter_10 (
    .load(cpu_core_loader_cpucl_3_load_0[0]), .D(cpu_core_loader_cpucl_3_data_out), .count(and_52_out),
    .Q(counter_10_q), .carry(counter_10_carry), .clk(clock_1_out), .clr(or_39_out));
  Comparator #(.width(16), .mode("unsigned")) comparator_28 (
    .a(register_35_q), .b(counter_10_q), .eq(comparator_28_eq), .lt(comparator_28_lt));  // open: gt
  Comparator #(.width(16), .mode("unsigned")) comparator_29 (
    .a(counter_10_q), .b({16{1'b0}}), .eq(comparator_29_eq));  // open: gt, lt
  Comparator #(.width(16), .mode("unsigned")) comparator_30 (
    .a(register_35_q), .b({16{1'b0}}), .eq(comparator_30_eq));  // open: gt, lt
  Counter #(.width(16), .max('hffff)) counter_11 (
    .load(cpu_core_loader_cpucl_3_load_0[1]), .D(cpu_core_loader_cpucl_3_data_out), .count(and_53_out),
    .Q(counter_11_q), .carry(counter_11_carry), .clk(clock_1_out), .clr(or_40_out));
  Comparator #(.width(16), .mode("unsigned")) comparator_31 (
    .a(register_36_q), .b(counter_11_q), .eq(comparator_31_eq), .lt(comparator_31_lt));  // open: gt
  Comparator #(.width(16), .mode("unsigned")) comparator_32 (
    .a(counter_11_q), .b({16{1'b0}}), .eq(comparator_32_eq));  // open: gt, lt
  Comparator #(.width(16), .mode("unsigned")) comparator_33 (
    .a(register_36_q), .b({16{1'b0}}), .eq(comparator_33_eq));  // open: gt, lt
  Counter #(.width(16), .max('hffff)) counter_12 (
    .load(cpu_core_loader_cpucl_3_load_0[2]), .D(cpu_core_loader_cpucl_3_data_out), .count(and_54_out),
    .Q(counter_12_q), .carry(counter_12_carry), .clk(clock_1_out), .clr(or_41_out));
  Comparator #(.width(16), .mode("unsigned")) comparator_34 (
    .a(register_37_q), .b(counter_12_q), .eq(comparator_34_eq), .lt(comparator_34_lt));  // open: gt
  Comparator #(.width(16), .mode("unsigned")) comparator_35 (
    .a(counter_12_q), .b({16{1'b0}}), .eq(comparator_35_eq));  // open: gt, lt
  Comparator #(.width(16), .mode("unsigned")) comparator_36 (
    .a(register_37_q), .b({16{1'b0}}), .eq(comparator_36_eq));  // open: gt, lt
  Counter #(.width(16), .max('hffff)) counter_13 (
    .load(cpu_core_loader_cpucl_3_load_0[3]), .D(cpu_core_loader_cpucl_3_data_out), .count(and_55_out),
    .Q(counter_13_q), .carry(counter_13_carry), .clk(clock_1_out), .clr(or_42_out));
  Comparator #(.width(16), .mode("unsigned")) comparator_37 (
    .a(register_38_q), .b(counter_13_q), .eq(comparator_37_eq), .lt(comparator_37_lt));  // open: gt
  Comparator #(.width(16), .mode("unsigned")) comparator_38 (
    .a(counter_13_q), .b({16{1'b0}}), .eq(comparator_38_eq));  // open: gt, lt
  Comparator #(.width(16), .mode("unsigned")) comparator_39 (
    .a(register_38_q), .b({16{1'b0}}), .eq(comparator_39_eq));  // open: gt, lt
  or or_31 (or_31_out[0], decoder_4_out0, 1'b0);
  or or_32 (or_31_out[1], decoder_4_out1, 1'b0);
  or or_33 (or_31_out[2], decoder_4_out2, 1'b0);
  or or_34 (or_31_out[3], decoder_4_out3, 1'b0);
  Register #(.width(1)) register_39 (
    .D(Power), .en(and_56_out), .Q(register_39_q[0]), .clk(clock_1_out), .clr(or_39_out));
  or or_35 (or_35_out, counter_10_carry, comparator_28_eq, comparator_28_lt);
  and and_56 (and_56_out, comparator_29_eq, cpu_core_loader_cpucl_3_load_0[0]);
  Register #(.width(1)) register_40 (
    .D(Power), .en(and_57_out), .Q(register_39_q[1]), .clk(clock_1_out), .clr(or_40_out));
  or or_36 (or_36_out, counter_11_carry, comparator_31_eq, comparator_31_lt);
  and and_57 (and_57_out, comparator_32_eq, cpu_core_loader_cpucl_3_load_0[1]);
  Register #(.width(1)) register_41 (
    .D(Power), .en(and_58_out), .Q(register_39_q[2]), .clk(clock_1_out), .clr(or_41_out));
  or or_37 (or_37_out, counter_12_carry, comparator_34_eq, comparator_34_lt);
  and and_58 (and_58_out, comparator_35_eq, cpu_core_loader_cpucl_3_load_0[2]);
  Register #(.width(1)) register_42 (
    .D(Power), .en(and_59_out), .Q(register_39_q[3]), .clk(clock_1_out), .clr(or_42_out));
  or or_38 (or_38_out, counter_13_carry, comparator_37_eq, comparator_37_lt);
  and and_59 (and_59_out, comparator_38_eq, cpu_core_loader_cpucl_3_load_0[3]);
  or or_39 (or_39_out, and_60_out, and_61_out, or_19_out[0]);
  and and_60 (and_60_out, or_35_out, ~comparator_29_eq, ~comparator_30_eq, ~cpu_core_loader_cpucl_3_load_0[0]);  // AND_Gate
  and and_61 (and_61_out, ~comparator_29_eq, comparator_30_eq);  // AND_Gate
  or or_40 (or_40_out, and_62_out, and_63_out, or_19_out[1]);
  and and_62 (and_62_out, or_36_out, ~comparator_32_eq, ~comparator_33_eq, ~cpu_core_loader_cpucl_3_load_0[1]);  // AND_Gate
  and and_63 (and_63_out, ~comparator_32_eq, comparator_33_eq);  // AND_Gate
  or or_41 (or_41_out, and_64_out, and_65_out, or_19_out[2]);
  and and_64 (and_64_out, or_37_out, ~comparator_35_eq, ~comparator_36_eq, ~cpu_core_loader_cpucl_3_load_0[2]);  // AND_Gate
  and and_65 (and_65_out, ~comparator_35_eq, comparator_36_eq);  // AND_Gate
  or or_42 (or_42_out, and_66_out, and_67_out, or_19_out[3]);
  and and_66 (and_66_out, or_38_out, ~comparator_38_eq, ~comparator_39_eq, ~cpu_core_loader_cpucl_3_load_0[3]);  // AND_Gate
  and and_67 (and_67_out, ~comparator_38_eq, comparator_39_eq);  // AND_Gate
  assign bit_extender_9_out = {{16{1'b0}}, counter_10_q};  // Bit_Extender bit_extender_9
  assign bit_extender_10_out = {{16{1'b0}}, counter_11_q};  // Bit_Extender bit_extender_10
  assign bit_extender_11_out = {{16{1'b0}}, counter_12_q};  // Bit_Extender bit_extender_11
  CPU_Core_Loader__CPUCL cpu_core_loader_cpucl_4 (
    .Clk(clock_1_out), .Cond_0(Occured__12), .Cond_1(Occured__13), .Cond_2(Occured__14),
    .Cond_3(Occured__15), .Load(undriven_69), .in_7(undriven_68), .Power(Power),
    .Load_cond_0(register_47_q[0]), .Load_cond_1(register_47_q[1]), .Load_cond_2(register_47_q[2]),
    .Load_cond_3(register_47_q[3]), .Data_in(undriven_67), .Load_0(cpu_core_loader_cpucl_4_load_0[0]),
    .Load_1(cpu_core_loader_cpucl_4_load_0[1]), .Load_2(cpu_core_loader_cpucl_4_load_0[2]),
    .Load_3(cpu_core_loader_cpucl_4_load_0[3]), .Data_out(cpu_core_loader_cpucl_4_data_out));
  assign bit_extender_12_out = {{16{1'b0}}, counter_13_q};  // Bit_Extender bit_extender_12
  Counter #(.width(16), .max('hffff)) counter_14 (
    .load(cpu_core_loader_cpucl_4_load_0[0]), .D(cpu_core_loader_cpucl_4_data_out[15:0]), .count(and_68_out),
    .Q(counter_14_q), .carry(counter_14_carry), .clk(clock_1_out), .clr(or_47_out));
  and and_68 (and_68_out, ~cpu_core_loader_cpucl_4_load_0[0], register_47_q[0]);  // AND_Gate
  Register #(.width(16)) register_43 (
    .D(cpu_core_loader_cpucl_4_data_out[31:16]), .en(cpu_core_loader_cpucl_4_load_0[0]), .Q(register_43_q),
    .clk(clock_1_out), .clr(or_47_out));
  Comparator #(.width(16), .mode("unsigned")) comparator_40 (
    .a(register_43_q), .b(counter_14_q), .eq(comparator_40_eq), .lt(comparator_40_lt));  // open: gt
  Comparator #(.width(16), .mode("unsigned")) comparator_41 (
    .a(counter_14_q), .b({16{1'b0}}), .eq(comparator_41_eq));  // open: gt, lt
  Comparator #(.width(16), .mode("unsigned")) comparator_42 (
    .a(register_43_q), .b({16{1'b0}}), .eq(comparator_42_eq));  // open: gt, lt
  Counter #(.width(16), .max('hffff)) counter_15 (
    .load(cpu_core_loader_cpucl_4_load_0[1]), .D(cpu_core_loader_cpucl_4_data_out[15:0]), .count(and_69_out),
    .Q(counter_15_q), .carry(counter_15_carry), .clk(clock_1_out), .clr(or_48_out));
  and and_69 (and_69_out, ~cpu_core_loader_cpucl_4_load_0[1], register_47_q[1]);  // AND_Gate
  Register #(.width(16)) register_44 (
    .D(cpu_core_loader_cpucl_4_data_out[31:16]), .en(cpu_core_loader_cpucl_4_load_0[1]), .Q(register_44_q),
    .clk(clock_1_out), .clr(or_48_out));
  Comparator #(.width(16), .mode("unsigned")) comparator_43 (
    .a(register_44_q), .b(counter_15_q), .eq(comparator_43_eq), .lt(comparator_43_lt));  // open: gt
  Comparator #(.width(16), .mode("unsigned")) comparator_44 (
    .a(counter_15_q), .b({16{1'b0}}), .eq(comparator_44_eq));  // open: gt, lt
  Comparator #(.width(16), .mode("unsigned")) comparator_45 (
    .a(register_44_q), .b({16{1'b0}}), .eq(comparator_45_eq));  // open: gt, lt
  Counter #(.width(16), .max('hffff)) counter_16 (
    .load(cpu_core_loader_cpucl_4_load_0[2]), .D(cpu_core_loader_cpucl_4_data_out[15:0]), .count(and_70_out),
    .Q(counter_16_q), .carry(counter_16_carry), .clk(clock_1_out), .clr(or_49_out));
  and and_70 (and_70_out, ~cpu_core_loader_cpucl_4_load_0[2], register_47_q[2]);  // AND_Gate
  Register #(.width(16)) register_45 (
    .D(cpu_core_loader_cpucl_4_data_out[31:16]), .en(cpu_core_loader_cpucl_4_load_0[2]), .Q(register_45_q),
    .clk(clock_1_out), .clr(or_49_out));
  Comparator #(.width(16), .mode("unsigned")) comparator_46 (
    .a(register_45_q), .b(counter_16_q), .eq(comparator_46_eq), .lt(comparator_46_lt));  // open: gt
  Comparator #(.width(16), .mode("unsigned")) comparator_47 (
    .a(counter_16_q), .b({16{1'b0}}), .eq(comparator_47_eq));  // open: gt, lt
  Comparator #(.width(16), .mode("unsigned")) comparator_48 (
    .a(register_45_q), .b({16{1'b0}}), .eq(comparator_48_eq));  // open: gt, lt
  Counter #(.width(16), .max('hffff)) counter_17 (
    .load(cpu_core_loader_cpucl_4_load_0[3]), .D(cpu_core_loader_cpucl_4_data_out[15:0]), .count(and_71_out),
    .Q(counter_17_q), .carry(counter_17_carry), .clk(clock_1_out), .clr(or_50_out));
  and and_71 (and_71_out, ~cpu_core_loader_cpucl_4_load_0[3], register_47_q[3]);  // AND_Gate
  Register #(.width(16)) register_46 (
    .D(cpu_core_loader_cpucl_4_data_out[31:16]), .en(cpu_core_loader_cpucl_4_load_0[3]), .Q(register_46_q),
    .clk(clock_1_out), .clr(or_50_out));
  Comparator #(.width(16), .mode("unsigned")) comparator_49 (
    .a(register_46_q), .b(counter_17_q), .eq(comparator_49_eq), .lt(comparator_49_lt));  // open: gt
  Comparator #(.width(16), .mode("unsigned")) comparator_50 (
    .a(counter_17_q), .b({16{1'b0}}), .eq(comparator_50_eq));  // open: gt, lt
  Comparator #(.width(16), .mode("unsigned")) comparator_51 (
    .a(register_46_q), .b({16{1'b0}}), .eq(comparator_51_eq));  // open: gt, lt
  Register #(.width(1)) register_47 (
    .D(Power), .en(and_72_out), .Q(register_47_q[0]), .clk(clock_1_out), .clr(or_47_out));
  or or_43 (or_43_out, counter_14_carry, comparator_40_eq, comparator_40_lt);
  and and_72 (and_72_out, comparator_41_eq, cpu_core_loader_cpucl_4_load_0[0]);
  Register #(.width(1)) register_48 (
    .D(Power), .en(and_73_out), .Q(register_47_q[1]), .clk(clock_1_out), .clr(or_48_out));
  or or_44 (or_44_out, counter_15_carry, comparator_43_eq, comparator_43_lt);
  and and_73 (and_73_out, comparator_44_eq, cpu_core_loader_cpucl_4_load_0[1]);
  Register #(.width(1)) register_49 (
    .D(Power), .en(and_74_out), .Q(register_47_q[2]), .clk(clock_1_out), .clr(or_49_out));
  or or_45 (or_45_out, counter_16_carry, comparator_46_eq, comparator_46_lt);
  and and_74 (and_74_out, comparator_47_eq, cpu_core_loader_cpucl_4_load_0[2]);
  Register #(.width(1)) register_50 (
    .D(Power), .en(and_75_out), .Q(register_47_q[3]), .clk(clock_1_out), .clr(or_50_out));
  or or_46 (or_46_out, counter_17_carry, comparator_49_eq, comparator_49_lt);
  and and_75 (and_75_out, comparator_50_eq, cpu_core_loader_cpucl_4_load_0[3]);
  or or_47 (or_47_out, and_76_out, and_77_out, or_31_out[0]);
  and and_76 (and_76_out, or_43_out, ~comparator_41_eq, ~comparator_42_eq, ~cpu_core_loader_cpucl_4_load_0[0]);  // AND_Gate
  and and_77 (and_77_out, ~comparator_41_eq, comparator_42_eq);  // AND_Gate
  or or_48 (or_48_out, and_78_out, and_79_out, or_31_out[1]);
  and and_78 (and_78_out, or_44_out, ~comparator_44_eq, ~comparator_45_eq, ~cpu_core_loader_cpucl_4_load_0[1]);  // AND_Gate
  and and_79 (and_79_out, ~comparator_44_eq, comparator_45_eq);  // AND_Gate
  or or_49 (or_49_out, and_80_out, and_81_out, or_31_out[2]);
  and and_80 (and_80_out, or_45_out, ~comparator_47_eq, ~comparator_48_eq, ~cpu_core_loader_cpucl_4_load_0[2]);  // AND_Gate
  and and_81 (and_81_out, ~comparator_47_eq, comparator_48_eq);  // AND_Gate
  or or_50 (or_50_out, and_82_out, and_83_out, or_31_out[3]);
  and and_82 (and_82_out, or_46_out, ~comparator_50_eq, ~comparator_51_eq, ~cpu_core_loader_cpucl_4_load_0[3]);  // AND_Gate
  and and_83 (and_83_out, ~comparator_50_eq, comparator_51_eq);  // AND_Gate
  assign bit_extender_13_out = {{16{1'b0}}, counter_14_q};  // Bit_Extender bit_extender_13
  assign bit_extender_14_out = {{16{1'b0}}, counter_15_q};  // Bit_Extender bit_extender_14
  assign bit_extender_15_out = {{16{1'b0}}, counter_16_q};  // Bit_Extender bit_extender_15
  assign bit_extender_16_out = {{16{1'b0}}, counter_17_q};  // Bit_Extender bit_extender_16

  // Notes on the sheet:
  //   power
  //   clk
  //   0
  //   1
  //   2
  //   3
  //   load
  //   Data out
  //   4
  //   5
  //   6
  //   7
  //   память приоритетов
  //   8
  //   9
  //   10
  //   11
  //   12
  //   13
  //   14
  //   15
endmodule

module CPU_Core_Loader__CPUCL (
  input  Clk,
  input  Cond_0,
  input  Cond_1,
  input  Cond_2,
  input  Cond_3,
  input  Load,
  input  [1:0] in_7,
  input  Power,
  input  Load_cond_0,
  input  Load_cond_1,
  input  Load_cond_2,
  input  Load_cond_3,
  input  [31:0] Data_in,
  output Load_0,
  output Load_1,
  output Load_2,
  output Load_3,
  output [31:0] Data_out
);

  wire and_1_out, and_2_out, and_3_out, comparator_1_eq, not_1_out, not_2_out, not_3_out, not_4_out,
       not_5_out, not_6_out, not_7_out, not_8_out, or_1_out, or_2_out, or_3_out, or_4_out, register_1_q;
  wire [1:0] counter_1_q;
  wire [31:0] multiplexer_1_out, pull_resistor_14_node;

  Pull_Resistor pull_resistor_1 (.node(Cond_1));
  Pull_Resistor pull_resistor_2 (.node(Clk));
  Pull_Resistor pull_resistor_3 (.node(Cond_0));
  not not_1 (not_1_out, Cond_0);
  not not_2 (not_2_out, Cond_1);
  Pull_Resistor pull_resistor_4 (.node(in_7));
  Pull_Resistor pull_resistor_5 (.node(Power));
  Pull_Resistor pull_resistor_6 (.node(Load_cond_0));
  Pull_Resistor pull_resistor_7 (.node(Load_cond_1));
  Pull_Resistor pull_resistor_8 (.node(Load_cond_2));
  Pull_Resistor pull_resistor_9 (.node(Load_cond_3));
  Pull_Resistor pull_resistor_10 (.node(Data_in));
  Pull_Resistor pull_resistor_11 (.node(Cond_2));
  Pull_Resistor pull_resistor_12 (.node(Cond_3));
  not not_3 (not_3_out, Cond_3);
  not not_4 (not_4_out, Cond_2);
  or or_1 (or_1_out, ~Cond_3, ~Cond_2, ~Cond_1, ~Cond_0);  // OR_Gate
  Pull_Resistor pull_resistor_13 (.node(Load));
  and and_1 (and_1_out, Load, ~register_1_q);  // AND_Gate
  Counter #(.width(2), .max('h3)) counter_1 (
    .load(Load), .D(in_7), .count(and_2_out), .Q(counter_1_q), .clk(Clk), .clr(not_8_out));  // open: carry
  and and_2 (and_2_out, or_1_out, comparator_1_eq, ~Load);  // AND_Gate
  Register #(.width(1)) register_1 (.D(and_1_out), .en(or_2_out), .Q(register_1_q), .clk(Clk), .clr(not_8_out));
  or or_2 (or_2_out, Load, register_1_q);
  Multiplexer #(.width(32), .disabled(0)) multiplexer_1 (
    .in0(Data_in), .in1({32{1'b0}}), .out(multiplexer_1_out), .sel(or_4_out), .en(Power));
  not not_5 (not_5_out, or_3_out);
  or or_3 (or_3_out, register_1_q, and_3_out);
  and and_3 (and_3_out, or_4_out, not_6_out);
  or or_4 (or_4_out, Load_3, Load_1, Load_2, Load_0);
  not not_6 (not_6_out, Clk);
  and and_4 (Load_0, not_1_out, ~comparator_1_eq, ~Load_cond_0);  // AND_Gate
  and and_5 (Load_1, not_2_out, ~comparator_1_eq, ~Load_cond_1);  // AND_Gate
  and and_6 (Load_2, not_4_out, ~comparator_1_eq, ~Load_cond_2);  // AND_Gate
  and and_7 (Load_3, not_3_out, ~comparator_1_eq, ~Load_cond_3);  // AND_Gate
  Pull_Resistor pull_resistor_14 (.node(pull_resistor_14_node));
  RAM #(.addrWidth(2), .dataWidth(32), .bus("separate")) ram_1 (
    .addr(counter_1_q), .din(multiplexer_1_out), .data(pull_resistor_14_node), .str(or_3_out), .sel(Power),
    .clk(Clk), .ld(not_5_out), .clr(not_8_out));
  Comparator #(.width(32), .mode("unsigned")) comparator_1 (
    .a({32{1'b0}}), .b(Data_out), .eq(comparator_1_eq));  // open: gt, lt
  Register #(.width(32)) register_2 (
    .D(pull_resistor_14_node), .en(Power), .Q(Data_out), .clk(not_7_out), .clr(not_8_out));
  not not_7 (not_7_out, Clk);
  not not_8 (not_8_out, Power);
endmodule
